// Logisim project M1_v0.1.5_single_cycle.circ as structural Verilog: 19 circuits, main circuit main
module main (
  input  srn
);

  wire b, clk, ecall, intr, m1b_if_1_is_branch, m1b_if_1_is_jal, m1b_if_1_is_jalr, misalign, ram_we, rd_we,
       unknown;
  wire [2:0] m1b_if_1_instr_3;
  wire [3:0] ram_be;
  wire [4:0] m1b_ex_1_rs2_sel, m1b_if_1_instr_2, m1b_if_1_instr_4, m1b_if_1_instr_5, rd_sel, rs1_sel, rs2_sel;
  wire [6:0] m1b_if_1_instr, m1b_if_1_instr_6;
  wire [7:0] m1b_ex_1_mem_ctrl, m1b_ex_1_wb_ctrl, m1b_id_1_ex_ctrl, m1b_id_1_mem_ctrl, m1b_id_1_wb_ctrl,
       m1b_mem_1_wb_ctrl;
  wire [9:0] ram_1_p1;
  wire [31:0] a, m1b_ex_1_m, m1b_ex_1_pc, m1b_id_1_a1, m1b_id_1_a2, m1b_id_1_b1, m1b_id_1_b2, m1b_id_1_m,
       m1b_id_1_pc, m1b_if_1_pc, m1b_mem_1_a, m1b_mem_1_m, ram_adr, ram_din, ram_dout, rd_dat, reg_rs1,
       reg_rs2, rom_adr, rom_dout;

  // Probe on m1b_if_1_instr_6
  // Probe on m1b_if_1_instr_5
  Clock u_clk (.out(clk));
  // Probe on m1b_if_1_instr_4
  // Probe on m1b_if_1_instr_3
  // Probe on m1b_if_1_instr_2
  ROM #(.dataWidth(32)) rom_1 (.addr(rom_adr[9:2]), .data(rom_dout));
  // Probe on m1b_if_1_instr
  // Probe on m1b_if_1_pc
  M1B_IF m1b_if_1 (
    .instr({m1b_if_1_instr_6, m1b_if_1_instr_5, m1b_if_1_instr_4, m1b_if_1_instr_3, m1b_if_1_instr_2, m1b_if_1_instr}),
    .is_branch(m1b_if_1_is_branch), .is_jal(m1b_if_1_is_jal), .is_jalr(m1b_if_1_is_jalr), .is_ecall(ecall),
    .pc(m1b_if_1_pc), .rom_adr(rom_adr), .pred_adr({32{1'b0}}), .jump_adr(a), .intr_adr(32'hf100),
    .stall_n(1'b1), .pred(1'b0), .jump(b), .intr(intr), .pc_we(1'b1), .pc_srn(srn), .clk(clk),
    .rom_dout(rom_dout));
  or or_1 (intr, unknown, ecall, misalign);
  // Probe on misalign
  // Probe on unknown
  // Probe on m1b_id_1_b1
  // Probe on m1b_id_1_b2
  // Probe on m1b_id_1_a1
  // Probe on m1b_id_1_a2
  M1B_ID m1b_id_1 (
    .unknown(unknown), .pc(m1b_id_1_pc), .EX_ctrl(m1b_id_1_ex_ctrl), .MEM_ctrl(m1b_id_1_mem_ctrl),
    .WB_ctrl(m1b_id_1_wb_ctrl), .rs1_sel(rs1_sel), .rs2_sel(rs2_sel), .b1(m1b_id_1_b1), .a1(m1b_id_1_a1),
    .a2(m1b_id_1_a2), .b2(m1b_id_1_b2), .m(m1b_id_1_m),
    .instr({m1b_if_1_instr_6, m1b_if_1_instr_5, m1b_if_1_instr_4, m1b_if_1_instr_3, m1b_if_1_instr_2, m1b_if_1_instr}),
    .is_branch(m1b_if_1_is_branch), .is_jal(m1b_if_1_is_jal), .is_jalr(m1b_if_1_is_jalr),
    .pc_in(m1b_if_1_pc), .rs1_src(reg_rs1), .rs2_src(reg_rs2));
  M1B_EX m1b_ex_1 (
    .pc(m1b_ex_1_pc), .b(b), .a(a), .m(m1b_ex_1_m), .MEM_ctrl(m1b_ex_1_mem_ctrl), .WB_ctrl(m1b_ex_1_wb_ctrl),
    .rs2_sel(m1b_ex_1_rs2_sel), .pc_in(m1b_id_1_pc), .rs2_sel_in(rs2_sel), .b1(m1b_id_1_b1),
    .b2(m1b_id_1_b2), .a1(m1b_id_1_a1), .a2(m1b_id_1_a2), .m_in(m1b_id_1_m), .EX_ctrl_in(m1b_id_1_ex_ctrl),
    .MEM_ctrl_in(m1b_id_1_mem_ctrl), .WB_ctrl_in(m1b_id_1_wb_ctrl));
  // Probe on ram_adr
  // Probe on ram_we
  // Probe on ram_be
  // Probe on ram_din
  // Probe on b
  // Probe on a
  // Probe on m1b_ex_1_m
  // NoConnect on m1b_ex_1_rs2_sel
  // RAM #(.addrWidth(10), .enables("line"), .line("quad"), .misaligned("true")) ram_1: pin names not known; wires that end beside it: ram_1_p1, ram_we, clk
  BitSelector #(.group(10), .width(32)) bitselector_1 (.in(ram_adr), .out(ram_1_p1), .sel(2'b00));
  M1B_MEM m1b_mem_1 (
    .WB_ctrl(m1b_mem_1_wb_ctrl), .a(m1b_mem_1_a), .ram_adr(ram_adr), .ram_we(ram_we), .ram_be(ram_be),
    .ram_din(ram_din), .m(m1b_mem_1_m), .misalign(misalign), .pc(m1b_ex_1_pc), .a_in(a), .m_in(m1b_ex_1_m),
    .MEM_ctrl_in(m1b_ex_1_mem_ctrl), .WB_ctrl_in(m1b_ex_1_wb_ctrl), .ram_dout(ram_dout));
  // Probe on ram_dout
  M1A_WB m1a_wb_1 (
    .rd_data(rd_dat), .rd_sel(rd_sel), .rd_we(rd_we), .a_in(m1b_mem_1_a), .m_in(m1b_mem_1_m),
    .WB_ctrl_in(m1b_mem_1_wb_ctrl));
  M1A_reg_file m1a_reg_file_1 (
    .rs2(reg_rs2), .rs1(reg_rs1), .rs2_sel(rs2_sel), .rs1_sel(rs1_sel), .rd_we(rd_we), .srn(srn), .clk(clk),
    .rd_sel(rd_sel), .rd_data(rd_dat));

  // Other names for the same wires on the sheet: jump = b; jump_adr[31:0] = a; rs1_src[31:0] = reg_rs1;
  //   rs2_src[31:0] = reg_rs2

  // Notes on the sheet:
  //   contents of rom_1 (hex, n*v repeats v):
  //   100006f 100513 2a00593 73 100093 20c113 416193 51f213 121293 12d313 40135393 fff3a413 fff43493
  //   1080b3 214133 21e1b3 327233 1292b3 135333 4013d3b3 3a433 434b3 100116b7 110717 168023 269123 36a223
  //   68503 269583 46a603 f8008ce3 fa109ce3 fc10cce3 fc10eae3 fe1058e3 fe1076e3 4007ef 4007e7
endmodule

module M1A_reg32 (
  input  [31:0] d,
  input  we,
  input  srn,
  input  clk,
  output [31:0] q
);

  wire [31:0] multiplexer_1_out;

  Multiplexer #(.width(32)) multiplexer_1 (.in0({32{1'b0}}), .in1(d), .out(multiplexer_1_out), .sel(srn));
  Register #(.width(32)) register_1 (.D(multiplexer_1_out), .en(we), .clk(clk), .Q(q));  // open: clr
endmodule

module M1A_pc_nxt (
  input  [31:0] pc,
  input  [31:0] pred_adr,
  input  [31:0] jump_adr,
  input  [31:0] intr_adr,
  input  stall_n,
  input  pred,
  input  jump,
  input  intr,
  output [31:0] nxt
);

  wire [31:0] adder_1_out, multiplexer_1_out, multiplexer_2_out, multiplexer_3_out;

  Adder #(.width(32)) adder_1 (.a(pc), .b(32'h4), .out(adder_1_out));  // open: cin, cout
  Multiplexer #(.width(32)) multiplexer_1 (.in0(pc), .in1(adder_1_out), .out(multiplexer_1_out), .sel(stall_n));
  Multiplexer #(.width(32)) multiplexer_2 (
    .in0(multiplexer_1_out), .in1(pred_adr), .out(multiplexer_2_out), .sel(pred));
  Multiplexer #(.width(32)) multiplexer_3 (
    .in0(multiplexer_2_out), .in1(jump_adr), .out(multiplexer_3_out), .sel(jump));
  Multiplexer #(.width(32)) multiplexer_4 (.in0(multiplexer_3_out), .in1(intr_adr), .out(nxt), .sel(intr));
endmodule

module M1A_mem_instr (
  input  [31:0] pc,
  output [31:0] instr
);

  ROM #(.dataWidth(32)) rom_1 (.addr(pc[9:2]), .data(instr));

  // Notes on the sheet:
  //   contents of rom_1 (hex, n*v repeats v):
  //   100006f 100513 2a00593 73 100093 20c113 416193 51f213 121293 12d313 40135393 fff3a413 fff43493
  //   1080b3 214133 21e1b3 327233 1292b3 135333 4013d3b3 3a433 434b3 100116b7 110717 168023 269123 36a223
  //   68503 269583 46a603 f8008ce3 fa109ce3 fc10cce3 fc10eae3 fe1058e3 fe1076e3 4007ef 4007e7
endmodule

module M1A_bj_type (
  input  [31:0] instr,
  output is_branch,
  output is_jal,
  output is_jalr
);

  wire [6:0] bitselector_1_out;

  BitSelector #(.group(7), .width(32)) bitselector_1 (.in(instr), .out(bitselector_1_out), .sel(3'b000));
  and and_1 (is_branch, bitselector_1_out[0], bitselector_1_out[1], ~bitselector_1_out[2], ~bitselector_1_out[3], ~bitselector_1_out[4], bitselector_1_out[5], bitselector_1_out[6]);  // AND_Gate
  and and_2 (is_jal, bitselector_1_out[0], bitselector_1_out[1], bitselector_1_out[2], bitselector_1_out[3], ~bitselector_1_out[4], bitselector_1_out[5], bitselector_1_out[6]);  // AND_Gate
  and and_3 (is_jalr, bitselector_1_out[0], bitselector_1_out[1], bitselector_1_out[2], ~bitselector_1_out[3], ~bitselector_1_out[4], bitselector_1_out[5], bitselector_1_out[6]);  // AND_Gate

  // Notes on the sheet:
  //   Branch：1100011 
  //   jal：1101111
  //   jalr：1100111
endmodule

module M1B_IF (
  input  [31:0] pred_adr,
  input  [31:0] jump_adr,
  input  [31:0] intr_adr,
  input  stall_n,
  input  pred,
  input  jump,
  input  intr,
  input  pc_we,
  input  pc_srn,
  input  clk,
  input  [31:0] rom_dout,
  output [31:0] pc,
  output [31:0] rom_adr,
  output [31:0] instr,
  output is_branch,
  output is_jal,
  output is_jalr,
  output is_ecall
);

  wire [6:0] bitselector_1_out;
  wire [31:0] m1a_pc_nxt_1_nxt;

  BitSelector #(.group(7), .width(32)) bitselector_1 (.in(rom_dout), .out(bitselector_1_out), .sel(3'b000));
  M1A_pc_nxt m1a_pc_nxt_1 (
    .nxt(m1a_pc_nxt_1_nxt), .pred_adr(pred_adr), .jump_adr(jump_adr), .intr_adr(intr_adr), .pc(pc),
    .stall_n(stall_n), .pred(pred), .jump(jump), .intr(intr));
  M1A_bj_type m1a_bj_type_1 (.is_branch(is_branch), .is_jal(is_jal), .is_jalr(is_jalr), .instr(rom_dout));
  and and_1 (is_ecall, bitselector_1_out[0], bitselector_1_out[1], ~bitselector_1_out[2], ~bitselector_1_out[3], bitselector_1_out[4], bitselector_1_out[5], bitselector_1_out[6]);  // AND_Gate
  M1A_reg32 m1a_reg32_1 (.q(pc), .srn(pc_srn), .d(m1a_pc_nxt_1_nxt), .we(pc_we), .clk(clk));

  assign instr = rom_dout;
  assign rom_adr = pc;

  // Notes on the sheet:
  //   opcode = 1110011
endmodule

module M1A_reg_file (
  input  [31:0] rd_data,
  input  srn,
  input  rd_we,
  input  [4:0] rd_sel,
  input  clk,
  input  [4:0] rs1_sel,
  input  [4:0] rs2_sel,
  output [31:0] rs1,
  output [31:0] rs2
);

  wire demultiplexer_1_out16, demultiplexer_1_out17, demultiplexer_1_out18, demultiplexer_1_out19,
       demultiplexer_1_out20, demultiplexer_1_out21, demultiplexer_1_out22, demultiplexer_1_out23,
       demultiplexer_1_out24, demultiplexer_1_out25, demultiplexer_1_out26, demultiplexer_1_out27,
       demultiplexer_1_out28, demultiplexer_1_out29, demultiplexer_1_out30, demultiplexer_1_out31, w0, w1,
       w2, w3, w4, w5, w6, w7, w8, w9, w10, w11, w12, w13, w14, w15;
  wire [15:0] bit_extender_1_out, demultiplexer_1_out0;
  wire [31:0] multiplexer_1_out, x1, x2, x3, x4, x5, x6, x7, x8, x9, x10, x11, x12, x13, x14, x15;

  Demultiplexer #(.select(5)) demultiplexer_1 (
    .out0(demultiplexer_1_out0[0]), .out1(demultiplexer_1_out0[1]), .out2(demultiplexer_1_out0[2]),
    .out3(demultiplexer_1_out0[3]), .out4(demultiplexer_1_out0[4]), .out5(demultiplexer_1_out0[5]),
    .out6(demultiplexer_1_out0[6]), .out7(demultiplexer_1_out0[7]), .out8(demultiplexer_1_out0[8]),
    .out9(demultiplexer_1_out0[9]), .out10(demultiplexer_1_out0[10]), .out11(demultiplexer_1_out0[11]),
    .out12(demultiplexer_1_out0[12]), .out13(demultiplexer_1_out0[13]), .out14(demultiplexer_1_out0[14]),
    .out15(demultiplexer_1_out0[15]), .out16(demultiplexer_1_out16), .out17(demultiplexer_1_out17),
    .out18(demultiplexer_1_out18), .out19(demultiplexer_1_out19), .out20(demultiplexer_1_out20),
    .out21(demultiplexer_1_out21), .out22(demultiplexer_1_out22), .out23(demultiplexer_1_out23),
    .out24(demultiplexer_1_out24), .out25(demultiplexer_1_out25), .out26(demultiplexer_1_out26),
    .out27(demultiplexer_1_out27), .out28(demultiplexer_1_out28), .out29(demultiplexer_1_out29),
    .out30(demultiplexer_1_out30), .out31(demultiplexer_1_out31), .in(rd_we), .sel(rd_sel));
  assign bit_extender_1_out = {{15{srn}}, srn};  // Bit_Extender bit_extender_1
  Multiplexer #(.width(32)) multiplexer_1 (.in0({32{1'b0}}), .in1(rd_data), .out(multiplexer_1_out), .sel(srn));
  assign {w15, w14, w13, w12, w11, w10, w9, w8, w7, w6, w5, w4, w3, w2, w1, w0} = ~bit_extender_1_out | demultiplexer_1_out0;  // OR_Gate or_1, 16 bits wide
  // NoConnect on w0
  Register #(.width(32)) register_1 (.D(multiplexer_1_out), .en(w1), .clk(clk), .Q(x1));  // open: clr
  Register #(.width(32)) register_2 (.D(multiplexer_1_out), .en(w2), .clk(clk), .Q(x2));  // open: clr
  Register #(.width(32)) register_3 (.D(multiplexer_1_out), .en(w3), .clk(clk), .Q(x3));  // open: clr
  Register #(.width(32)) register_4 (.D(multiplexer_1_out), .en(w4), .clk(clk), .Q(x4));  // open: clr
  Register #(.width(32)) register_5 (.D(multiplexer_1_out), .en(w5), .clk(clk), .Q(x5));  // open: clr
  Register #(.width(32)) register_6 (.D(multiplexer_1_out), .en(w6), .clk(clk), .Q(x6));  // open: clr
  Register #(.width(32)) register_7 (.D(multiplexer_1_out), .en(w7), .clk(clk), .Q(x7));  // open: clr
  Register #(.width(32)) register_8 (.D(multiplexer_1_out), .en(w8), .clk(clk), .Q(x8));  // open: clr
  Register #(.width(32)) register_9 (.D(multiplexer_1_out), .en(w9), .clk(clk), .Q(x9));  // open: clr
  Register #(.width(32)) register_10 (.D(multiplexer_1_out), .en(w10), .clk(clk), .Q(x10));  // open: clr
  Register #(.width(32)) register_11 (.D(multiplexer_1_out), .en(w11), .clk(clk), .Q(x11));  // open: clr
  Register #(.width(32)) register_12 (.D(multiplexer_1_out), .en(w12), .clk(clk), .Q(x12));  // open: clr
  Register #(.width(32)) register_13 (.D(multiplexer_1_out), .en(w13), .clk(clk), .Q(x13));  // open: clr
  Register #(.width(32)) register_14 (.D(multiplexer_1_out), .en(w14), .clk(clk), .Q(x14));  // open: clr
  Register #(.width(32)) register_15 (.D(multiplexer_1_out), .en(w15), .clk(clk), .Q(x15));  // open: clr
  Multiplexer #(.select(4), .width(32)) multiplexer_2 (
    .in0({32{1'b0}}), .in1(x1), .in2(x2), .in3(x3), .in4(x4), .in5(x5), .in6(x6), .in7(x7), .in8(x8),
    .in9(x9), .in10(x10), .in11(x11), .in12(x12), .in13(x13), .in14(x14), .in15(x15), .out(rs1),
    .sel(rs1_sel[3:0]));
  Multiplexer #(.select(4), .width(32)) multiplexer_3 (
    .in0({32{1'b0}}), .in1(x1), .in2(x2), .in3(x3), .in4(x4), .in5(x5), .in6(x6), .in7(x7), .in8(x8),
    .in9(x9), .in10(x10), .in11(x11), .in12(x12), .in13(x13), .in14(x14), .in15(x15), .out(rs2),
    .sel(rs2_sel[3:0]));
endmodule

module M1A_imm_gen (
  input  [31:0] instr,
  output [31:0] imm_I,
  output [31:0] imm_S,
  output [31:0] imm_B,
  output [31:0] imm_U,
  output [31:0] imm_J
);

  assign imm_I = {{20{instr[31]}}, instr[31:20]};  // Bit_Extender bit_extender_1
  assign imm_S = {{20{instr[31]}}, {instr[31:25], instr[11:7]}};  // Bit_Extender bit_extender_2
  assign imm_B = {{19{instr[31]}}, {instr[31], instr[7], instr[30:25], instr[11:8], 1'b0}};  // Bit_Extender bit_extender_3
  assign imm_J = {{11{instr[31]}}, {instr[31], instr[19:12], instr[20], instr[30:21], 1'b0}};  // Bit_Extender bit_extender_4

  assign imm_U = {instr[31:12], {12{1'b0}}};

  // Notes on the sheet:
  //   I-type: code[31:20] = imm[11:0]
  //   S-type: code[31:25] = imm[11:5], code[11:7]=imm[4:0]
  //   U-type: code[31:12] = imm[31:12]
  //   J-type: code[31:25] = imm[20|10:1|11|19:12]
  //   B-type: code[31:25] = imm[12|10:5], code[11:7]=imm[4:1|11]
endmodule

module M1A_decoder (
  input  [31:0] instr,
  input  is_branch,
  input  is_jal,
  input  is_jalr,
  output [7:0] ID_ctrl,
  output [7:0] EX_ctrl,
  output [7:0] MEM_ctrl,
  output [7:0] WB_ctrl,
  output unknown,
  output [4:0] rs1_sel,
  output [4:0] rs2_sel
);

  wire bitselector_1_out, code_auipc, code_ecall, code_imm, or_1_out;
  wire [2:0] bit_extender_1_out;

  and and_1 (ID_ctrl[7], instr[0], instr[1], ~instr[2], ~instr[3], instr[4], instr[5], ~instr[6]);  // AND_Gate
  and and_2 (code_imm, instr[0], instr[1], ~instr[2], ~instr[3], instr[4], ~instr[5], ~instr[6]);  // AND_Gate
  and and_3 (WB_ctrl[6], instr[0], instr[1], ~instr[2], ~instr[3], ~instr[4], ~instr[5], ~instr[6]);  // AND_Gate
  and and_4 (ID_ctrl[1], instr[0], instr[1], ~instr[2], ~instr[3], ~instr[4], instr[5], ~instr[6]);  // AND_Gate
  and and_5 (ID_ctrl[6], instr[0], instr[1], instr[2], ~instr[3], instr[4], instr[5], ~instr[6]);  // AND_Gate
  and and_6 (code_auipc, instr[0], instr[1], instr[2], ~instr[3], instr[4], ~instr[5], ~instr[6]);  // AND_Gate
  and and_7 (code_ecall, instr[0], instr[1], ~instr[2], ~instr[3], instr[4], instr[5], instr[6]);  // AND_Gate
  nor nor_1 (unknown, ID_ctrl[7], code_imm, WB_ctrl[6], ID_ctrl[1], ID_ctrl[6], code_auipc, code_ecall, is_branch, is_jal, is_jalr);
  or or_1 (or_1_out, ID_ctrl[7], code_imm);
  or or_2 (ID_ctrl[0], code_imm, WB_ctrl[6], is_jalr);
  or or_3 (ID_ctrl[3], ID_ctrl[6], code_auipc);
  or or_4 (ID_ctrl[5], is_branch, is_jal, code_auipc);
  BitSelector #(.width(7)) bitselector_1 (.in(instr[31:25]), .out(bitselector_1_out), .sel(3'b101));
  assign bit_extender_1_out = {{2{or_1_out}}, or_1_out};  // Bit_Extender bit_extender_1
  or or_5 (MEM_ctrl[0], instr[12], instr[13]);
  not not_1 (MEM_ctrl[2], instr[14]);
  and and_8 (EX_ctrl[3], bitselector_1_out, or_1_out);
  assign EX_ctrl[2:0] = bit_extender_1_out & instr[14:12];  // AND_Gate and_9, 3 bits wide
  or or_6 (WB_ctrl[5], WB_ctrl[6], ID_ctrl[7], code_imm, is_jal, is_jalr, ID_ctrl[6], code_auipc);

  assign EX_ctrl[6:4] = instr[14:12];
  assign {ID_ctrl[4], ID_ctrl[2]} = {is_jal, is_branch};
  assign {MEM_ctrl[6:3], MEM_ctrl[1]} = {is_jalr, is_jal, is_branch, ID_ctrl[1], instr[13]};
  assign rs1_sel = instr[19:15];
  assign rs2_sel = instr[24:20];
  assign WB_ctrl[4:0] = instr[11:7];

  // Other names for the same wires on the sheet: alu_op[2:0] = EX_ctrl[2:0]; alu_neg = EX_ctrl[3];
  //   bcu_op[2:0] = instr[14:12]; funct3[2:0] = instr[14:12]; FMT_I = ID_ctrl[0]; FMT_U = ID_ctrl[3];
  //   alu_a_sel[1:0] = ID_ctrl[6:5]; code_lui = ID_ctrl[6]; alu_b_sel = ID_ctrl[7]; code_arith = ID_ctrl[7];
  //   opcode[6:0] = instr[6:0]; rs1[4:0] = instr[19:15]; rs2[4:0] = instr[24:20]; funct7[6:0] = instr[31:25];
  //   mask[1:0] = {instr[13], MEM_ctrl[0]}; ext = MEM_ctrl[2]; code_store = ID_ctrl[1]; FMT_S = ID_ctrl[1];
  //   is_store = ID_ctrl[1]; FMT_B = is_branch; FMT_J = is_jal; rd[4:0] = instr[11:7]; rd_sel[4:0] = instr[11:7];
  //   reg_we = WB_ctrl[5]; code_load = WB_ctrl[6]; is_load = WB_ctrl[6]

  // Notes on the sheet:
  //   Immediate：0010011
  //   Arithmetic：0110011
  //   Load：0000011
  //   Store：0100011
  //   lui：0110111
  //   auipc：0010111
  //   ecall：1110011 
endmodule

module M1A_imm_mux (
  input  [31:0] imm_I,
  input  [31:0] imm_S,
  input  [31:0] imm_B,
  input  [31:0] imm_U,
  input  [31:0] imm_J,
  input  [4:0] fmt,
  output [31:0] imm
);

  wire [31:0] and_1_out, and_2_out, and_3_out, and_4_out, and_5_out, FMT_B, FMT_I, FMT_J, FMT_S, FMT_U;

  assign FMT_I = {{31{fmt[0]}}, fmt[0]};  // Bit_Extender bit_extender_1
  assign FMT_S = {{31{fmt[1]}}, fmt[1]};  // Bit_Extender bit_extender_2
  assign FMT_B = {{31{fmt[2]}}, fmt[2]};  // Bit_Extender bit_extender_3
  assign FMT_U = {{31{fmt[3]}}, fmt[3]};  // Bit_Extender bit_extender_4
  assign FMT_J = {{31{fmt[4]}}, fmt[4]};  // Bit_Extender bit_extender_5
  assign and_1_out = FMT_I & imm_I;  // AND_Gate and_1, 32 bits wide
  assign and_2_out = FMT_S & imm_S;  // AND_Gate and_2, 32 bits wide
  assign and_3_out = FMT_B & imm_B;  // AND_Gate and_3, 32 bits wide
  assign and_4_out = FMT_U & imm_U;  // AND_Gate and_4, 32 bits wide
  assign and_5_out = FMT_J & imm_J;  // AND_Gate and_5, 32 bits wide
  assign imm = and_1_out | and_2_out | and_3_out | and_4_out | and_5_out;  // OR_Gate or_1, 32 bits wide
endmodule

module M1B_ID (
  input  [31:0] pc_in,
  input  [31:0] instr,
  input  is_branch,
  input  is_jal,
  input  is_jalr,
  input  [31:0] rs1_src,
  input  [31:0] rs2_src,
  output [31:0] pc,
  output [31:0] b1,
  output [31:0] a1,
  output unknown,
  output [7:0] EX_ctrl,
  output [7:0] MEM_ctrl,
  output [31:0] a2,
  output [7:0] WB_ctrl,
  output [31:0] b2,
  output [4:0] rs1_sel,
  output [4:0] rs2_sel,
  output [31:0] m
);

  wire alu_b_sel;
  wire [1:0] alu_a_sel;
  wire [4:0] m1a_decoder_1_id_ctrl;
  wire [31:0] imm, m1a_imm_gen_1_imm_b, m1a_imm_gen_1_imm_i, m1a_imm_gen_1_imm_j, m1a_imm_gen_1_imm_s,
       m1a_imm_gen_1_imm_u;

  M1A_imm_gen m1a_imm_gen_1 (
    .imm_I(m1a_imm_gen_1_imm_i), .imm_S(m1a_imm_gen_1_imm_s), .imm_B(m1a_imm_gen_1_imm_b),
    .imm_U(m1a_imm_gen_1_imm_u), .imm_J(m1a_imm_gen_1_imm_j), .instr(instr));
  M1A_decoder m1a_decoder_1 (
    .rs1_sel(rs1_sel), .rs2_sel(rs2_sel), .ID_ctrl({alu_b_sel, alu_a_sel, m1a_decoder_1_id_ctrl}),
    .EX_ctrl(EX_ctrl), .MEM_ctrl(MEM_ctrl), .WB_ctrl(WB_ctrl), .unknown(unknown), .instr(instr),
    .is_branch(is_branch), .is_jal(is_jal), .is_jalr(is_jalr));
  M1A_imm_mux m1a_imm_mux_1 (
    .imm(imm), .fmt(m1a_decoder_1_id_ctrl), .imm_I(m1a_imm_gen_1_imm_i), .imm_S(m1a_imm_gen_1_imm_s),
    .imm_B(m1a_imm_gen_1_imm_b), .imm_U(m1a_imm_gen_1_imm_u), .imm_J(m1a_imm_gen_1_imm_j));
  Multiplexer #(.select(2), .width(32)) multiplexer_1 (
    .in0(rs1_src), .in1(pc_in), .in2({32{1'b0}}), .in3({32{1'b0}}), .out(a1), .sel(alu_a_sel));
  Multiplexer #(.width(32)) multiplexer_2 (.in0(imm), .in1(rs2_src), .out(a2), .sel(alu_b_sel));

  assign b1 = rs1_src;
  assign b2 = rs2_src;
  assign m = rs2_src;
  assign pc = pc_in;

  // Other names for the same wires on the sheet: rs1[31:0] = rs1_src; rs2[31:0] = rs2_src
endmodule

module M1A_alu (
  input  [2:0] op,
  input  neg,
  input  [31:0] a1,
  input  [31:0] a2,
  output [31:0] a
);

  wire comparator_1_lt, comparator_2_lt;
  wire [31:0] adder_1_out, and_1_out, bit_extender_1_out, bit_extender_2_out, multiplexer_1_out,
       multiplexer_2_out, or_1_out, shifter_1_out, shifter_2_out, shifter_3_out, subtractor_1_out, xor_1_out;

  Adder #(.width(32)) adder_1 (.a(a1), .b(a2), .out(adder_1_out));  // open: cin, cout
  Subtractor #(.width(32)) subtractor_1 (.a(a1), .b(a2), .out(subtractor_1_out));  // open: bin, bout
  Shifter #(.width(32)) shifter_1 (.in(a1), .\dist (a2[4:0]), .out(shifter_1_out));
  Comparator #(.width(32)) comparator_1 (.a(a1), .b(a2), .lt(comparator_1_lt));  // open: gt, eq
  Comparator #(.mode("unsigned"), .width(32)) comparator_2 (.a(a1), .b(a2), .lt(comparator_2_lt));  // open: gt, eq
  assign xor_1_out = a1 ^ a2;  // XOR_Gate xor_1, 32 bits wide
  Shifter #(.shift("lr"), .width(32)) shifter_2 (.in(a1), .\dist (a2[4:0]), .out(shifter_2_out));
  Shifter #(.shift("ar"), .width(32)) shifter_3 (.in(a1), .\dist (a2[4:0]), .out(shifter_3_out));
  assign or_1_out = a1 | a2;  // OR_Gate or_1, 32 bits wide
  assign and_1_out = a1 & a2;  // AND_Gate and_1, 32 bits wide
  Multiplexer #(.width(32)) multiplexer_1 (
    .in0(adder_1_out), .in1(subtractor_1_out), .out(multiplexer_1_out), .sel(neg));
  assign bit_extender_1_out = {{31{1'b0}}, comparator_1_lt};  // Bit_Extender bit_extender_1
  assign bit_extender_2_out = {{31{1'b0}}, comparator_2_lt};  // Bit_Extender bit_extender_2
  Multiplexer #(.width(32)) multiplexer_2 (
    .in0(shifter_2_out), .in1(shifter_3_out), .out(multiplexer_2_out), .sel(neg));
  Multiplexer #(.select(3), .width(32)) multiplexer_3 (
    .in0(multiplexer_1_out), .in1(shifter_1_out), .in2(bit_extender_1_out), .in3(bit_extender_2_out),
    .in4(xor_1_out), .in5(multiplexer_2_out), .in6(or_1_out), .in7(and_1_out), .out(a), .sel(op));
endmodule

module M1A_bcu (
  input  is_branch,
  input  is_jal,
  input  is_jalr,
  input  [2:0] op,
  input  [31:0] b1,
  input  [31:0] b2,
  output b
);

  wire comparator_1_eq, comparator_1_lt, comparator_2_lt, multiplexer_1_out, not_1_out, not_2_out, not_3_out,
       or_1_out, or_2_out;
  wire [2:0] or_3_out;

  Comparator #(.width(32)) comparator_1 (.a(b1), .b(b2), .eq(comparator_1_eq), .lt(comparator_1_lt));  // open: gt
  Comparator #(.mode("unsigned"), .width(32)) comparator_2 (.a(b1), .b(b2), .lt(comparator_2_lt));  // open: gt, eq
  or or_1 (or_1_out, is_branch, or_2_out);
  or or_2 (or_2_out, is_jal, is_jalr);
  or or_3 (or_3_out[0], op[0], or_2_out);
  or or_4 (or_3_out[1], op[1], or_2_out);
  and and_1 (or_3_out[2], op[2], ~or_2_out);  // AND_Gate
  not not_1 (not_1_out, comparator_1_eq);
  not not_2 (not_2_out, comparator_1_lt);
  not not_3 (not_3_out, comparator_2_lt);
  Multiplexer #(.select(3)) multiplexer_1 (
    .in0(comparator_1_eq), .in1(not_1_out), .in2(1'b0), .in3(1'b1), .in4(comparator_1_lt), .in5(not_2_out),
    .in6(comparator_2_lt), .in7(not_3_out), .out(multiplexer_1_out), .sel(or_3_out));
  and and_2 (b, or_1_out, multiplexer_1_out);
endmodule

module M1B_EX (
  input  [31:0] pc_in,
  input  [31:0] b1,
  input  [31:0] b2,
  input  [31:0] a1,
  input  [31:0] a2,
  input  [31:0] m_in,
  input  [7:0] EX_ctrl_in,
  input  [7:0] MEM_ctrl_in,
  input  [7:0] WB_ctrl_in,
  input  [4:0] rs2_sel_in,
  output [31:0] pc,
  output b,
  output [31:0] a,
  output [31:0] m,
  output [7:0] MEM_ctrl,
  output [7:0] WB_ctrl,
  output [4:0] rs2_sel
);

  M1A_bcu m1a_bcu_1 (
    .b(b), .is_branch(MEM_ctrl_in[4]), .is_jal(MEM_ctrl_in[5]), .is_jalr(MEM_ctrl_in[6]),
    .op(EX_ctrl_in[6:4]), .b1(b1), .b2(b2));
  M1A_alu m1a_alu_1 (.a(a), .op(EX_ctrl_in[2:0]), .a1(a1), .a2(a2), .neg(EX_ctrl_in[3]));

  assign m = m_in;
  assign MEM_ctrl = MEM_ctrl_in;
  assign pc = pc_in;
  assign rs2_sel = rs2_sel_in;
  assign WB_ctrl = WB_ctrl_in;

  // Other names for the same wires on the sheet: alu_op[2:0] = EX_ctrl_in[2:0]; alu_neg = EX_ctrl_in[3];
  //   bcu_op[2:0] = EX_ctrl_in[6:4]; is_branch = MEM_ctrl_in[4]; is_jal = MEM_ctrl_in[5]; is_jalr = MEM_ctrl_in[6]
endmodule

module M1A_align (
  input  [31:0] in_dat,
  input  [1:0] adr_lsb,
  input  [1:0] mask,
  output [31:0] out_dat,
  output [3:0] byte_ena
);

  Multiplexer #(.select(2), .width(8)) multiplexer_1 (
    .in0(in_dat[31:24]), .in1({8{1'b0}}), .in2(in_dat[15:8]), .in3(in_dat[7:0]), .out(out_dat[31:24]),
    .sel(adr_lsb));
  Multiplexer #(.select(2)) multiplexer_2 (
    .in0(mask[1]), .in1(1'b0), .in2(mask[0]), .in3(1'b1), .out(byte_ena[3]), .sel(adr_lsb));
  Multiplexer #(.select(2), .width(8)) multiplexer_3 (
    .in0(in_dat[23:16]), .in1({8{1'b0}}), .in2(in_dat[7:0]), .in3({8{1'b0}}), .out(out_dat[23:16]),
    .sel(adr_lsb));
  Multiplexer #(.select(2)) multiplexer_4 (
    .in0(mask[1]), .in1(1'b0), .in2(1'b1), .in3(1'b0), .out(byte_ena[2]), .sel(adr_lsb));
  Multiplexer #(.select(2), .width(8)) multiplexer_5 (
    .in0(in_dat[15:8]), .in1(in_dat[7:0]), .in2({8{1'b0}}), .in3({8{1'b0}}), .out(out_dat[15:8]),
    .sel(adr_lsb));
  Multiplexer #(.select(2)) multiplexer_6 (
    .in0(mask[0]), .in1(1'b1), .in2(1'b0), .in3(1'b0), .out(byte_ena[1]), .sel(adr_lsb));
  Multiplexer #(.select(2), .width(8)) multiplexer_7 (
    .in0(in_dat[7:0]), .in1({8{1'b0}}), .in2({8{1'b0}}), .in3({8{1'b0}}), .out(out_dat[7:0]), .sel(adr_lsb));
  Multiplexer #(.select(2)) multiplexer_8 (
    .in0(1'b1), .in1(1'b0), .in2(1'b0), .in3(1'b0), .out(byte_ena[0]), .sel(adr_lsb));

  // Other names for the same wires on the sheet: msk[1:0] = mask; shf[1:0] = adr_lsb
endmodule

module M1A_dealign (
  input  [31:0] in_dat,
  input  [1:0] adr_lsb,
  input  [1:0] mask,
  input  ext,
  output [31:0] out_dat
);

  wire and_1_out, bitselector_1_out, bitselector_2_out, sign;
  wire [7:0] bit_extender_1_out, bit_extender_2_out, bit_extender_3_out, bit_extender_4_out;
  wire [31:0] and_2_out, and_3_out, bit_extender_5_out, bit_extender_6_out, not_1_out, shf_dat;

  Multiplexer #(.select(2), .width(8)) multiplexer_1 (
    .in0(in_dat[31:24]), .in1(in_dat[15:8]), .in2(in_dat[31:24]), .in3(in_dat[31:24]), .out(shf_dat[31:24]),
    .sel(adr_lsb));
  assign bit_extender_1_out = {{7{1'b1}}, 1'b1};  // Bit_Extender bit_extender_1
  assign bit_extender_2_out = {{7{mask[0]}}, mask[0]};  // Bit_Extender bit_extender_2
  assign bit_extender_3_out = {{7{mask[1]}}, mask[1]};  // Bit_Extender bit_extender_3
  assign bit_extender_4_out = {{7{mask[1]}}, mask[1]};  // Bit_Extender bit_extender_4
  Multiplexer #(.select(2), .width(8)) multiplexer_2 (
    .in0(in_dat[23:16]), .in1(in_dat[15:8]), .in2(in_dat[23:16]), .in3(in_dat[31:24]), .out(shf_dat[23:16]),
    .sel(adr_lsb));
  assign not_1_out = ~{bit_extender_4_out, bit_extender_3_out, bit_extender_2_out, bit_extender_1_out};  // NOT_Gate not_1, 32 bits wide
  Multiplexer #(.select(2), .width(8)) multiplexer_3 (
    .in0(in_dat[15:8]), .in1(in_dat[15:8]), .in2(in_dat[31:24]), .in3(in_dat[31:24]), .out(shf_dat[15:8]),
    .sel(adr_lsb));
  Multiplexer #(.select(2), .width(8)) multiplexer_4 (
    .in0(in_dat[7:0]), .in1(in_dat[15:8]), .in2(in_dat[23:16]), .in3(in_dat[31:24]), .out(shf_dat[7:0]),
    .sel(adr_lsb));
  and and_1 (and_1_out, ~mask[0], ~mask[1]);  // AND_Gate
  BitSelector #(.width(32)) bitselector_1 (.in(shf_dat), .out(bitselector_1_out), .sel(5'b01111));
  Multiplexer multiplexer_5 (.in0(bitselector_1_out), .in1(bitselector_2_out), .out(sign), .sel(and_1_out));
  BitSelector #(.width(32)) bitselector_2 (.in(shf_dat), .out(bitselector_2_out), .sel(5'b00111));
  // Probe on shf_dat
  assign bit_extender_5_out = {{31{sign}}, sign};  // Bit_Extender bit_extender_5
  assign bit_extender_6_out = {{31{ext}}, ext};  // Bit_Extender bit_extender_6
  assign and_2_out = shf_dat & {bit_extender_4_out, bit_extender_3_out, bit_extender_2_out, bit_extender_1_out};  // AND_Gate and_2, 32 bits wide
  assign and_3_out = not_1_out & bit_extender_5_out & bit_extender_6_out;  // AND_Gate and_3, 32 bits wide
  assign out_dat = and_2_out | and_3_out;  // OR_Gate or_1, 32 bits wide

  // Other names for the same wires on the sheet: msk[1:0] = mask; shf[1:0] = adr_lsb

  // Notes on the sheet:
  //   Loading Byte
endmodule

module M1A_misalign (
  input  [1:0] mask,
  input  [1:0] adr_lsb,
  input  is_store,
  input  is_load,
  output misalign
);

  wire and_1_out, and_2_out, and_3_out, or_1_out, or_2_out, or_3_out;

  or or_1 (or_1_out, adr_lsb[0], adr_lsb[1]);
  and and_1 (and_1_out, mask[0], ~mask[1], adr_lsb[0]);  // AND_Gate
  and and_2 (and_2_out, mask[0], mask[1], or_1_out);
  or or_2 (or_2_out, and_1_out, and_2_out, and_3_out);
  and and_3 (and_3_out, ~mask[0], mask[1]);  // AND_Gate
  or or_3 (or_3_out, is_store, is_load);
  and and_4 (misalign, or_2_out, or_3_out);

  // Notes on the sheet:
  //   Store Half Word, but A[0] == 1
  //   Store Word, but A[1:0] != 0
  //   invalid "mask" value
endmodule

module M1B_MEM (
  input  [31:0] pc,
  input  [31:0] a_in,
  input  [31:0] m_in,
  input  [31:0] ram_dout,
  input  [7:0] MEM_ctrl_in,
  input  [7:0] WB_ctrl_in,
  output [31:0] a,
  output [31:0] m,
  output misalign,
  output [31:0] ram_adr,
  output ram_we,
  output [3:0] ram_be,
  output [31:0] ram_din,
  output [7:0] WB_ctrl
);

  wire nor_1_out;
  wire [31:0] adder_1_out;

  Adder #(.width(32)) adder_1 (.a(pc), .b(32'h4), .out(adder_1_out));  // open: cin, cout
  nor nor_1 (nor_1_out, MEM_ctrl_in[5], MEM_ctrl_in[6]);
  Multiplexer #(.width(32)) multiplexer_1 (.in0(adder_1_out), .in1(a_in), .out(a), .sel(nor_1_out));
  M1A_align m1a_align_1 (
    .out_dat(ram_din), .byte_ena(ram_be), .adr_lsb(a_in[1:0]), .mask(MEM_ctrl_in[1:0]), .in_dat(m_in));
  M1A_dealign m1a_dealign_1 (
    .out_dat(m), .ext(MEM_ctrl_in[2]), .adr_lsb(a_in[1:0]), .mask(MEM_ctrl_in[1:0]), .in_dat(ram_dout));
  M1A_misalign m1a_misalign_1 (
    .misalign(misalign), .mask(MEM_ctrl_in[1:0]), .adr_lsb(a_in[1:0]), .is_store(MEM_ctrl_in[3]),
    .is_load(WB_ctrl_in[6]));

  assign ram_adr = {a_in[31:2], 2'b00};
  assign ram_we = MEM_ctrl_in[3];
  assign WB_ctrl = WB_ctrl_in;

  // Other names for the same wires on the sheet: adr_lsb[1:0] = a_in[1:0]; mask[1:0] = MEM_ctrl_in[1:0];
  //   uext = MEM_ctrl_in[2]; is_store = MEM_ctrl_in[3]; is_branch = MEM_ctrl_in[4]; is_jal = MEM_ctrl_in[5];
  //   is_jalr = MEM_ctrl_in[6]; rd_sel[4:0] = WB_ctrl_in[4:0]; reg_we = WB_ctrl_in[5]; is_load = WB_ctrl_in[6]

  // Notes on the sheet:
  //   数据总线接口
endmodule

module M1A_WB (
  input  [31:0] a_in,
  input  [31:0] m_in,
  input  [7:0] WB_ctrl_in,
  output [31:0] rd_data,
  output [4:0] rd_sel,
  output rd_we
);

  Multiplexer #(.width(32)) multiplexer_1 (.in0(a_in), .in1(m_in), .out(rd_data), .sel(WB_ctrl_in[6]));

  assign rd_sel = WB_ctrl_in[4:0];
  assign rd_we = WB_ctrl_in[5];

  // Other names for the same wires on the sheet: reg_we = WB_ctrl_in[5]; is_load = WB_ctrl_in[6]
endmodule
