// Logisim project M2.circ as structural Verilog: 11 circuits, main circuit M2_addsub32
module M2_addsub32 (
  input  neg,
  input  [31:0] A,
  input  [31:0] B,
  output [31:0] S
);

  wire [31:0] bit_extender_1_out, xor_1_out;

  assign bit_extender_1_out = {{31{neg}}, neg};  // Bit_Extender bit_extender_1
  assign xor_1_out = B ^ bit_extender_1_out;  // XOR_Gate xor_1, 32 bits wide
  M2C_adder_cla_32 m2c_adder_cla_32_1 (.S(S), .B(xor_1_out), .Ci(neg), .A(A));  // open: Co
endmodule

module M2_incr4_32 (
  input  [31:0] i,
  output [31:0] o
);

  M2C_incr_four_32 m2c_incr_four_32_1 (.out_3(o), .en(1'b1), .in_2(i));
endmodule

module M2_comparator_32 (
  input  sgn,
  input  [31:0] A,
  input  [31:0] B,
  output G,
  output E,
  output L
);

  M2B_comparator_32 m2b_comparator_32_1 (.G(G), .E(E), .L(L), .A(A), .B(B), .sgn(sgn));
endmodule

module M2_is_equal_32 (
  input  [31:0] A,
  input  [31:0] B,
  output E
);

  wire [31:0] xnor_1_out;

  assign xnor_1_out = ~(A ^ B);  // XNOR_Gate xnor_1, 32 bits wide
  and and_1 (E, xnor_1_out[0], xnor_1_out[1], xnor_1_out[2], xnor_1_out[3], xnor_1_out[4], xnor_1_out[5], xnor_1_out[6], xnor_1_out[7], xnor_1_out[8], xnor_1_out[9], xnor_1_out[10], xnor_1_out[11], xnor_1_out[12], xnor_1_out[13], xnor_1_out[14], xnor_1_out[15], xnor_1_out[16], xnor_1_out[17], xnor_1_out[18], xnor_1_out[19], xnor_1_out[20], xnor_1_out[21], xnor_1_out[22], xnor_1_out[23], xnor_1_out[24], xnor_1_out[25], xnor_1_out[26], xnor_1_out[27], xnor_1_out[28], xnor_1_out[29], xnor_1_out[30], xnor_1_out[31]);
endmodule

module M2_is_equal_8 (
  input  [7:0] A,
  input  [7:0] B,
  output E
);

  wire [7:0] xnor_1_out;

  assign xnor_1_out = ~(A ^ B);  // XNOR_Gate xnor_1, 8 bits wide
  and and_1 (E, xnor_1_out[0], xnor_1_out[1], xnor_1_out[2], xnor_1_out[3], xnor_1_out[4], xnor_1_out[5], xnor_1_out[6], xnor_1_out[7]);
endmodule

module M2_is_equal_5 (
  input  [4:0] A,
  input  [4:0] B,
  output E
);

  wire [4:0] xnor_1_out;

  assign xnor_1_out = ~(A ^ B);  // XNOR_Gate xnor_1, 5 bits wide
  and and_1 (E, xnor_1_out[0], xnor_1_out[1], xnor_1_out[2], xnor_1_out[3], xnor_1_out[4]);
endmodule

module M2_shift_left_32 (
  input  [31:0] I,
  input  [4:0] len,
  output [31:0] O
);

  M2A_shift_left_32_s3 m2a_shift_left_32_s3_1 (.O(O), .Len(len), .I(I));
endmodule

module M2_shift_right_32 (
  input  arith,
  input  [31:0] I,
  input  [4:0] len,
  output [31:0] O
);

  M2A_shift_right_32_s3 m2a_shift_right_32_s3_1 (.O(O), .Arith(arith), .Len(len), .I(I));
endmodule

module M2_bpu_fsm (
  input  [2:0] i,
  output [1:0] o
);

  wire and_1_out, and_2_out, and_3_out, and_4_out, and_5_out, and_6_out, not_1_out;

  not not_1 (not_1_out, i[0]);
  and and_1 (and_1_out, i[2], i[1]);
  and and_2 (and_2_out, i[2], not_1_out);
  and and_3 (and_3_out, i[1], not_1_out);
  and and_4 (and_4_out, i[2], i[1]);
  and and_5 (and_5_out, i[2], i[0]);
  and and_6 (and_6_out, i[1], i[0]);
  or or_1 (o[0], and_1_out, and_2_out, and_3_out);
  or or_2 (o[1], and_4_out, and_5_out, and_6_out);
endmodule

module M2_counter_8 (
  input  load,
  input  en,
  input  [7:0] d,
  input  clk,
  input  srn,
  output [7:0] q
);

  wire not_1_out;
  wire [7:0] m2b_incrementer_8_1_out_3, multiplexer_1_out;

  not not_1 (not_1_out, srn);
  M2B_incrementer_8 m2b_incrementer_8_1 (.out_3(m2b_incrementer_8_1_out_3), .en(en), .in_2(q));
  Multiplexer #(.width(8)) multiplexer_1 (
    .in0(m2b_incrementer_8_1_out_3), .in1(d), .out(multiplexer_1_out), .sel(load));
  Register register_1 (.D(multiplexer_1_out), .clk(clk), .Q(q), .clr(not_1_out));  // open: en
endmodule

module M2_random_8 (
  input  ssn,
  input  clk,
  output [7:0] out_3
);

  wire not_1_out, xor_1_out, xor_2_out, xor_3_out;

  not not_1 (not_1_out, ssn);
  D_Flip_Flop d_ff_1 (.D(xor_1_out), .clk(clk), .Q(out_3[7]), .preset(not_1_out));  // open: Qn, reset
  xor xor_1 (xor_1_out, xor_2_out, out_3[6]);
  D_Flip_Flop d_ff_2 (.D(out_3[7]), .clk(clk), .Q(out_3[6]), .preset(not_1_out));  // open: Qn, reset
  xor xor_2 (xor_2_out, xor_3_out, out_3[5]);
  D_Flip_Flop d_ff_3 (.D(out_3[6]), .clk(clk), .Q(out_3[5]), .preset(not_1_out));  // open: Qn, reset
  xor xor_3 (xor_3_out, out_3[0], out_3[4]);
  D_Flip_Flop d_ff_4 (.D(out_3[5]), .clk(clk), .Q(out_3[4]), .preset(not_1_out));  // open: Qn, reset
  D_Flip_Flop d_ff_5 (.D(out_3[4]), .clk(clk), .Q(out_3[3]), .preset(not_1_out));  // open: Qn, reset
  D_Flip_Flop d_ff_6 (.D(out_3[3]), .clk(clk), .Q(out_3[2]), .preset(not_1_out));  // open: Qn, reset
  D_Flip_Flop d_ff_7 (.D(out_3[2]), .clk(clk), .Q(out_3[1]), .preset(not_1_out));  // open: Qn, reset
  D_Flip_Flop d_ff_8 (.D(out_3[1]), .clk(clk), .Q(out_3[0]), .preset(not_1_out));  // open: Qn, reset
endmodule
