// Logisim project M2_Arithmetic.circ as structural Verilog: 20 circuits, main circuit M2C_adder_cla_32
module M2C_adder_cla_32 (
  input  Ci,
  input  [31:0] A,
  input  [31:0] B,
  output [31:0] S,
  output Co
);

  wire C1, C2, C3, C4, m2b_adder_cla_8_1_g, m2b_adder_cla_8_1_p, m2b_adder_cla_8_2_g, m2b_adder_cla_8_2_p,
       m2b_adder_cla_8_3_g, m2b_adder_cla_8_3_p, m2b_adder_cla_8_4_g, m2b_adder_cla_8_4_p;

  M2B_adder_cla_8 m2b_adder_cla_8_1 (
    .C0(Ci), .A(A[7:0]), .B(B[7:0]), .P(m2b_adder_cla_8_1_p), .G(m2b_adder_cla_8_1_g), .S(S[7:0]));  // open: C8
  M2B_adder_cla_8 m2b_adder_cla_8_2 (
    .C0(C1), .A(A[15:8]), .B(B[15:8]), .P(m2b_adder_cla_8_2_p), .G(m2b_adder_cla_8_2_g), .S(S[15:8]));  // open: C8
  M2B_adder_cla_8 m2b_adder_cla_8_3 (
    .C0(C2), .A(A[23:16]), .B(B[23:16]), .P(m2b_adder_cla_8_3_p), .G(m2b_adder_cla_8_3_g), .S(S[23:16]));  // open: C8
  M2B_adder_cla_8 m2b_adder_cla_8_4 (
    .C0(C3), .A(A[31:24]), .B(B[31:24]), .P(m2b_adder_cla_8_4_p), .G(m2b_adder_cla_8_4_g), .C8(Co),
    .S(S[31:24]));
  M2A_lcu_4 m2a_lcu_4_1 (
    .C0(Ci), .P0(m2b_adder_cla_8_1_p), .G0(m2b_adder_cla_8_1_g), .P1(m2b_adder_cla_8_2_p),
    .G1(m2b_adder_cla_8_2_g), .P2(m2b_adder_cla_8_3_p), .G2(m2b_adder_cla_8_3_g), .P3(m2b_adder_cla_8_4_p),
    .G3(m2b_adder_cla_8_4_g), .C1(C1), .C2(C2), .C3(C3), .C4(C4));  // open: PG, GG

  // Other names for the same wires on the sheet: S0[7:0] = S[7:0]; S1[7:0] = S[15:8]; S2[7:0] = S[23:16];
  //   S3[7:0] = S[31:24]
endmodule

module M2B_adder_cla_8 (
  input  C0,
  input  [7:0] A,
  input  [7:0] B,
  output P,
  output G,
  output C8,
  output [7:0] S
);

  wire C1, C2, C3, C4, C5, C6, C7, m2a_full_adder_pg_1_g, m2a_full_adder_pg_1_p, m2a_full_adder_pg_2_g,
       m2a_full_adder_pg_2_p, m2a_full_adder_pg_3_g, m2a_full_adder_pg_3_p, m2a_full_adder_pg_4_g,
       m2a_full_adder_pg_4_p, m2a_full_adder_pg_5_g, m2a_full_adder_pg_5_p, m2a_full_adder_pg_6_g,
       m2a_full_adder_pg_6_p, m2a_full_adder_pg_7_g, m2a_full_adder_pg_7_p, m2a_full_adder_pg_8_g,
       m2a_full_adder_pg_8_p;

  M2A_full_adder_pg m2a_full_adder_pg_1 (
    .G(m2a_full_adder_pg_1_g), .P(m2a_full_adder_pg_1_p), .S(S[0]), .A(A[0]), .B(B[0]), .C(C0));
  M2A_full_adder_pg m2a_full_adder_pg_2 (
    .G(m2a_full_adder_pg_2_g), .P(m2a_full_adder_pg_2_p), .S(S[1]), .A(A[1]), .B(B[1]), .C(C1));
  M2A_full_adder_pg m2a_full_adder_pg_3 (
    .G(m2a_full_adder_pg_3_g), .P(m2a_full_adder_pg_3_p), .S(S[2]), .A(A[2]), .B(B[2]), .C(C2));
  M2A_full_adder_pg m2a_full_adder_pg_4 (
    .G(m2a_full_adder_pg_4_g), .P(m2a_full_adder_pg_4_p), .S(S[3]), .A(A[3]), .B(B[3]), .C(C3));
  M2A_full_adder_pg m2a_full_adder_pg_5 (
    .G(m2a_full_adder_pg_5_g), .P(m2a_full_adder_pg_5_p), .S(S[4]), .A(A[4]), .B(B[4]), .C(C4));
  M2A_full_adder_pg m2a_full_adder_pg_6 (
    .G(m2a_full_adder_pg_6_g), .P(m2a_full_adder_pg_6_p), .S(S[5]), .A(A[5]), .B(B[5]), .C(C5));
  M2A_full_adder_pg m2a_full_adder_pg_7 (
    .G(m2a_full_adder_pg_7_g), .P(m2a_full_adder_pg_7_p), .S(S[6]), .A(A[6]), .B(B[6]), .C(C6));
  M2A_full_adder_pg m2a_full_adder_pg_8 (
    .G(m2a_full_adder_pg_8_g), .P(m2a_full_adder_pg_8_p), .S(S[7]), .A(A[7]), .B(B[7]), .C(C7));
  M2A_lcu_8 m2a_lcu_8_1 (
    .C0(C0), .P0(m2a_full_adder_pg_1_p), .G0(m2a_full_adder_pg_1_g), .P1(m2a_full_adder_pg_2_p),
    .G1(m2a_full_adder_pg_2_g), .P2(m2a_full_adder_pg_3_p), .G2(m2a_full_adder_pg_3_g),
    .P3(m2a_full_adder_pg_4_p), .G3(m2a_full_adder_pg_4_g), .P4(m2a_full_adder_pg_5_p),
    .G4(m2a_full_adder_pg_5_g), .P5(m2a_full_adder_pg_6_p), .G5(m2a_full_adder_pg_6_g),
    .P6(m2a_full_adder_pg_7_p), .G6(m2a_full_adder_pg_7_g), .P7(m2a_full_adder_pg_8_p),
    .G7(m2a_full_adder_pg_8_g), .PG(P), .GG(G), .C1(C1), .C2(C2), .C3(C3), .C4(C4), .C5(C5), .C6(C6),
    .C7(C7), .C8(C8));
endmodule

module M2A_comparator_4 (
  input  [3:0] A,
  input  [3:0] B,
  output G,
  output E,
  output L
);

  wire and_1_out, and_2_out, and_3_out, and_4_out, and_5_out, and_6_out, and_7_out, and_8_out;
  wire [3:0] An, Bn, xnor_1_out;

  assign An = ~A;  // NOT_Gate not_1, 4 bits wide
  assign Bn = ~B;  // NOT_Gate not_2, 4 bits wide
  assign xnor_1_out = ~(A ^ B);  // XNOR_Gate xnor_1, 4 bits wide
  and and_1 (and_1_out, A[3], Bn[3]);
  and and_2 (and_2_out, An[3], B[3]);
  and and_3 (and_3_out, A[2], xnor_1_out[3], Bn[2]);
  and and_4 (and_4_out, An[2], xnor_1_out[3], B[2]);
  and and_5 (and_5_out, A[1], xnor_1_out[3], xnor_1_out[2], Bn[1]);
  and and_6 (and_6_out, An[1], xnor_1_out[3], xnor_1_out[2], B[1]);
  and and_7 (and_7_out, A[0], xnor_1_out[3], xnor_1_out[2], xnor_1_out[1], Bn[0]);
  and and_8 (and_8_out, An[0], xnor_1_out[3], xnor_1_out[2], xnor_1_out[1], B[0]);
  or or_1 (G, and_1_out, and_3_out, and_5_out, and_7_out);
  or or_2 (L, and_8_out, and_6_out, and_4_out, and_2_out);
  and and_9 (E, xnor_1_out[0], xnor_1_out[1], xnor_1_out[2], xnor_1_out[3]);
endmodule

module M2A_comparator_8 (
  input  [7:0] A,
  input  [7:0] B,
  output G,
  output E,
  output L
);

  wire and_1_out, and_2_out, and_3_out, and_4_out, and_5_out, and_6_out, and_7_out, and_8_out, and_9_out,
       and_10_out, and_11_out, and_12_out, and_13_out, and_14_out, and_15_out, and_16_out;
  wire [7:0] An, Bn, xnor_1_out;

  assign An = ~A;  // NOT_Gate not_1, 8 bits wide
  assign Bn = ~B;  // NOT_Gate not_2, 8 bits wide
  assign xnor_1_out = ~(A ^ B);  // XNOR_Gate xnor_1, 8 bits wide
  and and_1 (and_1_out, A[7], Bn[7]);
  and and_2 (and_2_out, An[7], B[7]);
  and and_3 (and_3_out, A[6], xnor_1_out[7], Bn[6]);
  and and_4 (and_4_out, An[6], xnor_1_out[7], B[6]);
  and and_5 (and_5_out, A[5], xnor_1_out[7], xnor_1_out[6], Bn[5]);
  and and_6 (and_6_out, An[5], xnor_1_out[7], xnor_1_out[6], B[5]);
  and and_7 (and_7_out, A[4], xnor_1_out[7], xnor_1_out[6], xnor_1_out[5], Bn[4]);
  and and_8 (and_8_out, An[4], xnor_1_out[7], xnor_1_out[6], xnor_1_out[5], B[4]);
  and and_9 (and_9_out, A[3], xnor_1_out[7], xnor_1_out[6], xnor_1_out[5], xnor_1_out[4], Bn[3]);
  and and_10 (and_10_out, An[3], xnor_1_out[7], xnor_1_out[6], xnor_1_out[5], xnor_1_out[4], B[3]);
  and and_11 (and_11_out, A[2], xnor_1_out[7], xnor_1_out[6], xnor_1_out[5], xnor_1_out[4], xnor_1_out[3], Bn[2]);
  and and_12 (and_12_out, An[2], xnor_1_out[7], xnor_1_out[6], xnor_1_out[5], xnor_1_out[4], xnor_1_out[3], B[2]);
  and and_13 (and_13_out, A[1], xnor_1_out[7], xnor_1_out[6], xnor_1_out[5], xnor_1_out[4], xnor_1_out[3], xnor_1_out[2], Bn[1]);
  and and_14 (and_14_out, An[1], xnor_1_out[7], xnor_1_out[6], xnor_1_out[5], xnor_1_out[4], xnor_1_out[3], xnor_1_out[2], B[1]);
  and and_15 (and_15_out, A[0], xnor_1_out[7], xnor_1_out[6], xnor_1_out[5], xnor_1_out[4], xnor_1_out[3], xnor_1_out[2], xnor_1_out[1], Bn[0]);
  and and_16 (and_16_out, An[0], xnor_1_out[7], xnor_1_out[6], xnor_1_out[5], xnor_1_out[4], xnor_1_out[3], xnor_1_out[2], xnor_1_out[1], B[0]);
  or or_1 (G, and_1_out, and_3_out, and_5_out, and_7_out, and_9_out, and_11_out, and_13_out, and_15_out);
  or or_2 (L, and_16_out, and_14_out, and_12_out, and_10_out, and_8_out, and_6_out, and_4_out, and_2_out);
  and and_17 (E, xnor_1_out[0], xnor_1_out[1], xnor_1_out[2], xnor_1_out[3], xnor_1_out[4], xnor_1_out[5], xnor_1_out[6], xnor_1_out[7]);
endmodule

module M2B_comparator_32 (
  input  [31:0] A,
  input  [31:0] B,
  input  sgn,
  output G,
  output E,
  output L
);

  wire [3:0] m2a_comparator_8_4_g, m2a_comparator_8_4_l;
  wire [31:0] m2a_msbn_32_1_out_3, m2a_msbn_32_2_out_3;

  M2A_MSBn_32 m2a_msbn_32_1 (.out_3(m2a_msbn_32_1_out_3), .in_1(A), .n(sgn));
  M2A_MSBn_32 m2a_msbn_32_2 (.out_3(m2a_msbn_32_2_out_3), .in_1(B), .n(sgn));
  M2A_comparator_8 m2a_comparator_8_1 (
    .A(m2a_msbn_32_1_out_3[31:24]), .B(m2a_msbn_32_2_out_3[31:24]), .G(m2a_comparator_8_4_g[3]),
    .L(m2a_comparator_8_4_l[3]));  // open: E
  M2A_comparator_8 m2a_comparator_8_2 (
    .A(m2a_msbn_32_1_out_3[23:16]), .B(m2a_msbn_32_2_out_3[23:16]), .G(m2a_comparator_8_4_g[2]),
    .L(m2a_comparator_8_4_l[2]));  // open: E
  M2A_comparator_8 m2a_comparator_8_3 (
    .A(m2a_msbn_32_1_out_3[15:8]), .B(m2a_msbn_32_2_out_3[15:8]), .G(m2a_comparator_8_4_g[1]),
    .L(m2a_comparator_8_4_l[1]));  // open: E
  M2A_comparator_8 m2a_comparator_8_4 (
    .A(m2a_msbn_32_1_out_3[7:0]), .B(m2a_msbn_32_2_out_3[7:0]), .G(m2a_comparator_8_4_g[0]),
    .L(m2a_comparator_8_4_l[0]));  // open: E
  M2A_comparator_4 m2a_comparator_4_1 (.A(m2a_comparator_8_4_g), .B(m2a_comparator_8_4_l), .G(G), .E(E), .L(L));

  // Notes on the sheet:
  //   sgn=0时进行有符号数比较
  //   sgn=1时进行无符号数比较
  //   ~MSB模块在n=0时将最高位取反，n=1时不变
endmodule

module M2B_comparator_32_442 (
  input  [31:0] A,
  input  [31:0] B,
  output G,
  output E,
  output L
);

  wire and_1_out, and_2_out, and_4_out, and_5_out, m2a_comparator_4_9_g, m2a_comparator_4_9_l,
       m2a_comparator_4_10_g, m2a_comparator_4_10_l, not_1_out, not_2_out, not_3_out, not_4_out, xnor_1_out,
       xnor_2_out;
  wire [3:0] m2a_comparator_4_4_g, m2a_comparator_4_4_l, m2a_comparator_4_8_g, m2a_comparator_4_8_l;

  M2A_comparator_4 m2a_comparator_4_1 (
    .A(A[31:28]), .B(B[31:28]), .G(m2a_comparator_4_4_g[3]), .L(m2a_comparator_4_4_l[3]));  // open: E
  M2A_comparator_4 m2a_comparator_4_2 (
    .A(A[27:24]), .B(B[27:24]), .G(m2a_comparator_4_4_g[2]), .L(m2a_comparator_4_4_l[2]));  // open: E
  M2A_comparator_4 m2a_comparator_4_3 (
    .A(A[23:20]), .B(B[23:20]), .G(m2a_comparator_4_4_g[1]), .L(m2a_comparator_4_4_l[1]));  // open: E
  M2A_comparator_4 m2a_comparator_4_4 (
    .A(A[19:16]), .B(B[19:16]), .G(m2a_comparator_4_4_g[0]), .L(m2a_comparator_4_4_l[0]));  // open: E
  M2A_comparator_4 m2a_comparator_4_5 (
    .A(A[15:12]), .B(B[15:12]), .G(m2a_comparator_4_8_g[3]), .L(m2a_comparator_4_8_l[3]));  // open: E
  M2A_comparator_4 m2a_comparator_4_6 (
    .A(A[11:8]), .B(B[11:8]), .G(m2a_comparator_4_8_g[2]), .L(m2a_comparator_4_8_l[2]));  // open: E
  M2A_comparator_4 m2a_comparator_4_7 (
    .A(A[7:4]), .B(B[7:4]), .G(m2a_comparator_4_8_g[1]), .L(m2a_comparator_4_8_l[1]));  // open: E
  M2A_comparator_4 m2a_comparator_4_8 (
    .A(A[3:0]), .B(B[3:0]), .G(m2a_comparator_4_8_g[0]), .L(m2a_comparator_4_8_l[0]));  // open: E
  M2A_comparator_4 m2a_comparator_4_9 (
    .A(m2a_comparator_4_4_g), .B(m2a_comparator_4_4_l), .G(m2a_comparator_4_9_g), .L(m2a_comparator_4_9_l));  // open: E
  M2A_comparator_4 m2a_comparator_4_10 (
    .A(m2a_comparator_4_8_g), .B(m2a_comparator_4_8_l), .G(m2a_comparator_4_10_g), .L(m2a_comparator_4_10_l));  // open: E
  not not_1 (not_1_out, m2a_comparator_4_9_g);
  not not_2 (not_2_out, m2a_comparator_4_9_l);
  not not_3 (not_3_out, m2a_comparator_4_10_g);
  not not_4 (not_4_out, m2a_comparator_4_10_l);
  xnor xnor_1 (xnor_1_out, m2a_comparator_4_9_g, m2a_comparator_4_9_l);
  xnor xnor_2 (xnor_2_out, m2a_comparator_4_10_g, m2a_comparator_4_10_l);
  and and_1 (and_1_out, m2a_comparator_4_9_g, not_2_out);
  and and_2 (and_2_out, m2a_comparator_4_10_g, not_4_out, xnor_1_out);
  and and_3 (E, xnor_1_out, xnor_2_out);
  and and_4 (and_4_out, xnor_1_out, m2a_comparator_4_10_l, not_3_out);
  and and_5 (and_5_out, m2a_comparator_4_9_l, not_1_out);
  or or_1 (G, and_1_out, and_2_out);
  or or_2 (L, and_4_out, and_5_out);
endmodule

module M2A_full_adder_pg (
  input  A,
  input  B,
  input  C,
  output G,
  output P,
  output S
);

  and and_1 (G, A, B);
  xor xor_1 (P, A, B);
  xor xor_2 (S, P, C);
endmodule

module M2B_incrementer_32 (
  input  en,
  input  [31:0] in_2,
  output [31:0] out_3
);

  wire AND1, AND2, AND3, AND4, AND5, AND6, AND7, AND8, AND9, AND10, AND11, AND12, AND13, AND14, AND15, AND16,
       AND17, AND18, AND19, AND20, AND21, AND22, AND23, AND24, AND25, AND26, AND27, AND28, AND29, AND30,
       AND31;

  M2A_reduction_and_32 m2a_reduction_and_32_1 (.out_2(AND1), .in_1({{31{en}}, in_2[0]}));
  M2A_reduction_and_32 m2a_reduction_and_32_2 (.out_2(AND2), .in_1({{30{en}}, in_2[1:0]}));
  M2A_reduction_and_32 m2a_reduction_and_32_3 (.out_2(AND3), .in_1({{29{en}}, in_2[2:0]}));
  M2A_reduction_and_32 m2a_reduction_and_32_4 (.out_2(AND4), .in_1({{28{en}}, in_2[3:0]}));
  M2A_reduction_and_32 m2a_reduction_and_32_5 (.out_2(AND5), .in_1({{27{en}}, in_2[4:0]}));
  M2A_reduction_and_32 m2a_reduction_and_32_6 (.out_2(AND6), .in_1({{26{en}}, in_2[5:0]}));
  M2A_reduction_and_32 m2a_reduction_and_32_7 (.out_2(AND7), .in_1({{25{en}}, in_2[6:0]}));
  M2A_reduction_and_32 m2a_reduction_and_32_8 (.out_2(AND8), .in_1({{24{en}}, in_2[7:0]}));
  M2A_reduction_and_32 m2a_reduction_and_32_9 (.out_2(AND9), .in_1({{23{en}}, in_2[8:0]}));
  M2A_reduction_and_32 m2a_reduction_and_32_10 (.out_2(AND10), .in_1({{22{en}}, in_2[9:0]}));
  M2A_reduction_and_32 m2a_reduction_and_32_11 (.out_2(AND11), .in_1({{21{en}}, in_2[10:0]}));
  M2A_reduction_and_32 m2a_reduction_and_32_12 (.out_2(AND12), .in_1({{20{en}}, in_2[11:0]}));
  M2A_reduction_and_32 m2a_reduction_and_32_13 (.out_2(AND13), .in_1({{19{en}}, in_2[12:0]}));
  M2A_reduction_and_32 m2a_reduction_and_32_14 (.out_2(AND14), .in_1({{18{en}}, in_2[13:0]}));
  M2A_reduction_and_32 m2a_reduction_and_32_15 (.out_2(AND15), .in_1({{17{en}}, in_2[14:0]}));
  M2A_reduction_and_32 m2a_reduction_and_32_16 (.out_2(AND16), .in_1({{16{en}}, in_2[15:0]}));
  xor xor_1 (out_3[0], en, in_2[0]);
  xor xor_2 (out_3[1], AND1, in_2[1]);
  xor xor_3 (out_3[2], AND2, in_2[2]);
  xor xor_4 (out_3[3], AND3, in_2[3]);
  xor xor_5 (out_3[4], AND4, in_2[4]);
  xor xor_6 (out_3[5], AND5, in_2[5]);
  xor xor_7 (out_3[6], AND6, in_2[6]);
  xor xor_8 (out_3[7], AND7, in_2[7]);
  xor xor_9 (out_3[8], AND8, in_2[8]);
  xor xor_10 (out_3[9], AND9, in_2[9]);
  xor xor_11 (out_3[10], AND10, in_2[10]);
  xor xor_12 (out_3[11], AND11, in_2[11]);
  xor xor_13 (out_3[12], AND12, in_2[12]);
  xor xor_14 (out_3[13], AND13, in_2[13]);
  xor xor_15 (out_3[14], AND14, in_2[14]);
  xor xor_16 (out_3[15], AND15, in_2[15]);
  xor xor_17 (out_3[16], AND16, in_2[16]);
  xor xor_18 (out_3[17], AND17, in_2[17]);
  xor xor_19 (out_3[18], AND18, in_2[18]);
  xor xor_20 (out_3[19], AND19, in_2[19]);
  xor xor_21 (out_3[20], AND20, in_2[20]);
  xor xor_22 (out_3[21], AND21, in_2[21]);
  xor xor_23 (out_3[22], AND22, in_2[22]);
  xor xor_24 (out_3[23], AND23, in_2[23]);
  xor xor_25 (out_3[24], AND24, in_2[24]);
  xor xor_26 (out_3[25], AND25, in_2[25]);
  xor xor_27 (out_3[26], AND26, in_2[26]);
  xor xor_28 (out_3[27], AND27, in_2[27]);
  xor xor_29 (out_3[28], AND28, in_2[28]);
  xor xor_30 (out_3[29], AND29, in_2[29]);
  xor xor_31 (out_3[30], AND30, in_2[30]);
  xor xor_32 (out_3[31], AND31, in_2[31]);
  M2A_reduction_and_32 m2a_reduction_and_32_17 (.out_2(AND17), .in_1({{15{en}}, in_2[16:0]}));
  M2A_reduction_and_32 m2a_reduction_and_32_18 (.out_2(AND18), .in_1({{14{en}}, in_2[17:0]}));
  M2A_reduction_and_32 m2a_reduction_and_32_19 (.out_2(AND19), .in_1({{13{en}}, in_2[18:0]}));
  M2A_reduction_and_32 m2a_reduction_and_32_20 (.out_2(AND20), .in_1({{12{en}}, in_2[19:0]}));
  M2A_reduction_and_32 m2a_reduction_and_32_21 (.out_2(AND21), .in_1({{11{en}}, in_2[20:0]}));
  M2A_reduction_and_32 m2a_reduction_and_32_22 (.out_2(AND22), .in_1({{10{en}}, in_2[21:0]}));
  M2A_reduction_and_32 m2a_reduction_and_32_23 (.out_2(AND23), .in_1({{9{en}}, in_2[22:0]}));
  M2A_reduction_and_32 m2a_reduction_and_32_24 (.out_2(AND24), .in_1({{8{en}}, in_2[23:0]}));
  M2A_reduction_and_32 m2a_reduction_and_32_25 (.out_2(AND25), .in_1({{7{en}}, in_2[24:0]}));
  M2A_reduction_and_32 m2a_reduction_and_32_26 (.out_2(AND26), .in_1({{6{en}}, in_2[25:0]}));
  M2A_reduction_and_32 m2a_reduction_and_32_27 (.out_2(AND27), .in_1({{5{en}}, in_2[26:0]}));
  M2A_reduction_and_32 m2a_reduction_and_32_28 (.out_2(AND28), .in_1({{4{en}}, in_2[27:0]}));
  M2A_reduction_and_32 m2a_reduction_and_32_29 (.out_2(AND29), .in_1({{3{en}}, in_2[28:0]}));
  M2A_reduction_and_32 m2a_reduction_and_32_30 (.out_2(AND30), .in_1({{2{en}}, in_2[29:0]}));
  M2A_reduction_and_32 m2a_reduction_and_32_31 (.out_2(AND31), .in_1({en, in_2[30:0]}));

  // Other names for the same wires on the sheet: i[31:0] = in_2
endmodule

module M2B_incrementer_8 (
  input  en,
  input  [7:0] in_2,
  output [7:0] out_3
);

  wire AND1, AND2, AND3, AND4, AND5, AND6, AND7;

  M2A_reduction_and_8 m2a_reduction_and_8_1 (.out_2(AND1), .in_1({{7{en}}, in_2[0]}));
  M2A_reduction_and_8 m2a_reduction_and_8_2 (.out_2(AND2), .in_1({{6{en}}, in_2[1:0]}));
  M2A_reduction_and_8 m2a_reduction_and_8_3 (.out_2(AND3), .in_1({{5{en}}, in_2[2:0]}));
  M2A_reduction_and_8 m2a_reduction_and_8_4 (.out_2(AND4), .in_1({{4{en}}, in_2[3:0]}));
  M2A_reduction_and_8 m2a_reduction_and_8_5 (.out_2(AND5), .in_1({{3{en}}, in_2[4:0]}));
  M2A_reduction_and_8 m2a_reduction_and_8_6 (.out_2(AND6), .in_1({{2{en}}, in_2[5:0]}));
  M2A_reduction_and_8 m2a_reduction_and_8_7 (.out_2(AND7), .in_1({en, in_2[6:0]}));
  xor xor_1 (out_3[0], en, in_2[0]);
  xor xor_2 (out_3[1], AND1, in_2[1]);
  xor xor_3 (out_3[2], AND2, in_2[2]);
  xor xor_4 (out_3[3], AND3, in_2[3]);
  xor xor_5 (out_3[4], AND4, in_2[4]);
  xor xor_6 (out_3[5], AND5, in_2[5]);
  xor xor_7 (out_3[6], AND6, in_2[6]);
  xor xor_8 (out_3[7], AND7, in_2[7]);

  // Other names for the same wires on the sheet: i[7:0] = in_2
endmodule

module M2C_incr_four_32 (
  input  en,
  input  [31:0] in_2,
  output [31:0] out_3
);

  wire [31:30] m2b_incrementer_32_1_out_3;

  M2B_incrementer_32 m2b_incrementer_32_1 (
    .out_3({m2b_incrementer_32_1_out_3, out_3[31:2]}), .en(en), .in_2({2'b00, in_2[31:2]}));

  assign out_3[1:0] = in_2[1:0];
endmodule

module M2A_logical_32 (
  input  [1:0] sel,
  input  [31:0] in_2,
  input  [31:0] in_3,
  output [31:0] out_4
);

  wire [31:0] and_1_out, not_1_out, or_1_out, xor_1_out;

  assign not_1_out = ~in_2;  // NOT_Gate not_1, 32 bits wide
  assign xor_1_out = in_2 ^ in_3;  // XOR_Gate xor_1, 32 bits wide
  assign or_1_out = in_2 | in_3;  // OR_Gate or_1, 32 bits wide
  assign and_1_out = in_2 & in_3;  // AND_Gate and_1, 32 bits wide
  M2A_mux4_32 m2a_mux4_32_1 (
    .out_6(out_4), .in_4(not_1_out), .in_5(xor_1_out), .in_1(sel), .in_2(and_1_out), .in_3(or_1_out));

  // Notes on the sheet:
  //   01处的非运算不是RV32I标准指令中的内容，仅目前作为占位符使用
  //   这里的顺序需要和RISC-V指令码对应
endmodule

module M2A_lcu_8 (
  input  C0,
  input  P0,
  input  G0,
  input  P1,
  input  G1,
  input  P2,
  input  G2,
  input  P3,
  input  G3,
  input  P4,
  input  G4,
  input  P5,
  input  G5,
  input  P6,
  input  G6,
  input  P7,
  input  G7,
  output PG,
  output GG,
  output C1,
  output C2,
  output C3,
  output C4,
  output C5,
  output C6,
  output C7,
  output C8
);

  wire and_1_out, and_2_out, and_3_out, and_4_out, and_5_out, and_6_out, and_7_out, and_8_out, and_9_out,
       and_10_out, and_11_out, and_12_out, and_13_out, and_14_out, and_15_out, and_16_out, and_17_out,
       and_18_out, and_19_out, and_20_out, and_21_out, and_22_out, and_23_out, and_24_out, and_25_out,
       and_26_out, and_27_out, and_28_out, and_29_out, and_30_out, and_31_out, and_32_out, and_33_out,
       and_34_out, and_35_out, and_36_out;

  or or_1 (C1, G0, and_1_out);
  and and_1 (and_1_out, C0, P0);
  and and_2 (and_2_out, G0, P1);
  or or_2 (C2, G1, and_2_out, and_3_out);
  and and_3 (and_3_out, C0, P0, P1);
  or or_3 (C3, G2, and_4_out, and_5_out, and_6_out);
  and and_4 (and_4_out, G1, P2);
  and and_5 (and_5_out, G0, P1, P2);
  and and_6 (and_6_out, C0, P0, P1, P2);
  and and_7 (and_7_out, G2, P3);
  or or_4 (C4, G3, and_7_out, and_8_out, and_9_out, and_10_out);
  and and_8 (and_8_out, G1, P2, P3);
  and and_9 (and_9_out, G0, P1, P2, P3);
  and and_10 (and_10_out, C0, P0, P1, P2, P3);
  and and_11 (and_11_out, G3, P4);
  or or_5 (C5, G4, and_11_out, and_12_out, and_13_out, and_14_out, and_15_out);
  and and_12 (and_12_out, G2, P3, P4);
  and and_13 (and_13_out, G1, P2, P3, P4);
  and and_14 (and_14_out, G0, P1, P2, P3, P4);
  and and_15 (and_15_out, C0, P0, P1, P2, P3, P4);
  and and_16 (and_16_out, G4, P5);
  or or_6 (C6, G5, and_16_out, and_17_out, and_18_out, and_19_out, and_20_out, and_21_out);
  and and_17 (and_17_out, G3, P4, P5);
  and and_18 (and_18_out, G2, P3, P4, P5);
  and and_19 (and_19_out, G1, P2, P3, P4, P5);
  and and_20 (and_20_out, G0, P1, P2, P3, P4, P5);
  and and_21 (and_21_out, C0, P0, P1, P2, P3, P4, P5);
  and and_22 (and_22_out, G5, P6);
  or or_7 (C7, G6, and_22_out, and_23_out, and_24_out, and_25_out, and_26_out, and_27_out, and_28_out);
  and and_23 (and_23_out, G4, P5, P6);
  and and_24 (and_24_out, G3, P4, P5, P6);
  and and_25 (and_25_out, G2, P3, P4, P5, P6);
  and and_26 (and_26_out, G1, P2, P3, P4, P5, P6);
  and and_27 (and_27_out, G0, P1, P2, P3, P4, P5, P6);
  and and_28 (and_28_out, C0, P0, P1, P2, P3, P4, P5, P6);
  and and_29 (and_29_out, G6, P7);
  or or_8 (C8, G7, and_29_out, and_30_out, and_31_out, and_32_out, and_33_out, and_34_out, and_35_out, and_36_out);
  and and_30 (and_30_out, G5, P6, P7);
  and and_31 (and_31_out, G4, P5, P6, P7);
  and and_32 (and_32_out, G3, P4, P5, P6, P7);
  and and_33 (and_33_out, G2, P3, P4, P5, P6, P7);
  and and_34 (and_34_out, G1, P2, P3, P4, P5, P6, P7);
  and and_35 (and_35_out, G0, P1, P2, P3, P4, P5, P6, P7);
  and and_36 (and_36_out, C0, P0, P1, P2, P3, P4, P5, P6, P7);
  and and_37 (PG, P0, P1, P2, P3, P4, P5, P6, P7);

  assign GG = C8;
endmodule

module M2A_lcu_4 (
  input  C0,
  input  P0,
  input  G0,
  input  P1,
  input  G1,
  input  P2,
  input  G2,
  input  P3,
  input  G3,
  output PG,
  output GG,
  output C1,
  output C2,
  output C3,
  output C4
);

  wire and_1_out, and_2_out, and_3_out, and_4_out, and_5_out, and_6_out, and_7_out, and_8_out, and_9_out,
       and_10_out;

  or or_1 (C1, G0, and_1_out);
  and and_1 (and_1_out, P0, C0);
  and and_2 (and_2_out, G0, P1);
  or or_2 (C2, G1, and_2_out, and_3_out);
  and and_3 (and_3_out, C0, P0, P1);
  or or_3 (C3, G2, and_4_out, and_5_out, and_6_out);
  and and_4 (and_4_out, G1, P2);
  and and_5 (and_5_out, G0, P1, P2);
  and and_6 (and_6_out, C0, P0, P1, P2);
  and and_7 (and_7_out, G2, P3);
  or or_4 (C4, G3, and_7_out, and_8_out, and_9_out, and_10_out);
  and and_8 (and_8_out, G1, P2, P3);
  and and_9 (and_9_out, G0, P1, P2, P3);
  and and_10 (and_10_out, C0, P0, P1, P2, P3);
  and and_11 (PG, P0, P1, P2, P3);

  assign GG = C4;
endmodule

module M2A_reduction_and_32 (
  input  [31:0] in_1,
  output out_2
);

  and and_1 (out_2, in_1[0], in_1[1], in_1[2], in_1[3], in_1[4], in_1[5], in_1[6], in_1[7], in_1[8], in_1[9], in_1[10], in_1[11], in_1[12], in_1[13], in_1[14], in_1[15], in_1[16], in_1[17], in_1[18], in_1[19], in_1[20], in_1[21], in_1[22], in_1[23], in_1[24], in_1[25], in_1[26], in_1[27], in_1[28], in_1[29], in_1[30], in_1[31]);
endmodule

module M2A_reduction_and_8 (
  input  [7:0] in_1,
  output out_2
);

  and and_1 (out_2, in_1[0], in_1[1], in_1[2], in_1[3], in_1[5], in_1[6], in_1[7], in_1[4]);
endmodule

module M2A_shift_left_32 (
  input  [31:0] I,
  input  [4:0] Len,
  output [31:0] O
);

  wire [31:0] m2a_mux2_1_out_4, m2a_mux2_33_out_4, m2a_mux4_1_out_6;

  M2A_mux4 m2a_mux4_1 (
    .out_6(m2a_mux4_1_out_6[0]), .in_2(1'b0), .in_3(1'b0), .in_4(1'b0), .in_5(I[0]), .in_1(Len[1:0]));
  M2A_mux4 m2a_mux4_2 (
    .out_6(m2a_mux4_1_out_6[1]), .in_2(1'b0), .in_3(1'b0), .in_4(I[0]), .in_5(I[1]), .in_1(Len[1:0]));
  M2A_mux4 m2a_mux4_3 (
    .out_6(m2a_mux4_1_out_6[2]), .in_2(1'b0), .in_3(I[0]), .in_4(I[1]), .in_5(I[2]), .in_1(Len[1:0]));
  M2A_mux4 m2a_mux4_4 (
    .out_6(m2a_mux4_1_out_6[3]), .in_2(I[0]), .in_3(I[1]), .in_4(I[2]), .in_5(I[3]), .in_1(Len[1:0]));
  M2A_mux4 m2a_mux4_5 (
    .out_6(m2a_mux4_1_out_6[4]), .in_2(I[1]), .in_3(I[2]), .in_4(I[3]), .in_5(I[4]), .in_1(Len[1:0]));
  M2A_mux4 m2a_mux4_6 (
    .out_6(m2a_mux4_1_out_6[5]), .in_2(I[2]), .in_3(I[3]), .in_4(I[4]), .in_5(I[5]), .in_1(Len[1:0]));
  M2A_mux4 m2a_mux4_7 (
    .out_6(m2a_mux4_1_out_6[6]), .in_2(I[3]), .in_3(I[4]), .in_4(I[5]), .in_5(I[6]), .in_1(Len[1:0]));
  M2A_mux4 m2a_mux4_8 (
    .out_6(m2a_mux4_1_out_6[7]), .in_2(I[4]), .in_3(I[5]), .in_4(I[6]), .in_5(I[7]), .in_1(Len[1:0]));
  M2A_mux4 m2a_mux4_9 (
    .out_6(m2a_mux4_1_out_6[8]), .in_2(I[5]), .in_3(I[6]), .in_4(I[7]), .in_5(I[8]), .in_1(Len[1:0]));
  M2A_mux4 m2a_mux4_10 (
    .out_6(m2a_mux4_1_out_6[9]), .in_2(I[6]), .in_3(I[7]), .in_4(I[8]), .in_5(I[9]), .in_1(Len[1:0]));
  M2A_mux4 m2a_mux4_11 (
    .out_6(m2a_mux4_1_out_6[10]), .in_2(I[7]), .in_3(I[8]), .in_4(I[9]), .in_5(I[10]), .in_1(Len[1:0]));
  M2A_mux4 m2a_mux4_12 (
    .out_6(m2a_mux4_1_out_6[11]), .in_2(I[8]), .in_3(I[9]), .in_4(I[10]), .in_5(I[11]), .in_1(Len[1:0]));
  M2A_mux4 m2a_mux4_13 (
    .out_6(m2a_mux4_1_out_6[12]), .in_2(I[9]), .in_3(I[10]), .in_4(I[11]), .in_5(I[12]), .in_1(Len[1:0]));
  M2A_mux4 m2a_mux4_14 (
    .out_6(m2a_mux4_1_out_6[13]), .in_2(I[10]), .in_3(I[11]), .in_4(I[12]), .in_5(I[13]), .in_1(Len[1:0]));
  M2A_mux4 m2a_mux4_15 (
    .out_6(m2a_mux4_1_out_6[14]), .in_2(I[11]), .in_3(I[12]), .in_4(I[13]), .in_5(I[14]), .in_1(Len[1:0]));
  M2A_mux4 m2a_mux4_16 (
    .out_6(m2a_mux4_1_out_6[15]), .in_2(I[12]), .in_3(I[13]), .in_4(I[14]), .in_5(I[15]), .in_1(Len[1:0]));
  M2A_mux4 m2a_mux4_17 (
    .out_6(m2a_mux4_1_out_6[16]), .in_2(I[13]), .in_3(I[14]), .in_4(I[15]), .in_5(I[16]), .in_1(Len[1:0]));
  M2A_mux4 m2a_mux4_18 (
    .out_6(m2a_mux4_1_out_6[17]), .in_2(I[14]), .in_3(I[15]), .in_4(I[16]), .in_5(I[17]), .in_1(Len[1:0]));
  M2A_mux4 m2a_mux4_19 (
    .out_6(m2a_mux4_1_out_6[18]), .in_2(I[15]), .in_3(I[16]), .in_4(I[17]), .in_5(I[18]), .in_1(Len[1:0]));
  M2A_mux4 m2a_mux4_20 (
    .out_6(m2a_mux4_1_out_6[19]), .in_2(I[16]), .in_3(I[17]), .in_4(I[18]), .in_5(I[19]), .in_1(Len[1:0]));
  M2A_mux4 m2a_mux4_21 (
    .out_6(m2a_mux4_1_out_6[20]), .in_2(I[17]), .in_3(I[18]), .in_4(I[19]), .in_5(I[20]), .in_1(Len[1:0]));
  M2A_mux4 m2a_mux4_22 (
    .out_6(m2a_mux4_1_out_6[21]), .in_2(I[18]), .in_3(I[19]), .in_4(I[20]), .in_5(I[21]), .in_1(Len[1:0]));
  M2A_mux4 m2a_mux4_23 (
    .out_6(m2a_mux4_1_out_6[22]), .in_2(I[19]), .in_3(I[20]), .in_4(I[21]), .in_5(I[22]), .in_1(Len[1:0]));
  M2A_mux4 m2a_mux4_24 (
    .out_6(m2a_mux4_1_out_6[23]), .in_2(I[20]), .in_3(I[21]), .in_4(I[22]), .in_5(I[23]), .in_1(Len[1:0]));
  M2A_mux4 m2a_mux4_25 (
    .out_6(m2a_mux4_1_out_6[24]), .in_2(I[21]), .in_3(I[22]), .in_4(I[23]), .in_5(I[24]), .in_1(Len[1:0]));
  M2A_mux4 m2a_mux4_26 (
    .out_6(m2a_mux4_1_out_6[25]), .in_2(I[22]), .in_3(I[23]), .in_4(I[24]), .in_5(I[25]), .in_1(Len[1:0]));
  M2A_mux4 m2a_mux4_27 (
    .out_6(m2a_mux4_1_out_6[26]), .in_2(I[23]), .in_3(I[24]), .in_4(I[25]), .in_5(I[26]), .in_1(Len[1:0]));
  M2A_mux4 m2a_mux4_28 (
    .out_6(m2a_mux4_1_out_6[27]), .in_2(I[24]), .in_3(I[25]), .in_4(I[26]), .in_5(I[27]), .in_1(Len[1:0]));
  M2A_mux4 m2a_mux4_29 (
    .out_6(m2a_mux4_1_out_6[28]), .in_2(I[25]), .in_3(I[26]), .in_4(I[27]), .in_5(I[28]), .in_1(Len[1:0]));
  M2A_mux4 m2a_mux4_30 (
    .out_6(m2a_mux4_1_out_6[29]), .in_2(I[26]), .in_3(I[27]), .in_4(I[28]), .in_5(I[29]), .in_1(Len[1:0]));
  M2A_mux4 m2a_mux4_31 (
    .out_6(m2a_mux4_1_out_6[30]), .in_2(I[27]), .in_3(I[28]), .in_4(I[29]), .in_5(I[30]), .in_1(Len[1:0]));
  M2A_mux4 m2a_mux4_32 (
    .out_6(m2a_mux4_1_out_6[31]), .in_2(I[28]), .in_3(I[29]), .in_4(I[30]), .in_5(I[31]), .in_1(Len[1:0]));
  M2A_mux2 m2a_mux2_1 (.out_4(m2a_mux2_1_out_4[0]), .in_2(1'b0), .in_3(m2a_mux4_1_out_6[0]), .in_1(Len[2]));
  M2A_mux2 m2a_mux2_2 (.out_4(m2a_mux2_1_out_4[1]), .in_2(1'b0), .in_3(m2a_mux4_1_out_6[1]), .in_1(Len[2]));
  M2A_mux2 m2a_mux2_3 (.out_4(m2a_mux2_1_out_4[2]), .in_2(1'b0), .in_3(m2a_mux4_1_out_6[2]), .in_1(Len[2]));
  M2A_mux2 m2a_mux2_4 (.out_4(m2a_mux2_1_out_4[3]), .in_2(1'b0), .in_3(m2a_mux4_1_out_6[3]), .in_1(Len[2]));
  M2A_mux2 m2a_mux2_5 (
    .out_4(m2a_mux2_1_out_4[4]), .in_2(m2a_mux4_1_out_6[0]), .in_3(m2a_mux4_1_out_6[4]), .in_1(Len[2]));
  M2A_mux2 m2a_mux2_6 (
    .out_4(m2a_mux2_1_out_4[5]), .in_2(m2a_mux4_1_out_6[1]), .in_3(m2a_mux4_1_out_6[5]), .in_1(Len[2]));
  M2A_mux2 m2a_mux2_7 (
    .out_4(m2a_mux2_1_out_4[6]), .in_2(m2a_mux4_1_out_6[2]), .in_3(m2a_mux4_1_out_6[6]), .in_1(Len[2]));
  M2A_mux2 m2a_mux2_8 (
    .out_4(m2a_mux2_1_out_4[7]), .in_2(m2a_mux4_1_out_6[3]), .in_3(m2a_mux4_1_out_6[7]), .in_1(Len[2]));
  M2A_mux2 m2a_mux2_9 (
    .out_4(m2a_mux2_1_out_4[8]), .in_2(m2a_mux4_1_out_6[4]), .in_3(m2a_mux4_1_out_6[8]), .in_1(Len[2]));
  M2A_mux2 m2a_mux2_10 (
    .out_4(m2a_mux2_1_out_4[9]), .in_2(m2a_mux4_1_out_6[5]), .in_3(m2a_mux4_1_out_6[9]), .in_1(Len[2]));
  M2A_mux2 m2a_mux2_11 (
    .out_4(m2a_mux2_1_out_4[10]), .in_2(m2a_mux4_1_out_6[6]), .in_3(m2a_mux4_1_out_6[10]), .in_1(Len[2]));
  M2A_mux2 m2a_mux2_12 (
    .out_4(m2a_mux2_1_out_4[11]), .in_2(m2a_mux4_1_out_6[7]), .in_3(m2a_mux4_1_out_6[11]), .in_1(Len[2]));
  M2A_mux2 m2a_mux2_13 (
    .out_4(m2a_mux2_1_out_4[12]), .in_2(m2a_mux4_1_out_6[8]), .in_3(m2a_mux4_1_out_6[12]), .in_1(Len[2]));
  M2A_mux2 m2a_mux2_14 (
    .out_4(m2a_mux2_1_out_4[13]), .in_2(m2a_mux4_1_out_6[9]), .in_3(m2a_mux4_1_out_6[13]), .in_1(Len[2]));
  M2A_mux2 m2a_mux2_15 (
    .out_4(m2a_mux2_1_out_4[14]), .in_2(m2a_mux4_1_out_6[10]), .in_3(m2a_mux4_1_out_6[14]), .in_1(Len[2]));
  M2A_mux2 m2a_mux2_16 (
    .out_4(m2a_mux2_1_out_4[15]), .in_2(m2a_mux4_1_out_6[11]), .in_3(m2a_mux4_1_out_6[15]), .in_1(Len[2]));
  M2A_mux2 m2a_mux2_17 (
    .out_4(m2a_mux2_1_out_4[16]), .in_2(m2a_mux4_1_out_6[12]), .in_3(m2a_mux4_1_out_6[16]), .in_1(Len[2]));
  M2A_mux2 m2a_mux2_18 (
    .out_4(m2a_mux2_1_out_4[17]), .in_2(m2a_mux4_1_out_6[13]), .in_3(m2a_mux4_1_out_6[17]), .in_1(Len[2]));
  M2A_mux2 m2a_mux2_19 (
    .out_4(m2a_mux2_1_out_4[18]), .in_2(m2a_mux4_1_out_6[14]), .in_3(m2a_mux4_1_out_6[18]), .in_1(Len[2]));
  M2A_mux2 m2a_mux2_20 (
    .out_4(m2a_mux2_1_out_4[19]), .in_2(m2a_mux4_1_out_6[15]), .in_3(m2a_mux4_1_out_6[19]), .in_1(Len[2]));
  M2A_mux2 m2a_mux2_21 (
    .out_4(m2a_mux2_1_out_4[20]), .in_2(m2a_mux4_1_out_6[16]), .in_3(m2a_mux4_1_out_6[20]), .in_1(Len[2]));
  M2A_mux2 m2a_mux2_22 (
    .out_4(m2a_mux2_1_out_4[21]), .in_2(m2a_mux4_1_out_6[17]), .in_3(m2a_mux4_1_out_6[21]), .in_1(Len[2]));
  M2A_mux2 m2a_mux2_23 (
    .out_4(m2a_mux2_1_out_4[22]), .in_2(m2a_mux4_1_out_6[18]), .in_3(m2a_mux4_1_out_6[22]), .in_1(Len[2]));
  M2A_mux2 m2a_mux2_24 (
    .out_4(m2a_mux2_1_out_4[23]), .in_2(m2a_mux4_1_out_6[19]), .in_3(m2a_mux4_1_out_6[23]), .in_1(Len[2]));
  M2A_mux2 m2a_mux2_25 (
    .out_4(m2a_mux2_1_out_4[24]), .in_2(m2a_mux4_1_out_6[20]), .in_3(m2a_mux4_1_out_6[24]), .in_1(Len[2]));
  M2A_mux2 m2a_mux2_26 (
    .out_4(m2a_mux2_1_out_4[25]), .in_2(m2a_mux4_1_out_6[21]), .in_3(m2a_mux4_1_out_6[25]), .in_1(Len[2]));
  M2A_mux2 m2a_mux2_27 (
    .out_4(m2a_mux2_1_out_4[26]), .in_2(m2a_mux4_1_out_6[22]), .in_3(m2a_mux4_1_out_6[26]), .in_1(Len[2]));
  M2A_mux2 m2a_mux2_28 (
    .out_4(m2a_mux2_1_out_4[27]), .in_2(m2a_mux4_1_out_6[23]), .in_3(m2a_mux4_1_out_6[27]), .in_1(Len[2]));
  M2A_mux2 m2a_mux2_29 (
    .out_4(m2a_mux2_1_out_4[28]), .in_2(m2a_mux4_1_out_6[24]), .in_3(m2a_mux4_1_out_6[28]), .in_1(Len[2]));
  M2A_mux2 m2a_mux2_30 (
    .out_4(m2a_mux2_1_out_4[29]), .in_2(m2a_mux4_1_out_6[25]), .in_3(m2a_mux4_1_out_6[29]), .in_1(Len[2]));
  M2A_mux2 m2a_mux2_31 (
    .out_4(m2a_mux2_1_out_4[30]), .in_2(m2a_mux4_1_out_6[26]), .in_3(m2a_mux4_1_out_6[30]), .in_1(Len[2]));
  M2A_mux2 m2a_mux2_32 (
    .out_4(m2a_mux2_1_out_4[31]), .in_2(m2a_mux4_1_out_6[27]), .in_3(m2a_mux4_1_out_6[31]), .in_1(Len[2]));
  M2A_mux2 m2a_mux2_33 (.out_4(m2a_mux2_33_out_4[0]), .in_2(1'b0), .in_3(m2a_mux2_1_out_4[0]), .in_1(Len[3]));
  M2A_mux2 m2a_mux2_34 (.out_4(m2a_mux2_33_out_4[1]), .in_2(1'b0), .in_3(m2a_mux2_1_out_4[1]), .in_1(Len[3]));
  M2A_mux2 m2a_mux2_35 (.out_4(m2a_mux2_33_out_4[2]), .in_2(1'b0), .in_3(m2a_mux2_1_out_4[2]), .in_1(Len[3]));
  M2A_mux2 m2a_mux2_36 (.out_4(m2a_mux2_33_out_4[3]), .in_2(1'b0), .in_3(m2a_mux2_1_out_4[3]), .in_1(Len[3]));
  M2A_mux2 m2a_mux2_37 (.out_4(m2a_mux2_33_out_4[4]), .in_2(1'b0), .in_3(m2a_mux2_1_out_4[4]), .in_1(Len[3]));
  M2A_mux2 m2a_mux2_38 (.out_4(m2a_mux2_33_out_4[5]), .in_2(1'b0), .in_3(m2a_mux2_1_out_4[5]), .in_1(Len[3]));
  M2A_mux2 m2a_mux2_39 (.out_4(m2a_mux2_33_out_4[6]), .in_2(1'b0), .in_3(m2a_mux2_1_out_4[6]), .in_1(Len[3]));
  M2A_mux2 m2a_mux2_40 (.out_4(m2a_mux2_33_out_4[7]), .in_2(1'b0), .in_3(m2a_mux2_1_out_4[7]), .in_1(Len[3]));
  M2A_mux2 m2a_mux2_41 (
    .out_4(m2a_mux2_33_out_4[8]), .in_2(m2a_mux2_1_out_4[0]), .in_3(m2a_mux2_1_out_4[8]), .in_1(Len[3]));
  M2A_mux2 m2a_mux2_42 (
    .out_4(m2a_mux2_33_out_4[9]), .in_2(m2a_mux2_1_out_4[1]), .in_3(m2a_mux2_1_out_4[9]), .in_1(Len[3]));
  M2A_mux2 m2a_mux2_43 (
    .out_4(m2a_mux2_33_out_4[10]), .in_2(m2a_mux2_1_out_4[2]), .in_3(m2a_mux2_1_out_4[10]), .in_1(Len[3]));
  M2A_mux2 m2a_mux2_44 (
    .out_4(m2a_mux2_33_out_4[11]), .in_2(m2a_mux2_1_out_4[3]), .in_3(m2a_mux2_1_out_4[11]), .in_1(Len[3]));
  M2A_mux2 m2a_mux2_45 (
    .out_4(m2a_mux2_33_out_4[12]), .in_2(m2a_mux2_1_out_4[4]), .in_3(m2a_mux2_1_out_4[12]), .in_1(Len[3]));
  M2A_mux2 m2a_mux2_46 (
    .out_4(m2a_mux2_33_out_4[13]), .in_2(m2a_mux2_1_out_4[5]), .in_3(m2a_mux2_1_out_4[13]), .in_1(Len[3]));
  M2A_mux2 m2a_mux2_47 (
    .out_4(m2a_mux2_33_out_4[14]), .in_2(m2a_mux2_1_out_4[6]), .in_3(m2a_mux2_1_out_4[14]), .in_1(Len[3]));
  M2A_mux2 m2a_mux2_48 (
    .out_4(m2a_mux2_33_out_4[15]), .in_2(m2a_mux2_1_out_4[7]), .in_3(m2a_mux2_1_out_4[15]), .in_1(Len[3]));
  M2A_mux2 m2a_mux2_49 (
    .out_4(m2a_mux2_33_out_4[16]), .in_2(m2a_mux2_1_out_4[8]), .in_3(m2a_mux2_1_out_4[16]), .in_1(Len[3]));
  M2A_mux2 m2a_mux2_50 (
    .out_4(m2a_mux2_33_out_4[17]), .in_2(m2a_mux2_1_out_4[9]), .in_3(m2a_mux2_1_out_4[17]), .in_1(Len[3]));
  M2A_mux2 m2a_mux2_51 (
    .out_4(m2a_mux2_33_out_4[18]), .in_2(m2a_mux2_1_out_4[10]), .in_3(m2a_mux2_1_out_4[18]), .in_1(Len[3]));
  M2A_mux2 m2a_mux2_52 (
    .out_4(m2a_mux2_33_out_4[19]), .in_2(m2a_mux2_1_out_4[11]), .in_3(m2a_mux2_1_out_4[19]), .in_1(Len[3]));
  M2A_mux2 m2a_mux2_53 (
    .out_4(m2a_mux2_33_out_4[20]), .in_2(m2a_mux2_1_out_4[12]), .in_3(m2a_mux2_1_out_4[20]), .in_1(Len[3]));
  M2A_mux2 m2a_mux2_54 (
    .out_4(m2a_mux2_33_out_4[21]), .in_2(m2a_mux2_1_out_4[13]), .in_3(m2a_mux2_1_out_4[21]), .in_1(Len[3]));
  M2A_mux2 m2a_mux2_55 (
    .out_4(m2a_mux2_33_out_4[22]), .in_2(m2a_mux2_1_out_4[14]), .in_3(m2a_mux2_1_out_4[22]), .in_1(Len[3]));
  M2A_mux2 m2a_mux2_56 (
    .out_4(m2a_mux2_33_out_4[23]), .in_2(m2a_mux2_1_out_4[15]), .in_3(m2a_mux2_1_out_4[23]), .in_1(Len[3]));
  M2A_mux2 m2a_mux2_57 (
    .out_4(m2a_mux2_33_out_4[24]), .in_2(m2a_mux2_1_out_4[16]), .in_3(m2a_mux2_1_out_4[24]), .in_1(Len[3]));
  M2A_mux2 m2a_mux2_58 (
    .out_4(m2a_mux2_33_out_4[25]), .in_2(m2a_mux2_1_out_4[17]), .in_3(m2a_mux2_1_out_4[25]), .in_1(Len[3]));
  M2A_mux2 m2a_mux2_59 (
    .out_4(m2a_mux2_33_out_4[26]), .in_2(m2a_mux2_1_out_4[18]), .in_3(m2a_mux2_1_out_4[26]), .in_1(Len[3]));
  M2A_mux2 m2a_mux2_60 (
    .out_4(m2a_mux2_33_out_4[27]), .in_2(m2a_mux2_1_out_4[19]), .in_3(m2a_mux2_1_out_4[27]), .in_1(Len[3]));
  M2A_mux2 m2a_mux2_61 (
    .out_4(m2a_mux2_33_out_4[28]), .in_2(m2a_mux2_1_out_4[20]), .in_3(m2a_mux2_1_out_4[28]), .in_1(Len[3]));
  M2A_mux2 m2a_mux2_62 (
    .out_4(m2a_mux2_33_out_4[29]), .in_2(m2a_mux2_1_out_4[21]), .in_3(m2a_mux2_1_out_4[29]), .in_1(Len[3]));
  M2A_mux2 m2a_mux2_63 (
    .out_4(m2a_mux2_33_out_4[30]), .in_2(m2a_mux2_1_out_4[22]), .in_3(m2a_mux2_1_out_4[30]), .in_1(Len[3]));
  M2A_mux2 m2a_mux2_64 (
    .out_4(m2a_mux2_33_out_4[31]), .in_2(m2a_mux2_1_out_4[23]), .in_3(m2a_mux2_1_out_4[31]), .in_1(Len[3]));
  M2A_mux2 m2a_mux2_65 (.out_4(O[0]), .in_2(1'b0), .in_3(m2a_mux2_33_out_4[0]), .in_1(Len[4]));
  M2A_mux2 m2a_mux2_66 (.out_4(O[1]), .in_2(1'b0), .in_3(m2a_mux2_33_out_4[1]), .in_1(Len[4]));
  M2A_mux2 m2a_mux2_67 (.out_4(O[2]), .in_2(1'b0), .in_3(m2a_mux2_33_out_4[2]), .in_1(Len[4]));
  M2A_mux2 m2a_mux2_68 (.out_4(O[3]), .in_2(1'b0), .in_3(m2a_mux2_33_out_4[3]), .in_1(Len[4]));
  M2A_mux2 m2a_mux2_69 (.out_4(O[4]), .in_2(1'b0), .in_3(m2a_mux2_33_out_4[4]), .in_1(Len[4]));
  M2A_mux2 m2a_mux2_70 (.out_4(O[5]), .in_2(1'b0), .in_3(m2a_mux2_33_out_4[5]), .in_1(Len[4]));
  M2A_mux2 m2a_mux2_71 (.out_4(O[6]), .in_2(1'b0), .in_3(m2a_mux2_33_out_4[6]), .in_1(Len[4]));
  M2A_mux2 m2a_mux2_72 (.out_4(O[7]), .in_2(1'b0), .in_3(m2a_mux2_33_out_4[7]), .in_1(Len[4]));
  M2A_mux2 m2a_mux2_73 (.out_4(O[8]), .in_2(1'b0), .in_3(m2a_mux2_33_out_4[8]), .in_1(Len[4]));
  M2A_mux2 m2a_mux2_74 (.out_4(O[9]), .in_2(1'b0), .in_3(m2a_mux2_33_out_4[9]), .in_1(Len[4]));
  M2A_mux2 m2a_mux2_75 (.out_4(O[10]), .in_2(1'b0), .in_3(m2a_mux2_33_out_4[10]), .in_1(Len[4]));
  M2A_mux2 m2a_mux2_76 (.out_4(O[11]), .in_2(1'b0), .in_3(m2a_mux2_33_out_4[11]), .in_1(Len[4]));
  M2A_mux2 m2a_mux2_77 (.out_4(O[12]), .in_2(1'b0), .in_3(m2a_mux2_33_out_4[12]), .in_1(Len[4]));
  M2A_mux2 m2a_mux2_78 (.out_4(O[13]), .in_2(1'b0), .in_3(m2a_mux2_33_out_4[13]), .in_1(Len[4]));
  M2A_mux2 m2a_mux2_79 (.out_4(O[14]), .in_2(1'b0), .in_3(m2a_mux2_33_out_4[14]), .in_1(Len[4]));
  M2A_mux2 m2a_mux2_80 (.out_4(O[15]), .in_2(1'b0), .in_3(m2a_mux2_33_out_4[15]), .in_1(Len[4]));
  M2A_mux2 m2a_mux2_81 (.out_4(O[16]), .in_2(m2a_mux2_33_out_4[0]), .in_3(m2a_mux2_33_out_4[16]), .in_1(Len[4]));
  M2A_mux2 m2a_mux2_82 (.out_4(O[17]), .in_2(m2a_mux2_33_out_4[1]), .in_3(m2a_mux2_33_out_4[17]), .in_1(Len[4]));
  M2A_mux2 m2a_mux2_83 (.out_4(O[18]), .in_2(m2a_mux2_33_out_4[2]), .in_3(m2a_mux2_33_out_4[18]), .in_1(Len[4]));
  M2A_mux2 m2a_mux2_84 (.out_4(O[19]), .in_2(m2a_mux2_33_out_4[3]), .in_3(m2a_mux2_33_out_4[19]), .in_1(Len[4]));
  M2A_mux2 m2a_mux2_85 (.out_4(O[20]), .in_2(m2a_mux2_33_out_4[4]), .in_3(m2a_mux2_33_out_4[20]), .in_1(Len[4]));
  M2A_mux2 m2a_mux2_86 (.out_4(O[21]), .in_2(m2a_mux2_33_out_4[5]), .in_3(m2a_mux2_33_out_4[21]), .in_1(Len[4]));
  M2A_mux2 m2a_mux2_87 (.out_4(O[22]), .in_2(m2a_mux2_33_out_4[6]), .in_3(m2a_mux2_33_out_4[22]), .in_1(Len[4]));
  M2A_mux2 m2a_mux2_88 (.out_4(O[23]), .in_2(m2a_mux2_33_out_4[7]), .in_3(m2a_mux2_33_out_4[23]), .in_1(Len[4]));
  M2A_mux2 m2a_mux2_89 (.out_4(O[24]), .in_2(m2a_mux2_33_out_4[8]), .in_3(m2a_mux2_33_out_4[24]), .in_1(Len[4]));
  M2A_mux2 m2a_mux2_90 (.out_4(O[25]), .in_2(m2a_mux2_33_out_4[9]), .in_3(m2a_mux2_33_out_4[25]), .in_1(Len[4]));
  M2A_mux2 m2a_mux2_91 (.out_4(O[26]), .in_2(m2a_mux2_33_out_4[10]), .in_3(m2a_mux2_33_out_4[26]), .in_1(Len[4]));
  M2A_mux2 m2a_mux2_92 (.out_4(O[27]), .in_2(m2a_mux2_33_out_4[11]), .in_3(m2a_mux2_33_out_4[27]), .in_1(Len[4]));
  M2A_mux2 m2a_mux2_93 (.out_4(O[28]), .in_2(m2a_mux2_33_out_4[12]), .in_3(m2a_mux2_33_out_4[28]), .in_1(Len[4]));
  M2A_mux2 m2a_mux2_94 (.out_4(O[29]), .in_2(m2a_mux2_33_out_4[13]), .in_3(m2a_mux2_33_out_4[29]), .in_1(Len[4]));
  M2A_mux2 m2a_mux2_95 (.out_4(O[30]), .in_2(m2a_mux2_33_out_4[14]), .in_3(m2a_mux2_33_out_4[30]), .in_1(Len[4]));
  M2A_mux2 m2a_mux2_96 (.out_4(O[31]), .in_2(m2a_mux2_33_out_4[15]), .in_3(m2a_mux2_33_out_4[31]), .in_1(Len[4]));
endmodule

module M2A_shift_right_32 (
  input  [31:0] I,
  input  [4:0] Len,
  input  Arith,
  output [31:0] O
);

  wire MSB, shf_in;
  wire [31:0] m2a_mux2_32_out_4, m2a_mux2_64_out_4, m2a_mux4_32_out_6;

  BitSelector #(.width(32)) bitselector_1 (.in(I), .out(MSB), .sel({5{1'b1}}));
  and and_1 (shf_in, Arith, MSB);
  M2A_mux4 m2a_mux4_1 (
    .out_6(m2a_mux4_32_out_6[31]), .in_2(shf_in), .in_3(shf_in), .in_4(shf_in), .in_5(I[31]), .in_1(Len[1:0]));
  M2A_mux4 m2a_mux4_2 (
    .out_6(m2a_mux4_32_out_6[30]), .in_2(shf_in), .in_3(shf_in), .in_4(I[31]), .in_5(I[30]), .in_1(Len[1:0]));
  M2A_mux4 m2a_mux4_3 (
    .out_6(m2a_mux4_32_out_6[29]), .in_2(shf_in), .in_3(I[31]), .in_4(I[30]), .in_5(I[29]), .in_1(Len[1:0]));
  M2A_mux4 m2a_mux4_4 (
    .out_6(m2a_mux4_32_out_6[28]), .in_2(I[31]), .in_3(I[30]), .in_4(I[29]), .in_5(I[28]), .in_1(Len[1:0]));
  M2A_mux4 m2a_mux4_5 (
    .out_6(m2a_mux4_32_out_6[27]), .in_2(I[30]), .in_3(I[29]), .in_4(I[28]), .in_5(I[27]), .in_1(Len[1:0]));
  M2A_mux4 m2a_mux4_6 (
    .out_6(m2a_mux4_32_out_6[26]), .in_2(I[29]), .in_3(I[28]), .in_4(I[27]), .in_5(I[26]), .in_1(Len[1:0]));
  M2A_mux4 m2a_mux4_7 (
    .out_6(m2a_mux4_32_out_6[25]), .in_2(I[28]), .in_3(I[27]), .in_4(I[26]), .in_5(I[25]), .in_1(Len[1:0]));
  M2A_mux4 m2a_mux4_8 (
    .out_6(m2a_mux4_32_out_6[24]), .in_2(I[27]), .in_3(I[26]), .in_4(I[25]), .in_5(I[24]), .in_1(Len[1:0]));
  M2A_mux4 m2a_mux4_9 (
    .out_6(m2a_mux4_32_out_6[23]), .in_2(I[26]), .in_3(I[25]), .in_4(I[24]), .in_5(I[23]), .in_1(Len[1:0]));
  M2A_mux4 m2a_mux4_10 (
    .out_6(m2a_mux4_32_out_6[22]), .in_2(I[25]), .in_3(I[24]), .in_4(I[23]), .in_5(I[22]), .in_1(Len[1:0]));
  M2A_mux4 m2a_mux4_11 (
    .out_6(m2a_mux4_32_out_6[21]), .in_2(I[24]), .in_3(I[23]), .in_4(I[22]), .in_5(I[21]), .in_1(Len[1:0]));
  M2A_mux4 m2a_mux4_12 (
    .out_6(m2a_mux4_32_out_6[20]), .in_2(I[23]), .in_3(I[22]), .in_4(I[21]), .in_5(I[20]), .in_1(Len[1:0]));
  M2A_mux4 m2a_mux4_13 (
    .out_6(m2a_mux4_32_out_6[19]), .in_2(I[22]), .in_3(I[21]), .in_4(I[20]), .in_5(I[19]), .in_1(Len[1:0]));
  M2A_mux4 m2a_mux4_14 (
    .out_6(m2a_mux4_32_out_6[18]), .in_2(I[21]), .in_3(I[20]), .in_4(I[19]), .in_5(I[18]), .in_1(Len[1:0]));
  M2A_mux4 m2a_mux4_15 (
    .out_6(m2a_mux4_32_out_6[17]), .in_2(I[20]), .in_3(I[19]), .in_4(I[18]), .in_5(I[17]), .in_1(Len[1:0]));
  M2A_mux4 m2a_mux4_16 (
    .out_6(m2a_mux4_32_out_6[16]), .in_2(I[19]), .in_3(I[18]), .in_4(I[17]), .in_5(I[16]), .in_1(Len[1:0]));
  M2A_mux4 m2a_mux4_17 (
    .out_6(m2a_mux4_32_out_6[15]), .in_2(I[18]), .in_3(I[17]), .in_4(I[16]), .in_5(I[15]), .in_1(Len[1:0]));
  M2A_mux4 m2a_mux4_18 (
    .out_6(m2a_mux4_32_out_6[14]), .in_2(I[17]), .in_3(I[16]), .in_4(I[15]), .in_5(I[14]), .in_1(Len[1:0]));
  M2A_mux4 m2a_mux4_19 (
    .out_6(m2a_mux4_32_out_6[13]), .in_2(I[16]), .in_3(I[15]), .in_4(I[14]), .in_5(I[13]), .in_1(Len[1:0]));
  M2A_mux4 m2a_mux4_20 (
    .out_6(m2a_mux4_32_out_6[12]), .in_2(I[15]), .in_3(I[14]), .in_4(I[13]), .in_5(I[12]), .in_1(Len[1:0]));
  M2A_mux4 m2a_mux4_21 (
    .out_6(m2a_mux4_32_out_6[11]), .in_2(I[14]), .in_3(I[13]), .in_4(I[12]), .in_5(I[11]), .in_1(Len[1:0]));
  M2A_mux4 m2a_mux4_22 (
    .out_6(m2a_mux4_32_out_6[10]), .in_2(I[13]), .in_3(I[12]), .in_4(I[11]), .in_5(I[10]), .in_1(Len[1:0]));
  M2A_mux4 m2a_mux4_23 (
    .out_6(m2a_mux4_32_out_6[9]), .in_2(I[12]), .in_3(I[11]), .in_4(I[10]), .in_5(I[9]), .in_1(Len[1:0]));
  M2A_mux4 m2a_mux4_24 (
    .out_6(m2a_mux4_32_out_6[8]), .in_2(I[11]), .in_3(I[10]), .in_4(I[9]), .in_5(I[8]), .in_1(Len[1:0]));
  M2A_mux4 m2a_mux4_25 (
    .out_6(m2a_mux4_32_out_6[7]), .in_2(I[10]), .in_3(I[9]), .in_4(I[8]), .in_5(I[7]), .in_1(Len[1:0]));
  M2A_mux4 m2a_mux4_26 (
    .out_6(m2a_mux4_32_out_6[6]), .in_2(I[9]), .in_3(I[8]), .in_4(I[7]), .in_5(I[6]), .in_1(Len[1:0]));
  M2A_mux4 m2a_mux4_27 (
    .out_6(m2a_mux4_32_out_6[5]), .in_2(I[8]), .in_3(I[7]), .in_4(I[6]), .in_5(I[5]), .in_1(Len[1:0]));
  M2A_mux4 m2a_mux4_28 (
    .out_6(m2a_mux4_32_out_6[4]), .in_2(I[7]), .in_3(I[6]), .in_4(I[5]), .in_5(I[4]), .in_1(Len[1:0]));
  M2A_mux4 m2a_mux4_29 (
    .out_6(m2a_mux4_32_out_6[3]), .in_2(I[6]), .in_3(I[5]), .in_4(I[4]), .in_5(I[3]), .in_1(Len[1:0]));
  M2A_mux4 m2a_mux4_30 (
    .out_6(m2a_mux4_32_out_6[2]), .in_2(I[5]), .in_3(I[4]), .in_4(I[3]), .in_5(I[2]), .in_1(Len[1:0]));
  M2A_mux4 m2a_mux4_31 (
    .out_6(m2a_mux4_32_out_6[1]), .in_2(I[4]), .in_3(I[3]), .in_4(I[2]), .in_5(I[1]), .in_1(Len[1:0]));
  M2A_mux4 m2a_mux4_32 (
    .out_6(m2a_mux4_32_out_6[0]), .in_2(I[3]), .in_3(I[2]), .in_4(I[1]), .in_5(I[0]), .in_1(Len[1:0]));
  M2A_mux2 m2a_mux2_1 (.out_4(m2a_mux2_32_out_4[31]), .in_2(shf_in), .in_3(m2a_mux4_32_out_6[31]), .in_1(Len[2]));
  M2A_mux2 m2a_mux2_2 (.out_4(m2a_mux2_32_out_4[30]), .in_2(shf_in), .in_3(m2a_mux4_32_out_6[30]), .in_1(Len[2]));
  M2A_mux2 m2a_mux2_3 (.out_4(m2a_mux2_32_out_4[29]), .in_2(shf_in), .in_3(m2a_mux4_32_out_6[29]), .in_1(Len[2]));
  M2A_mux2 m2a_mux2_4 (.out_4(m2a_mux2_32_out_4[28]), .in_2(shf_in), .in_3(m2a_mux4_32_out_6[28]), .in_1(Len[2]));
  M2A_mux2 m2a_mux2_5 (
    .out_4(m2a_mux2_32_out_4[27]), .in_2(m2a_mux4_32_out_6[31]), .in_3(m2a_mux4_32_out_6[27]), .in_1(Len[2]));
  M2A_mux2 m2a_mux2_6 (
    .out_4(m2a_mux2_32_out_4[26]), .in_2(m2a_mux4_32_out_6[30]), .in_3(m2a_mux4_32_out_6[26]), .in_1(Len[2]));
  M2A_mux2 m2a_mux2_7 (
    .out_4(m2a_mux2_32_out_4[25]), .in_2(m2a_mux4_32_out_6[29]), .in_3(m2a_mux4_32_out_6[25]), .in_1(Len[2]));
  M2A_mux2 m2a_mux2_8 (
    .out_4(m2a_mux2_32_out_4[24]), .in_2(m2a_mux4_32_out_6[28]), .in_3(m2a_mux4_32_out_6[24]), .in_1(Len[2]));
  M2A_mux2 m2a_mux2_9 (
    .out_4(m2a_mux2_32_out_4[23]), .in_2(m2a_mux4_32_out_6[27]), .in_3(m2a_mux4_32_out_6[23]), .in_1(Len[2]));
  M2A_mux2 m2a_mux2_10 (
    .out_4(m2a_mux2_32_out_4[22]), .in_2(m2a_mux4_32_out_6[26]), .in_3(m2a_mux4_32_out_6[22]), .in_1(Len[2]));
  M2A_mux2 m2a_mux2_11 (
    .out_4(m2a_mux2_32_out_4[21]), .in_2(m2a_mux4_32_out_6[25]), .in_3(m2a_mux4_32_out_6[21]), .in_1(Len[2]));
  M2A_mux2 m2a_mux2_12 (
    .out_4(m2a_mux2_32_out_4[20]), .in_2(m2a_mux4_32_out_6[24]), .in_3(m2a_mux4_32_out_6[20]), .in_1(Len[2]));
  M2A_mux2 m2a_mux2_13 (
    .out_4(m2a_mux2_32_out_4[19]), .in_2(m2a_mux4_32_out_6[23]), .in_3(m2a_mux4_32_out_6[19]), .in_1(Len[2]));
  M2A_mux2 m2a_mux2_14 (
    .out_4(m2a_mux2_32_out_4[18]), .in_2(m2a_mux4_32_out_6[22]), .in_3(m2a_mux4_32_out_6[18]), .in_1(Len[2]));
  M2A_mux2 m2a_mux2_15 (
    .out_4(m2a_mux2_32_out_4[17]), .in_2(m2a_mux4_32_out_6[21]), .in_3(m2a_mux4_32_out_6[17]), .in_1(Len[2]));
  M2A_mux2 m2a_mux2_16 (
    .out_4(m2a_mux2_32_out_4[16]), .in_2(m2a_mux4_32_out_6[20]), .in_3(m2a_mux4_32_out_6[16]), .in_1(Len[2]));
  M2A_mux2 m2a_mux2_17 (
    .out_4(m2a_mux2_32_out_4[15]), .in_2(m2a_mux4_32_out_6[19]), .in_3(m2a_mux4_32_out_6[15]), .in_1(Len[2]));
  M2A_mux2 m2a_mux2_18 (
    .out_4(m2a_mux2_32_out_4[14]), .in_2(m2a_mux4_32_out_6[18]), .in_3(m2a_mux4_32_out_6[14]), .in_1(Len[2]));
  M2A_mux2 m2a_mux2_19 (
    .out_4(m2a_mux2_32_out_4[13]), .in_2(m2a_mux4_32_out_6[17]), .in_3(m2a_mux4_32_out_6[13]), .in_1(Len[2]));
  M2A_mux2 m2a_mux2_20 (
    .out_4(m2a_mux2_32_out_4[12]), .in_2(m2a_mux4_32_out_6[16]), .in_3(m2a_mux4_32_out_6[12]), .in_1(Len[2]));
  M2A_mux2 m2a_mux2_21 (
    .out_4(m2a_mux2_32_out_4[11]), .in_2(m2a_mux4_32_out_6[15]), .in_3(m2a_mux4_32_out_6[11]), .in_1(Len[2]));
  M2A_mux2 m2a_mux2_22 (
    .out_4(m2a_mux2_32_out_4[10]), .in_2(m2a_mux4_32_out_6[14]), .in_3(m2a_mux4_32_out_6[10]), .in_1(Len[2]));
  M2A_mux2 m2a_mux2_23 (
    .out_4(m2a_mux2_32_out_4[9]), .in_2(m2a_mux4_32_out_6[13]), .in_3(m2a_mux4_32_out_6[9]), .in_1(Len[2]));
  M2A_mux2 m2a_mux2_24 (
    .out_4(m2a_mux2_32_out_4[8]), .in_2(m2a_mux4_32_out_6[12]), .in_3(m2a_mux4_32_out_6[8]), .in_1(Len[2]));
  M2A_mux2 m2a_mux2_25 (
    .out_4(m2a_mux2_32_out_4[7]), .in_2(m2a_mux4_32_out_6[11]), .in_3(m2a_mux4_32_out_6[7]), .in_1(Len[2]));
  M2A_mux2 m2a_mux2_26 (
    .out_4(m2a_mux2_32_out_4[6]), .in_2(m2a_mux4_32_out_6[10]), .in_3(m2a_mux4_32_out_6[6]), .in_1(Len[2]));
  M2A_mux2 m2a_mux2_27 (
    .out_4(m2a_mux2_32_out_4[5]), .in_2(m2a_mux4_32_out_6[9]), .in_3(m2a_mux4_32_out_6[5]), .in_1(Len[2]));
  M2A_mux2 m2a_mux2_28 (
    .out_4(m2a_mux2_32_out_4[4]), .in_2(m2a_mux4_32_out_6[8]), .in_3(m2a_mux4_32_out_6[4]), .in_1(Len[2]));
  M2A_mux2 m2a_mux2_29 (
    .out_4(m2a_mux2_32_out_4[3]), .in_2(m2a_mux4_32_out_6[7]), .in_3(m2a_mux4_32_out_6[3]), .in_1(Len[2]));
  M2A_mux2 m2a_mux2_30 (
    .out_4(m2a_mux2_32_out_4[2]), .in_2(m2a_mux4_32_out_6[6]), .in_3(m2a_mux4_32_out_6[2]), .in_1(Len[2]));
  M2A_mux2 m2a_mux2_31 (
    .out_4(m2a_mux2_32_out_4[1]), .in_2(m2a_mux4_32_out_6[5]), .in_3(m2a_mux4_32_out_6[1]), .in_1(Len[2]));
  M2A_mux2 m2a_mux2_32 (
    .out_4(m2a_mux2_32_out_4[0]), .in_2(m2a_mux4_32_out_6[4]), .in_3(m2a_mux4_32_out_6[0]), .in_1(Len[2]));
  M2A_mux2 m2a_mux2_33 (.out_4(m2a_mux2_64_out_4[31]), .in_2(shf_in), .in_3(m2a_mux2_32_out_4[31]), .in_1(Len[3]));
  M2A_mux2 m2a_mux2_34 (.out_4(m2a_mux2_64_out_4[30]), .in_2(shf_in), .in_3(m2a_mux2_32_out_4[30]), .in_1(Len[3]));
  M2A_mux2 m2a_mux2_35 (.out_4(m2a_mux2_64_out_4[29]), .in_2(shf_in), .in_3(m2a_mux2_32_out_4[29]), .in_1(Len[3]));
  M2A_mux2 m2a_mux2_36 (.out_4(m2a_mux2_64_out_4[28]), .in_2(shf_in), .in_3(m2a_mux2_32_out_4[28]), .in_1(Len[3]));
  M2A_mux2 m2a_mux2_37 (.out_4(m2a_mux2_64_out_4[27]), .in_2(shf_in), .in_3(m2a_mux2_32_out_4[27]), .in_1(Len[3]));
  M2A_mux2 m2a_mux2_38 (.out_4(m2a_mux2_64_out_4[26]), .in_2(shf_in), .in_3(m2a_mux2_32_out_4[26]), .in_1(Len[3]));
  M2A_mux2 m2a_mux2_39 (.out_4(m2a_mux2_64_out_4[25]), .in_2(shf_in), .in_3(m2a_mux2_32_out_4[25]), .in_1(Len[3]));
  M2A_mux2 m2a_mux2_40 (.out_4(m2a_mux2_64_out_4[24]), .in_2(shf_in), .in_3(m2a_mux2_32_out_4[24]), .in_1(Len[3]));
  M2A_mux2 m2a_mux2_41 (
    .out_4(m2a_mux2_64_out_4[23]), .in_2(m2a_mux2_32_out_4[31]), .in_3(m2a_mux2_32_out_4[23]), .in_1(Len[3]));
  M2A_mux2 m2a_mux2_42 (
    .out_4(m2a_mux2_64_out_4[22]), .in_2(m2a_mux2_32_out_4[30]), .in_3(m2a_mux2_32_out_4[22]), .in_1(Len[3]));
  M2A_mux2 m2a_mux2_43 (
    .out_4(m2a_mux2_64_out_4[21]), .in_2(m2a_mux2_32_out_4[29]), .in_3(m2a_mux2_32_out_4[21]), .in_1(Len[3]));
  M2A_mux2 m2a_mux2_44 (
    .out_4(m2a_mux2_64_out_4[20]), .in_2(m2a_mux2_32_out_4[28]), .in_3(m2a_mux2_32_out_4[20]), .in_1(Len[3]));
  M2A_mux2 m2a_mux2_45 (
    .out_4(m2a_mux2_64_out_4[19]), .in_2(m2a_mux2_32_out_4[27]), .in_3(m2a_mux2_32_out_4[19]), .in_1(Len[3]));
  M2A_mux2 m2a_mux2_46 (
    .out_4(m2a_mux2_64_out_4[18]), .in_2(m2a_mux2_32_out_4[26]), .in_3(m2a_mux2_32_out_4[18]), .in_1(Len[3]));
  M2A_mux2 m2a_mux2_47 (
    .out_4(m2a_mux2_64_out_4[17]), .in_2(m2a_mux2_32_out_4[25]), .in_3(m2a_mux2_32_out_4[17]), .in_1(Len[3]));
  M2A_mux2 m2a_mux2_48 (
    .out_4(m2a_mux2_64_out_4[16]), .in_2(m2a_mux2_32_out_4[24]), .in_3(m2a_mux2_32_out_4[16]), .in_1(Len[3]));
  M2A_mux2 m2a_mux2_49 (
    .out_4(m2a_mux2_64_out_4[15]), .in_2(m2a_mux2_32_out_4[23]), .in_3(m2a_mux2_32_out_4[15]), .in_1(Len[3]));
  M2A_mux2 m2a_mux2_50 (
    .out_4(m2a_mux2_64_out_4[14]), .in_2(m2a_mux2_32_out_4[22]), .in_3(m2a_mux2_32_out_4[14]), .in_1(Len[3]));
  M2A_mux2 m2a_mux2_51 (
    .out_4(m2a_mux2_64_out_4[13]), .in_2(m2a_mux2_32_out_4[21]), .in_3(m2a_mux2_32_out_4[13]), .in_1(Len[3]));
  M2A_mux2 m2a_mux2_52 (
    .out_4(m2a_mux2_64_out_4[12]), .in_2(m2a_mux2_32_out_4[20]), .in_3(m2a_mux2_32_out_4[12]), .in_1(Len[3]));
  M2A_mux2 m2a_mux2_53 (
    .out_4(m2a_mux2_64_out_4[11]), .in_2(m2a_mux2_32_out_4[19]), .in_3(m2a_mux2_32_out_4[11]), .in_1(Len[3]));
  M2A_mux2 m2a_mux2_54 (
    .out_4(m2a_mux2_64_out_4[10]), .in_2(m2a_mux2_32_out_4[18]), .in_3(m2a_mux2_32_out_4[10]), .in_1(Len[3]));
  M2A_mux2 m2a_mux2_55 (
    .out_4(m2a_mux2_64_out_4[9]), .in_2(m2a_mux2_32_out_4[17]), .in_3(m2a_mux2_32_out_4[9]), .in_1(Len[3]));
  M2A_mux2 m2a_mux2_56 (
    .out_4(m2a_mux2_64_out_4[8]), .in_2(m2a_mux2_32_out_4[16]), .in_3(m2a_mux2_32_out_4[8]), .in_1(Len[3]));
  M2A_mux2 m2a_mux2_57 (
    .out_4(m2a_mux2_64_out_4[7]), .in_2(m2a_mux2_32_out_4[15]), .in_3(m2a_mux2_32_out_4[7]), .in_1(Len[3]));
  M2A_mux2 m2a_mux2_58 (
    .out_4(m2a_mux2_64_out_4[6]), .in_2(m2a_mux2_32_out_4[14]), .in_3(m2a_mux2_32_out_4[6]), .in_1(Len[3]));
  M2A_mux2 m2a_mux2_59 (
    .out_4(m2a_mux2_64_out_4[5]), .in_2(m2a_mux2_32_out_4[13]), .in_3(m2a_mux2_32_out_4[5]), .in_1(Len[3]));
  M2A_mux2 m2a_mux2_60 (
    .out_4(m2a_mux2_64_out_4[4]), .in_2(m2a_mux2_32_out_4[12]), .in_3(m2a_mux2_32_out_4[4]), .in_1(Len[3]));
  M2A_mux2 m2a_mux2_61 (
    .out_4(m2a_mux2_64_out_4[3]), .in_2(m2a_mux2_32_out_4[11]), .in_3(m2a_mux2_32_out_4[3]), .in_1(Len[3]));
  M2A_mux2 m2a_mux2_62 (
    .out_4(m2a_mux2_64_out_4[2]), .in_2(m2a_mux2_32_out_4[10]), .in_3(m2a_mux2_32_out_4[2]), .in_1(Len[3]));
  M2A_mux2 m2a_mux2_63 (
    .out_4(m2a_mux2_64_out_4[1]), .in_2(m2a_mux2_32_out_4[9]), .in_3(m2a_mux2_32_out_4[1]), .in_1(Len[3]));
  M2A_mux2 m2a_mux2_64 (
    .out_4(m2a_mux2_64_out_4[0]), .in_2(m2a_mux2_32_out_4[8]), .in_3(m2a_mux2_32_out_4[0]), .in_1(Len[3]));
  M2A_mux2 m2a_mux2_65 (.out_4(O[31]), .in_2(shf_in), .in_3(m2a_mux2_64_out_4[31]), .in_1(Len[4]));
  M2A_mux2 m2a_mux2_66 (.out_4(O[30]), .in_2(shf_in), .in_3(m2a_mux2_64_out_4[30]), .in_1(Len[4]));
  M2A_mux2 m2a_mux2_67 (.out_4(O[29]), .in_2(shf_in), .in_3(m2a_mux2_64_out_4[29]), .in_1(Len[4]));
  M2A_mux2 m2a_mux2_68 (.out_4(O[28]), .in_2(shf_in), .in_3(m2a_mux2_64_out_4[28]), .in_1(Len[4]));
  M2A_mux2 m2a_mux2_69 (.out_4(O[27]), .in_2(shf_in), .in_3(m2a_mux2_64_out_4[27]), .in_1(Len[4]));
  M2A_mux2 m2a_mux2_70 (.out_4(O[26]), .in_2(shf_in), .in_3(m2a_mux2_64_out_4[26]), .in_1(Len[4]));
  M2A_mux2 m2a_mux2_71 (.out_4(O[25]), .in_2(shf_in), .in_3(m2a_mux2_64_out_4[25]), .in_1(Len[4]));
  M2A_mux2 m2a_mux2_72 (.out_4(O[24]), .in_2(shf_in), .in_3(m2a_mux2_64_out_4[24]), .in_1(Len[4]));
  M2A_mux2 m2a_mux2_73 (.out_4(O[23]), .in_2(shf_in), .in_3(m2a_mux2_64_out_4[23]), .in_1(Len[4]));
  M2A_mux2 m2a_mux2_74 (.out_4(O[22]), .in_2(shf_in), .in_3(m2a_mux2_64_out_4[22]), .in_1(Len[4]));
  M2A_mux2 m2a_mux2_75 (.out_4(O[21]), .in_2(shf_in), .in_3(m2a_mux2_64_out_4[21]), .in_1(Len[4]));
  M2A_mux2 m2a_mux2_76 (.out_4(O[20]), .in_2(shf_in), .in_3(m2a_mux2_64_out_4[20]), .in_1(Len[4]));
  M2A_mux2 m2a_mux2_77 (.out_4(O[19]), .in_2(shf_in), .in_3(m2a_mux2_64_out_4[19]), .in_1(Len[4]));
  M2A_mux2 m2a_mux2_78 (.out_4(O[18]), .in_2(shf_in), .in_3(m2a_mux2_64_out_4[18]), .in_1(Len[4]));
  M2A_mux2 m2a_mux2_79 (.out_4(O[17]), .in_2(shf_in), .in_3(m2a_mux2_64_out_4[17]), .in_1(Len[4]));
  M2A_mux2 m2a_mux2_80 (.out_4(O[16]), .in_2(shf_in), .in_3(m2a_mux2_64_out_4[16]), .in_1(Len[4]));
  M2A_mux2 m2a_mux2_81 (.out_4(O[15]), .in_2(m2a_mux2_64_out_4[31]), .in_3(m2a_mux2_64_out_4[15]), .in_1(Len[4]));
  M2A_mux2 m2a_mux2_82 (.out_4(O[14]), .in_2(m2a_mux2_64_out_4[30]), .in_3(m2a_mux2_64_out_4[14]), .in_1(Len[4]));
  M2A_mux2 m2a_mux2_83 (.out_4(O[13]), .in_2(m2a_mux2_64_out_4[29]), .in_3(m2a_mux2_64_out_4[13]), .in_1(Len[4]));
  M2A_mux2 m2a_mux2_84 (.out_4(O[12]), .in_2(m2a_mux2_64_out_4[28]), .in_3(m2a_mux2_64_out_4[12]), .in_1(Len[4]));
  M2A_mux2 m2a_mux2_85 (.out_4(O[11]), .in_2(m2a_mux2_64_out_4[27]), .in_3(m2a_mux2_64_out_4[11]), .in_1(Len[4]));
  M2A_mux2 m2a_mux2_86 (.out_4(O[10]), .in_2(m2a_mux2_64_out_4[26]), .in_3(m2a_mux2_64_out_4[10]), .in_1(Len[4]));
  M2A_mux2 m2a_mux2_87 (.out_4(O[9]), .in_2(m2a_mux2_64_out_4[25]), .in_3(m2a_mux2_64_out_4[9]), .in_1(Len[4]));
  M2A_mux2 m2a_mux2_88 (.out_4(O[8]), .in_2(m2a_mux2_64_out_4[24]), .in_3(m2a_mux2_64_out_4[8]), .in_1(Len[4]));
  M2A_mux2 m2a_mux2_89 (.out_4(O[7]), .in_2(m2a_mux2_64_out_4[23]), .in_3(m2a_mux2_64_out_4[7]), .in_1(Len[4]));
  M2A_mux2 m2a_mux2_90 (.out_4(O[6]), .in_2(m2a_mux2_64_out_4[22]), .in_3(m2a_mux2_64_out_4[6]), .in_1(Len[4]));
  M2A_mux2 m2a_mux2_91 (.out_4(O[5]), .in_2(m2a_mux2_64_out_4[21]), .in_3(m2a_mux2_64_out_4[5]), .in_1(Len[4]));
  M2A_mux2 m2a_mux2_92 (.out_4(O[4]), .in_2(m2a_mux2_64_out_4[20]), .in_3(m2a_mux2_64_out_4[4]), .in_1(Len[4]));
  M2A_mux2 m2a_mux2_93 (.out_4(O[3]), .in_2(m2a_mux2_64_out_4[19]), .in_3(m2a_mux2_64_out_4[3]), .in_1(Len[4]));
  M2A_mux2 m2a_mux2_94 (.out_4(O[2]), .in_2(m2a_mux2_64_out_4[18]), .in_3(m2a_mux2_64_out_4[2]), .in_1(Len[4]));
  M2A_mux2 m2a_mux2_95 (.out_4(O[1]), .in_2(m2a_mux2_64_out_4[17]), .in_3(m2a_mux2_64_out_4[1]), .in_1(Len[4]));
  M2A_mux2 m2a_mux2_96 (.out_4(O[0]), .in_2(m2a_mux2_64_out_4[16]), .in_3(m2a_mux2_64_out_4[0]), .in_1(Len[4]));

  // Notes on the sheet:
  //   注意水平和垂直总线中LSB和MSB的位置，是和左移时相反的
endmodule

module M2A_shift_left_32_s3 (
  input  [31:0] I,
  input  [4:0] Len,
  output [31:0] O
);

  wire [31:0] m2a_mux4_1_out_6, m2a_mux4_33_out_6;

  M2A_mux4 m2a_mux4_1 (
    .out_6(m2a_mux4_1_out_6[0]), .in_2(1'b0), .in_3(1'b0), .in_4(1'b0), .in_5(I[0]), .in_1(Len[1:0]));
  M2A_mux4 m2a_mux4_2 (
    .out_6(m2a_mux4_1_out_6[1]), .in_2(1'b0), .in_3(1'b0), .in_4(I[0]), .in_5(I[1]), .in_1(Len[1:0]));
  M2A_mux4 m2a_mux4_3 (
    .out_6(m2a_mux4_1_out_6[2]), .in_2(1'b0), .in_3(I[0]), .in_4(I[1]), .in_5(I[2]), .in_1(Len[1:0]));
  M2A_mux4 m2a_mux4_4 (
    .out_6(m2a_mux4_1_out_6[3]), .in_2(I[0]), .in_3(I[1]), .in_4(I[2]), .in_5(I[3]), .in_1(Len[1:0]));
  M2A_mux4 m2a_mux4_5 (
    .out_6(m2a_mux4_1_out_6[4]), .in_2(I[1]), .in_3(I[2]), .in_4(I[3]), .in_5(I[4]), .in_1(Len[1:0]));
  M2A_mux4 m2a_mux4_6 (
    .out_6(m2a_mux4_1_out_6[5]), .in_2(I[2]), .in_3(I[3]), .in_4(I[4]), .in_5(I[5]), .in_1(Len[1:0]));
  M2A_mux4 m2a_mux4_7 (
    .out_6(m2a_mux4_1_out_6[6]), .in_2(I[3]), .in_3(I[4]), .in_4(I[5]), .in_5(I[6]), .in_1(Len[1:0]));
  M2A_mux4 m2a_mux4_8 (
    .out_6(m2a_mux4_1_out_6[7]), .in_2(I[4]), .in_3(I[5]), .in_4(I[6]), .in_5(I[7]), .in_1(Len[1:0]));
  M2A_mux4 m2a_mux4_9 (
    .out_6(m2a_mux4_1_out_6[8]), .in_2(I[5]), .in_3(I[6]), .in_4(I[7]), .in_5(I[8]), .in_1(Len[1:0]));
  M2A_mux4 m2a_mux4_10 (
    .out_6(m2a_mux4_1_out_6[9]), .in_2(I[6]), .in_3(I[7]), .in_4(I[8]), .in_5(I[9]), .in_1(Len[1:0]));
  M2A_mux4 m2a_mux4_11 (
    .out_6(m2a_mux4_1_out_6[10]), .in_2(I[7]), .in_3(I[8]), .in_4(I[9]), .in_5(I[10]), .in_1(Len[1:0]));
  M2A_mux4 m2a_mux4_12 (
    .out_6(m2a_mux4_1_out_6[11]), .in_2(I[8]), .in_3(I[9]), .in_4(I[10]), .in_5(I[11]), .in_1(Len[1:0]));
  M2A_mux4 m2a_mux4_13 (
    .out_6(m2a_mux4_1_out_6[12]), .in_2(I[9]), .in_3(I[10]), .in_4(I[11]), .in_5(I[12]), .in_1(Len[1:0]));
  M2A_mux4 m2a_mux4_14 (
    .out_6(m2a_mux4_1_out_6[13]), .in_2(I[10]), .in_3(I[11]), .in_4(I[12]), .in_5(I[13]), .in_1(Len[1:0]));
  M2A_mux4 m2a_mux4_15 (
    .out_6(m2a_mux4_1_out_6[14]), .in_2(I[11]), .in_3(I[12]), .in_4(I[13]), .in_5(I[14]), .in_1(Len[1:0]));
  M2A_mux4 m2a_mux4_16 (
    .out_6(m2a_mux4_1_out_6[15]), .in_2(I[12]), .in_3(I[13]), .in_4(I[14]), .in_5(I[15]), .in_1(Len[1:0]));
  M2A_mux4 m2a_mux4_17 (
    .out_6(m2a_mux4_1_out_6[16]), .in_2(I[13]), .in_3(I[14]), .in_4(I[15]), .in_5(I[16]), .in_1(Len[1:0]));
  M2A_mux4 m2a_mux4_18 (
    .out_6(m2a_mux4_1_out_6[17]), .in_2(I[14]), .in_3(I[15]), .in_4(I[16]), .in_5(I[17]), .in_1(Len[1:0]));
  M2A_mux4 m2a_mux4_19 (
    .out_6(m2a_mux4_1_out_6[18]), .in_2(I[15]), .in_3(I[16]), .in_4(I[17]), .in_5(I[18]), .in_1(Len[1:0]));
  M2A_mux4 m2a_mux4_20 (
    .out_6(m2a_mux4_1_out_6[19]), .in_2(I[16]), .in_3(I[17]), .in_4(I[18]), .in_5(I[19]), .in_1(Len[1:0]));
  M2A_mux4 m2a_mux4_21 (
    .out_6(m2a_mux4_1_out_6[20]), .in_2(I[17]), .in_3(I[18]), .in_4(I[19]), .in_5(I[20]), .in_1(Len[1:0]));
  M2A_mux4 m2a_mux4_22 (
    .out_6(m2a_mux4_1_out_6[21]), .in_2(I[18]), .in_3(I[19]), .in_4(I[20]), .in_5(I[21]), .in_1(Len[1:0]));
  M2A_mux4 m2a_mux4_23 (
    .out_6(m2a_mux4_1_out_6[22]), .in_2(I[19]), .in_3(I[20]), .in_4(I[21]), .in_5(I[22]), .in_1(Len[1:0]));
  M2A_mux4 m2a_mux4_24 (
    .out_6(m2a_mux4_1_out_6[23]), .in_2(I[20]), .in_3(I[21]), .in_4(I[22]), .in_5(I[23]), .in_1(Len[1:0]));
  M2A_mux4 m2a_mux4_25 (
    .out_6(m2a_mux4_1_out_6[24]), .in_2(I[21]), .in_3(I[22]), .in_4(I[23]), .in_5(I[24]), .in_1(Len[1:0]));
  M2A_mux4 m2a_mux4_26 (
    .out_6(m2a_mux4_1_out_6[25]), .in_2(I[22]), .in_3(I[23]), .in_4(I[24]), .in_5(I[25]), .in_1(Len[1:0]));
  M2A_mux4 m2a_mux4_27 (
    .out_6(m2a_mux4_1_out_6[26]), .in_2(I[23]), .in_3(I[24]), .in_4(I[25]), .in_5(I[26]), .in_1(Len[1:0]));
  M2A_mux4 m2a_mux4_28 (
    .out_6(m2a_mux4_1_out_6[27]), .in_2(I[24]), .in_3(I[25]), .in_4(I[26]), .in_5(I[27]), .in_1(Len[1:0]));
  M2A_mux4 m2a_mux4_29 (
    .out_6(m2a_mux4_1_out_6[28]), .in_2(I[25]), .in_3(I[26]), .in_4(I[27]), .in_5(I[28]), .in_1(Len[1:0]));
  M2A_mux4 m2a_mux4_30 (
    .out_6(m2a_mux4_1_out_6[29]), .in_2(I[26]), .in_3(I[27]), .in_4(I[28]), .in_5(I[29]), .in_1(Len[1:0]));
  M2A_mux4 m2a_mux4_31 (
    .out_6(m2a_mux4_1_out_6[30]), .in_2(I[27]), .in_3(I[28]), .in_4(I[29]), .in_5(I[30]), .in_1(Len[1:0]));
  M2A_mux4 m2a_mux4_32 (
    .out_6(m2a_mux4_1_out_6[31]), .in_2(I[28]), .in_3(I[29]), .in_4(I[30]), .in_5(I[31]), .in_1(Len[1:0]));
  M2A_mux4 m2a_mux4_33 (
    .out_6(m2a_mux4_33_out_6[0]), .in_2(1'b0), .in_3(1'b0), .in_4(1'b0), .in_5(m2a_mux4_1_out_6[0]),
    .in_1(Len[3:2]));
  M2A_mux4 m2a_mux4_34 (
    .out_6(m2a_mux4_33_out_6[1]), .in_2(1'b0), .in_3(1'b0), .in_4(1'b0), .in_5(m2a_mux4_1_out_6[1]),
    .in_1(Len[3:2]));
  M2A_mux4 m2a_mux4_35 (
    .out_6(m2a_mux4_33_out_6[2]), .in_2(1'b0), .in_3(1'b0), .in_4(1'b0), .in_5(m2a_mux4_1_out_6[2]),
    .in_1(Len[3:2]));
  M2A_mux4 m2a_mux4_36 (
    .out_6(m2a_mux4_33_out_6[3]), .in_2(1'b0), .in_3(1'b0), .in_4(1'b0), .in_5(m2a_mux4_1_out_6[3]),
    .in_1(Len[3:2]));
  M2A_mux4 m2a_mux4_37 (
    .out_6(m2a_mux4_33_out_6[4]), .in_2(1'b0), .in_3(1'b0), .in_4(m2a_mux4_1_out_6[0]),
    .in_5(m2a_mux4_1_out_6[4]), .in_1(Len[3:2]));
  M2A_mux4 m2a_mux4_38 (
    .out_6(m2a_mux4_33_out_6[5]), .in_2(1'b0), .in_3(1'b0), .in_4(m2a_mux4_1_out_6[1]),
    .in_5(m2a_mux4_1_out_6[5]), .in_1(Len[3:2]));
  M2A_mux4 m2a_mux4_39 (
    .out_6(m2a_mux4_33_out_6[6]), .in_2(1'b0), .in_3(1'b0), .in_4(m2a_mux4_1_out_6[2]),
    .in_5(m2a_mux4_1_out_6[6]), .in_1(Len[3:2]));
  M2A_mux4 m2a_mux4_40 (
    .out_6(m2a_mux4_33_out_6[7]), .in_2(1'b0), .in_3(1'b0), .in_4(m2a_mux4_1_out_6[3]),
    .in_5(m2a_mux4_1_out_6[7]), .in_1(Len[3:2]));
  M2A_mux4 m2a_mux4_41 (
    .out_6(m2a_mux4_33_out_6[8]), .in_2(1'b0), .in_3(m2a_mux4_1_out_6[0]), .in_4(m2a_mux4_1_out_6[4]),
    .in_5(m2a_mux4_1_out_6[8]), .in_1(Len[3:2]));
  M2A_mux4 m2a_mux4_42 (
    .out_6(m2a_mux4_33_out_6[9]), .in_2(1'b0), .in_3(m2a_mux4_1_out_6[1]), .in_4(m2a_mux4_1_out_6[5]),
    .in_5(m2a_mux4_1_out_6[9]), .in_1(Len[3:2]));
  M2A_mux4 m2a_mux4_43 (
    .out_6(m2a_mux4_33_out_6[10]), .in_2(1'b0), .in_3(m2a_mux4_1_out_6[2]), .in_4(m2a_mux4_1_out_6[6]),
    .in_5(m2a_mux4_1_out_6[10]), .in_1(Len[3:2]));
  M2A_mux4 m2a_mux4_44 (
    .out_6(m2a_mux4_33_out_6[11]), .in_2(1'b0), .in_3(m2a_mux4_1_out_6[3]), .in_4(m2a_mux4_1_out_6[7]),
    .in_5(m2a_mux4_1_out_6[11]), .in_1(Len[3:2]));
  M2A_mux4 m2a_mux4_45 (
    .out_6(m2a_mux4_33_out_6[12]), .in_2(m2a_mux4_1_out_6[0]), .in_3(m2a_mux4_1_out_6[4]),
    .in_4(m2a_mux4_1_out_6[8]), .in_5(m2a_mux4_1_out_6[12]), .in_1(Len[3:2]));
  M2A_mux4 m2a_mux4_46 (
    .out_6(m2a_mux4_33_out_6[13]), .in_2(m2a_mux4_1_out_6[1]), .in_3(m2a_mux4_1_out_6[5]),
    .in_4(m2a_mux4_1_out_6[9]), .in_5(m2a_mux4_1_out_6[13]), .in_1(Len[3:2]));
  M2A_mux4 m2a_mux4_47 (
    .out_6(m2a_mux4_33_out_6[14]), .in_2(m2a_mux4_1_out_6[2]), .in_3(m2a_mux4_1_out_6[6]),
    .in_4(m2a_mux4_1_out_6[10]), .in_5(m2a_mux4_1_out_6[14]), .in_1(Len[3:2]));
  M2A_mux4 m2a_mux4_48 (
    .out_6(m2a_mux4_33_out_6[15]), .in_2(m2a_mux4_1_out_6[3]), .in_3(m2a_mux4_1_out_6[7]),
    .in_4(m2a_mux4_1_out_6[11]), .in_5(m2a_mux4_1_out_6[15]), .in_1(Len[3:2]));
  M2A_mux4 m2a_mux4_49 (
    .out_6(m2a_mux4_33_out_6[16]), .in_2(m2a_mux4_1_out_6[4]), .in_3(m2a_mux4_1_out_6[8]),
    .in_4(m2a_mux4_1_out_6[12]), .in_5(m2a_mux4_1_out_6[16]), .in_1(Len[3:2]));
  M2A_mux4 m2a_mux4_50 (
    .out_6(m2a_mux4_33_out_6[17]), .in_2(m2a_mux4_1_out_6[5]), .in_3(m2a_mux4_1_out_6[9]),
    .in_4(m2a_mux4_1_out_6[13]), .in_5(m2a_mux4_1_out_6[17]), .in_1(Len[3:2]));
  M2A_mux4 m2a_mux4_51 (
    .out_6(m2a_mux4_33_out_6[18]), .in_2(m2a_mux4_1_out_6[6]), .in_3(m2a_mux4_1_out_6[10]),
    .in_4(m2a_mux4_1_out_6[14]), .in_5(m2a_mux4_1_out_6[18]), .in_1(Len[3:2]));
  M2A_mux4 m2a_mux4_52 (
    .out_6(m2a_mux4_33_out_6[19]), .in_2(m2a_mux4_1_out_6[7]), .in_3(m2a_mux4_1_out_6[11]),
    .in_4(m2a_mux4_1_out_6[15]), .in_5(m2a_mux4_1_out_6[19]), .in_1(Len[3:2]));
  M2A_mux4 m2a_mux4_53 (
    .out_6(m2a_mux4_33_out_6[20]), .in_2(m2a_mux4_1_out_6[8]), .in_3(m2a_mux4_1_out_6[12]),
    .in_4(m2a_mux4_1_out_6[16]), .in_5(m2a_mux4_1_out_6[20]), .in_1(Len[3:2]));
  M2A_mux4 m2a_mux4_54 (
    .out_6(m2a_mux4_33_out_6[21]), .in_2(m2a_mux4_1_out_6[9]), .in_3(m2a_mux4_1_out_6[13]),
    .in_4(m2a_mux4_1_out_6[17]), .in_5(m2a_mux4_1_out_6[21]), .in_1(Len[3:2]));
  M2A_mux4 m2a_mux4_55 (
    .out_6(m2a_mux4_33_out_6[22]), .in_2(m2a_mux4_1_out_6[10]), .in_3(m2a_mux4_1_out_6[14]),
    .in_4(m2a_mux4_1_out_6[18]), .in_5(m2a_mux4_1_out_6[22]), .in_1(Len[3:2]));
  M2A_mux4 m2a_mux4_56 (
    .out_6(m2a_mux4_33_out_6[23]), .in_2(m2a_mux4_1_out_6[11]), .in_3(m2a_mux4_1_out_6[15]),
    .in_4(m2a_mux4_1_out_6[19]), .in_5(m2a_mux4_1_out_6[23]), .in_1(Len[3:2]));
  M2A_mux4 m2a_mux4_57 (
    .out_6(m2a_mux4_33_out_6[24]), .in_2(m2a_mux4_1_out_6[12]), .in_3(m2a_mux4_1_out_6[16]),
    .in_4(m2a_mux4_1_out_6[20]), .in_5(m2a_mux4_1_out_6[24]), .in_1(Len[3:2]));
  M2A_mux4 m2a_mux4_58 (
    .out_6(m2a_mux4_33_out_6[25]), .in_2(m2a_mux4_1_out_6[13]), .in_3(m2a_mux4_1_out_6[17]),
    .in_4(m2a_mux4_1_out_6[21]), .in_5(m2a_mux4_1_out_6[25]), .in_1(Len[3:2]));
  M2A_mux4 m2a_mux4_59 (
    .out_6(m2a_mux4_33_out_6[26]), .in_2(m2a_mux4_1_out_6[14]), .in_3(m2a_mux4_1_out_6[18]),
    .in_4(m2a_mux4_1_out_6[22]), .in_5(m2a_mux4_1_out_6[26]), .in_1(Len[3:2]));
  M2A_mux4 m2a_mux4_60 (
    .out_6(m2a_mux4_33_out_6[27]), .in_2(m2a_mux4_1_out_6[15]), .in_3(m2a_mux4_1_out_6[19]),
    .in_4(m2a_mux4_1_out_6[23]), .in_5(m2a_mux4_1_out_6[27]), .in_1(Len[3:2]));
  M2A_mux4 m2a_mux4_61 (
    .out_6(m2a_mux4_33_out_6[28]), .in_2(m2a_mux4_1_out_6[16]), .in_3(m2a_mux4_1_out_6[20]),
    .in_4(m2a_mux4_1_out_6[24]), .in_5(m2a_mux4_1_out_6[28]), .in_1(Len[3:2]));
  M2A_mux4 m2a_mux4_62 (
    .out_6(m2a_mux4_33_out_6[29]), .in_2(m2a_mux4_1_out_6[17]), .in_3(m2a_mux4_1_out_6[21]),
    .in_4(m2a_mux4_1_out_6[25]), .in_5(m2a_mux4_1_out_6[29]), .in_1(Len[3:2]));
  M2A_mux4 m2a_mux4_63 (
    .out_6(m2a_mux4_33_out_6[30]), .in_2(m2a_mux4_1_out_6[18]), .in_3(m2a_mux4_1_out_6[22]),
    .in_4(m2a_mux4_1_out_6[26]), .in_5(m2a_mux4_1_out_6[30]), .in_1(Len[3:2]));
  M2A_mux4 m2a_mux4_64 (
    .out_6(m2a_mux4_33_out_6[31]), .in_2(m2a_mux4_1_out_6[19]), .in_3(m2a_mux4_1_out_6[23]),
    .in_4(m2a_mux4_1_out_6[27]), .in_5(m2a_mux4_1_out_6[31]), .in_1(Len[3:2]));
  M2A_mux2 m2a_mux2_1 (.out_4(O[0]), .in_2(1'b0), .in_3(m2a_mux4_33_out_6[0]), .in_1(Len[4]));
  M2A_mux2 m2a_mux2_2 (.out_4(O[1]), .in_2(1'b0), .in_3(m2a_mux4_33_out_6[1]), .in_1(Len[4]));
  M2A_mux2 m2a_mux2_3 (.out_4(O[2]), .in_2(1'b0), .in_3(m2a_mux4_33_out_6[2]), .in_1(Len[4]));
  M2A_mux2 m2a_mux2_4 (.out_4(O[3]), .in_2(1'b0), .in_3(m2a_mux4_33_out_6[3]), .in_1(Len[4]));
  M2A_mux2 m2a_mux2_5 (.out_4(O[4]), .in_2(1'b0), .in_3(m2a_mux4_33_out_6[4]), .in_1(Len[4]));
  M2A_mux2 m2a_mux2_6 (.out_4(O[5]), .in_2(1'b0), .in_3(m2a_mux4_33_out_6[5]), .in_1(Len[4]));
  M2A_mux2 m2a_mux2_7 (.out_4(O[6]), .in_2(1'b0), .in_3(m2a_mux4_33_out_6[6]), .in_1(Len[4]));
  M2A_mux2 m2a_mux2_8 (.out_4(O[7]), .in_2(1'b0), .in_3(m2a_mux4_33_out_6[7]), .in_1(Len[4]));
  M2A_mux2 m2a_mux2_9 (.out_4(O[8]), .in_2(1'b0), .in_3(m2a_mux4_33_out_6[8]), .in_1(Len[4]));
  M2A_mux2 m2a_mux2_10 (.out_4(O[9]), .in_2(1'b0), .in_3(m2a_mux4_33_out_6[9]), .in_1(Len[4]));
  M2A_mux2 m2a_mux2_11 (.out_4(O[10]), .in_2(1'b0), .in_3(m2a_mux4_33_out_6[10]), .in_1(Len[4]));
  M2A_mux2 m2a_mux2_12 (.out_4(O[11]), .in_2(1'b0), .in_3(m2a_mux4_33_out_6[11]), .in_1(Len[4]));
  M2A_mux2 m2a_mux2_13 (.out_4(O[12]), .in_2(1'b0), .in_3(m2a_mux4_33_out_6[12]), .in_1(Len[4]));
  M2A_mux2 m2a_mux2_14 (.out_4(O[13]), .in_2(1'b0), .in_3(m2a_mux4_33_out_6[13]), .in_1(Len[4]));
  M2A_mux2 m2a_mux2_15 (.out_4(O[14]), .in_2(1'b0), .in_3(m2a_mux4_33_out_6[14]), .in_1(Len[4]));
  M2A_mux2 m2a_mux2_16 (.out_4(O[15]), .in_2(1'b0), .in_3(m2a_mux4_33_out_6[15]), .in_1(Len[4]));
  M2A_mux2 m2a_mux2_17 (.out_4(O[16]), .in_2(m2a_mux4_33_out_6[0]), .in_3(m2a_mux4_33_out_6[16]), .in_1(Len[4]));
  M2A_mux2 m2a_mux2_18 (.out_4(O[17]), .in_2(m2a_mux4_33_out_6[1]), .in_3(m2a_mux4_33_out_6[17]), .in_1(Len[4]));
  M2A_mux2 m2a_mux2_19 (.out_4(O[18]), .in_2(m2a_mux4_33_out_6[2]), .in_3(m2a_mux4_33_out_6[18]), .in_1(Len[4]));
  M2A_mux2 m2a_mux2_20 (.out_4(O[19]), .in_2(m2a_mux4_33_out_6[3]), .in_3(m2a_mux4_33_out_6[19]), .in_1(Len[4]));
  M2A_mux2 m2a_mux2_21 (.out_4(O[20]), .in_2(m2a_mux4_33_out_6[4]), .in_3(m2a_mux4_33_out_6[20]), .in_1(Len[4]));
  M2A_mux2 m2a_mux2_22 (.out_4(O[21]), .in_2(m2a_mux4_33_out_6[5]), .in_3(m2a_mux4_33_out_6[21]), .in_1(Len[4]));
  M2A_mux2 m2a_mux2_23 (.out_4(O[22]), .in_2(m2a_mux4_33_out_6[6]), .in_3(m2a_mux4_33_out_6[22]), .in_1(Len[4]));
  M2A_mux2 m2a_mux2_24 (.out_4(O[23]), .in_2(m2a_mux4_33_out_6[7]), .in_3(m2a_mux4_33_out_6[23]), .in_1(Len[4]));
  M2A_mux2 m2a_mux2_25 (.out_4(O[24]), .in_2(m2a_mux4_33_out_6[8]), .in_3(m2a_mux4_33_out_6[24]), .in_1(Len[4]));
  M2A_mux2 m2a_mux2_26 (.out_4(O[25]), .in_2(m2a_mux4_33_out_6[9]), .in_3(m2a_mux4_33_out_6[25]), .in_1(Len[4]));
  M2A_mux2 m2a_mux2_27 (.out_4(O[26]), .in_2(m2a_mux4_33_out_6[10]), .in_3(m2a_mux4_33_out_6[26]), .in_1(Len[4]));
  M2A_mux2 m2a_mux2_28 (.out_4(O[27]), .in_2(m2a_mux4_33_out_6[11]), .in_3(m2a_mux4_33_out_6[27]), .in_1(Len[4]));
  M2A_mux2 m2a_mux2_29 (.out_4(O[28]), .in_2(m2a_mux4_33_out_6[12]), .in_3(m2a_mux4_33_out_6[28]), .in_1(Len[4]));
  M2A_mux2 m2a_mux2_30 (.out_4(O[29]), .in_2(m2a_mux4_33_out_6[13]), .in_3(m2a_mux4_33_out_6[29]), .in_1(Len[4]));
  M2A_mux2 m2a_mux2_31 (.out_4(O[30]), .in_2(m2a_mux4_33_out_6[14]), .in_3(m2a_mux4_33_out_6[30]), .in_1(Len[4]));
  M2A_mux2 m2a_mux2_32 (.out_4(O[31]), .in_2(m2a_mux4_33_out_6[15]), .in_3(m2a_mux4_33_out_6[31]), .in_1(Len[4]));
endmodule

module M2A_shift_right_32_s3 (
  input  [31:0] I,
  input  [4:0] Len,
  input  Arith,
  output [31:0] O
);

  wire MSB, shf_in;
  wire [31:0] m2a_mux4_32_out_6, m2a_mux4_64_out_6;

  BitSelector #(.width(32)) bitselector_1 (.in(I), .out(MSB), .sel({5{1'b1}}));
  and and_1 (shf_in, Arith, MSB);
  M2A_mux4 m2a_mux4_1 (
    .out_6(m2a_mux4_32_out_6[31]), .in_2(shf_in), .in_3(shf_in), .in_4(shf_in), .in_5(I[31]), .in_1(Len[1:0]));
  M2A_mux4 m2a_mux4_2 (
    .out_6(m2a_mux4_32_out_6[30]), .in_2(shf_in), .in_3(shf_in), .in_4(I[31]), .in_5(I[30]), .in_1(Len[1:0]));
  M2A_mux4 m2a_mux4_3 (
    .out_6(m2a_mux4_32_out_6[29]), .in_2(shf_in), .in_3(I[31]), .in_4(I[30]), .in_5(I[29]), .in_1(Len[1:0]));
  M2A_mux4 m2a_mux4_4 (
    .out_6(m2a_mux4_32_out_6[28]), .in_2(I[31]), .in_3(I[30]), .in_4(I[29]), .in_5(I[28]), .in_1(Len[1:0]));
  M2A_mux4 m2a_mux4_5 (
    .out_6(m2a_mux4_32_out_6[27]), .in_2(I[30]), .in_3(I[29]), .in_4(I[28]), .in_5(I[27]), .in_1(Len[1:0]));
  M2A_mux4 m2a_mux4_6 (
    .out_6(m2a_mux4_32_out_6[26]), .in_2(I[29]), .in_3(I[28]), .in_4(I[27]), .in_5(I[26]), .in_1(Len[1:0]));
  M2A_mux4 m2a_mux4_7 (
    .out_6(m2a_mux4_32_out_6[25]), .in_2(I[28]), .in_3(I[27]), .in_4(I[26]), .in_5(I[25]), .in_1(Len[1:0]));
  M2A_mux4 m2a_mux4_8 (
    .out_6(m2a_mux4_32_out_6[24]), .in_2(I[27]), .in_3(I[26]), .in_4(I[25]), .in_5(I[24]), .in_1(Len[1:0]));
  M2A_mux4 m2a_mux4_9 (
    .out_6(m2a_mux4_32_out_6[23]), .in_2(I[26]), .in_3(I[25]), .in_4(I[24]), .in_5(I[23]), .in_1(Len[1:0]));
  M2A_mux4 m2a_mux4_10 (
    .out_6(m2a_mux4_32_out_6[22]), .in_2(I[25]), .in_3(I[24]), .in_4(I[23]), .in_5(I[22]), .in_1(Len[1:0]));
  M2A_mux4 m2a_mux4_11 (
    .out_6(m2a_mux4_32_out_6[21]), .in_2(I[24]), .in_3(I[23]), .in_4(I[22]), .in_5(I[21]), .in_1(Len[1:0]));
  M2A_mux4 m2a_mux4_12 (
    .out_6(m2a_mux4_32_out_6[20]), .in_2(I[23]), .in_3(I[22]), .in_4(I[21]), .in_5(I[20]), .in_1(Len[1:0]));
  M2A_mux4 m2a_mux4_13 (
    .out_6(m2a_mux4_32_out_6[19]), .in_2(I[22]), .in_3(I[21]), .in_4(I[20]), .in_5(I[19]), .in_1(Len[1:0]));
  M2A_mux4 m2a_mux4_14 (
    .out_6(m2a_mux4_32_out_6[18]), .in_2(I[21]), .in_3(I[20]), .in_4(I[19]), .in_5(I[18]), .in_1(Len[1:0]));
  M2A_mux4 m2a_mux4_15 (
    .out_6(m2a_mux4_32_out_6[17]), .in_2(I[20]), .in_3(I[19]), .in_4(I[18]), .in_5(I[17]), .in_1(Len[1:0]));
  M2A_mux4 m2a_mux4_16 (
    .out_6(m2a_mux4_32_out_6[16]), .in_2(I[19]), .in_3(I[18]), .in_4(I[17]), .in_5(I[16]), .in_1(Len[1:0]));
  M2A_mux4 m2a_mux4_17 (
    .out_6(m2a_mux4_32_out_6[15]), .in_2(I[18]), .in_3(I[17]), .in_4(I[16]), .in_5(I[15]), .in_1(Len[1:0]));
  M2A_mux4 m2a_mux4_18 (
    .out_6(m2a_mux4_32_out_6[14]), .in_2(I[17]), .in_3(I[16]), .in_4(I[15]), .in_5(I[14]), .in_1(Len[1:0]));
  M2A_mux4 m2a_mux4_19 (
    .out_6(m2a_mux4_32_out_6[13]), .in_2(I[16]), .in_3(I[15]), .in_4(I[14]), .in_5(I[13]), .in_1(Len[1:0]));
  M2A_mux4 m2a_mux4_20 (
    .out_6(m2a_mux4_32_out_6[12]), .in_2(I[15]), .in_3(I[14]), .in_4(I[13]), .in_5(I[12]), .in_1(Len[1:0]));
  M2A_mux4 m2a_mux4_21 (
    .out_6(m2a_mux4_32_out_6[11]), .in_2(I[14]), .in_3(I[13]), .in_4(I[12]), .in_5(I[11]), .in_1(Len[1:0]));
  M2A_mux4 m2a_mux4_22 (
    .out_6(m2a_mux4_32_out_6[10]), .in_2(I[13]), .in_3(I[12]), .in_4(I[11]), .in_5(I[10]), .in_1(Len[1:0]));
  M2A_mux4 m2a_mux4_23 (
    .out_6(m2a_mux4_32_out_6[9]), .in_2(I[12]), .in_3(I[11]), .in_4(I[10]), .in_5(I[9]), .in_1(Len[1:0]));
  M2A_mux4 m2a_mux4_24 (
    .out_6(m2a_mux4_32_out_6[8]), .in_2(I[11]), .in_3(I[10]), .in_4(I[9]), .in_5(I[8]), .in_1(Len[1:0]));
  M2A_mux4 m2a_mux4_25 (
    .out_6(m2a_mux4_32_out_6[7]), .in_2(I[10]), .in_3(I[9]), .in_4(I[8]), .in_5(I[7]), .in_1(Len[1:0]));
  M2A_mux4 m2a_mux4_26 (
    .out_6(m2a_mux4_32_out_6[6]), .in_2(I[9]), .in_3(I[8]), .in_4(I[7]), .in_5(I[6]), .in_1(Len[1:0]));
  M2A_mux4 m2a_mux4_27 (
    .out_6(m2a_mux4_32_out_6[5]), .in_2(I[8]), .in_3(I[7]), .in_4(I[6]), .in_5(I[5]), .in_1(Len[1:0]));
  M2A_mux4 m2a_mux4_28 (
    .out_6(m2a_mux4_32_out_6[4]), .in_2(I[7]), .in_3(I[6]), .in_4(I[5]), .in_5(I[4]), .in_1(Len[1:0]));
  M2A_mux4 m2a_mux4_29 (
    .out_6(m2a_mux4_32_out_6[3]), .in_2(I[6]), .in_3(I[5]), .in_4(I[4]), .in_5(I[3]), .in_1(Len[1:0]));
  M2A_mux4 m2a_mux4_30 (
    .out_6(m2a_mux4_32_out_6[2]), .in_2(I[5]), .in_3(I[4]), .in_4(I[3]), .in_5(I[2]), .in_1(Len[1:0]));
  M2A_mux4 m2a_mux4_31 (
    .out_6(m2a_mux4_32_out_6[1]), .in_2(I[4]), .in_3(I[3]), .in_4(I[2]), .in_5(I[1]), .in_1(Len[1:0]));
  M2A_mux4 m2a_mux4_32 (
    .out_6(m2a_mux4_32_out_6[0]), .in_2(I[3]), .in_3(I[2]), .in_4(I[1]), .in_5(I[0]), .in_1(Len[1:0]));
  M2A_mux4 m2a_mux4_33 (
    .out_6(m2a_mux4_64_out_6[31]), .in_2(shf_in), .in_3(shf_in), .in_4(shf_in), .in_5(m2a_mux4_32_out_6[31]),
    .in_1(Len[3:2]));
  M2A_mux4 m2a_mux4_34 (
    .out_6(m2a_mux4_64_out_6[30]), .in_2(shf_in), .in_3(shf_in), .in_4(shf_in), .in_5(m2a_mux4_32_out_6[30]),
    .in_1(Len[3:2]));
  M2A_mux4 m2a_mux4_35 (
    .out_6(m2a_mux4_64_out_6[29]), .in_2(shf_in), .in_3(shf_in), .in_4(shf_in), .in_5(m2a_mux4_32_out_6[29]),
    .in_1(Len[3:2]));
  M2A_mux4 m2a_mux4_36 (
    .out_6(m2a_mux4_64_out_6[28]), .in_2(shf_in), .in_3(shf_in), .in_4(shf_in), .in_5(m2a_mux4_32_out_6[28]),
    .in_1(Len[3:2]));
  M2A_mux4 m2a_mux4_37 (
    .out_6(m2a_mux4_64_out_6[27]), .in_2(shf_in), .in_3(shf_in), .in_4(m2a_mux4_32_out_6[31]),
    .in_5(m2a_mux4_32_out_6[27]), .in_1(Len[3:2]));
  M2A_mux4 m2a_mux4_38 (
    .out_6(m2a_mux4_64_out_6[26]), .in_2(shf_in), .in_3(shf_in), .in_4(m2a_mux4_32_out_6[30]),
    .in_5(m2a_mux4_32_out_6[26]), .in_1(Len[3:2]));
  M2A_mux4 m2a_mux4_39 (
    .out_6(m2a_mux4_64_out_6[25]), .in_2(shf_in), .in_3(shf_in), .in_4(m2a_mux4_32_out_6[29]),
    .in_5(m2a_mux4_32_out_6[25]), .in_1(Len[3:2]));
  M2A_mux4 m2a_mux4_40 (
    .out_6(m2a_mux4_64_out_6[24]), .in_2(shf_in), .in_3(shf_in), .in_4(m2a_mux4_32_out_6[28]),
    .in_5(m2a_mux4_32_out_6[24]), .in_1(Len[3:2]));
  M2A_mux4 m2a_mux4_41 (
    .out_6(m2a_mux4_64_out_6[23]), .in_2(shf_in), .in_3(m2a_mux4_32_out_6[31]), .in_4(m2a_mux4_32_out_6[27]),
    .in_5(m2a_mux4_32_out_6[23]), .in_1(Len[3:2]));
  M2A_mux4 m2a_mux4_42 (
    .out_6(m2a_mux4_64_out_6[22]), .in_2(shf_in), .in_3(m2a_mux4_32_out_6[30]), .in_4(m2a_mux4_32_out_6[26]),
    .in_5(m2a_mux4_32_out_6[22]), .in_1(Len[3:2]));
  M2A_mux4 m2a_mux4_43 (
    .out_6(m2a_mux4_64_out_6[21]), .in_2(shf_in), .in_3(m2a_mux4_32_out_6[29]), .in_4(m2a_mux4_32_out_6[25]),
    .in_5(m2a_mux4_32_out_6[21]), .in_1(Len[3:2]));
  M2A_mux4 m2a_mux4_44 (
    .out_6(m2a_mux4_64_out_6[20]), .in_2(shf_in), .in_3(m2a_mux4_32_out_6[28]), .in_4(m2a_mux4_32_out_6[24]),
    .in_5(m2a_mux4_32_out_6[20]), .in_1(Len[3:2]));
  M2A_mux4 m2a_mux4_45 (
    .out_6(m2a_mux4_64_out_6[19]), .in_2(m2a_mux4_32_out_6[31]), .in_3(m2a_mux4_32_out_6[27]),
    .in_4(m2a_mux4_32_out_6[23]), .in_5(m2a_mux4_32_out_6[19]), .in_1(Len[3:2]));
  M2A_mux4 m2a_mux4_46 (
    .out_6(m2a_mux4_64_out_6[18]), .in_2(m2a_mux4_32_out_6[30]), .in_3(m2a_mux4_32_out_6[26]),
    .in_4(m2a_mux4_32_out_6[22]), .in_5(m2a_mux4_32_out_6[18]), .in_1(Len[3:2]));
  M2A_mux4 m2a_mux4_47 (
    .out_6(m2a_mux4_64_out_6[17]), .in_2(m2a_mux4_32_out_6[29]), .in_3(m2a_mux4_32_out_6[25]),
    .in_4(m2a_mux4_32_out_6[21]), .in_5(m2a_mux4_32_out_6[17]), .in_1(Len[3:2]));
  M2A_mux4 m2a_mux4_48 (
    .out_6(m2a_mux4_64_out_6[16]), .in_2(m2a_mux4_32_out_6[28]), .in_3(m2a_mux4_32_out_6[24]),
    .in_4(m2a_mux4_32_out_6[20]), .in_5(m2a_mux4_32_out_6[16]), .in_1(Len[3:2]));
  M2A_mux4 m2a_mux4_49 (
    .out_6(m2a_mux4_64_out_6[15]), .in_2(m2a_mux4_32_out_6[27]), .in_3(m2a_mux4_32_out_6[23]),
    .in_4(m2a_mux4_32_out_6[19]), .in_5(m2a_mux4_32_out_6[15]), .in_1(Len[3:2]));
  M2A_mux4 m2a_mux4_50 (
    .out_6(m2a_mux4_64_out_6[14]), .in_2(m2a_mux4_32_out_6[26]), .in_3(m2a_mux4_32_out_6[22]),
    .in_4(m2a_mux4_32_out_6[18]), .in_5(m2a_mux4_32_out_6[14]), .in_1(Len[3:2]));
  M2A_mux4 m2a_mux4_51 (
    .out_6(m2a_mux4_64_out_6[13]), .in_2(m2a_mux4_32_out_6[25]), .in_3(m2a_mux4_32_out_6[21]),
    .in_4(m2a_mux4_32_out_6[17]), .in_5(m2a_mux4_32_out_6[13]), .in_1(Len[3:2]));
  M2A_mux4 m2a_mux4_52 (
    .out_6(m2a_mux4_64_out_6[12]), .in_2(m2a_mux4_32_out_6[24]), .in_3(m2a_mux4_32_out_6[20]),
    .in_4(m2a_mux4_32_out_6[16]), .in_5(m2a_mux4_32_out_6[12]), .in_1(Len[3:2]));
  M2A_mux4 m2a_mux4_53 (
    .out_6(m2a_mux4_64_out_6[11]), .in_2(m2a_mux4_32_out_6[23]), .in_3(m2a_mux4_32_out_6[19]),
    .in_4(m2a_mux4_32_out_6[15]), .in_5(m2a_mux4_32_out_6[11]), .in_1(Len[3:2]));
  M2A_mux4 m2a_mux4_54 (
    .out_6(m2a_mux4_64_out_6[10]), .in_2(m2a_mux4_32_out_6[22]), .in_3(m2a_mux4_32_out_6[18]),
    .in_4(m2a_mux4_32_out_6[14]), .in_5(m2a_mux4_32_out_6[10]), .in_1(Len[3:2]));
  M2A_mux4 m2a_mux4_55 (
    .out_6(m2a_mux4_64_out_6[9]), .in_2(m2a_mux4_32_out_6[21]), .in_3(m2a_mux4_32_out_6[17]),
    .in_4(m2a_mux4_32_out_6[13]), .in_5(m2a_mux4_32_out_6[9]), .in_1(Len[3:2]));
  M2A_mux4 m2a_mux4_56 (
    .out_6(m2a_mux4_64_out_6[8]), .in_2(m2a_mux4_32_out_6[20]), .in_3(m2a_mux4_32_out_6[16]),
    .in_4(m2a_mux4_32_out_6[12]), .in_5(m2a_mux4_32_out_6[8]), .in_1(Len[3:2]));
  M2A_mux4 m2a_mux4_57 (
    .out_6(m2a_mux4_64_out_6[7]), .in_2(m2a_mux4_32_out_6[19]), .in_3(m2a_mux4_32_out_6[15]),
    .in_4(m2a_mux4_32_out_6[11]), .in_5(m2a_mux4_32_out_6[7]), .in_1(Len[3:2]));
  M2A_mux4 m2a_mux4_58 (
    .out_6(m2a_mux4_64_out_6[6]), .in_2(m2a_mux4_32_out_6[18]), .in_3(m2a_mux4_32_out_6[14]),
    .in_4(m2a_mux4_32_out_6[10]), .in_5(m2a_mux4_32_out_6[6]), .in_1(Len[3:2]));
  M2A_mux4 m2a_mux4_59 (
    .out_6(m2a_mux4_64_out_6[5]), .in_2(m2a_mux4_32_out_6[17]), .in_3(m2a_mux4_32_out_6[13]),
    .in_4(m2a_mux4_32_out_6[9]), .in_5(m2a_mux4_32_out_6[5]), .in_1(Len[3:2]));
  M2A_mux4 m2a_mux4_60 (
    .out_6(m2a_mux4_64_out_6[4]), .in_2(m2a_mux4_32_out_6[16]), .in_3(m2a_mux4_32_out_6[12]),
    .in_4(m2a_mux4_32_out_6[8]), .in_5(m2a_mux4_32_out_6[4]), .in_1(Len[3:2]));
  M2A_mux4 m2a_mux4_61 (
    .out_6(m2a_mux4_64_out_6[3]), .in_2(m2a_mux4_32_out_6[15]), .in_3(m2a_mux4_32_out_6[11]),
    .in_4(m2a_mux4_32_out_6[7]), .in_5(m2a_mux4_32_out_6[3]), .in_1(Len[3:2]));
  M2A_mux4 m2a_mux4_62 (
    .out_6(m2a_mux4_64_out_6[2]), .in_2(m2a_mux4_32_out_6[14]), .in_3(m2a_mux4_32_out_6[10]),
    .in_4(m2a_mux4_32_out_6[6]), .in_5(m2a_mux4_32_out_6[2]), .in_1(Len[3:2]));
  M2A_mux4 m2a_mux4_63 (
    .out_6(m2a_mux4_64_out_6[1]), .in_2(m2a_mux4_32_out_6[13]), .in_3(m2a_mux4_32_out_6[9]),
    .in_4(m2a_mux4_32_out_6[5]), .in_5(m2a_mux4_32_out_6[1]), .in_1(Len[3:2]));
  M2A_mux4 m2a_mux4_64 (
    .out_6(m2a_mux4_64_out_6[0]), .in_2(m2a_mux4_32_out_6[12]), .in_3(m2a_mux4_32_out_6[8]),
    .in_4(m2a_mux4_32_out_6[4]), .in_5(m2a_mux4_32_out_6[0]), .in_1(Len[3:2]));
  M2A_mux2 m2a_mux2_1 (.out_4(O[31]), .in_2(shf_in), .in_3(m2a_mux4_64_out_6[31]), .in_1(Len[4]));
  M2A_mux2 m2a_mux2_2 (.out_4(O[30]), .in_2(shf_in), .in_3(m2a_mux4_64_out_6[30]), .in_1(Len[4]));
  M2A_mux2 m2a_mux2_3 (.out_4(O[29]), .in_2(shf_in), .in_3(m2a_mux4_64_out_6[29]), .in_1(Len[4]));
  M2A_mux2 m2a_mux2_4 (.out_4(O[28]), .in_2(shf_in), .in_3(m2a_mux4_64_out_6[28]), .in_1(Len[4]));
  M2A_mux2 m2a_mux2_5 (.out_4(O[27]), .in_2(shf_in), .in_3(m2a_mux4_64_out_6[27]), .in_1(Len[4]));
  M2A_mux2 m2a_mux2_6 (.out_4(O[26]), .in_2(shf_in), .in_3(m2a_mux4_64_out_6[26]), .in_1(Len[4]));
  M2A_mux2 m2a_mux2_7 (.out_4(O[25]), .in_2(shf_in), .in_3(m2a_mux4_64_out_6[25]), .in_1(Len[4]));
  M2A_mux2 m2a_mux2_8 (.out_4(O[24]), .in_2(shf_in), .in_3(m2a_mux4_64_out_6[24]), .in_1(Len[4]));
  M2A_mux2 m2a_mux2_9 (.out_4(O[23]), .in_2(shf_in), .in_3(m2a_mux4_64_out_6[23]), .in_1(Len[4]));
  M2A_mux2 m2a_mux2_10 (.out_4(O[22]), .in_2(shf_in), .in_3(m2a_mux4_64_out_6[22]), .in_1(Len[4]));
  M2A_mux2 m2a_mux2_11 (.out_4(O[21]), .in_2(shf_in), .in_3(m2a_mux4_64_out_6[21]), .in_1(Len[4]));
  M2A_mux2 m2a_mux2_12 (.out_4(O[20]), .in_2(shf_in), .in_3(m2a_mux4_64_out_6[20]), .in_1(Len[4]));
  M2A_mux2 m2a_mux2_13 (.out_4(O[19]), .in_2(shf_in), .in_3(m2a_mux4_64_out_6[19]), .in_1(Len[4]));
  M2A_mux2 m2a_mux2_14 (.out_4(O[18]), .in_2(shf_in), .in_3(m2a_mux4_64_out_6[18]), .in_1(Len[4]));
  M2A_mux2 m2a_mux2_15 (.out_4(O[17]), .in_2(shf_in), .in_3(m2a_mux4_64_out_6[17]), .in_1(Len[4]));
  M2A_mux2 m2a_mux2_16 (.out_4(O[16]), .in_2(shf_in), .in_3(m2a_mux4_64_out_6[16]), .in_1(Len[4]));
  M2A_mux2 m2a_mux2_17 (.out_4(O[15]), .in_2(m2a_mux4_64_out_6[31]), .in_3(m2a_mux4_64_out_6[15]), .in_1(Len[4]));
  M2A_mux2 m2a_mux2_18 (.out_4(O[14]), .in_2(m2a_mux4_64_out_6[30]), .in_3(m2a_mux4_64_out_6[14]), .in_1(Len[4]));
  M2A_mux2 m2a_mux2_19 (.out_4(O[13]), .in_2(m2a_mux4_64_out_6[29]), .in_3(m2a_mux4_64_out_6[13]), .in_1(Len[4]));
  M2A_mux2 m2a_mux2_20 (.out_4(O[12]), .in_2(m2a_mux4_64_out_6[28]), .in_3(m2a_mux4_64_out_6[12]), .in_1(Len[4]));
  M2A_mux2 m2a_mux2_21 (.out_4(O[11]), .in_2(m2a_mux4_64_out_6[27]), .in_3(m2a_mux4_64_out_6[11]), .in_1(Len[4]));
  M2A_mux2 m2a_mux2_22 (.out_4(O[10]), .in_2(m2a_mux4_64_out_6[26]), .in_3(m2a_mux4_64_out_6[10]), .in_1(Len[4]));
  M2A_mux2 m2a_mux2_23 (.out_4(O[9]), .in_2(m2a_mux4_64_out_6[25]), .in_3(m2a_mux4_64_out_6[9]), .in_1(Len[4]));
  M2A_mux2 m2a_mux2_24 (.out_4(O[8]), .in_2(m2a_mux4_64_out_6[24]), .in_3(m2a_mux4_64_out_6[8]), .in_1(Len[4]));
  M2A_mux2 m2a_mux2_25 (.out_4(O[7]), .in_2(m2a_mux4_64_out_6[23]), .in_3(m2a_mux4_64_out_6[7]), .in_1(Len[4]));
  M2A_mux2 m2a_mux2_26 (.out_4(O[6]), .in_2(m2a_mux4_64_out_6[22]), .in_3(m2a_mux4_64_out_6[6]), .in_1(Len[4]));
  M2A_mux2 m2a_mux2_27 (.out_4(O[5]), .in_2(m2a_mux4_64_out_6[21]), .in_3(m2a_mux4_64_out_6[5]), .in_1(Len[4]));
  M2A_mux2 m2a_mux2_28 (.out_4(O[4]), .in_2(m2a_mux4_64_out_6[20]), .in_3(m2a_mux4_64_out_6[4]), .in_1(Len[4]));
  M2A_mux2 m2a_mux2_29 (.out_4(O[3]), .in_2(m2a_mux4_64_out_6[19]), .in_3(m2a_mux4_64_out_6[3]), .in_1(Len[4]));
  M2A_mux2 m2a_mux2_30 (.out_4(O[2]), .in_2(m2a_mux4_64_out_6[18]), .in_3(m2a_mux4_64_out_6[2]), .in_1(Len[4]));
  M2A_mux2 m2a_mux2_31 (.out_4(O[1]), .in_2(m2a_mux4_64_out_6[17]), .in_3(m2a_mux4_64_out_6[1]), .in_1(Len[4]));
  M2A_mux2 m2a_mux2_32 (.out_4(O[0]), .in_2(m2a_mux4_64_out_6[16]), .in_3(m2a_mux4_64_out_6[0]), .in_1(Len[4]));

  // Notes on the sheet:
  //   注意水平和垂直总线中LSB和MSB的位置，是和左移时相反的
endmodule

module M2A_MSBn_32 (
  input  [31:0] in_1,
  input  n,
  output [31:0] out_3
);

  xnor xnor_1 (out_3[31], in_1[31], n);

  assign out_3[30:0] = in_1[30:0];
endmodule
