// Logisim project M2_Plexers.circ as structural Verilog: 7 circuits, main circuit M2A_mux2
module M2A_mux2 (
  input  in_1,
  input  in_2,
  input  in_3,
  output out_4
);

  wire and_1_out, and_2_out, not_1_out;

  not not_1 (not_1_out, in_1);
  and and_1 (and_1_out, in_1, in_2);
  and and_2 (and_2_out, not_1_out, in_3);
  or or_1 (out_4, and_1_out, and_2_out);
endmodule

module M2A_mux4 (
  input  [1:0] in_1,
  input  in_2,
  input  in_3,
  input  in_4,
  input  in_5,
  output out_6
);

  wire and_1_out, and_2_out, and_3_out, and_4_out, not_1_out, not_2_out;

  not not_1 (not_1_out, in_1[0]);
  not not_2 (not_2_out, in_1[1]);
  and and_1 (and_1_out, in_1[1], in_1[0], in_2);
  and and_2 (and_2_out, in_1[1], not_1_out, in_3);
  and and_3 (and_3_out, not_2_out, in_1[0], in_4);
  and and_4 (and_4_out, not_2_out, not_1_out, in_5);
  or or_1 (out_6, and_1_out, and_2_out, and_3_out, and_4_out);
endmodule

module M2A_mux8 (
  input  [2:0] in_1,
  input  in_2,
  input  in_3,
  input  in_4,
  input  in_5,
  input  in_6,
  input  in_7,
  input  in_8,
  input  in_9,
  output out_10
);

  wire and_1_out, and_2_out, and_3_out, and_4_out, and_5_out, and_6_out, and_7_out, and_8_out, not_1_out,
       not_2_out, not_3_out;

  not not_1 (not_1_out, in_1[2]);
  not not_2 (not_2_out, in_1[1]);
  not not_3 (not_3_out, in_1[0]);
  and and_1 (and_1_out, not_3_out, not_2_out, not_1_out, in_2);
  and and_2 (and_2_out, in_1[0], not_2_out, not_1_out, in_3);
  and and_3 (and_3_out, not_3_out, in_1[1], not_1_out, in_4);
  and and_4 (and_4_out, in_1[0], in_1[1], not_1_out, in_5);
  and and_5 (and_5_out, not_3_out, not_2_out, in_1[2], in_6);
  and and_6 (and_6_out, in_1[0], not_2_out, in_1[2], in_7);
  and and_7 (and_7_out, not_3_out, in_1[1], in_1[2], in_8);
  and and_8 (and_8_out, in_1[0], in_1[1], in_1[2], in_9);
  or or_1 (out_10, and_1_out, and_2_out, and_3_out, and_4_out, and_5_out, and_6_out, and_7_out, and_8_out);
endmodule

module M2A_mux2_32 (
  input  in_1,
  input  [31:0] in_2,
  input  [31:0] in_3,
  output [31:0] out_4
);

  M2A_mux2 m2a_mux2_1 (.out_4(out_4[0]), .in_2(in_2[0]), .in_3(in_3[0]), .in_1(in_1));
  M2A_mux2 m2a_mux2_2 (.out_4(out_4[1]), .in_2(in_2[1]), .in_3(in_3[1]), .in_1(in_1));
  M2A_mux2 m2a_mux2_3 (.out_4(out_4[2]), .in_2(in_2[2]), .in_3(in_3[2]), .in_1(in_1));
  M2A_mux2 m2a_mux2_4 (.out_4(out_4[3]), .in_2(in_2[3]), .in_3(in_3[3]), .in_1(in_1));
  M2A_mux2 m2a_mux2_5 (.out_4(out_4[4]), .in_2(in_2[4]), .in_3(in_3[4]), .in_1(in_1));
  M2A_mux2 m2a_mux2_6 (.out_4(out_4[5]), .in_2(in_2[5]), .in_3(in_3[5]), .in_1(in_1));
  M2A_mux2 m2a_mux2_7 (.out_4(out_4[6]), .in_2(in_2[6]), .in_3(in_3[6]), .in_1(in_1));
  M2A_mux2 m2a_mux2_8 (.out_4(out_4[7]), .in_2(in_2[7]), .in_3(in_3[7]), .in_1(in_1));
  M2A_mux2 m2a_mux2_9 (.out_4(out_4[8]), .in_2(in_2[8]), .in_3(in_3[8]), .in_1(in_1));
  M2A_mux2 m2a_mux2_10 (.out_4(out_4[9]), .in_2(in_2[9]), .in_3(in_3[9]), .in_1(in_1));
  M2A_mux2 m2a_mux2_11 (.out_4(out_4[10]), .in_2(in_2[10]), .in_3(in_3[10]), .in_1(in_1));
  M2A_mux2 m2a_mux2_12 (.out_4(out_4[11]), .in_2(in_2[11]), .in_3(in_3[11]), .in_1(in_1));
  M2A_mux2 m2a_mux2_13 (.out_4(out_4[12]), .in_2(in_2[12]), .in_3(in_3[12]), .in_1(in_1));
  M2A_mux2 m2a_mux2_14 (.out_4(out_4[13]), .in_2(in_2[13]), .in_3(in_3[13]), .in_1(in_1));
  M2A_mux2 m2a_mux2_15 (.out_4(out_4[14]), .in_2(in_2[14]), .in_3(in_3[14]), .in_1(in_1));
  M2A_mux2 m2a_mux2_16 (.out_4(out_4[15]), .in_2(in_2[15]), .in_3(in_3[15]), .in_1(in_1));
  M2A_mux2 m2a_mux2_17 (.out_4(out_4[16]), .in_2(in_2[16]), .in_3(in_3[16]), .in_1(in_1));
  M2A_mux2 m2a_mux2_18 (.out_4(out_4[17]), .in_2(in_2[17]), .in_3(in_3[17]), .in_1(in_1));
  M2A_mux2 m2a_mux2_19 (.out_4(out_4[18]), .in_2(in_2[18]), .in_3(in_3[18]), .in_1(in_1));
  M2A_mux2 m2a_mux2_20 (.out_4(out_4[19]), .in_2(in_2[19]), .in_3(in_3[19]), .in_1(in_1));
  M2A_mux2 m2a_mux2_21 (.out_4(out_4[20]), .in_2(in_2[20]), .in_3(in_3[20]), .in_1(in_1));
  M2A_mux2 m2a_mux2_22 (.out_4(out_4[21]), .in_2(in_2[21]), .in_3(in_3[21]), .in_1(in_1));
  M2A_mux2 m2a_mux2_23 (.out_4(out_4[22]), .in_2(in_2[22]), .in_3(in_3[22]), .in_1(in_1));
  M2A_mux2 m2a_mux2_24 (.out_4(out_4[23]), .in_2(in_2[23]), .in_3(in_3[23]), .in_1(in_1));
  M2A_mux2 m2a_mux2_25 (.out_4(out_4[24]), .in_2(in_2[24]), .in_3(in_3[24]), .in_1(in_1));
  M2A_mux2 m2a_mux2_26 (.out_4(out_4[25]), .in_2(in_2[25]), .in_3(in_3[25]), .in_1(in_1));
  M2A_mux2 m2a_mux2_27 (.out_4(out_4[26]), .in_2(in_2[26]), .in_3(in_3[26]), .in_1(in_1));
  M2A_mux2 m2a_mux2_28 (.out_4(out_4[27]), .in_2(in_2[27]), .in_3(in_3[27]), .in_1(in_1));
  M2A_mux2 m2a_mux2_29 (.out_4(out_4[28]), .in_2(in_2[28]), .in_3(in_3[28]), .in_1(in_1));
  M2A_mux2 m2a_mux2_30 (.out_4(out_4[29]), .in_2(in_2[29]), .in_3(in_3[29]), .in_1(in_1));
  M2A_mux2 m2a_mux2_31 (.out_4(out_4[30]), .in_2(in_2[30]), .in_3(in_3[30]), .in_1(in_1));
  M2A_mux2 m2a_mux2_32 (.out_4(out_4[31]), .in_2(in_2[31]), .in_3(in_3[31]), .in_1(in_1));
endmodule

module M2A_mux4_32 (
  input  [1:0] in_1,
  input  [31:0] in_2,
  input  [31:0] in_3,
  input  [31:0] in_4,
  input  [31:0] in_5,
  output [31:0] out_6
);

  M2A_mux4 m2a_mux4_1 (.out_6(out_6[0]), .in_2(in_2[0]), .in_3(in_3[0]), .in_4(in_4[0]), .in_5(in_5[0]), .in_1(in_1));
  M2A_mux4 m2a_mux4_2 (.out_6(out_6[1]), .in_2(in_2[1]), .in_3(in_3[1]), .in_4(in_4[1]), .in_5(in_5[1]), .in_1(in_1));
  M2A_mux4 m2a_mux4_3 (.out_6(out_6[2]), .in_2(in_2[2]), .in_3(in_3[2]), .in_4(in_4[2]), .in_5(in_5[2]), .in_1(in_1));
  M2A_mux4 m2a_mux4_4 (.out_6(out_6[3]), .in_2(in_2[3]), .in_3(in_3[3]), .in_4(in_4[3]), .in_5(in_5[3]), .in_1(in_1));
  M2A_mux4 m2a_mux4_5 (.out_6(out_6[4]), .in_2(in_2[4]), .in_3(in_3[4]), .in_4(in_4[4]), .in_5(in_5[4]), .in_1(in_1));
  M2A_mux4 m2a_mux4_6 (.out_6(out_6[5]), .in_2(in_2[5]), .in_3(in_3[5]), .in_4(in_4[5]), .in_5(in_5[5]), .in_1(in_1));
  M2A_mux4 m2a_mux4_7 (.out_6(out_6[6]), .in_2(in_2[6]), .in_3(in_3[6]), .in_4(in_4[6]), .in_5(in_5[6]), .in_1(in_1));
  M2A_mux4 m2a_mux4_8 (.out_6(out_6[7]), .in_2(in_2[7]), .in_3(in_3[7]), .in_4(in_4[7]), .in_5(in_5[7]), .in_1(in_1));
  M2A_mux4 m2a_mux4_9 (.out_6(out_6[8]), .in_2(in_2[8]), .in_3(in_3[8]), .in_4(in_4[8]), .in_5(in_5[8]), .in_1(in_1));
  M2A_mux4 m2a_mux4_10 (.out_6(out_6[9]), .in_2(in_2[9]), .in_3(in_3[9]), .in_4(in_4[9]), .in_5(in_5[9]), .in_1(in_1));
  M2A_mux4 m2a_mux4_11 (
    .out_6(out_6[10]), .in_2(in_2[10]), .in_3(in_3[10]), .in_4(in_4[10]), .in_5(in_5[10]), .in_1(in_1));
  M2A_mux4 m2a_mux4_12 (
    .out_6(out_6[11]), .in_2(in_2[11]), .in_3(in_3[11]), .in_4(in_4[11]), .in_5(in_5[11]), .in_1(in_1));
  M2A_mux4 m2a_mux4_13 (
    .out_6(out_6[12]), .in_2(in_2[12]), .in_3(in_3[12]), .in_4(in_4[12]), .in_5(in_5[12]), .in_1(in_1));
  M2A_mux4 m2a_mux4_14 (
    .out_6(out_6[13]), .in_2(in_2[13]), .in_3(in_3[13]), .in_4(in_4[13]), .in_5(in_5[13]), .in_1(in_1));
  M2A_mux4 m2a_mux4_15 (
    .out_6(out_6[14]), .in_2(in_2[14]), .in_3(in_3[14]), .in_4(in_4[14]), .in_5(in_5[14]), .in_1(in_1));
  M2A_mux4 m2a_mux4_16 (
    .out_6(out_6[15]), .in_2(in_2[15]), .in_3(in_3[15]), .in_4(in_4[15]), .in_5(in_5[15]), .in_1(in_1));
  M2A_mux4 m2a_mux4_17 (
    .out_6(out_6[16]), .in_2(in_2[16]), .in_3(in_3[16]), .in_4(in_4[16]), .in_5(in_5[16]), .in_1(in_1));
  M2A_mux4 m2a_mux4_18 (
    .out_6(out_6[17]), .in_2(in_2[17]), .in_3(in_3[17]), .in_4(in_4[17]), .in_5(in_5[17]), .in_1(in_1));
  M2A_mux4 m2a_mux4_19 (
    .out_6(out_6[18]), .in_2(in_2[18]), .in_3(in_3[18]), .in_4(in_4[18]), .in_5(in_5[18]), .in_1(in_1));
  M2A_mux4 m2a_mux4_20 (
    .out_6(out_6[19]), .in_2(in_2[19]), .in_3(in_3[19]), .in_4(in_4[19]), .in_5(in_5[19]), .in_1(in_1));
  M2A_mux4 m2a_mux4_21 (
    .out_6(out_6[20]), .in_2(in_2[20]), .in_3(in_3[20]), .in_4(in_4[20]), .in_5(in_5[20]), .in_1(in_1));
  M2A_mux4 m2a_mux4_22 (
    .out_6(out_6[21]), .in_2(in_2[21]), .in_3(in_3[21]), .in_4(in_4[21]), .in_5(in_5[21]), .in_1(in_1));
  M2A_mux4 m2a_mux4_23 (
    .out_6(out_6[22]), .in_2(in_2[22]), .in_3(in_3[22]), .in_4(in_4[22]), .in_5(in_5[22]), .in_1(in_1));
  M2A_mux4 m2a_mux4_24 (
    .out_6(out_6[23]), .in_2(in_2[23]), .in_3(in_3[23]), .in_4(in_4[23]), .in_5(in_5[23]), .in_1(in_1));
  M2A_mux4 m2a_mux4_25 (
    .out_6(out_6[24]), .in_2(in_2[24]), .in_3(in_3[24]), .in_4(in_4[24]), .in_5(in_5[24]), .in_1(in_1));
  M2A_mux4 m2a_mux4_26 (
    .out_6(out_6[25]), .in_2(in_2[25]), .in_3(in_3[25]), .in_4(in_4[25]), .in_5(in_5[25]), .in_1(in_1));
  M2A_mux4 m2a_mux4_27 (
    .out_6(out_6[26]), .in_2(in_2[26]), .in_3(in_3[26]), .in_4(in_4[26]), .in_5(in_5[26]), .in_1(in_1));
  M2A_mux4 m2a_mux4_28 (
    .out_6(out_6[27]), .in_2(in_2[27]), .in_3(in_3[27]), .in_4(in_4[27]), .in_5(in_5[27]), .in_1(in_1));
  M2A_mux4 m2a_mux4_29 (
    .out_6(out_6[28]), .in_2(in_2[28]), .in_3(in_3[28]), .in_4(in_4[28]), .in_5(in_5[28]), .in_1(in_1));
  M2A_mux4 m2a_mux4_30 (
    .out_6(out_6[29]), .in_2(in_2[29]), .in_3(in_3[29]), .in_4(in_4[29]), .in_5(in_5[29]), .in_1(in_1));
  M2A_mux4 m2a_mux4_31 (
    .out_6(out_6[30]), .in_2(in_2[30]), .in_3(in_3[30]), .in_4(in_4[30]), .in_5(in_5[30]), .in_1(in_1));
  M2A_mux4 m2a_mux4_32 (
    .out_6(out_6[31]), .in_2(in_2[31]), .in_3(in_3[31]), .in_4(in_4[31]), .in_5(in_5[31]), .in_1(in_1));
endmodule

module M2A_mux8_32 (
  input  [2:0] in_1,
  input  [31:0] in_2,
  input  [31:0] in_3,
  input  [31:0] in_4,
  input  [31:0] in_5,
  input  [31:0] in_6,
  input  [31:0] in_7,
  input  [31:0] in_8,
  input  [31:0] in_9,
  output [31:0] out_10
);

  M2A_mux8 m2a_mux8_1 (
    .out_10(out_10[0]), .in_2(in_2[0]), .in_3(in_3[0]), .in_4(in_4[0]), .in_5(in_5[0]), .in_6(in_6[0]),
    .in_7(in_7[0]), .in_8(in_8[0]), .in_9(in_9[0]), .in_1(in_1));
  M2A_mux8 m2a_mux8_2 (
    .out_10(out_10[1]), .in_2(in_2[1]), .in_3(in_3[1]), .in_4(in_4[1]), .in_5(in_5[1]), .in_6(in_6[1]),
    .in_7(in_7[1]), .in_8(in_8[1]), .in_9(in_9[1]), .in_1(in_1));
  M2A_mux8 m2a_mux8_3 (
    .out_10(out_10[2]), .in_2(in_2[2]), .in_3(in_3[2]), .in_4(in_4[2]), .in_5(in_5[2]), .in_6(in_6[2]),
    .in_7(in_7[2]), .in_8(in_8[2]), .in_9(in_9[2]), .in_1(in_1));
  M2A_mux8 m2a_mux8_4 (
    .out_10(out_10[3]), .in_2(in_2[3]), .in_3(in_3[3]), .in_4(in_4[3]), .in_5(in_5[3]), .in_6(in_6[3]),
    .in_7(in_7[3]), .in_8(in_8[3]), .in_9(in_9[3]), .in_1(in_1));
  M2A_mux8 m2a_mux8_5 (
    .out_10(out_10[4]), .in_2(in_2[4]), .in_3(in_3[4]), .in_4(in_4[4]), .in_5(in_5[4]), .in_6(in_6[4]),
    .in_7(in_7[4]), .in_8(in_8[4]), .in_9(in_9[4]), .in_1(in_1));
  M2A_mux8 m2a_mux8_6 (
    .out_10(out_10[5]), .in_2(in_2[5]), .in_3(in_3[5]), .in_4(in_4[5]), .in_5(in_5[5]), .in_6(in_6[5]),
    .in_7(in_7[5]), .in_8(in_8[5]), .in_9(in_9[5]), .in_1(in_1));
  M2A_mux8 m2a_mux8_7 (
    .out_10(out_10[6]), .in_2(in_2[6]), .in_3(in_3[6]), .in_4(in_4[6]), .in_5(in_5[6]), .in_6(in_6[6]),
    .in_7(in_7[6]), .in_8(in_8[6]), .in_9(in_9[6]), .in_1(in_1));
  M2A_mux8 m2a_mux8_8 (
    .out_10(out_10[7]), .in_2(in_2[7]), .in_3(in_3[7]), .in_4(in_4[7]), .in_5(in_5[7]), .in_6(in_6[7]),
    .in_7(in_7[7]), .in_8(in_8[7]), .in_9(in_9[7]), .in_1(in_1));
  M2A_mux8 m2a_mux8_9 (
    .out_10(out_10[8]), .in_2(in_2[8]), .in_3(in_3[8]), .in_4(in_4[8]), .in_5(in_5[8]), .in_6(in_6[8]),
    .in_7(in_7[8]), .in_8(in_8[8]), .in_9(in_9[8]), .in_1(in_1));
  M2A_mux8 m2a_mux8_10 (
    .out_10(out_10[9]), .in_2(in_2[9]), .in_3(in_3[9]), .in_4(in_4[9]), .in_5(in_5[9]), .in_6(in_6[9]),
    .in_7(in_7[9]), .in_8(in_8[9]), .in_9(in_9[9]), .in_1(in_1));
  M2A_mux8 m2a_mux8_11 (
    .out_10(out_10[10]), .in_2(in_2[10]), .in_3(in_3[10]), .in_4(in_4[10]), .in_5(in_5[10]), .in_6(in_6[10]),
    .in_7(in_7[10]), .in_8(in_8[10]), .in_9(in_9[10]), .in_1(in_1));
  M2A_mux8 m2a_mux8_12 (
    .out_10(out_10[11]), .in_2(in_2[11]), .in_3(in_3[11]), .in_4(in_4[11]), .in_5(in_5[11]), .in_6(in_6[11]),
    .in_7(in_7[11]), .in_8(in_8[11]), .in_9(in_9[11]), .in_1(in_1));
  M2A_mux8 m2a_mux8_13 (
    .out_10(out_10[12]), .in_2(in_2[12]), .in_3(in_3[12]), .in_4(in_4[12]), .in_5(in_5[12]), .in_6(in_6[12]),
    .in_7(in_7[12]), .in_8(in_8[12]), .in_9(in_9[12]), .in_1(in_1));
  M2A_mux8 m2a_mux8_14 (
    .out_10(out_10[13]), .in_2(in_2[13]), .in_3(in_3[13]), .in_4(in_4[13]), .in_5(in_5[13]), .in_6(in_6[13]),
    .in_7(in_7[13]), .in_8(in_8[13]), .in_9(in_9[13]), .in_1(in_1));
  M2A_mux8 m2a_mux8_15 (
    .out_10(out_10[14]), .in_2(in_2[14]), .in_3(in_3[14]), .in_4(in_4[14]), .in_5(in_5[14]), .in_6(in_6[14]),
    .in_7(in_7[14]), .in_8(in_8[14]), .in_9(in_9[14]), .in_1(in_1));
  M2A_mux8 m2a_mux8_16 (
    .out_10(out_10[15]), .in_2(in_2[15]), .in_3(in_3[15]), .in_4(in_4[15]), .in_5(in_5[15]), .in_6(in_6[15]),
    .in_7(in_7[15]), .in_8(in_8[15]), .in_9(in_9[15]), .in_1(in_1));
  M2A_mux8 m2a_mux8_17 (
    .out_10(out_10[16]), .in_2(in_2[16]), .in_3(in_3[16]), .in_4(in_4[16]), .in_5(in_5[16]), .in_6(in_6[16]),
    .in_7(in_7[16]), .in_8(in_8[16]), .in_9(in_9[16]), .in_1(in_1));
  M2A_mux8 m2a_mux8_18 (
    .out_10(out_10[17]), .in_2(in_2[17]), .in_3(in_3[17]), .in_4(in_4[17]), .in_5(in_5[17]), .in_6(in_6[17]),
    .in_7(in_7[17]), .in_8(in_8[17]), .in_9(in_9[17]), .in_1(in_1));
  M2A_mux8 m2a_mux8_19 (
    .out_10(out_10[18]), .in_2(in_2[18]), .in_3(in_3[18]), .in_4(in_4[18]), .in_5(in_5[18]), .in_6(in_6[18]),
    .in_7(in_7[18]), .in_8(in_8[18]), .in_9(in_9[18]), .in_1(in_1));
  M2A_mux8 m2a_mux8_20 (
    .out_10(out_10[19]), .in_2(in_2[19]), .in_3(in_3[19]), .in_4(in_4[19]), .in_5(in_5[19]), .in_6(in_6[19]),
    .in_7(in_7[19]), .in_8(in_8[19]), .in_9(in_9[19]), .in_1(in_1));
  M2A_mux8 m2a_mux8_21 (
    .out_10(out_10[20]), .in_2(in_2[20]), .in_3(in_3[20]), .in_4(in_4[20]), .in_5(in_5[20]), .in_6(in_6[20]),
    .in_7(in_7[20]), .in_8(in_8[20]), .in_9(in_9[20]), .in_1(in_1));
  M2A_mux8 m2a_mux8_22 (
    .out_10(out_10[21]), .in_2(in_2[21]), .in_3(in_3[21]), .in_4(in_4[21]), .in_5(in_5[21]), .in_6(in_6[21]),
    .in_7(in_7[21]), .in_8(in_8[21]), .in_9(in_9[21]), .in_1(in_1));
  M2A_mux8 m2a_mux8_23 (
    .out_10(out_10[22]), .in_2(in_2[22]), .in_3(in_3[22]), .in_4(in_4[22]), .in_5(in_5[22]), .in_6(in_6[22]),
    .in_7(in_7[22]), .in_8(in_8[22]), .in_9(in_9[22]), .in_1(in_1));
  M2A_mux8 m2a_mux8_24 (
    .out_10(out_10[23]), .in_2(in_2[23]), .in_3(in_3[23]), .in_4(in_4[23]), .in_5(in_5[23]), .in_6(in_6[23]),
    .in_7(in_7[23]), .in_8(in_8[23]), .in_9(in_9[23]), .in_1(in_1));
  M2A_mux8 m2a_mux8_25 (
    .out_10(out_10[24]), .in_2(in_2[24]), .in_3(in_3[24]), .in_4(in_4[24]), .in_5(in_5[24]), .in_6(in_6[24]),
    .in_7(in_7[24]), .in_8(in_8[24]), .in_9(in_9[24]), .in_1(in_1));
  M2A_mux8 m2a_mux8_26 (
    .out_10(out_10[25]), .in_2(in_2[25]), .in_3(in_3[25]), .in_4(in_4[25]), .in_5(in_5[25]), .in_6(in_6[25]),
    .in_7(in_7[25]), .in_8(in_8[25]), .in_9(in_9[25]), .in_1(in_1));
  M2A_mux8 m2a_mux8_27 (
    .out_10(out_10[26]), .in_2(in_2[26]), .in_3(in_3[26]), .in_4(in_4[26]), .in_5(in_5[26]), .in_6(in_6[26]),
    .in_7(in_7[26]), .in_8(in_8[26]), .in_9(in_9[26]), .in_1(in_1));
  M2A_mux8 m2a_mux8_28 (
    .out_10(out_10[27]), .in_2(in_2[27]), .in_3(in_3[27]), .in_4(in_4[27]), .in_5(in_5[27]), .in_6(in_6[27]),
    .in_7(in_7[27]), .in_8(in_8[27]), .in_9(in_9[27]), .in_1(in_1));
  M2A_mux8 m2a_mux8_29 (
    .out_10(out_10[28]), .in_2(in_2[28]), .in_3(in_3[28]), .in_4(in_4[28]), .in_5(in_5[28]), .in_6(in_6[28]),
    .in_7(in_7[28]), .in_8(in_8[28]), .in_9(in_9[28]), .in_1(in_1));
  M2A_mux8 m2a_mux8_30 (
    .out_10(out_10[29]), .in_2(in_2[29]), .in_3(in_3[29]), .in_4(in_4[29]), .in_5(in_5[29]), .in_6(in_6[29]),
    .in_7(in_7[29]), .in_8(in_8[29]), .in_9(in_9[29]), .in_1(in_1));
  M2A_mux8 m2a_mux8_31 (
    .out_10(out_10[30]), .in_2(in_2[30]), .in_3(in_3[30]), .in_4(in_4[30]), .in_5(in_5[30]), .in_6(in_6[30]),
    .in_7(in_7[30]), .in_8(in_8[30]), .in_9(in_9[30]), .in_1(in_1));
  M2A_mux8 m2a_mux8_32 (
    .out_10(out_10[31]), .in_2(in_2[31]), .in_3(in_3[31]), .in_4(in_4[31]), .in_5(in_5[31]), .in_6(in_6[31]),
    .in_7(in_7[31]), .in_8(in_8[31]), .in_9(in_9[31]), .in_1(in_1));
endmodule

module M2A_demux32 (
  input  [4:0] in_1,
  input  in_2,
  output out_3,
  output out_4,
  output out_5,
  output _4,
  output out_7,
  output out_8,
  output out_9,
  output _8,
  output out_11,
  output out_12,
  output out_13,
  output _12,
  output out_15,
  output out_16,
  output out_17,
  output _16,
  output out_19,
  output out_20,
  output out_21,
  output _20,
  output out_23,
  output out_24,
  output out_25,
  output _24,
  output out_27,
  output out_28,
  output out_29,
  output _28,
  output out_31,
  output out_32,
  output out_33,
  output _32
);

  wire and_1_out, and_2_out, and_3_out, and_4_out, and_5_out, and_6_out, and_7_out, and_8_out, and_9_out,
       and_10_out, and_11_out, and_12_out, and_13_out, and_14_out, and_15_out, and_16_out, and_17_out,
       and_18_out, and_19_out, and_20_out, and_21_out, and_22_out, and_23_out, and_24_out, and_25_out,
       and_26_out, and_27_out, and_28_out, and_29_out, and_30_out, and_31_out, and_32_out, not_1_out,
       not_2_out, not_3_out, not_4_out, not_5_out;

  not not_1 (not_1_out, in_1[4]);
  not not_2 (not_2_out, in_1[3]);
  not not_3 (not_3_out, in_1[2]);
  not not_4 (not_4_out, in_1[1]);
  not not_5 (not_5_out, in_1[0]);
  and and_1 (and_1_out, not_5_out, not_4_out, not_3_out, not_2_out, not_1_out);
  and and_2 (and_2_out, in_1[0], not_4_out, not_3_out, not_2_out, not_1_out);
  and and_3 (and_3_out, not_5_out, in_1[1], not_3_out, not_2_out, not_1_out);
  and and_4 (and_4_out, in_1[0], in_1[1], not_3_out, not_2_out, not_1_out);
  and and_5 (and_5_out, not_5_out, not_4_out, in_1[2], not_2_out, not_1_out);
  and and_6 (and_6_out, in_1[0], not_4_out, in_1[2], not_2_out, not_1_out);
  and and_7 (and_7_out, not_5_out, in_1[1], in_1[2], not_2_out, not_1_out);
  and and_8 (and_8_out, in_1[0], in_1[1], in_1[2], not_2_out, not_1_out);
  and and_9 (and_9_out, not_5_out, not_4_out, not_3_out, in_1[3], not_1_out);
  and and_10 (and_10_out, in_1[0], not_4_out, not_3_out, in_1[3], not_1_out);
  and and_11 (and_11_out, not_5_out, in_1[1], not_3_out, in_1[3], not_1_out);
  and and_12 (and_12_out, in_1[0], in_1[1], not_3_out, in_1[3], not_1_out);
  and and_13 (and_13_out, not_5_out, not_4_out, in_1[2], in_1[3], not_1_out);
  and and_14 (and_14_out, in_1[0], not_4_out, in_1[2], in_1[3], not_1_out);
  and and_15 (and_15_out, not_5_out, in_1[1], in_1[2], in_1[3], not_1_out);
  and and_16 (and_16_out, in_1[0], in_1[1], in_1[2], in_1[3], not_1_out);
  and and_17 (and_17_out, not_5_out, not_4_out, not_3_out, not_2_out, in_1[4]);
  and and_18 (and_18_out, in_1[0], not_4_out, not_3_out, not_2_out, in_1[4]);
  and and_19 (and_19_out, not_5_out, in_1[1], not_3_out, not_2_out, in_1[4]);
  and and_20 (and_20_out, in_1[0], in_1[1], not_3_out, not_2_out, in_1[4]);
  and and_21 (and_21_out, not_5_out, not_4_out, in_1[2], not_2_out, in_1[4]);
  and and_22 (and_22_out, in_1[0], not_4_out, in_1[2], not_2_out, in_1[4]);
  and and_23 (and_23_out, not_5_out, in_1[1], in_1[2], not_2_out, in_1[4]);
  and and_24 (and_24_out, in_1[0], in_1[1], in_1[2], not_2_out, in_1[4]);
  and and_25 (and_25_out, not_5_out, not_4_out, not_3_out, in_1[3], in_1[4]);
  and and_26 (and_26_out, in_1[0], not_4_out, not_3_out, in_1[3], in_1[4]);
  and and_27 (and_27_out, not_5_out, in_1[1], not_3_out, in_1[3], in_1[4]);
  and and_28 (and_28_out, in_1[0], in_1[1], not_3_out, in_1[3], in_1[4]);
  and and_29 (and_29_out, not_5_out, not_4_out, in_1[2], in_1[3], in_1[4]);
  and and_30 (and_30_out, in_1[0], not_4_out, in_1[2], in_1[3], in_1[4]);
  and and_31 (and_31_out, not_5_out, in_1[1], in_1[2], in_1[3], in_1[4]);
  and and_32 (and_32_out, in_1[0], in_1[1], in_1[2], in_1[3], in_1[4]);
  and and_33 (out_3, in_2, and_1_out);
  and and_34 (out_4, in_2, and_2_out);
  and and_35 (out_5, in_2, and_3_out);
  and and_36 (_4, in_2, and_4_out);
  and and_37 (out_7, in_2, and_5_out);
  and and_38 (out_8, in_2, and_6_out);
  and and_39 (out_9, in_2, and_7_out);
  and and_40 (_8, in_2, and_8_out);
  and and_41 (out_11, in_2, and_9_out);
  and and_42 (out_12, in_2, and_10_out);
  and and_43 (out_13, in_2, and_11_out);
  and and_44 (_12, in_2, and_12_out);
  and and_45 (out_15, in_2, and_13_out);
  and and_46 (out_16, in_2, and_14_out);
  and and_47 (out_17, in_2, and_15_out);
  and and_48 (_16, in_2, and_16_out);
  and and_49 (out_19, in_2, and_17_out);
  and and_50 (out_20, in_2, and_18_out);
  and and_51 (out_21, in_2, and_19_out);
  and and_52 (_20, in_2, and_20_out);
  and and_53 (out_23, in_2, and_21_out);
  and and_54 (out_24, in_2, and_22_out);
  and and_55 (out_25, in_2, and_23_out);
  and and_56 (_24, in_2, and_24_out);
  and and_57 (out_27, in_2, and_25_out);
  and and_58 (out_28, in_2, and_26_out);
  and and_59 (out_29, in_2, and_27_out);
  and and_60 (_28, in_2, and_28_out);
  and and_61 (out_31, in_2, and_29_out);
  and and_62 (out_32, in_2, and_30_out);
  and and_63 (out_33, in_2, and_31_out);
  and and_64 (_32, in_2, and_32_out);
endmodule
