// Logisim project M2_utility.circ as structural Verilog: 12 circuits, main circuit main
module main (
  input  in_1,
  input  clk,
  input  srn,
  output out_4
);

  wire and_1_out, and_2_out, buffer_1_out, buffer_2_out, buffer_3_out, buffer_4_out, buffer_5_out,
       buffer_6_out, buffer_7_out, buffer_8_out, buffer_9_out, buffer_10_out, buffer_11_out, buffer_12_out,
       nand_1_out, nand_2_out, nand_4_out, not_1_out, not_2_out, or_1_out, or_2_out;

  and and_1 (and_1_out, clk, not_1_out);
  not not_1 (not_1_out, clk);
  buf buffer_1 (buffer_1_out, srn);
  and and_2 (and_2_out, in_1, and_1_out);
  buf buffer_2 (buffer_2_out, and_1_out);
  buf buffer_3 (buffer_3_out, buffer_2_out);
  buf buffer_4 (buffer_4_out, and_2_out);
  buf buffer_5 (buffer_5_out, buffer_4_out);
  or or_1 (or_1_out, and_1_out, buffer_2_out, buffer_3_out);
  buf buffer_6 (buffer_6_out, or_1_out);
  buf buffer_7 (buffer_7_out, buffer_1_out);
  buf buffer_8 (buffer_8_out, buffer_7_out);
  or or_2 (or_2_out, and_2_out, buffer_4_out, buffer_5_out);
  buf buffer_9 (buffer_9_out, or_2_out);
  buf buffer_10 (buffer_10_out, buffer_6_out);
  buf buffer_11 (buffer_11_out, buffer_8_out);
  not not_2 (not_2_out, or_2_out);
  nand nand_1 (nand_1_out, buffer_9_out, buffer_10_out, buffer_11_out);
  nand nand_2 (nand_2_out, buffer_10_out, not_2_out);
  nand nand_3 (out_4, nand_1_out, nand_4_out);
  buf buffer_12 (buffer_12_out, out_4);
  nand nand_4 (nand_4_out, buffer_12_out, nand_2_out, buffer_11_out);
endmodule

module clock_gen (
  input  ena,
  output clk
);

  wire buffer_1_out, buffer_2_out, buffer_3_out, buffer_4_out, buffer_5_out, buffer_6_out, buffer_7_out,
       buffer_8_out, buffer_9_out, buffer_10_out, buffer_11_out, buffer_12_out, buffer_13_out, buffer_14_out,
       buffer_15_out, buffer_16_out, buffer_17_out, not_1_out, or_1_out, or_2_out, or_3_out;

  buf buffer_1 (buffer_1_out, ena);
  not not_1 (not_1_out, ena);
  or or_1 (or_1_out, not_1_out, buffer_2_out);
  buf buffer_2 (buffer_2_out, buffer_3_out);
  buf buffer_3 (buffer_3_out, buffer_4_out);
  buf buffer_4 (buffer_4_out, buffer_5_out);
  or or_2 (or_2_out, not_1_out, or_1_out);
  buf buffer_5 (buffer_5_out, buffer_6_out);
  buf buffer_6 (buffer_6_out, buffer_7_out);
  buf buffer_7 (buffer_7_out, buffer_8_out);
  buf buffer_8 (buffer_8_out, buffer_9_out);
  or or_3 (or_3_out, not_1_out, or_2_out);
  and and_1 (clk, buffer_1_out, or_3_out);
  buf buffer_9 (buffer_9_out, buffer_10_out);
  buf buffer_10 (buffer_10_out, buffer_11_out);
  buf buffer_11 (buffer_11_out, buffer_12_out);
  buf buffer_12 (buffer_12_out, buffer_13_out);
  buf buffer_13 (buffer_13_out, buffer_14_out);
  buf buffer_14 (buffer_14_out, buffer_15_out);
  buf buffer_15 (buffer_15_out, buffer_16_out);
  buf buffer_16 (buffer_16_out, buffer_17_out);
  buf buffer_17 (buffer_17_out, clk);

  // Notes on the sheet:
  //   16
endmodule

module rst_gen (
  input  clk,
  input  arn,
  output srn
);

  wire arn_q, buffer_2_out, buffer_3_out, buffer_4_out, buffer_5_out, buffer_6_out, ena, nand_1_out,
       nand_2_out, nand_3_out, nand_4_out, nand_5_out, not_1_out, not_2_out, not_3_out;

  buf buffer_1 (ena, clk);
  not not_1 (not_1_out, clk);
  not not_2 (not_2_out, arn);
  buf buffer_2 (buffer_2_out, arn);
  nand nand_1 (nand_1_out, not_1_out, clk, not_2_out);
  buf buffer_3 (buffer_3_out, nand_1_out);
  and and_1 (arn_q, buffer_3_out, nand_1_out, buffer_2_out);
  not not_3 (not_3_out, nand_3_out);
  nand nand_2 (nand_2_out, not_3_out, buffer_5_out);
  buf buffer_4 (buffer_4_out, not_3_out);
  buf buffer_5 (buffer_5_out, nand_4_out);
  nand nand_3 (nand_3_out, buffer_4_out, ena, nand_4_out);
  nand nand_4 (nand_4_out, ena, nand_2_out, arn_q);
  nand nand_5 (nand_5_out, nand_3_out, arn_q, buffer_6_out);
  buf buffer_6 (buffer_6_out, srn);
  nand nand_6 (srn, nand_5_out, nand_4_out);

  // Notes on the sheet:
  //   async rstn DFF with I_d = 1
endmodule

module dff (
  input  d,
  input  clk,
  input  srn,
  input  ena,
  output q
);

  wire buffer_1_out, buffer_2_out, buffer_3_out, buffer_4_out, ena_t, nand_1_out, nand_2_out, nand_3_out,
       nand_4_out, nand_5_out, not_1_out;

  nand nand_1 (nand_1_out, nand_3_out, d, srn);
  nand nand_2 (nand_2_out, nand_1_out, buffer_3_out);
  not not_1 (not_1_out, srn);
  buf buffer_1 (buffer_1_out, ena);
  buf buffer_2 (buffer_2_out, nand_1_out);
  buf buffer_3 (buffer_3_out, nand_4_out);
  or or_1 (ena_t, not_1_out, buffer_1_out);
  nand nand_3 (nand_3_out, buffer_2_out, ena_t, clk, nand_4_out);
  nand nand_4 (nand_4_out, clk, ena_t, nand_2_out);
  nand nand_5 (nand_5_out, nand_3_out, buffer_4_out);
  buf buffer_4 (buffer_4_out, q);
  nand nand_6 (q, nand_5_out, nand_4_out);
endmodule

module cdc (
  input  in_1,
  input  clk,
  input  srn,
  output out_4
);

  wire and_1_out, and_2_out, buffer_1_out, buffer_2_out, buffer_3_out, buffer_4_out, buffer_5_out,
       buffer_6_out, buffer_7_out, buffer_8_out, not_1_out, or_1_out, or_2_out;

  and and_1 (and_1_out, clk, not_1_out);
  not not_1 (not_1_out, clk);
  buf buffer_1 (buffer_1_out, srn);
  and and_2 (and_2_out, in_1, and_1_out);
  buf buffer_2 (buffer_2_out, and_1_out);
  buf buffer_3 (buffer_3_out, buffer_2_out);
  buf buffer_4 (buffer_4_out, and_2_out);
  buf buffer_5 (buffer_5_out, buffer_4_out);
  or or_1 (or_1_out, and_1_out, buffer_2_out, buffer_3_out);
  buf buffer_6 (buffer_6_out, or_1_out);
  buf buffer_7 (buffer_7_out, buffer_1_out);
  buf buffer_8 (buffer_8_out, buffer_7_out);
  or or_2 (or_2_out, and_2_out, buffer_4_out, buffer_5_out);
  d_latch d_latch_1 (.out_4(out_4), .en(buffer_6_out), .d(or_2_out), .srn(buffer_8_out));
endmodule

module cdc_8 (
  input  [7:0] in_1,
  input  clk,
  input  arn,
  output [7:0] out_4
);

  wire and_1_out, buffer_1_out, buffer_2_out, buffer_3_out, buffer_6_out, buffer_7_out, buffer_8_out,
       not_1_out, or_1_out;
  wire [7:0] and_2_out, bit_extender_1_out, buffer_4_out, buffer_5_out, or_2_out;

  assign bit_extender_1_out = {{7{and_1_out}}, and_1_out};  // Bit_Extender bit_extender_1
  and and_1 (and_1_out, clk, not_1_out);
  not not_1 (not_1_out, clk);
  buf buffer_1 (buffer_1_out, arn);
  assign and_2_out = in_1 & bit_extender_1_out;  // AND_Gate and_2, 8 bits wide
  buf buffer_2 (buffer_2_out, and_1_out);
  buf buffer_3 (buffer_3_out, buffer_2_out);
  assign buffer_4_out = and_2_out;  // Buffer buffer_4, 8 bits wide
  assign buffer_5_out = buffer_4_out;  // Buffer buffer_5, 8 bits wide
  or or_1 (or_1_out, and_1_out, buffer_2_out, buffer_3_out);
  buf buffer_6 (buffer_6_out, or_1_out);
  buf buffer_7 (buffer_7_out, buffer_1_out);
  buf buffer_8 (buffer_8_out, buffer_7_out);
  assign or_2_out = and_2_out | buffer_4_out | buffer_5_out;  // OR_Gate or_2, 8 bits wide
  d_latch_8 d_latch_8_1 (.out_4(out_4), .d(or_2_out), .srn(buffer_8_out), .en(buffer_6_out));
endmodule

module d_latch (
  input  d,
  input  en,
  input  srn,
  output out_4
);

  wire buffer_1_out, buffer_2_out, buffer_3_out, buffer_4_out, nand_1_out, nand_2_out, nand_4_out, not_1_out;

  buf buffer_1 (buffer_1_out, d);
  buf buffer_2 (buffer_2_out, en);
  not not_1 (not_1_out, d);
  buf buffer_3 (buffer_3_out, srn);
  nand nand_1 (nand_1_out, buffer_1_out, buffer_2_out, buffer_3_out);
  nand nand_2 (nand_2_out, buffer_2_out, not_1_out);
  nand nand_3 (out_4, nand_1_out, nand_4_out);
  buf buffer_4 (buffer_4_out, out_4);
  nand nand_4 (nand_4_out, buffer_4_out, nand_2_out, buffer_3_out);
endmodule

module d_latch_8 (
  input  [7:0] d,
  input  en,
  input  srn,
  output [7:0] out_4
);

  wire [7:0] bit_extender_1_out, bit_extender_2_out, buffer_1_out, buffer_2_out, buffer_3_out, nand_1_out,
       nand_2_out, nand_4_out, not_1_out;

  assign bit_extender_1_out = {{7{srn}}, srn};  // Bit_Extender bit_extender_1
  assign buffer_1_out = d;  // Buffer buffer_1, 8 bits wide
  assign bit_extender_2_out = {{7{en}}, en};  // Bit_Extender bit_extender_2
  assign buffer_2_out = bit_extender_2_out;  // Buffer buffer_2, 8 bits wide
  assign not_1_out = ~d;  // NOT_Gate not_1, 8 bits wide
  assign nand_1_out = ~(buffer_1_out & bit_extender_1_out & buffer_2_out);  // NAND_Gate nand_1, 8 bits wide
  assign nand_2_out = ~(buffer_2_out & not_1_out);  // NAND_Gate nand_2, 8 bits wide
  assign out_4 = ~(nand_1_out & nand_4_out);  // NAND_Gate nand_3, 8 bits wide
  assign nand_4_out = ~(buffer_3_out & nand_2_out & bit_extender_1_out);  // NAND_Gate nand_4, 8 bits wide
  assign buffer_3_out = out_4;  // Buffer buffer_3, 8 bits wide
endmodule

module ROM_gate (
  input  [2:0] adr,
  output [31:0] out_2
);

  wire and_1_out, and_2_out, and_3_out, and_4_out, and_5_out, and_6_out, and_7_out, and_8_out, buffer_1_out,
       buffer_2_out, buffer_3_out, not_1_out, not_2_out, not_3_out;
  wire [31:0] and_9_out, and_10_out, and_11_out, and_12_out, and_13_out, and_14_out, and_15_out, and_16_out,
       bit_extender_1_out, bit_extender_2_out, bit_extender_3_out, bit_extender_4_out, bit_extender_5_out,
       bit_extender_6_out, bit_extender_7_out, bit_extender_8_out;

  buf buffer_1 (buffer_1_out, adr[2]);
  buf buffer_2 (buffer_2_out, adr[1]);
  not not_1 (not_1_out, adr[2]);
  not not_2 (not_2_out, adr[1]);
  buf buffer_3 (buffer_3_out, adr[0]);
  not not_3 (not_3_out, adr[0]);
  and and_1 (and_1_out, not_3_out, not_2_out, not_1_out);
  and and_2 (and_2_out, buffer_3_out, not_2_out, not_1_out);
  and and_3 (and_3_out, not_3_out, buffer_2_out, not_1_out);
  and and_4 (and_4_out, buffer_3_out, buffer_2_out, not_1_out);
  and and_5 (and_5_out, not_3_out, not_2_out, buffer_1_out);
  and and_6 (and_6_out, buffer_3_out, not_2_out, buffer_1_out);
  and and_7 (and_7_out, not_3_out, buffer_2_out, buffer_1_out);
  and and_8 (and_8_out, buffer_3_out, buffer_2_out, buffer_1_out);
  assign bit_extender_1_out = {{31{and_1_out}}, and_1_out};  // Bit_Extender bit_extender_1
  assign bit_extender_2_out = {{31{and_2_out}}, and_2_out};  // Bit_Extender bit_extender_2
  assign bit_extender_3_out = {{31{and_3_out}}, and_3_out};  // Bit_Extender bit_extender_3
  assign bit_extender_4_out = {{31{and_4_out}}, and_4_out};  // Bit_Extender bit_extender_4
  assign bit_extender_5_out = {{31{and_5_out}}, and_5_out};  // Bit_Extender bit_extender_5
  assign bit_extender_6_out = {{31{and_6_out}}, and_6_out};  // Bit_Extender bit_extender_6
  assign bit_extender_7_out = {{31{and_7_out}}, and_7_out};  // Bit_Extender bit_extender_7
  assign bit_extender_8_out = {{31{and_8_out}}, and_8_out};  // Bit_Extender bit_extender_8
  assign and_9_out = bit_extender_1_out & {32{1'b0}};  // AND_Gate and_9, 32 bits wide
  assign and_10_out = bit_extender_2_out & 32'h1;  // AND_Gate and_10, 32 bits wide
  assign and_11_out = bit_extender_3_out & 32'h2;  // AND_Gate and_11, 32 bits wide
  assign and_12_out = bit_extender_4_out & 32'h3;  // AND_Gate and_12, 32 bits wide
  assign and_13_out = bit_extender_5_out & 32'h4;  // AND_Gate and_13, 32 bits wide
  assign and_14_out = bit_extender_6_out & 32'h5;  // AND_Gate and_14, 32 bits wide
  assign and_15_out = bit_extender_7_out & 32'h6;  // AND_Gate and_15, 32 bits wide
  assign and_16_out = bit_extender_8_out & 32'h7;  // AND_Gate and_16, 32 bits wide
  assign out_2 = and_9_out | and_10_out | and_11_out | and_12_out | and_13_out | and_14_out | and_15_out | and_16_out;  // OR_Gate or_1, 32 bits wide
endmodule

module RAM_gate (
  input  d,
  input  arn,
  input  clk,
  input  [2:0] rd_adr,
  input  we,
  input  [2:0] wr_adr,
  output rd_dat
);

  wire buffer_1_out, not_1_out;
  wire [7:0] demultiplexer_1_out0, ram_bit_1_q;

  Demultiplexer #(.select(3)) demultiplexer_1 (
    .out0(demultiplexer_1_out0[0]), .out1(demultiplexer_1_out0[1]), .out2(demultiplexer_1_out0[2]),
    .out3(demultiplexer_1_out0[3]), .out4(demultiplexer_1_out0[4]), .out5(demultiplexer_1_out0[5]),
    .out6(demultiplexer_1_out0[6]), .out7(demultiplexer_1_out0[7]), .in(we), .sel(wr_adr));
  buf buffer_1 (buffer_1_out, d);
  not not_1 (not_1_out, d);
  ram_bit ram_bit_1 (
    .q(ram_bit_1_q[0]), .d(buffer_1_out), .ena(demultiplexer_1_out0[0]), .dn(not_1_out), .arn(arn), .clk(clk));
  ram_bit ram_bit_2 (
    .q(ram_bit_1_q[1]), .d(buffer_1_out), .ena(demultiplexer_1_out0[1]), .dn(not_1_out), .arn(arn), .clk(clk));
  ram_bit ram_bit_3 (
    .q(ram_bit_1_q[2]), .d(buffer_1_out), .ena(demultiplexer_1_out0[2]), .dn(not_1_out), .arn(arn), .clk(clk));
  ram_bit ram_bit_4 (
    .q(ram_bit_1_q[3]), .d(buffer_1_out), .ena(demultiplexer_1_out0[3]), .dn(not_1_out), .arn(arn), .clk(clk));
  ram_bit ram_bit_5 (
    .q(ram_bit_1_q[4]), .d(buffer_1_out), .ena(demultiplexer_1_out0[4]), .dn(not_1_out), .arn(arn), .clk(clk));
  ram_bit ram_bit_6 (
    .q(ram_bit_1_q[5]), .d(buffer_1_out), .ena(demultiplexer_1_out0[5]), .dn(not_1_out), .arn(arn), .clk(clk));
  ram_bit ram_bit_7 (
    .q(ram_bit_1_q[6]), .d(buffer_1_out), .ena(demultiplexer_1_out0[6]), .dn(not_1_out), .arn(arn), .clk(clk));
  ram_bit ram_bit_8 (
    .q(ram_bit_1_q[7]), .d(buffer_1_out), .ena(demultiplexer_1_out0[7]), .dn(not_1_out), .arn(arn), .clk(clk));
  Multiplexer #(.select(3)) multiplexer_1 (
    .in0(ram_bit_1_q[0]), .in1(ram_bit_1_q[1]), .in2(ram_bit_1_q[2]), .in3(ram_bit_1_q[3]),
    .in4(ram_bit_1_q[4]), .in5(ram_bit_1_q[5]), .in6(ram_bit_1_q[6]), .in7(ram_bit_1_q[7]), .out(rd_dat),
    .sel(rd_adr));
endmodule

module ram_bit (
  input  d,
  input  ena,
  input  clk,
  input  dn,
  input  arn,
  output q
);

  wire buffer_1_out, nand_1_out, nand_2_out, nand_4_out;

  nand nand_1 (nand_1_out, d, ena, clk);
  nand nand_2 (nand_2_out, clk, ena, dn);
  nand nand_3 (q, nand_1_out, buffer_1_out);
  buf buffer_1 (buffer_1_out, nand_4_out);
  nand nand_4 (nand_4_out, q, arn, nand_2_out);
endmodule

module dmux_8 (
  input  en,
  input  [2:0] sel,
  output out_3,
  output out_4,
  output out_5,
  output out_6,
  output out_7,
  output out_8,
  output out_9,
  output out_10
);

  wire [2:0] buffer_3_out, not_3_out;

  buf buffer_1 (buffer_3_out[2], sel[2]);
  buf buffer_2 (buffer_3_out[1], sel[1]);
  buf buffer_3 (buffer_3_out[0], sel[0]);
  not not_1 (not_3_out[2], sel[2]);
  not not_2 (not_3_out[1], sel[1]);
  not not_3 (not_3_out[0], sel[0]);
  and and_1 (out_3, not_3_out[0], not_3_out[1], not_3_out[2], en);
  and and_2 (out_4, buffer_3_out[0], not_3_out[1], not_3_out[2], en);
  and and_3 (out_5, not_3_out[0], buffer_3_out[1], not_3_out[2], en);
  and and_4 (out_6, buffer_3_out[0], buffer_3_out[1], not_3_out[2], en);
  and and_5 (out_7, not_3_out[0], not_3_out[1], buffer_3_out[2], en);
  and and_6 (out_8, buffer_3_out[0], not_3_out[1], buffer_3_out[2], en);
  and and_7 (out_9, not_3_out[0], buffer_3_out[1], buffer_3_out[2], en);
  and and_8 (out_10, buffer_3_out[0], buffer_3_out[1], buffer_3_out[2], en);
endmodule
