// Logisim project M3.circ as structural Verilog: 48 circuits, main circuit main
module main (
  input  srn
);

  wire clk, clk_out, csn, data_ram_we, dbg, dbg_break_out, dbg_clk_out, dbg_run_out, ebreak, ext_intr_out,
       gpio_we, m1a_led_1_led0, m1a_led_1_led1, m1a_led_1_led2, m1a_led_1_led3, m1a_led_1_led4,
       m1a_led_1_led5, m1a_led_1_led6, m1a_led_1_led7, m2d_cpu_1_ram_re, m2d_cpu_1_ram_we, matrix_we,
       or_1_out;
  wire [3:0] data_ram_be, gpio_be, m2b_matrix_1_dbg_pos, m2b_matrix_1_dbg_pos_2, m2d_cpu_1_ram_be,
       m2d_cpu_1_scause, matrix_be;
  wire [7:0] Data_RAM_p1, m2b_matrix_1_sync_cnt, up_out;
  wire [15:0] decoder_1_out15, decoder_2_out0, m2b_matrix_1_line0, m2b_matrix_1_line1, m2b_matrix_1_line2,
       m2b_matrix_1_line3, m2b_matrix_1_line4, m2b_matrix_1_line5, m2b_matrix_1_line6, m2b_matrix_1_line7,
       m2b_matrix_1_line8, m2b_matrix_1_line9, m2b_matrix_1_line10, m2b_matrix_1_line11, m2b_matrix_1_line12,
       m2b_matrix_1_line13, m2b_matrix_1_line14, m2b_matrix_1_line15;
  wire [31:0] data_ram_adr, data_ram_din, data_ram_dout, data_rom_adr, data_rom_dout, gpio_adr, gpio_din,
       key_dout, m2a_bus_interconnect_1_ram_dout, m2d_cpu_1_ram_adr, m2d_cpu_1_ram_din, m2d_cpu_1_sepc,
       matrix_adr, matrix_din, matrix_dout, rom_adr, rom_dout;

  Button ext_intr (.out(ext_intr_out));
  Clock u_clk (.out(clk_out));
  Button dbg_clk (.out(dbg_clk_out));
  Button dbg_run (.out(dbg_run_out));
  Button dbg_break (.out(dbg_break_out));
  ROM #(.addrWidth(7), .dataWidth(32)) rom_1 (.addr(rom_adr[8:2]), .data(rom_dout));
  Multiplexer multiplexer_1 (.in0(clk_out), .in1(dbg_clk_out), .out(clk), .sel(dbg));
  or or_1 (or_1_out, dbg_break_out, ebreak);
  M2D_CPU m2d_cpu_1 (
    .rom_adr(rom_adr), .ram_adr(m2d_cpu_1_ram_adr), .ram_re(m2d_cpu_1_ram_re), .ram_we(m2d_cpu_1_ram_we),
    .ram_be(m2d_cpu_1_ram_be), .ram_din(m2d_cpu_1_ram_din), .SCAUSE(m2d_cpu_1_scause), .SEPC(m2d_cpu_1_sepc),
    .ebreak(ebreak), .rom_dout(rom_dout), .ram_dout(m2a_bus_interconnect_1_ram_dout),
    .ext_intr(ext_intr_out), .clk(clk), .srn(srn));
  // Probe on m2d_cpu_1_sepc
  // Probe on m2d_cpu_1_scause
  M2A_rs_latch m2a_rs_latch_1 (.q(dbg), .r(dbg_run_out), .rn(srn), .s(or_1_out));
  // Probe on m2d_cpu_1_ram_adr
  // Probe on m2d_cpu_1_ram_we
  // Probe on m2d_cpu_1_ram_be
  // Probe on m2d_cpu_1_ram_din
  // Probe on m2a_bus_interconnect_1_ram_dout
  M2A_bus_interconnect m2a_bus_interconnect_1 (
    .s0_we(data_ram_we), .s2_we(matrix_we), .s3_we(gpio_we), .ram_dout(m2a_bus_interconnect_1_ram_dout),
    .s0_adr(data_ram_adr), .s1_adr(data_rom_adr), .s2_adr(matrix_adr), .s3_adr(gpio_adr),
    .s0_be(data_ram_be), .s2_be(matrix_be), .s3_be(gpio_be), .s0_din(data_ram_din), .s2_din(matrix_din),
    .s3_din(gpio_din), .s0_dout(data_ram_dout), .s1_dout(data_rom_dout), .s2_dout(matrix_dout),
    .s3_dout(key_dout), .ram_adr(m2d_cpu_1_ram_adr), .ram_we(m2d_cpu_1_ram_we), .ram_be(m2d_cpu_1_ram_be),
    .ram_din(m2d_cpu_1_ram_din), .ram_re(m2d_cpu_1_ram_re));  // open: s1_we, s1_be, s1_din
  // RAM #(.enables("line"), .line("quad"), .misaligned("true")) Data_RAM: pin names not known; wires that end beside it: Data_RAM_p1, data_ram_we, clk
  BitSelector #(.group(8), .width(32)) bitselector_1 (.in(data_ram_adr), .out(Data_RAM_p1), .sel(2'b00));
  // ROM #(.line("quad")) Data_ROM: pin names not known; wires that end beside it: data_rom_adr[7:0]
  Decoder #(.select(4)) decoder_1 (
    .out0(decoder_1_out15[15]), .out1(decoder_1_out15[14]), .out2(decoder_1_out15[13]),
    .out3(decoder_1_out15[12]), .out4(decoder_1_out15[11]), .out5(decoder_1_out15[10]),
    .out6(decoder_1_out15[9]), .out7(decoder_1_out15[8]), .out8(decoder_1_out15[7]),
    .out9(decoder_1_out15[6]), .out10(decoder_1_out15[5]), .out11(decoder_1_out15[4]),
    .out12(decoder_1_out15[3]), .out13(decoder_1_out15[2]), .out14(decoder_1_out15[1]),
    .out15(decoder_1_out15[0]), .sel(m2b_matrix_1_dbg_pos_2));  // open: en
  M2B_matrix m2b_matrix_1 (
    .dbg_pos({m2b_matrix_1_dbg_pos_2, m2b_matrix_1_dbg_pos}), .line0(m2b_matrix_1_line0),
    .line1(m2b_matrix_1_line1), .line2(m2b_matrix_1_line2), .line3(m2b_matrix_1_line3),
    .line4(m2b_matrix_1_line4), .line5(m2b_matrix_1_line5), .line6(m2b_matrix_1_line6),
    .line7(m2b_matrix_1_line7), .line8(m2b_matrix_1_line8), .line9(m2b_matrix_1_line9),
    .line10(m2b_matrix_1_line10), .line11(m2b_matrix_1_line11), .line12(m2b_matrix_1_line12),
    .line13(m2b_matrix_1_line13), .line14(m2b_matrix_1_line14), .line15(m2b_matrix_1_line15),
    .ram_dout(matrix_dout), .sync_cnt(m2b_matrix_1_sync_cnt), .ram_we(matrix_we), .clk(clk), .srn(srn),
    .ram_be(matrix_be), .ram_adr(matrix_adr), .ram_din(matrix_din));
  // Probe on {m2b_matrix_1_dbg_pos_2, m2b_matrix_1_dbg_pos}
  // Probe on m2b_matrix_1_sync_cnt
  Decoder #(.select(4)) decoder_2 (
    .out0(decoder_2_out0[0]), .out1(decoder_2_out0[1]), .out2(decoder_2_out0[2]), .out3(decoder_2_out0[3]),
    .out4(decoder_2_out0[4]), .out5(decoder_2_out0[5]), .out6(decoder_2_out0[6]), .out7(decoder_2_out0[7]),
    .out8(decoder_2_out0[8]), .out9(decoder_2_out0[9]), .out10(decoder_2_out0[10]),
    .out11(decoder_2_out0[11]), .out12(decoder_2_out0[12]), .out13(decoder_2_out0[13]),
    .out14(decoder_2_out0[14]), .out15(decoder_2_out0[15]), .sel(m2b_matrix_1_dbg_pos));  // open: en
  DotMatrix #(.inputtype("row"), .matrixcols(16), .matrixrows(16)) dotmatrix_1 (
    .row0(m2b_matrix_1_line0), .row1(m2b_matrix_1_line1), .row2(m2b_matrix_1_line2),
    .row3(m2b_matrix_1_line3), .row4(m2b_matrix_1_line4), .row5(m2b_matrix_1_line5),
    .row6(m2b_matrix_1_line6), .row7(m2b_matrix_1_line7), .row8(m2b_matrix_1_line8),
    .row9(m2b_matrix_1_line9), .row10(m2b_matrix_1_line10), .row11(m2b_matrix_1_line11),
    .row12(m2b_matrix_1_line12), .row13(m2b_matrix_1_line13), .row14(m2b_matrix_1_line14),
    .row15(m2b_matrix_1_line15));
  // DotMatrix #(.inputtype("select"), .matrixcols(16), .matrixrows(16)) dotmatrix_2: pin names not known; wires that end beside it: decoder_2_out0, decoder_1_out15
  Button up (.out(up_out[0]));
  Button left (.out(up_out[2]));
  Button down (.out(up_out[1]));
  // Probe on key_dout
  M2A_key m2a_key_1 (
    .key_out(key_dout), .csn(csn), .up(up_out[0]), .down(up_out[1]), .left(up_out[2]), .right(up_out[3]),
    .x(up_out[4]), .y(up_out[5]), .ok(up_out[6]), .esc(up_out[7]), .clk(clk), .srn(srn));
  BitSelector #(.width(32)) bitselector_2 (.in(gpio_adr), .out(csn), .sel(5'b00010));
  Button right (.out(up_out[3]));
  Button esc (.out(up_out[7]));
  LED led_1 (.in(m1a_led_1_led0));
  M1A_led m1a_led_1 (
    .led0(m1a_led_1_led0), .led1(m1a_led_1_led1), .led2(m1a_led_1_led2), .led3(m1a_led_1_led3),
    .led4(m1a_led_1_led4), .led5(m1a_led_1_led5), .led6(m1a_led_1_led6), .led7(m1a_led_1_led7),
    .led_we(gpio_we), .clk(clk), .srn(srn), .led_be(gpio_be), .led_din(gpio_din));
  LED initializing (.in(m1a_led_1_led1));
  LED paused (.in(m1a_led_1_led2));
  LED running (.in(m1a_led_1_led3));
  LED reading_key (.in(m1a_led_1_led4));
  LED rendering (.in(m1a_led_1_led5));
  LED vsync (.in(m1a_led_1_led6));
  LED dead (.in(m1a_led_1_led7));
  Button Y (.out(up_out[5]));
  Button ok (.out(up_out[6]));
  Button X (.out(up_out[4]));

  // Notes on the sheet:
  //   0x0000_0000 ~ 0x0000_01FF
  //   contents of rom_1 (hex, n*v repeats v):
  //   80000137 c00001b7 1237 10000293 313 100393 fff00413 820023 100413 8200a3 fef00413 820123 ff000413
  //   8201a3 ff100413 820223 f00413 8202a3 1000413 820323 1100413 8203a3 2020413 fff40413 40823 440463
  //   ff5ff06f 1020493 100413 8481a3 848523 8485a3 2020493 ff000413 8480a3 848223 8483a3 1000413 848423
  //   848523 8486a3 10000437 100100a3 6404b3 4c783 10f10023 130313 530463 fedff06f 90000ef 720493 693
  //   244ca63 4c403 830533 130413 f47413 200593 4b46663 ff57513 250533 54703 e686b3 fff48493 fd1ff06f
  //   610533 54603 361613 d60633 460633 1060613 64603 10c10023 130313 fa5340e3 28000ef f99ff06f 341413
  //   940433 f47413 440433 2040413 40403 850533 f9dff06f 313 10710123 8067
  //   Instrunction ROM Address Range:
  //   Data RAM Address Range:
  //   Data ROM Address Range:
  //   contents of Data_ROM (hex, n*v repeats v):
  //   156*0 1 1 1 11*0 1 15*0 1 15*0 1
  //   0x0000_1000 ~ 0x0000_10FF
  //   0x1000_0000 ~ 0x1000_00FF
  //   Matrix Address Range:
  //   0x8000_0000 ~ 0x8000_01FF
  //   当前光标位置
  //   GPIO Address Range:
  //   0xC000_0000 ~ 0xC000_00007
endmodule

module M2A_rs_latch (
  input  r,
  input  rn,
  input  s,
  output q
);

  wire buffer_1_out, nor_1_out, not_1_out;

  not not_1 (not_1_out, rn);
  buf buffer_1 (buffer_1_out, nor_1_out);
  nor nor_1 (nor_1_out, q, s);
  nor nor_2 (q, r, not_1_out, buffer_1_out);
endmodule

module M1A_reg32 (
  input  [31:0] d,
  input  we,
  input  srn,
  input  clk,
  output [31:0] q
);

  wire [31:0] multiplexer_1_out;

  Multiplexer #(.width(32)) multiplexer_1 (.in0({32{1'b0}}), .in1(d), .out(multiplexer_1_out), .sel(srn));
  Register #(.width(32)) register_1 (.D(multiplexer_1_out), .en(we), .clk(clk), .Q(q));  // open: clr
endmodule

module M2A_pc_nxt (
  input  [31:0] intr_adr,
  input  intr,
  input  [31:0] jump_adr,
  input  jump,
  input  [31:0] pc,
  input  stall_n,
  input  pred,
  input  [31:0] pred_adr,
  output [31:0] nxt
);

  wire and_1_out, and_2_out, and_3_out, and_4_out, not_1_out, not_2_out, not_3_out, not_4_out, not_5_out,
       not_6_out, not_7_out, not_8_out, not_9_out;
  wire [31:0] and_5_out, and_6_out, and_7_out, and_8_out, and_9_out, bit_extender_1_out, bit_extender_2_out,
       bit_extender_3_out, bit_extender_4_out, bit_extender_5_out, m2_incr4_32_1_o;

  not not_1 (not_1_out, intr);
  and and_1 (and_1_out, not_1_out, jump);
  not not_2 (not_2_out, intr);
  not not_3 (not_3_out, jump);
  and and_2 (and_2_out, not_2_out, not_3_out, not_4_out);
  not not_4 (not_4_out, stall_n);
  not not_5 (not_5_out, intr);
  not not_6 (not_6_out, jump);
  and and_3 (and_3_out, not_5_out, not_6_out, stall_n, not_7_out);
  not not_7 (not_7_out, pred);
  not not_8 (not_8_out, intr);
  not not_9 (not_9_out, jump);
  and and_4 (and_4_out, not_8_out, not_9_out, stall_n, pred);
  assign bit_extender_1_out = {{31{intr}}, intr};  // Bit_Extender bit_extender_1
  assign bit_extender_2_out = {{31{and_1_out}}, and_1_out};  // Bit_Extender bit_extender_2
  assign bit_extender_3_out = {{31{and_2_out}}, and_2_out};  // Bit_Extender bit_extender_3
  assign bit_extender_4_out = {{31{and_3_out}}, and_3_out};  // Bit_Extender bit_extender_4
  assign bit_extender_5_out = {{31{and_4_out}}, and_4_out};  // Bit_Extender bit_extender_5
  M2_incr4_32 m2_incr4_32_1 (.o(m2_incr4_32_1_o), .i(pc));
  assign and_5_out = intr_adr & bit_extender_1_out;  // AND_Gate and_5, 32 bits wide
  assign and_6_out = jump_adr & bit_extender_2_out;  // AND_Gate and_6, 32 bits wide
  assign and_7_out = pc & bit_extender_3_out;  // AND_Gate and_7, 32 bits wide
  assign and_8_out = m2_incr4_32_1_o & bit_extender_4_out;  // AND_Gate and_8, 32 bits wide
  assign and_9_out = pred_adr & bit_extender_5_out;  // AND_Gate and_9, 32 bits wide
  assign nxt = and_5_out | and_6_out | and_7_out | and_8_out | and_9_out;  // OR_Gate or_1, 32 bits wide
endmodule

module M2A_bj_type (
  input  [31:0] instr,
  output is_branch,
  output is_jal,
  output is_jalr
);

  wire not_1_out, not_2_out, not_3_out, not_4_out, not_5_out, not_6_out;
  wire [6:0] bitselector_1_out;

  BitSelector #(.group(7), .width(32)) bitselector_1 (.in(instr), .out(bitselector_1_out), .sel(3'b000));
  not not_1 (not_1_out, bitselector_1_out[2]);
  not not_2 (not_2_out, bitselector_1_out[3]);
  not not_3 (not_3_out, bitselector_1_out[4]);
  not not_4 (not_4_out, bitselector_1_out[4]);
  not not_5 (not_5_out, bitselector_1_out[3]);
  not not_6 (not_6_out, bitselector_1_out[4]);
  and and_1 (is_branch, bitselector_1_out[0], bitselector_1_out[1], not_1_out, not_2_out, not_3_out, bitselector_1_out[5], bitselector_1_out[6]);
  and and_2 (is_jal, bitselector_1_out[0], bitselector_1_out[1], bitselector_1_out[2], bitselector_1_out[3], not_4_out, bitselector_1_out[5], bitselector_1_out[6]);
  and and_3 (is_jalr, bitselector_1_out[0], bitselector_1_out[1], bitselector_1_out[2], not_5_out, not_6_out, bitselector_1_out[5], bitselector_1_out[6]);

  // Notes on the sheet:
  //   Branch：1100011 
  //   jal：1101111
  //   jalr：1100111
endmodule

module M2B_IF (
  input  [31:0] pred_adr,
  input  [31:0] jump_adr,
  input  [31:0] intr_adr,
  input  stall_n,
  input  pred,
  input  jump,
  input  intr,
  input  pc_we,
  input  pc_srn,
  input  clk,
  input  [31:0] rom_dout,
  output [31:0] pc,
  output [31:0] rom_adr,
  output is_ecall,
  output is_ebreak,
  output [31:0] instr,
  output is_branch,
  output is_jal,
  output is_jalr
);

  wire env, funct3_0, funct7_0, not_1_out, not_2_out, not_3_out, not_4_out, not_5_out, not_6_out, not_7_out,
       not_8_out, not_9_out, not_10_out, not_11_out, not_12_out, not_13_out, not_14_out, not_15_out,
       not_16_out, not_17_out, not_18_out, not_19_out, not_20_out, not_21_out, rs2_0, rs2_1;
  wire [31:0] m2a_pc_nxt_1_nxt;

  // Probe on m2a_pc_nxt_1_nxt
  M2A_pc_nxt m2a_pc_nxt_1 (
    .nxt(m2a_pc_nxt_1_nxt), .intr(intr), .jump(jump), .stall_n(stall_n), .pred(pred), .intr_adr(intr_adr),
    .jump_adr(jump_adr), .pc(pc), .pred_adr(pred_adr));
  M2A_bj_type m2a_bj_type_1 (.is_branch(is_branch), .is_jal(is_jal), .is_jalr(is_jalr), .instr(rom_dout));
  M1A_reg32 m1a_reg32_1 (.q(pc), .srn(pc_srn), .d(m2a_pc_nxt_1_nxt), .we(pc_we), .clk(clk));
  not not_1 (not_1_out, rom_dout[2]);
  not not_2 (not_2_out, rom_dout[3]);
  not not_3 (not_3_out, rom_dout[12]);
  not not_4 (not_4_out, rom_dout[13]);
  not not_5 (not_5_out, rom_dout[14]);
  not not_6 (not_6_out, rom_dout[20]);
  not not_7 (not_7_out, rom_dout[21]);
  not not_8 (not_8_out, rom_dout[22]);
  not not_9 (not_9_out, rom_dout[23]);
  not not_10 (not_10_out, rom_dout[24]);
  not not_11 (not_11_out, rom_dout[21]);
  not not_12 (not_12_out, rom_dout[22]);
  not not_13 (not_13_out, rom_dout[23]);
  not not_14 (not_14_out, rom_dout[24]);
  not not_15 (not_15_out, rom_dout[25]);
  not not_16 (not_16_out, rom_dout[26]);
  not not_17 (not_17_out, rom_dout[27]);
  not not_18 (not_18_out, rom_dout[28]);
  not not_19 (not_19_out, rom_dout[29]);
  not not_20 (not_20_out, rom_dout[30]);
  not not_21 (not_21_out, rom_dout[31]);
  and and_1 (env, rom_dout[0], rom_dout[1], not_1_out, not_2_out, rom_dout[4], rom_dout[5], rom_dout[6]);
  and and_2 (funct3_0, not_3_out, not_4_out, not_5_out);
  and and_3 (rs2_0, not_6_out, not_7_out, not_8_out, not_9_out, not_10_out);
  and and_4 (rs2_1, rom_dout[20], not_11_out, not_12_out, not_13_out, not_14_out);
  and and_5 (funct7_0, not_15_out, not_16_out, not_17_out, not_18_out, not_19_out, not_20_out, not_21_out);
  and and_6 (is_ecall, env, funct3_0, funct7_0, rs2_0);
  and and_7 (is_ebreak, env, funct3_0, funct7_0, rs2_1);

  assign instr = rom_dout;
  assign rom_adr = pc;

  // Other names for the same wires on the sheet: opcode[6:0] = rom_dout[6:0]; rd[4:0] = rom_dout[11:7];
  //   funct3[2:0] = rom_dout[14:12]; rs1[4:0] = rom_dout[19:15]; rs2[4:0] = rom_dout[24:20];
  //   funct7[6:0] = rom_dout[31:25]

  // Notes on the sheet:
  //   opcode = 1110011
endmodule

module M1A_reg_file (
  input  [31:0] rd_data,
  input  srn,
  input  rd_we,
  input  [4:0] rd_sel,
  input  clk,
  input  [4:0] rs1_sel,
  input  [4:0] rs2_sel,
  output [31:0] rs1,
  output [31:0] rs2
);

  wire demultiplexer_1_out16, demultiplexer_1_out17, demultiplexer_1_out18, demultiplexer_1_out19,
       demultiplexer_1_out20, demultiplexer_1_out21, demultiplexer_1_out22, demultiplexer_1_out23,
       demultiplexer_1_out24, demultiplexer_1_out25, demultiplexer_1_out26, demultiplexer_1_out27,
       demultiplexer_1_out28, demultiplexer_1_out29, demultiplexer_1_out30, demultiplexer_1_out31, w0, w1,
       w2, w3, w4, w5, w6, w7, w8, w9, w10, w11, w12, w13, w14, w15;
  wire [15:0] bit_extender_1_out, demultiplexer_1_out0;
  wire [31:0] multiplexer_1_out, x1, x2, x3, x4, x5, x6, x7, x8, x9, x10, x11, x12, x13, x14, x15;

  Demultiplexer #(.select(5)) demultiplexer_1 (
    .out0(demultiplexer_1_out0[0]), .out1(demultiplexer_1_out0[1]), .out2(demultiplexer_1_out0[2]),
    .out3(demultiplexer_1_out0[3]), .out4(demultiplexer_1_out0[4]), .out5(demultiplexer_1_out0[5]),
    .out6(demultiplexer_1_out0[6]), .out7(demultiplexer_1_out0[7]), .out8(demultiplexer_1_out0[8]),
    .out9(demultiplexer_1_out0[9]), .out10(demultiplexer_1_out0[10]), .out11(demultiplexer_1_out0[11]),
    .out12(demultiplexer_1_out0[12]), .out13(demultiplexer_1_out0[13]), .out14(demultiplexer_1_out0[14]),
    .out15(demultiplexer_1_out0[15]), .out16(demultiplexer_1_out16), .out17(demultiplexer_1_out17),
    .out18(demultiplexer_1_out18), .out19(demultiplexer_1_out19), .out20(demultiplexer_1_out20),
    .out21(demultiplexer_1_out21), .out22(demultiplexer_1_out22), .out23(demultiplexer_1_out23),
    .out24(demultiplexer_1_out24), .out25(demultiplexer_1_out25), .out26(demultiplexer_1_out26),
    .out27(demultiplexer_1_out27), .out28(demultiplexer_1_out28), .out29(demultiplexer_1_out29),
    .out30(demultiplexer_1_out30), .out31(demultiplexer_1_out31), .in(rd_we), .sel(rd_sel));
  assign bit_extender_1_out = {{15{srn}}, srn};  // Bit_Extender bit_extender_1
  Multiplexer #(.width(32)) multiplexer_1 (.in0({32{1'b0}}), .in1(rd_data), .out(multiplexer_1_out), .sel(srn));
  assign {w15, w14, w13, w12, w11, w10, w9, w8, w7, w6, w5, w4, w3, w2, w1, w0} = ~bit_extender_1_out | demultiplexer_1_out0;  // OR_Gate or_1, 16 bits wide
  // NoConnect on w0
  Register #(.width(32)) register_1 (.D(multiplexer_1_out), .en(w1), .clk(clk), .Q(x1));  // open: clr
  Register #(.width(32)) register_2 (.D(multiplexer_1_out), .en(w2), .clk(clk), .Q(x2));  // open: clr
  Register #(.width(32)) register_3 (.D(multiplexer_1_out), .en(w3), .clk(clk), .Q(x3));  // open: clr
  Register #(.width(32)) register_4 (.D(multiplexer_1_out), .en(w4), .clk(clk), .Q(x4));  // open: clr
  Register #(.width(32)) register_5 (.D(multiplexer_1_out), .en(w5), .clk(clk), .Q(x5));  // open: clr
  Register #(.width(32)) register_6 (.D(multiplexer_1_out), .en(w6), .clk(clk), .Q(x6));  // open: clr
  Register #(.width(32)) register_7 (.D(multiplexer_1_out), .en(w7), .clk(clk), .Q(x7));  // open: clr
  Register #(.width(32)) register_8 (.D(multiplexer_1_out), .en(w8), .clk(clk), .Q(x8));  // open: clr
  Register #(.width(32)) register_9 (.D(multiplexer_1_out), .en(w9), .clk(clk), .Q(x9));  // open: clr
  Register #(.width(32)) register_10 (.D(multiplexer_1_out), .en(w10), .clk(clk), .Q(x10));  // open: clr
  Register #(.width(32)) register_11 (.D(multiplexer_1_out), .en(w11), .clk(clk), .Q(x11));  // open: clr
  Register #(.width(32)) register_12 (.D(multiplexer_1_out), .en(w12), .clk(clk), .Q(x12));  // open: clr
  Register #(.width(32)) register_13 (.D(multiplexer_1_out), .en(w13), .clk(clk), .Q(x13));  // open: clr
  Register #(.width(32)) register_14 (.D(multiplexer_1_out), .en(w14), .clk(clk), .Q(x14));  // open: clr
  Register #(.width(32)) register_15 (.D(multiplexer_1_out), .en(w15), .clk(clk), .Q(x15));  // open: clr
  Multiplexer #(.select(4), .width(32)) multiplexer_2 (
    .in0({32{1'b0}}), .in1(x1), .in2(x2), .in3(x3), .in4(x4), .in5(x5), .in6(x6), .in7(x7), .in8(x8),
    .in9(x9), .in10(x10), .in11(x11), .in12(x12), .in13(x13), .in14(x14), .in15(x15), .out(rs1),
    .sel(rs1_sel[3:0]));
  Multiplexer #(.select(4), .width(32)) multiplexer_3 (
    .in0({32{1'b0}}), .in1(x1), .in2(x2), .in3(x3), .in4(x4), .in5(x5), .in6(x6), .in7(x7), .in8(x8),
    .in9(x9), .in10(x10), .in11(x11), .in12(x12), .in13(x13), .in14(x14), .in15(x15), .out(rs2),
    .sel(rs2_sel[3:0]));
endmodule

module M2A_imm_gen (
  input  [31:0] instr,
  output [31:0] imm_I,
  output [31:0] imm_S,
  output [31:0] imm_B,
  output [31:0] imm_U,
  output [31:0] imm_J
);

  assign imm_I = {{20{instr[31]}}, instr[31:20]};  // Bit_Extender bit_extender_1
  assign imm_S = {{20{instr[31]}}, {instr[31:25], instr[11:7]}};  // Bit_Extender bit_extender_2
  assign imm_B = {{19{instr[31]}}, {instr[31], instr[7], instr[30:25], instr[11:8], 1'b0}};  // Bit_Extender bit_extender_3
  assign imm_J = {{11{instr[31]}}, {instr[31], instr[19:12], instr[20], instr[30:21], 1'b0}};  // Bit_Extender bit_extender_4

  assign imm_U = {instr[31:12], {12{1'b0}}};

  // Notes on the sheet:
  //   I-type: code[31:20] = imm[11:0]
  //   S-type: code[31:25] = imm[11:5], code[11:7]=imm[4:0]
  //   U-type: code[31:12] = imm[31:12]
  //   J-type: code[31:25] = imm[20|10:1|11|19:12]
  //   B-type: code[31:25] = imm[12|10:5], code[11:7]=imm[4:1|11]
endmodule

module M2A_decoder (
  input  [31:0] instr,
  input  is_branch,
  input  is_jal,
  input  is_jalr,
  output [7:0] ID_ctrl,
  output [7:0] EX_ctrl,
  output [7:0] MEM_ctrl,
  output [7:0] WB_ctrl,
  output unknown,
  output [4:0] rs1_sel,
  output [4:0] rs2_sel
);

  wire bitselector_1_out, code_auipc, code_ecall, code_imm, not_1_out, not_2_out, not_3_out, not_4_out,
       not_5_out, not_6_out, not_7_out, not_8_out, not_9_out, not_10_out, not_11_out, not_12_out, not_13_out,
       not_14_out, not_15_out, not_16_out, not_17_out, not_18_out, not_19_out, not_20_out, not_21_out,
       not_22_out, not_23_out, or_1_out, zero;
  wire [2:0] bit_extender_1_out;

  not not_1 (not_1_out, instr[2]);
  not not_2 (not_2_out, instr[3]);
  not not_3 (not_3_out, instr[6]);
  not not_4 (not_4_out, instr[2]);
  not not_5 (not_5_out, instr[3]);
  not not_6 (not_6_out, instr[5]);
  not not_7 (not_7_out, instr[6]);
  not not_8 (not_8_out, instr[2]);
  not not_9 (not_9_out, instr[3]);
  not not_10 (not_10_out, instr[4]);
  not not_11 (not_11_out, instr[5]);
  not not_12 (not_12_out, instr[6]);
  not not_13 (not_13_out, instr[2]);
  not not_14 (not_14_out, instr[3]);
  not not_15 (not_15_out, instr[4]);
  not not_16 (not_16_out, instr[6]);
  not not_17 (not_17_out, instr[3]);
  not not_18 (not_18_out, instr[6]);
  not not_19 (not_19_out, instr[3]);
  not not_20 (not_20_out, instr[5]);
  not not_21 (not_21_out, instr[6]);
  not not_22 (not_22_out, instr[2]);
  not not_23 (not_23_out, instr[3]);
  and and_1 (ID_ctrl[7], instr[0], instr[1], not_1_out, not_2_out, instr[4], instr[5], not_3_out);
  and and_2 (code_imm, instr[0], instr[1], not_4_out, not_5_out, instr[4], not_6_out, not_7_out);
  and and_3 (WB_ctrl[6], instr[0], instr[1], not_8_out, not_9_out, not_10_out, not_11_out, not_12_out);
  and and_4 (ID_ctrl[1], instr[0], instr[1], not_13_out, not_14_out, not_15_out, instr[5], not_16_out);
  and and_5 (ID_ctrl[6], instr[0], instr[1], instr[2], not_17_out, instr[4], instr[5], not_18_out);
  and and_6 (code_auipc, instr[0], instr[1], instr[2], not_19_out, instr[4], not_20_out, not_21_out);
  and and_7 (code_ecall, instr[0], instr[1], not_22_out, not_23_out, instr[4], instr[5], instr[6]);
  nor nor_1 (unknown, ID_ctrl[7], code_imm, WB_ctrl[6], ID_ctrl[1], ID_ctrl[6], zero, code_auipc, code_ecall, is_branch, is_jal, is_jalr);
  M2_is_equal_32 m2_is_equal_32_1 (.E(zero), .A(instr), .B({32{1'b0}}));
  or or_1 (or_1_out, ID_ctrl[7], code_imm);
  or or_2 (ID_ctrl[0], code_imm, WB_ctrl[6], is_jalr);
  or or_3 (ID_ctrl[3], ID_ctrl[6], code_auipc);
  or or_4 (ID_ctrl[5], is_branch, is_jal, code_auipc);
  BitSelector #(.width(7)) bitselector_1 (.in(instr[31:25]), .out(bitselector_1_out), .sel(3'b101));
  assign bit_extender_1_out = {{2{or_1_out}}, or_1_out};  // Bit_Extender bit_extender_1
  or or_5 (MEM_ctrl[0], instr[12], instr[13]);
  not not_24 (MEM_ctrl[2], instr[14]);
  and and_8 (EX_ctrl[3], bitselector_1_out, ID_ctrl[7]);
  assign EX_ctrl[2:0] = bit_extender_1_out & instr[14:12];  // AND_Gate and_9, 3 bits wide
  or or_6 (WB_ctrl[5], WB_ctrl[6], ID_ctrl[7], code_imm, is_jal, is_jalr, ID_ctrl[6], code_auipc);

  assign EX_ctrl[6:4] = instr[14:12];
  assign {ID_ctrl[4], ID_ctrl[2]} = {is_jal, is_branch};
  assign {MEM_ctrl[6:3], MEM_ctrl[1]} = {is_jalr, is_jal, is_branch, ID_ctrl[1], instr[13]};
  assign rs1_sel = instr[19:15];
  assign rs2_sel = instr[24:20];
  assign WB_ctrl[4:0] = instr[11:7];

  // Other names for the same wires on the sheet: alu_op[2:0] = EX_ctrl[2:0]; alu_neg = EX_ctrl[3];
  //   bcu_op[2:0] = instr[14:12]; funct3[2:0] = instr[14:12]; FMT_I = ID_ctrl[0]; FMT_U = ID_ctrl[3];
  //   alu_a_sel[1:0] = ID_ctrl[6:5]; code_lui = ID_ctrl[6]; alu_b_sel = ID_ctrl[7]; code_arith = ID_ctrl[7];
  //   opcode[6:0] = instr[6:0]; rs1[4:0] = instr[19:15]; rs2[4:0] = instr[24:20]; funct7[6:0] = instr[31:25];
  //   mask[1:0] = {instr[13], MEM_ctrl[0]}; ext = MEM_ctrl[2]; code_store = ID_ctrl[1]; FMT_S = ID_ctrl[1];
  //   is_store = ID_ctrl[1]; FMT_B = is_branch; FMT_J = is_jal; rd[4:0] = instr[11:7]; rd_sel[4:0] = instr[11:7];
  //   reg_we = WB_ctrl[5]; code_load = WB_ctrl[6]; is_load = WB_ctrl[6]

  // Notes on the sheet:
  //   流水线冲刷的全0结果不看作非法指令
  //   Arithmetic：0110011
  //   Immediate：0010011
  //   Load：0000011
  //   Store：0100011
  //   lui：0110111
  //   auipc：0010111
  //   ecall：1110011 
endmodule

module M2A_imm_mux (
  input  [31:0] imm_I,
  input  [31:0] imm_S,
  input  [31:0] imm_B,
  input  [31:0] imm_U,
  input  [31:0] imm_J,
  input  [4:0] fmt,
  output [31:0] imm
);

  wire [31:0] and_1_out, and_2_out, and_3_out, and_4_out, and_5_out, FMT_B, FMT_I, FMT_J, FMT_S, FMT_U;

  assign FMT_I = {{31{fmt[0]}}, fmt[0]};  // Bit_Extender bit_extender_1
  assign FMT_S = {{31{fmt[1]}}, fmt[1]};  // Bit_Extender bit_extender_2
  assign FMT_B = {{31{fmt[2]}}, fmt[2]};  // Bit_Extender bit_extender_3
  assign FMT_U = {{31{fmt[3]}}, fmt[3]};  // Bit_Extender bit_extender_4
  assign FMT_J = {{31{fmt[4]}}, fmt[4]};  // Bit_Extender bit_extender_5
  assign and_1_out = FMT_I & imm_I;  // AND_Gate and_1, 32 bits wide
  assign and_2_out = FMT_S & imm_S;  // AND_Gate and_2, 32 bits wide
  assign and_3_out = FMT_B & imm_B;  // AND_Gate and_3, 32 bits wide
  assign and_4_out = FMT_U & imm_U;  // AND_Gate and_4, 32 bits wide
  assign and_5_out = FMT_J & imm_J;  // AND_Gate and_5, 32 bits wide
  assign imm = and_1_out | and_2_out | and_3_out | and_4_out | and_5_out;  // OR_Gate or_1, 32 bits wide
endmodule

module M2B_ID (
  input  [31:0] pc_in,
  input  [31:0] instr,
  input  is_branch,
  input  is_jal,
  input  is_jalr,
  input  [31:0] rs1_src,
  input  [31:0] rs2_src,
  output [31:0] pc,
  output [31:0] b1,
  output [31:0] a1,
  output unknown,
  output [7:0] EX_ctrl,
  output [7:0] MEM_ctrl,
  output [31:0] a2,
  output [7:0] WB_ctrl,
  output [31:0] b2,
  output [4:0] rs1_sel,
  output [4:0] rs2_sel,
  output [31:0] m
);

  wire alu_b_sel;
  wire [1:0] alu_a_sel;
  wire [4:0] m2a_decoder_1_id_ctrl;
  wire [31:0] imm, m2a_imm_gen_1_imm_b, m2a_imm_gen_1_imm_i, m2a_imm_gen_1_imm_j, m2a_imm_gen_1_imm_s,
       m2a_imm_gen_1_imm_u;

  M2A_imm_gen m2a_imm_gen_1 (
    .imm_I(m2a_imm_gen_1_imm_i), .imm_S(m2a_imm_gen_1_imm_s), .imm_B(m2a_imm_gen_1_imm_b),
    .imm_U(m2a_imm_gen_1_imm_u), .imm_J(m2a_imm_gen_1_imm_j), .instr(instr));
  M2A_decoder m2a_decoder_1 (
    .rs1_sel(rs1_sel), .rs2_sel(rs2_sel), .ID_ctrl({alu_b_sel, alu_a_sel, m2a_decoder_1_id_ctrl}),
    .EX_ctrl(EX_ctrl), .MEM_ctrl(MEM_ctrl), .WB_ctrl(WB_ctrl), .unknown(unknown), .instr(instr),
    .is_branch(is_branch), .is_jal(is_jal), .is_jalr(is_jalr));
  M2A_imm_mux m2a_imm_mux_1 (
    .imm(imm), .fmt(m2a_decoder_1_id_ctrl), .imm_I(m2a_imm_gen_1_imm_i), .imm_S(m2a_imm_gen_1_imm_s),
    .imm_B(m2a_imm_gen_1_imm_b), .imm_U(m2a_imm_gen_1_imm_u), .imm_J(m2a_imm_gen_1_imm_j));
  Multiplexer #(.select(2), .width(32)) multiplexer_1 (
    .in0(rs1_src), .in1(pc_in), .in2({32{1'b0}}), .in3({32{1'b0}}), .out(a1), .sel(alu_a_sel));
  Multiplexer #(.width(32)) multiplexer_2 (.in0(imm), .in1(rs2_src), .out(a2), .sel(alu_b_sel));

  assign b1 = rs1_src;
  assign b2 = rs2_src;
  assign m = rs2_src;
  assign pc = pc_in;

  // Other names for the same wires on the sheet: rs1[31:0] = rs1_src; rs2[31:0] = rs2_src
endmodule

module M2A_alu (
  input  [2:0] op,
  input  neg,
  input  [31:0] a1,
  input  [31:0] a2,
  output [31:0] a
);

  wire bitselector_1_out, m2_comparator_32_1_l;
  wire [31:0] and_1_out, bit_extender_1_out, m2_addsub32_1_s, m2_shift_left_32_1_o, m2_shift_right_32_1_o,
       or_1_out, xor_1_out;

  BitSelector #(.width(3)) bitselector_1 (.in(op), .out(bitselector_1_out), .sel(2'b00));
  assign xor_1_out = a1 ^ a2;  // XOR_Gate xor_1, 32 bits wide
  assign or_1_out = a1 | a2;  // OR_Gate or_1, 32 bits wide
  assign and_1_out = a1 & a2;  // AND_Gate and_1, 32 bits wide
  M2_addsub32 m2_addsub32_1 (.S(m2_addsub32_1_s), .neg(neg), .A(a1), .B(a2));
  M2_shift_left_32 m2_shift_left_32_1 (.O(m2_shift_left_32_1_o), .I(a1), .len(a2[4:0]));
  M2_comparator_32 m2_comparator_32_1 (
    .L(m2_comparator_32_1_l), .sgn(bitselector_1_out), .A(a1), .B(a2));  // open: G, E
  assign bit_extender_1_out = {{31{1'b0}}, m2_comparator_32_1_l};  // Bit_Extender bit_extender_1
  M2_shift_right_32 m2_shift_right_32_1 (.O(m2_shift_right_32_1_o), .arith(neg), .I(a1), .len(a2[4:0]));
  Multiplexer #(.select(3), .width(32)) multiplexer_1 (
    .in0(m2_addsub32_1_s), .in1(m2_shift_left_32_1_o), .in2(bit_extender_1_out), .in3(bit_extender_1_out),
    .in4(xor_1_out), .in5(m2_shift_right_32_1_o), .in6(or_1_out), .in7(and_1_out), .out(a), .sel(op));
endmodule

module M2A_bcu (
  input  is_branch,
  input  is_jal,
  input  is_jalr,
  input  [2:0] op,
  input  [31:0] b1,
  input  [31:0] b2,
  output b
);

  wire m2_comparator_32_1_e, m2_comparator_32_1_l, m2_comparator_32_2_l, multiplexer_1_out, not_1_out,
       not_2_out, not_3_out, not_4_out, or_1_out, or_2_out;
  wire [2:0] or_3_out;

  or or_1 (or_1_out, is_jal, is_jalr);
  not not_1 (not_1_out, or_1_out);
  M2_comparator_32 m2_comparator_32_1 (
    .E(m2_comparator_32_1_e), .L(m2_comparator_32_1_l), .sgn(1'b0), .A(b1), .B(b2));  // open: G
  M2_comparator_32 m2_comparator_32_2 (.L(m2_comparator_32_2_l), .sgn(1'b1), .A(b1), .B(b2));  // open: G, E
  or or_2 (or_2_out, is_branch, or_1_out);
  or or_3 (or_3_out[0], op[0], or_1_out);
  or or_4 (or_3_out[1], op[1], or_1_out);
  and and_1 (or_3_out[2], op[2], not_1_out);
  not not_2 (not_2_out, m2_comparator_32_1_e);
  not not_3 (not_3_out, m2_comparator_32_1_l);
  not not_4 (not_4_out, m2_comparator_32_2_l);
  and and_2 (b, or_2_out, multiplexer_1_out);
  Multiplexer #(.select(3)) multiplexer_1 (
    .in0(m2_comparator_32_1_e), .in1(not_2_out), .in2(1'b0), .in3(1'b1), .in4(m2_comparator_32_1_l),
    .in5(not_3_out), .in6(m2_comparator_32_2_l), .in7(not_4_out), .out(multiplexer_1_out), .sel(or_3_out));
endmodule

module M2B_EX (
  input  [31:0] pc_in,
  input  [31:0] b1,
  input  [31:0] b2,
  input  [31:0] a1,
  input  [31:0] a2,
  input  [31:0] m_in,
  input  [7:0] EX_ctrl_in,
  input  [7:0] MEM_ctrl_in,
  input  [7:0] WB_ctrl_in,
  input  [4:0] rs2_sel_in,
  output [31:0] pc,
  output b,
  output [31:0] a,
  output [31:0] m,
  output [7:0] MEM_ctrl,
  output [7:0] WB_ctrl,
  output [4:0] rs2_sel
);

  M2A_bcu m2a_bcu_1 (
    .b(b), .is_branch(MEM_ctrl_in[4]), .is_jal(MEM_ctrl_in[5]), .is_jalr(MEM_ctrl_in[6]),
    .op(EX_ctrl_in[6:4]), .b1(b1), .b2(b2));
  M2A_alu m2a_alu_1 (.a(a), .op(EX_ctrl_in[2:0]), .a1(a1), .a2(a2), .neg(EX_ctrl_in[3]));

  assign m = m_in;
  assign MEM_ctrl = MEM_ctrl_in;
  assign pc = pc_in;
  assign rs2_sel = rs2_sel_in;
  assign WB_ctrl = WB_ctrl_in;

  // Other names for the same wires on the sheet: alu_op[2:0] = EX_ctrl_in[2:0]; alu_neg = EX_ctrl_in[3];
  //   bcu_op[2:0] = EX_ctrl_in[6:4]; is_branch = MEM_ctrl_in[4]; is_jal = MEM_ctrl_in[5]; is_jalr = MEM_ctrl_in[6]
endmodule

module M2A_align (
  input  [31:0] in_dat,
  input  [1:0] adr_lsb,
  input  [1:0] mask,
  output [31:0] out_dat,
  output [3:0] byte_ena
);

  Multiplexer #(.select(2), .width(8)) multiplexer_1 (
    .in0(in_dat[31:24]), .in1({8{1'b0}}), .in2(in_dat[15:8]), .in3(in_dat[7:0]), .out(out_dat[31:24]),
    .sel(adr_lsb));
  Multiplexer #(.select(2)) multiplexer_2 (
    .in0(mask[1]), .in1(1'b0), .in2(mask[0]), .in3(1'b1), .out(byte_ena[3]), .sel(adr_lsb));
  Multiplexer #(.select(2), .width(8)) multiplexer_3 (
    .in0(in_dat[23:16]), .in1({8{1'b0}}), .in2(in_dat[7:0]), .in3({8{1'b0}}), .out(out_dat[23:16]),
    .sel(adr_lsb));
  Multiplexer #(.select(2)) multiplexer_4 (
    .in0(mask[1]), .in1(1'b0), .in2(1'b1), .in3(1'b0), .out(byte_ena[2]), .sel(adr_lsb));
  Multiplexer #(.select(2), .width(8)) multiplexer_5 (
    .in0(in_dat[15:8]), .in1(in_dat[7:0]), .in2({8{1'b0}}), .in3({8{1'b0}}), .out(out_dat[15:8]),
    .sel(adr_lsb));
  Multiplexer #(.select(2)) multiplexer_6 (
    .in0(mask[0]), .in1(1'b1), .in2(1'b0), .in3(1'b0), .out(byte_ena[1]), .sel(adr_lsb));
  Multiplexer #(.select(2), .width(8)) multiplexer_7 (
    .in0(in_dat[7:0]), .in1({8{1'b0}}), .in2({8{1'b0}}), .in3({8{1'b0}}), .out(out_dat[7:0]), .sel(adr_lsb));
  Multiplexer #(.select(2)) multiplexer_8 (
    .in0(1'b1), .in1(1'b0), .in2(1'b0), .in3(1'b0), .out(byte_ena[0]), .sel(adr_lsb));

  // Other names for the same wires on the sheet: msk[1:0] = mask; shf[1:0] = adr_lsb
endmodule

module M2A_dealign (
  input  [31:0] in_dat,
  input  [1:0] adr_lsb,
  input  [1:0] mask,
  input  ext,
  output [31:0] out_dat
);

  wire and_1_out, bitselector_1_out, bitselector_2_out, not_2_out, not_3_out, sign;
  wire [7:0] bit_extender_1_out, bit_extender_2_out, bit_extender_3_out, bit_extender_4_out;
  wire [31:0] and_2_out, and_3_out, bit_extender_5_out, bit_extender_6_out, not_1_out, shf_dat;

  Multiplexer #(.select(2), .width(8)) multiplexer_1 (
    .in0(in_dat[31:24]), .in1(in_dat[15:8]), .in2(in_dat[31:24]), .in3(in_dat[31:24]), .out(shf_dat[31:24]),
    .sel(adr_lsb));
  assign bit_extender_1_out = {{7{1'b1}}, 1'b1};  // Bit_Extender bit_extender_1
  assign bit_extender_2_out = {{7{mask[0]}}, mask[0]};  // Bit_Extender bit_extender_2
  assign bit_extender_3_out = {{7{mask[1]}}, mask[1]};  // Bit_Extender bit_extender_3
  assign bit_extender_4_out = {{7{mask[1]}}, mask[1]};  // Bit_Extender bit_extender_4
  Multiplexer #(.select(2), .width(8)) multiplexer_2 (
    .in0(in_dat[23:16]), .in1(in_dat[15:8]), .in2(in_dat[23:16]), .in3(in_dat[31:24]), .out(shf_dat[23:16]),
    .sel(adr_lsb));
  assign not_1_out = ~{bit_extender_4_out, bit_extender_3_out, bit_extender_2_out, bit_extender_1_out};  // NOT_Gate not_1, 32 bits wide
  Multiplexer #(.select(2), .width(8)) multiplexer_3 (
    .in0(in_dat[15:8]), .in1(in_dat[15:8]), .in2(in_dat[31:24]), .in3(in_dat[31:24]), .out(shf_dat[15:8]),
    .sel(adr_lsb));
  not not_2 (not_2_out, mask[0]);
  not not_3 (not_3_out, mask[1]);
  Multiplexer #(.select(2), .width(8)) multiplexer_4 (
    .in0(in_dat[7:0]), .in1(in_dat[15:8]), .in2(in_dat[23:16]), .in3(in_dat[31:24]), .out(shf_dat[7:0]),
    .sel(adr_lsb));
  and and_1 (and_1_out, not_2_out, not_3_out);
  BitSelector #(.width(32)) bitselector_1 (.in(shf_dat), .out(bitselector_1_out), .sel(5'b01111));
  Multiplexer multiplexer_5 (.in0(bitselector_1_out), .in1(bitselector_2_out), .out(sign), .sel(and_1_out));
  BitSelector #(.width(32)) bitselector_2 (.in(shf_dat), .out(bitselector_2_out), .sel(5'b00111));
  // Probe on shf_dat
  assign bit_extender_5_out = {{31{sign}}, sign};  // Bit_Extender bit_extender_5
  assign bit_extender_6_out = {{31{ext}}, ext};  // Bit_Extender bit_extender_6
  assign and_2_out = shf_dat & {bit_extender_4_out, bit_extender_3_out, bit_extender_2_out, bit_extender_1_out};  // AND_Gate and_2, 32 bits wide
  assign and_3_out = not_1_out & bit_extender_5_out & bit_extender_6_out;  // AND_Gate and_3, 32 bits wide
  assign out_dat = and_2_out | and_3_out;  // OR_Gate or_1, 32 bits wide

  // Other names for the same wires on the sheet: msk[1:0] = mask; shf[1:0] = adr_lsb

  // Notes on the sheet:
  //   Loading Byte
endmodule

module M2A_misalign (
  input  [1:0] mask,
  input  [1:0] adr_lsb,
  input  is_store,
  input  is_load,
  output misalign
);

  wire and_1_out, and_2_out, and_3_out, not_1_out, not_2_out, or_1_out, or_2_out, or_3_out;

  not not_1 (not_1_out, mask[1]);
  or or_1 (or_1_out, adr_lsb[0], adr_lsb[1]);
  not not_2 (not_2_out, mask[0]);
  and and_1 (and_1_out, mask[0], not_1_out, adr_lsb[0]);
  and and_2 (and_2_out, mask[0], mask[1], or_1_out);
  or or_2 (or_2_out, and_1_out, and_2_out, and_3_out);
  and and_3 (and_3_out, not_2_out, mask[1]);
  or or_3 (or_3_out, is_store, is_load);
  and and_4 (misalign, or_2_out, or_3_out);

  // Notes on the sheet:
  //   Store Half Word, but A[0] == 1
  //   Store Word, but A[1:0] != 0
  //   invalid "mask" value
endmodule

module M2B_MEM (
  input  [31:0] pc_in,
  input  [31:0] a_in,
  input  [31:0] m_in,
  input  [7:0] MEM_ctrl_in,
  input  [31:0] ram_dout,
  input  [7:0] WB_ctrl_in,
  output [31:0] pc,
  output [31:0] pc4,
  output [31:0] a,
  output [31:0] m,
  output misalign,
  output [31:0] ram_adr,
  output ram_re,
  output ram_we,
  output [3:0] ram_be,
  output [31:0] ram_din,
  output [7:0] WB_ctrl
);

  wire nor_1_out;

  M2_incr4_32 m2_incr4_32_1 (.o(pc4), .i(pc_in));
  nor nor_1 (nor_1_out, MEM_ctrl_in[5], MEM_ctrl_in[6]);
  Multiplexer #(.width(32)) multiplexer_1 (.in0(pc4), .in1(a_in), .out(a), .sel(nor_1_out));
  M2A_align m2a_align_1 (
    .out_dat(ram_din), .byte_ena(ram_be), .adr_lsb(a_in[1:0]), .mask(MEM_ctrl_in[1:0]), .in_dat(m_in));
  M2A_dealign m2a_dealign_1 (
    .out_dat(m), .ext(MEM_ctrl_in[2]), .adr_lsb(a_in[1:0]), .mask(MEM_ctrl_in[1:0]), .in_dat(ram_dout));
  M2A_misalign m2a_misalign_1 (
    .misalign(misalign), .mask(MEM_ctrl_in[1:0]), .adr_lsb(a_in[1:0]), .is_store(MEM_ctrl_in[3]),
    .is_load(WB_ctrl_in[6]));

  assign pc = pc_in;
  assign ram_adr = {a_in[31:2], 2'b00};
  assign ram_re = WB_ctrl_in[6];
  assign ram_we = MEM_ctrl_in[3];
  assign WB_ctrl = WB_ctrl_in;

  // Other names for the same wires on the sheet: adr_lsb[1:0] = a_in[1:0]; mask[1:0] = MEM_ctrl_in[1:0];
  //   uext = MEM_ctrl_in[2]; is_store = MEM_ctrl_in[3]; is_branch = MEM_ctrl_in[4]; is_jal = MEM_ctrl_in[5];
  //   is_jalr = MEM_ctrl_in[6]; rd_sel[4:0] = WB_ctrl_in[4:0]; reg_we = WB_ctrl_in[5]; is_load = WB_ctrl_in[6]

  // Notes on the sheet:
  //   数据总线接口
endmodule

module M2A_WB (
  input  [31:0] a_in,
  input  [31:0] m_in,
  input  [7:0] WB_ctrl_in,
  output [31:0] rd_data,
  output [4:0] rd_sel,
  output rd_we
);

  Multiplexer #(.width(32)) multiplexer_1 (.in0(a_in), .in1(m_in), .out(rd_data), .sel(WB_ctrl_in[6]));

  assign rd_sel = WB_ctrl_in[4:0];
  assign rd_we = WB_ctrl_in[5];

  // Other names for the same wires on the sheet: reg_we = WB_ctrl_in[5]; is_load = WB_ctrl_in[6]
endmodule

module M1A_pixel (
  input  r,
  input  d,
  input  c,
  input  clk,
  input  srn,
  output q
);

  wire and_1_out, not_1_out;

  Register #(.width(1)) register_1 (.D(d), .en(and_1_out), .clk(clk), .Q(q), .clr(not_1_out));
  and and_1 (and_1_out, r, c);
  not not_1 (not_1_out, srn);
endmodule

module M1A_frame_buffer (
  input  [7:0] pos,
  input  we,
  input  d,
  input  clk,
  input  srn,
  output [15:0] line0,
  output [15:0] line1,
  output [15:0] line2,
  output [15:0] line3,
  output [15:0] line4,
  output [15:0] line5,
  output [15:0] line6,
  output [15:0] line7,
  output [15:0] line8,
  output [15:0] line9,
  output [15:0] line10,
  output [15:0] line11,
  output [15:0] line12,
  output [15:0] line13,
  output [15:0] line14,
  output [15:0] line15
);

  wire and_1_out, and_2_out, not_1_out, not_2_out;
  wire [15:0] col_sel, decoder_1_out0, decoder_2_out15, row_sel, we_t;

  assign we_t = {{15{we}}, we};  // Bit_Extender bit_extender_1
  not not_1 (not_1_out, clk);
  not not_2 (not_2_out, srn);
  and and_1 (and_1_out, clk, not_1_out);
  and and_2 (and_2_out, and_1_out, not_2_out);
  M1A_pixel m1a_pixel_1 (.q(line0[15]), .d(d), .c(row_sel[0]), .clk(clk), .srn(and_2_out), .r(col_sel[15]));
  M1A_pixel m1a_pixel_2 (.q(line1[15]), .d(d), .c(row_sel[1]), .clk(clk), .srn(and_2_out), .r(col_sel[15]));
  M1A_pixel m1a_pixel_3 (.q(line2[15]), .d(d), .c(row_sel[2]), .clk(clk), .srn(and_2_out), .r(col_sel[15]));
  M1A_pixel m1a_pixel_4 (.q(line3[15]), .d(d), .c(row_sel[3]), .clk(clk), .srn(and_2_out), .r(col_sel[15]));
  M1A_pixel m1a_pixel_5 (.q(line4[15]), .d(d), .c(row_sel[4]), .clk(clk), .srn(and_2_out), .r(col_sel[15]));
  M1A_pixel m1a_pixel_6 (.q(line5[15]), .d(d), .c(row_sel[5]), .clk(clk), .srn(and_2_out), .r(col_sel[15]));
  M1A_pixel m1a_pixel_7 (.q(line6[15]), .d(d), .c(row_sel[6]), .clk(clk), .srn(and_2_out), .r(col_sel[15]));
  M1A_pixel m1a_pixel_8 (.q(line7[15]), .d(d), .c(row_sel[7]), .clk(clk), .srn(and_2_out), .r(col_sel[15]));
  M1A_pixel m1a_pixel_9 (.q(line8[15]), .d(d), .c(row_sel[8]), .clk(clk), .srn(and_2_out), .r(col_sel[15]));
  M1A_pixel m1a_pixel_10 (.q(line9[15]), .d(d), .c(row_sel[9]), .clk(clk), .srn(and_2_out), .r(col_sel[15]));
  M1A_pixel m1a_pixel_11 (.q(line10[15]), .d(d), .c(row_sel[10]), .clk(clk), .srn(and_2_out), .r(col_sel[15]));
  M1A_pixel m1a_pixel_12 (.q(line11[15]), .d(d), .c(row_sel[11]), .clk(clk), .srn(and_2_out), .r(col_sel[15]));
  M1A_pixel m1a_pixel_13 (.q(line12[15]), .d(d), .c(row_sel[12]), .clk(clk), .srn(and_2_out), .r(col_sel[15]));
  M1A_pixel m1a_pixel_14 (.q(line13[15]), .d(d), .c(row_sel[13]), .clk(clk), .srn(and_2_out), .r(col_sel[15]));
  M1A_pixel m1a_pixel_15 (.q(line14[15]), .d(d), .c(row_sel[14]), .clk(clk), .srn(and_2_out), .r(col_sel[15]));
  M1A_pixel m1a_pixel_16 (.q(line15[15]), .d(d), .c(row_sel[15]), .clk(clk), .srn(and_2_out), .r(col_sel[15]));
  M1A_pixel m1a_pixel_17 (.q(line0[14]), .d(d), .c(row_sel[0]), .clk(clk), .srn(and_2_out), .r(col_sel[14]));
  M1A_pixel m1a_pixel_18 (.q(line1[14]), .d(d), .c(row_sel[1]), .clk(clk), .srn(and_2_out), .r(col_sel[14]));
  M1A_pixel m1a_pixel_19 (.q(line2[14]), .d(d), .c(row_sel[2]), .clk(clk), .srn(and_2_out), .r(col_sel[14]));
  M1A_pixel m1a_pixel_20 (.q(line3[14]), .d(d), .c(row_sel[3]), .clk(clk), .srn(and_2_out), .r(col_sel[14]));
  M1A_pixel m1a_pixel_21 (.q(line4[14]), .d(d), .c(row_sel[4]), .clk(clk), .srn(and_2_out), .r(col_sel[14]));
  M1A_pixel m1a_pixel_22 (.q(line5[14]), .d(d), .c(row_sel[5]), .clk(clk), .srn(and_2_out), .r(col_sel[14]));
  M1A_pixel m1a_pixel_23 (.q(line6[14]), .d(d), .c(row_sel[6]), .clk(clk), .srn(and_2_out), .r(col_sel[14]));
  M1A_pixel m1a_pixel_24 (.q(line7[14]), .d(d), .c(row_sel[7]), .clk(clk), .srn(and_2_out), .r(col_sel[14]));
  M1A_pixel m1a_pixel_25 (.q(line8[14]), .d(d), .c(row_sel[8]), .clk(clk), .srn(and_2_out), .r(col_sel[14]));
  M1A_pixel m1a_pixel_26 (.q(line9[14]), .d(d), .c(row_sel[9]), .clk(clk), .srn(and_2_out), .r(col_sel[14]));
  M1A_pixel m1a_pixel_27 (.q(line10[14]), .d(d), .c(row_sel[10]), .clk(clk), .srn(and_2_out), .r(col_sel[14]));
  M1A_pixel m1a_pixel_28 (.q(line11[14]), .d(d), .c(row_sel[11]), .clk(clk), .srn(and_2_out), .r(col_sel[14]));
  M1A_pixel m1a_pixel_29 (.q(line12[14]), .d(d), .c(row_sel[12]), .clk(clk), .srn(and_2_out), .r(col_sel[14]));
  M1A_pixel m1a_pixel_30 (.q(line13[14]), .d(d), .c(row_sel[13]), .clk(clk), .srn(and_2_out), .r(col_sel[14]));
  M1A_pixel m1a_pixel_31 (.q(line14[14]), .d(d), .c(row_sel[14]), .clk(clk), .srn(and_2_out), .r(col_sel[14]));
  M1A_pixel m1a_pixel_32 (.q(line15[14]), .d(d), .c(row_sel[15]), .clk(clk), .srn(and_2_out), .r(col_sel[14]));
  Decoder #(.select(4)) decoder_1 (
    .out0(decoder_1_out0[0]), .out1(decoder_1_out0[1]), .out2(decoder_1_out0[2]), .out3(decoder_1_out0[3]),
    .out4(decoder_1_out0[4]), .out5(decoder_1_out0[5]), .out6(decoder_1_out0[6]), .out7(decoder_1_out0[7]),
    .out8(decoder_1_out0[8]), .out9(decoder_1_out0[9]), .out10(decoder_1_out0[10]),
    .out11(decoder_1_out0[11]), .out12(decoder_1_out0[12]), .out13(decoder_1_out0[13]),
    .out14(decoder_1_out0[14]), .out15(decoder_1_out0[15]), .sel(pos[7:4]));  // open: en
  M1A_pixel m1a_pixel_33 (.q(line0[13]), .d(d), .c(row_sel[0]), .clk(clk), .srn(and_2_out), .r(col_sel[13]));
  M1A_pixel m1a_pixel_34 (.q(line1[13]), .d(d), .c(row_sel[1]), .clk(clk), .srn(and_2_out), .r(col_sel[13]));
  M1A_pixel m1a_pixel_35 (.q(line2[13]), .d(d), .c(row_sel[2]), .clk(clk), .srn(and_2_out), .r(col_sel[13]));
  M1A_pixel m1a_pixel_36 (.q(line3[13]), .d(d), .c(row_sel[3]), .clk(clk), .srn(and_2_out), .r(col_sel[13]));
  M1A_pixel m1a_pixel_37 (.q(line4[13]), .d(d), .c(row_sel[4]), .clk(clk), .srn(and_2_out), .r(col_sel[13]));
  M1A_pixel m1a_pixel_38 (.q(line5[13]), .d(d), .c(row_sel[5]), .clk(clk), .srn(and_2_out), .r(col_sel[13]));
  M1A_pixel m1a_pixel_39 (.q(line6[13]), .d(d), .c(row_sel[6]), .clk(clk), .srn(and_2_out), .r(col_sel[13]));
  M1A_pixel m1a_pixel_40 (.q(line7[13]), .d(d), .c(row_sel[7]), .clk(clk), .srn(and_2_out), .r(col_sel[13]));
  M1A_pixel m1a_pixel_41 (.q(line8[13]), .d(d), .c(row_sel[8]), .clk(clk), .srn(and_2_out), .r(col_sel[13]));
  M1A_pixel m1a_pixel_42 (.q(line9[13]), .d(d), .c(row_sel[9]), .clk(clk), .srn(and_2_out), .r(col_sel[13]));
  M1A_pixel m1a_pixel_43 (.q(line10[13]), .d(d), .c(row_sel[10]), .clk(clk), .srn(and_2_out), .r(col_sel[13]));
  M1A_pixel m1a_pixel_44 (.q(line11[13]), .d(d), .c(row_sel[11]), .clk(clk), .srn(and_2_out), .r(col_sel[13]));
  M1A_pixel m1a_pixel_45 (.q(line12[13]), .d(d), .c(row_sel[12]), .clk(clk), .srn(and_2_out), .r(col_sel[13]));
  M1A_pixel m1a_pixel_46 (.q(line13[13]), .d(d), .c(row_sel[13]), .clk(clk), .srn(and_2_out), .r(col_sel[13]));
  M1A_pixel m1a_pixel_47 (.q(line14[13]), .d(d), .c(row_sel[14]), .clk(clk), .srn(and_2_out), .r(col_sel[13]));
  M1A_pixel m1a_pixel_48 (.q(line15[13]), .d(d), .c(row_sel[15]), .clk(clk), .srn(and_2_out), .r(col_sel[13]));
  Decoder #(.select(4)) decoder_2 (
    .out0(decoder_2_out15[15]), .out1(decoder_2_out15[14]), .out2(decoder_2_out15[13]),
    .out3(decoder_2_out15[12]), .out4(decoder_2_out15[11]), .out5(decoder_2_out15[10]),
    .out6(decoder_2_out15[9]), .out7(decoder_2_out15[8]), .out8(decoder_2_out15[7]),
    .out9(decoder_2_out15[6]), .out10(decoder_2_out15[5]), .out11(decoder_2_out15[4]),
    .out12(decoder_2_out15[3]), .out13(decoder_2_out15[2]), .out14(decoder_2_out15[1]),
    .out15(decoder_2_out15[0]), .sel(pos[3:0]));  // open: en
  assign row_sel = decoder_1_out0 & we_t;  // AND_Gate and_3, 16 bits wide
  M1A_pixel m1a_pixel_49 (.q(line0[12]), .d(d), .c(row_sel[0]), .clk(clk), .srn(and_2_out), .r(col_sel[12]));
  M1A_pixel m1a_pixel_50 (.q(line1[12]), .d(d), .c(row_sel[1]), .clk(clk), .srn(and_2_out), .r(col_sel[12]));
  M1A_pixel m1a_pixel_51 (.q(line2[12]), .d(d), .c(row_sel[2]), .clk(clk), .srn(and_2_out), .r(col_sel[12]));
  M1A_pixel m1a_pixel_52 (.q(line3[12]), .d(d), .c(row_sel[3]), .clk(clk), .srn(and_2_out), .r(col_sel[12]));
  M1A_pixel m1a_pixel_53 (.q(line4[12]), .d(d), .c(row_sel[4]), .clk(clk), .srn(and_2_out), .r(col_sel[12]));
  M1A_pixel m1a_pixel_54 (.q(line5[12]), .d(d), .c(row_sel[5]), .clk(clk), .srn(and_2_out), .r(col_sel[12]));
  M1A_pixel m1a_pixel_55 (.q(line6[12]), .d(d), .c(row_sel[6]), .clk(clk), .srn(and_2_out), .r(col_sel[12]));
  M1A_pixel m1a_pixel_56 (.q(line7[12]), .d(d), .c(row_sel[7]), .clk(clk), .srn(and_2_out), .r(col_sel[12]));
  M1A_pixel m1a_pixel_57 (.q(line8[12]), .d(d), .c(row_sel[8]), .clk(clk), .srn(and_2_out), .r(col_sel[12]));
  M1A_pixel m1a_pixel_58 (.q(line9[12]), .d(d), .c(row_sel[9]), .clk(clk), .srn(and_2_out), .r(col_sel[12]));
  M1A_pixel m1a_pixel_59 (.q(line10[12]), .d(d), .c(row_sel[10]), .clk(clk), .srn(and_2_out), .r(col_sel[12]));
  M1A_pixel m1a_pixel_60 (.q(line11[12]), .d(d), .c(row_sel[11]), .clk(clk), .srn(and_2_out), .r(col_sel[12]));
  M1A_pixel m1a_pixel_61 (.q(line12[12]), .d(d), .c(row_sel[12]), .clk(clk), .srn(and_2_out), .r(col_sel[12]));
  M1A_pixel m1a_pixel_62 (.q(line13[12]), .d(d), .c(row_sel[13]), .clk(clk), .srn(and_2_out), .r(col_sel[12]));
  M1A_pixel m1a_pixel_63 (.q(line14[12]), .d(d), .c(row_sel[14]), .clk(clk), .srn(and_2_out), .r(col_sel[12]));
  M1A_pixel m1a_pixel_64 (.q(line15[12]), .d(d), .c(row_sel[15]), .clk(clk), .srn(and_2_out), .r(col_sel[12]));
  M1A_pixel m1a_pixel_65 (.q(line0[11]), .d(d), .c(row_sel[0]), .clk(clk), .srn(and_2_out), .r(col_sel[11]));
  M1A_pixel m1a_pixel_66 (.q(line1[11]), .d(d), .c(row_sel[1]), .clk(clk), .srn(and_2_out), .r(col_sel[11]));
  M1A_pixel m1a_pixel_67 (.q(line2[11]), .d(d), .c(row_sel[2]), .clk(clk), .srn(and_2_out), .r(col_sel[11]));
  M1A_pixel m1a_pixel_68 (.q(line3[11]), .d(d), .c(row_sel[3]), .clk(clk), .srn(and_2_out), .r(col_sel[11]));
  M1A_pixel m1a_pixel_69 (.q(line4[11]), .d(d), .c(row_sel[4]), .clk(clk), .srn(and_2_out), .r(col_sel[11]));
  M1A_pixel m1a_pixel_70 (.q(line5[11]), .d(d), .c(row_sel[5]), .clk(clk), .srn(and_2_out), .r(col_sel[11]));
  M1A_pixel m1a_pixel_71 (.q(line6[11]), .d(d), .c(row_sel[6]), .clk(clk), .srn(and_2_out), .r(col_sel[11]));
  M1A_pixel m1a_pixel_72 (.q(line7[11]), .d(d), .c(row_sel[7]), .clk(clk), .srn(and_2_out), .r(col_sel[11]));
  M1A_pixel m1a_pixel_73 (.q(line8[11]), .d(d), .c(row_sel[8]), .clk(clk), .srn(and_2_out), .r(col_sel[11]));
  M1A_pixel m1a_pixel_74 (.q(line9[11]), .d(d), .c(row_sel[9]), .clk(clk), .srn(and_2_out), .r(col_sel[11]));
  M1A_pixel m1a_pixel_75 (.q(line10[11]), .d(d), .c(row_sel[10]), .clk(clk), .srn(and_2_out), .r(col_sel[11]));
  M1A_pixel m1a_pixel_76 (.q(line11[11]), .d(d), .c(row_sel[11]), .clk(clk), .srn(and_2_out), .r(col_sel[11]));
  M1A_pixel m1a_pixel_77 (.q(line12[11]), .d(d), .c(row_sel[12]), .clk(clk), .srn(and_2_out), .r(col_sel[11]));
  M1A_pixel m1a_pixel_78 (.q(line13[11]), .d(d), .c(row_sel[13]), .clk(clk), .srn(and_2_out), .r(col_sel[11]));
  M1A_pixel m1a_pixel_79 (.q(line14[11]), .d(d), .c(row_sel[14]), .clk(clk), .srn(and_2_out), .r(col_sel[11]));
  M1A_pixel m1a_pixel_80 (.q(line15[11]), .d(d), .c(row_sel[15]), .clk(clk), .srn(and_2_out), .r(col_sel[11]));
  assign col_sel = decoder_2_out15 & we_t;  // AND_Gate and_4, 16 bits wide
  M1A_pixel m1a_pixel_81 (.q(line0[10]), .d(d), .c(row_sel[0]), .clk(clk), .srn(and_2_out), .r(col_sel[10]));
  M1A_pixel m1a_pixel_82 (.q(line1[10]), .d(d), .c(row_sel[1]), .clk(clk), .srn(and_2_out), .r(col_sel[10]));
  M1A_pixel m1a_pixel_83 (.q(line2[10]), .d(d), .c(row_sel[2]), .clk(clk), .srn(and_2_out), .r(col_sel[10]));
  M1A_pixel m1a_pixel_84 (.q(line3[10]), .d(d), .c(row_sel[3]), .clk(clk), .srn(and_2_out), .r(col_sel[10]));
  M1A_pixel m1a_pixel_85 (.q(line4[10]), .d(d), .c(row_sel[4]), .clk(clk), .srn(and_2_out), .r(col_sel[10]));
  M1A_pixel m1a_pixel_86 (.q(line5[10]), .d(d), .c(row_sel[5]), .clk(clk), .srn(and_2_out), .r(col_sel[10]));
  M1A_pixel m1a_pixel_87 (.q(line6[10]), .d(d), .c(row_sel[6]), .clk(clk), .srn(and_2_out), .r(col_sel[10]));
  M1A_pixel m1a_pixel_88 (.q(line7[10]), .d(d), .c(row_sel[7]), .clk(clk), .srn(and_2_out), .r(col_sel[10]));
  M1A_pixel m1a_pixel_89 (.q(line8[10]), .d(d), .c(row_sel[8]), .clk(clk), .srn(and_2_out), .r(col_sel[10]));
  M1A_pixel m1a_pixel_90 (.q(line9[10]), .d(d), .c(row_sel[9]), .clk(clk), .srn(and_2_out), .r(col_sel[10]));
  M1A_pixel m1a_pixel_91 (.q(line10[10]), .d(d), .c(row_sel[10]), .clk(clk), .srn(and_2_out), .r(col_sel[10]));
  M1A_pixel m1a_pixel_92 (.q(line11[10]), .d(d), .c(row_sel[11]), .clk(clk), .srn(and_2_out), .r(col_sel[10]));
  M1A_pixel m1a_pixel_93 (.q(line12[10]), .d(d), .c(row_sel[12]), .clk(clk), .srn(and_2_out), .r(col_sel[10]));
  M1A_pixel m1a_pixel_94 (.q(line13[10]), .d(d), .c(row_sel[13]), .clk(clk), .srn(and_2_out), .r(col_sel[10]));
  M1A_pixel m1a_pixel_95 (.q(line14[10]), .d(d), .c(row_sel[14]), .clk(clk), .srn(and_2_out), .r(col_sel[10]));
  M1A_pixel m1a_pixel_96 (.q(line15[10]), .d(d), .c(row_sel[15]), .clk(clk), .srn(and_2_out), .r(col_sel[10]));
  M1A_pixel m1a_pixel_97 (.q(line0[9]), .d(d), .c(row_sel[0]), .clk(clk), .srn(and_2_out), .r(col_sel[9]));
  M1A_pixel m1a_pixel_98 (.q(line1[9]), .d(d), .c(row_sel[1]), .clk(clk), .srn(and_2_out), .r(col_sel[9]));
  M1A_pixel m1a_pixel_99 (.q(line2[9]), .d(d), .c(row_sel[2]), .clk(clk), .srn(and_2_out), .r(col_sel[9]));
  M1A_pixel m1a_pixel_100 (.q(line3[9]), .d(d), .c(row_sel[3]), .clk(clk), .srn(and_2_out), .r(col_sel[9]));
  M1A_pixel m1a_pixel_101 (.q(line4[9]), .d(d), .c(row_sel[4]), .clk(clk), .srn(and_2_out), .r(col_sel[9]));
  M1A_pixel m1a_pixel_102 (.q(line5[9]), .d(d), .c(row_sel[5]), .clk(clk), .srn(and_2_out), .r(col_sel[9]));
  M1A_pixel m1a_pixel_103 (.q(line6[9]), .d(d), .c(row_sel[6]), .clk(clk), .srn(and_2_out), .r(col_sel[9]));
  M1A_pixel m1a_pixel_104 (.q(line7[9]), .d(d), .c(row_sel[7]), .clk(clk), .srn(and_2_out), .r(col_sel[9]));
  M1A_pixel m1a_pixel_105 (.q(line8[9]), .d(d), .c(row_sel[8]), .clk(clk), .srn(and_2_out), .r(col_sel[9]));
  M1A_pixel m1a_pixel_106 (.q(line9[9]), .d(d), .c(row_sel[9]), .clk(clk), .srn(and_2_out), .r(col_sel[9]));
  M1A_pixel m1a_pixel_107 (.q(line10[9]), .d(d), .c(row_sel[10]), .clk(clk), .srn(and_2_out), .r(col_sel[9]));
  M1A_pixel m1a_pixel_108 (.q(line11[9]), .d(d), .c(row_sel[11]), .clk(clk), .srn(and_2_out), .r(col_sel[9]));
  M1A_pixel m1a_pixel_109 (.q(line12[9]), .d(d), .c(row_sel[12]), .clk(clk), .srn(and_2_out), .r(col_sel[9]));
  M1A_pixel m1a_pixel_110 (.q(line13[9]), .d(d), .c(row_sel[13]), .clk(clk), .srn(and_2_out), .r(col_sel[9]));
  M1A_pixel m1a_pixel_111 (.q(line14[9]), .d(d), .c(row_sel[14]), .clk(clk), .srn(and_2_out), .r(col_sel[9]));
  M1A_pixel m1a_pixel_112 (.q(line15[9]), .d(d), .c(row_sel[15]), .clk(clk), .srn(and_2_out), .r(col_sel[9]));
  M1A_pixel m1a_pixel_113 (.q(line0[8]), .d(d), .c(row_sel[0]), .clk(clk), .srn(and_2_out), .r(col_sel[8]));
  M1A_pixel m1a_pixel_114 (.q(line1[8]), .d(d), .c(row_sel[1]), .clk(clk), .srn(and_2_out), .r(col_sel[8]));
  M1A_pixel m1a_pixel_115 (.q(line2[8]), .d(d), .c(row_sel[2]), .clk(clk), .srn(and_2_out), .r(col_sel[8]));
  M1A_pixel m1a_pixel_116 (.q(line3[8]), .d(d), .c(row_sel[3]), .clk(clk), .srn(and_2_out), .r(col_sel[8]));
  M1A_pixel m1a_pixel_117 (.q(line4[8]), .d(d), .c(row_sel[4]), .clk(clk), .srn(and_2_out), .r(col_sel[8]));
  M1A_pixel m1a_pixel_118 (.q(line5[8]), .d(d), .c(row_sel[5]), .clk(clk), .srn(and_2_out), .r(col_sel[8]));
  M1A_pixel m1a_pixel_119 (.q(line6[8]), .d(d), .c(row_sel[6]), .clk(clk), .srn(and_2_out), .r(col_sel[8]));
  M1A_pixel m1a_pixel_120 (.q(line7[8]), .d(d), .c(row_sel[7]), .clk(clk), .srn(and_2_out), .r(col_sel[8]));
  M1A_pixel m1a_pixel_121 (.q(line8[8]), .d(d), .c(row_sel[8]), .clk(clk), .srn(and_2_out), .r(col_sel[8]));
  M1A_pixel m1a_pixel_122 (.q(line9[8]), .d(d), .c(row_sel[9]), .clk(clk), .srn(and_2_out), .r(col_sel[8]));
  M1A_pixel m1a_pixel_123 (.q(line10[8]), .d(d), .c(row_sel[10]), .clk(clk), .srn(and_2_out), .r(col_sel[8]));
  M1A_pixel m1a_pixel_124 (.q(line11[8]), .d(d), .c(row_sel[11]), .clk(clk), .srn(and_2_out), .r(col_sel[8]));
  M1A_pixel m1a_pixel_125 (.q(line12[8]), .d(d), .c(row_sel[12]), .clk(clk), .srn(and_2_out), .r(col_sel[8]));
  M1A_pixel m1a_pixel_126 (.q(line13[8]), .d(d), .c(row_sel[13]), .clk(clk), .srn(and_2_out), .r(col_sel[8]));
  M1A_pixel m1a_pixel_127 (.q(line14[8]), .d(d), .c(row_sel[14]), .clk(clk), .srn(and_2_out), .r(col_sel[8]));
  M1A_pixel m1a_pixel_128 (.q(line15[8]), .d(d), .c(row_sel[15]), .clk(clk), .srn(and_2_out), .r(col_sel[8]));
  M1A_pixel m1a_pixel_129 (.q(line0[7]), .d(d), .c(row_sel[0]), .clk(clk), .srn(and_2_out), .r(col_sel[7]));
  M1A_pixel m1a_pixel_130 (.q(line1[7]), .d(d), .c(row_sel[1]), .clk(clk), .srn(and_2_out), .r(col_sel[7]));
  M1A_pixel m1a_pixel_131 (.q(line2[7]), .d(d), .c(row_sel[2]), .clk(clk), .srn(and_2_out), .r(col_sel[7]));
  M1A_pixel m1a_pixel_132 (.q(line3[7]), .d(d), .c(row_sel[3]), .clk(clk), .srn(and_2_out), .r(col_sel[7]));
  M1A_pixel m1a_pixel_133 (.q(line4[7]), .d(d), .c(row_sel[4]), .clk(clk), .srn(and_2_out), .r(col_sel[7]));
  M1A_pixel m1a_pixel_134 (.q(line5[7]), .d(d), .c(row_sel[5]), .clk(clk), .srn(and_2_out), .r(col_sel[7]));
  M1A_pixel m1a_pixel_135 (.q(line6[7]), .d(d), .c(row_sel[6]), .clk(clk), .srn(and_2_out), .r(col_sel[7]));
  M1A_pixel m1a_pixel_136 (.q(line7[7]), .d(d), .c(row_sel[7]), .clk(clk), .srn(and_2_out), .r(col_sel[7]));
  M1A_pixel m1a_pixel_137 (.q(line8[7]), .d(d), .c(row_sel[8]), .clk(clk), .srn(and_2_out), .r(col_sel[7]));
  M1A_pixel m1a_pixel_138 (.q(line9[7]), .d(d), .c(row_sel[9]), .clk(clk), .srn(and_2_out), .r(col_sel[7]));
  M1A_pixel m1a_pixel_139 (.q(line10[7]), .d(d), .c(row_sel[10]), .clk(clk), .srn(and_2_out), .r(col_sel[7]));
  M1A_pixel m1a_pixel_140 (.q(line11[7]), .d(d), .c(row_sel[11]), .clk(clk), .srn(and_2_out), .r(col_sel[7]));
  M1A_pixel m1a_pixel_141 (.q(line12[7]), .d(d), .c(row_sel[12]), .clk(clk), .srn(and_2_out), .r(col_sel[7]));
  M1A_pixel m1a_pixel_142 (.q(line13[7]), .d(d), .c(row_sel[13]), .clk(clk), .srn(and_2_out), .r(col_sel[7]));
  M1A_pixel m1a_pixel_143 (.q(line14[7]), .d(d), .c(row_sel[14]), .clk(clk), .srn(and_2_out), .r(col_sel[7]));
  M1A_pixel m1a_pixel_144 (.q(line15[7]), .d(d), .c(row_sel[15]), .clk(clk), .srn(and_2_out), .r(col_sel[7]));
  M1A_pixel m1a_pixel_145 (.q(line0[6]), .d(d), .c(row_sel[0]), .clk(clk), .srn(and_2_out), .r(col_sel[6]));
  M1A_pixel m1a_pixel_146 (.q(line1[6]), .d(d), .c(row_sel[1]), .clk(clk), .srn(and_2_out), .r(col_sel[6]));
  M1A_pixel m1a_pixel_147 (.q(line2[6]), .d(d), .c(row_sel[2]), .clk(clk), .srn(and_2_out), .r(col_sel[6]));
  M1A_pixel m1a_pixel_148 (.q(line3[6]), .d(d), .c(row_sel[3]), .clk(clk), .srn(and_2_out), .r(col_sel[6]));
  M1A_pixel m1a_pixel_149 (.q(line4[6]), .d(d), .c(row_sel[4]), .clk(clk), .srn(and_2_out), .r(col_sel[6]));
  M1A_pixel m1a_pixel_150 (.q(line5[6]), .d(d), .c(row_sel[5]), .clk(clk), .srn(and_2_out), .r(col_sel[6]));
  M1A_pixel m1a_pixel_151 (.q(line6[6]), .d(d), .c(row_sel[6]), .clk(clk), .srn(and_2_out), .r(col_sel[6]));
  M1A_pixel m1a_pixel_152 (.q(line7[6]), .d(d), .c(row_sel[7]), .clk(clk), .srn(and_2_out), .r(col_sel[6]));
  M1A_pixel m1a_pixel_153 (.q(line8[6]), .d(d), .c(row_sel[8]), .clk(clk), .srn(and_2_out), .r(col_sel[6]));
  M1A_pixel m1a_pixel_154 (.q(line9[6]), .d(d), .c(row_sel[9]), .clk(clk), .srn(and_2_out), .r(col_sel[6]));
  M1A_pixel m1a_pixel_155 (.q(line10[6]), .d(d), .c(row_sel[10]), .clk(clk), .srn(and_2_out), .r(col_sel[6]));
  M1A_pixel m1a_pixel_156 (.q(line11[6]), .d(d), .c(row_sel[11]), .clk(clk), .srn(and_2_out), .r(col_sel[6]));
  M1A_pixel m1a_pixel_157 (.q(line12[6]), .d(d), .c(row_sel[12]), .clk(clk), .srn(and_2_out), .r(col_sel[6]));
  M1A_pixel m1a_pixel_158 (.q(line13[6]), .d(d), .c(row_sel[13]), .clk(clk), .srn(and_2_out), .r(col_sel[6]));
  M1A_pixel m1a_pixel_159 (.q(line14[6]), .d(d), .c(row_sel[14]), .clk(clk), .srn(and_2_out), .r(col_sel[6]));
  M1A_pixel m1a_pixel_160 (.q(line15[6]), .d(d), .c(row_sel[15]), .clk(clk), .srn(and_2_out), .r(col_sel[6]));
  M1A_pixel m1a_pixel_161 (.q(line0[5]), .d(d), .c(row_sel[0]), .clk(clk), .srn(and_2_out), .r(col_sel[5]));
  M1A_pixel m1a_pixel_162 (.q(line1[5]), .d(d), .c(row_sel[1]), .clk(clk), .srn(and_2_out), .r(col_sel[5]));
  M1A_pixel m1a_pixel_163 (.q(line2[5]), .d(d), .c(row_sel[2]), .clk(clk), .srn(and_2_out), .r(col_sel[5]));
  M1A_pixel m1a_pixel_164 (.q(line3[5]), .d(d), .c(row_sel[3]), .clk(clk), .srn(and_2_out), .r(col_sel[5]));
  M1A_pixel m1a_pixel_165 (.q(line4[5]), .d(d), .c(row_sel[4]), .clk(clk), .srn(and_2_out), .r(col_sel[5]));
  M1A_pixel m1a_pixel_166 (.q(line5[5]), .d(d), .c(row_sel[5]), .clk(clk), .srn(and_2_out), .r(col_sel[5]));
  M1A_pixel m1a_pixel_167 (.q(line6[5]), .d(d), .c(row_sel[6]), .clk(clk), .srn(and_2_out), .r(col_sel[5]));
  M1A_pixel m1a_pixel_168 (.q(line7[5]), .d(d), .c(row_sel[7]), .clk(clk), .srn(and_2_out), .r(col_sel[5]));
  M1A_pixel m1a_pixel_169 (.q(line8[5]), .d(d), .c(row_sel[8]), .clk(clk), .srn(and_2_out), .r(col_sel[5]));
  M1A_pixel m1a_pixel_170 (.q(line9[5]), .d(d), .c(row_sel[9]), .clk(clk), .srn(and_2_out), .r(col_sel[5]));
  M1A_pixel m1a_pixel_171 (.q(line10[5]), .d(d), .c(row_sel[10]), .clk(clk), .srn(and_2_out), .r(col_sel[5]));
  M1A_pixel m1a_pixel_172 (.q(line11[5]), .d(d), .c(row_sel[11]), .clk(clk), .srn(and_2_out), .r(col_sel[5]));
  M1A_pixel m1a_pixel_173 (.q(line12[5]), .d(d), .c(row_sel[12]), .clk(clk), .srn(and_2_out), .r(col_sel[5]));
  M1A_pixel m1a_pixel_174 (.q(line13[5]), .d(d), .c(row_sel[13]), .clk(clk), .srn(and_2_out), .r(col_sel[5]));
  M1A_pixel m1a_pixel_175 (.q(line14[5]), .d(d), .c(row_sel[14]), .clk(clk), .srn(and_2_out), .r(col_sel[5]));
  M1A_pixel m1a_pixel_176 (.q(line15[5]), .d(d), .c(row_sel[15]), .clk(clk), .srn(and_2_out), .r(col_sel[5]));
  M1A_pixel m1a_pixel_177 (.q(line0[4]), .d(d), .c(row_sel[0]), .clk(clk), .srn(and_2_out), .r(col_sel[4]));
  M1A_pixel m1a_pixel_178 (.q(line1[4]), .d(d), .c(row_sel[1]), .clk(clk), .srn(and_2_out), .r(col_sel[4]));
  M1A_pixel m1a_pixel_179 (.q(line2[4]), .d(d), .c(row_sel[2]), .clk(clk), .srn(and_2_out), .r(col_sel[4]));
  M1A_pixel m1a_pixel_180 (.q(line3[4]), .d(d), .c(row_sel[3]), .clk(clk), .srn(and_2_out), .r(col_sel[4]));
  M1A_pixel m1a_pixel_181 (.q(line4[4]), .d(d), .c(row_sel[4]), .clk(clk), .srn(and_2_out), .r(col_sel[4]));
  M1A_pixel m1a_pixel_182 (.q(line5[4]), .d(d), .c(row_sel[5]), .clk(clk), .srn(and_2_out), .r(col_sel[4]));
  M1A_pixel m1a_pixel_183 (.q(line6[4]), .d(d), .c(row_sel[6]), .clk(clk), .srn(and_2_out), .r(col_sel[4]));
  M1A_pixel m1a_pixel_184 (.q(line7[4]), .d(d), .c(row_sel[7]), .clk(clk), .srn(and_2_out), .r(col_sel[4]));
  M1A_pixel m1a_pixel_185 (.q(line8[4]), .d(d), .c(row_sel[8]), .clk(clk), .srn(and_2_out), .r(col_sel[4]));
  M1A_pixel m1a_pixel_186 (.q(line9[4]), .d(d), .c(row_sel[9]), .clk(clk), .srn(and_2_out), .r(col_sel[4]));
  M1A_pixel m1a_pixel_187 (.q(line10[4]), .d(d), .c(row_sel[10]), .clk(clk), .srn(and_2_out), .r(col_sel[4]));
  M1A_pixel m1a_pixel_188 (.q(line11[4]), .d(d), .c(row_sel[11]), .clk(clk), .srn(and_2_out), .r(col_sel[4]));
  M1A_pixel m1a_pixel_189 (.q(line12[4]), .d(d), .c(row_sel[12]), .clk(clk), .srn(and_2_out), .r(col_sel[4]));
  M1A_pixel m1a_pixel_190 (.q(line13[4]), .d(d), .c(row_sel[13]), .clk(clk), .srn(and_2_out), .r(col_sel[4]));
  M1A_pixel m1a_pixel_191 (.q(line14[4]), .d(d), .c(row_sel[14]), .clk(clk), .srn(and_2_out), .r(col_sel[4]));
  M1A_pixel m1a_pixel_192 (.q(line15[4]), .d(d), .c(row_sel[15]), .clk(clk), .srn(and_2_out), .r(col_sel[4]));
  M1A_pixel m1a_pixel_193 (.q(line0[3]), .d(d), .c(row_sel[0]), .clk(clk), .srn(and_2_out), .r(col_sel[3]));
  M1A_pixel m1a_pixel_194 (.q(line1[3]), .d(d), .c(row_sel[1]), .clk(clk), .srn(and_2_out), .r(col_sel[3]));
  M1A_pixel m1a_pixel_195 (.q(line2[3]), .d(d), .c(row_sel[2]), .clk(clk), .srn(and_2_out), .r(col_sel[3]));
  M1A_pixel m1a_pixel_196 (.q(line3[3]), .d(d), .c(row_sel[3]), .clk(clk), .srn(and_2_out), .r(col_sel[3]));
  M1A_pixel m1a_pixel_197 (.q(line4[3]), .d(d), .c(row_sel[4]), .clk(clk), .srn(and_2_out), .r(col_sel[3]));
  M1A_pixel m1a_pixel_198 (.q(line5[3]), .d(d), .c(row_sel[5]), .clk(clk), .srn(and_2_out), .r(col_sel[3]));
  M1A_pixel m1a_pixel_199 (.q(line6[3]), .d(d), .c(row_sel[6]), .clk(clk), .srn(and_2_out), .r(col_sel[3]));
  M1A_pixel m1a_pixel_200 (.q(line7[3]), .d(d), .c(row_sel[7]), .clk(clk), .srn(and_2_out), .r(col_sel[3]));
  M1A_pixel m1a_pixel_201 (.q(line8[3]), .d(d), .c(row_sel[8]), .clk(clk), .srn(and_2_out), .r(col_sel[3]));
  M1A_pixel m1a_pixel_202 (.q(line9[3]), .d(d), .c(row_sel[9]), .clk(clk), .srn(and_2_out), .r(col_sel[3]));
  M1A_pixel m1a_pixel_203 (.q(line10[3]), .d(d), .c(row_sel[10]), .clk(clk), .srn(and_2_out), .r(col_sel[3]));
  M1A_pixel m1a_pixel_204 (.q(line11[3]), .d(d), .c(row_sel[11]), .clk(clk), .srn(and_2_out), .r(col_sel[3]));
  M1A_pixel m1a_pixel_205 (.q(line12[3]), .d(d), .c(row_sel[12]), .clk(clk), .srn(and_2_out), .r(col_sel[3]));
  M1A_pixel m1a_pixel_206 (.q(line13[3]), .d(d), .c(row_sel[13]), .clk(clk), .srn(and_2_out), .r(col_sel[3]));
  M1A_pixel m1a_pixel_207 (.q(line14[3]), .d(d), .c(row_sel[14]), .clk(clk), .srn(and_2_out), .r(col_sel[3]));
  M1A_pixel m1a_pixel_208 (.q(line15[3]), .d(d), .c(row_sel[15]), .clk(clk), .srn(and_2_out), .r(col_sel[3]));
  M1A_pixel m1a_pixel_209 (.q(line0[2]), .d(d), .c(row_sel[0]), .clk(clk), .srn(and_2_out), .r(col_sel[2]));
  M1A_pixel m1a_pixel_210 (.q(line1[2]), .d(d), .c(row_sel[1]), .clk(clk), .srn(and_2_out), .r(col_sel[2]));
  M1A_pixel m1a_pixel_211 (.q(line2[2]), .d(d), .c(row_sel[2]), .clk(clk), .srn(and_2_out), .r(col_sel[2]));
  M1A_pixel m1a_pixel_212 (.q(line3[2]), .d(d), .c(row_sel[3]), .clk(clk), .srn(and_2_out), .r(col_sel[2]));
  M1A_pixel m1a_pixel_213 (.q(line4[2]), .d(d), .c(row_sel[4]), .clk(clk), .srn(and_2_out), .r(col_sel[2]));
  M1A_pixel m1a_pixel_214 (.q(line5[2]), .d(d), .c(row_sel[5]), .clk(clk), .srn(and_2_out), .r(col_sel[2]));
  M1A_pixel m1a_pixel_215 (.q(line6[2]), .d(d), .c(row_sel[6]), .clk(clk), .srn(and_2_out), .r(col_sel[2]));
  M1A_pixel m1a_pixel_216 (.q(line7[2]), .d(d), .c(row_sel[7]), .clk(clk), .srn(and_2_out), .r(col_sel[2]));
  M1A_pixel m1a_pixel_217 (.q(line8[2]), .d(d), .c(row_sel[8]), .clk(clk), .srn(and_2_out), .r(col_sel[2]));
  M1A_pixel m1a_pixel_218 (.q(line9[2]), .d(d), .c(row_sel[9]), .clk(clk), .srn(and_2_out), .r(col_sel[2]));
  M1A_pixel m1a_pixel_219 (.q(line10[2]), .d(d), .c(row_sel[10]), .clk(clk), .srn(and_2_out), .r(col_sel[2]));
  M1A_pixel m1a_pixel_220 (.q(line11[2]), .d(d), .c(row_sel[11]), .clk(clk), .srn(and_2_out), .r(col_sel[2]));
  M1A_pixel m1a_pixel_221 (.q(line12[2]), .d(d), .c(row_sel[12]), .clk(clk), .srn(and_2_out), .r(col_sel[2]));
  M1A_pixel m1a_pixel_222 (.q(line13[2]), .d(d), .c(row_sel[13]), .clk(clk), .srn(and_2_out), .r(col_sel[2]));
  M1A_pixel m1a_pixel_223 (.q(line14[2]), .d(d), .c(row_sel[14]), .clk(clk), .srn(and_2_out), .r(col_sel[2]));
  M1A_pixel m1a_pixel_224 (.q(line15[2]), .d(d), .c(row_sel[15]), .clk(clk), .srn(and_2_out), .r(col_sel[2]));
  M1A_pixel m1a_pixel_225 (.q(line0[1]), .d(d), .c(row_sel[0]), .clk(clk), .srn(and_2_out), .r(col_sel[1]));
  M1A_pixel m1a_pixel_226 (.q(line1[1]), .d(d), .c(row_sel[1]), .clk(clk), .srn(and_2_out), .r(col_sel[1]));
  M1A_pixel m1a_pixel_227 (.q(line2[1]), .d(d), .c(row_sel[2]), .clk(clk), .srn(and_2_out), .r(col_sel[1]));
  M1A_pixel m1a_pixel_228 (.q(line3[1]), .d(d), .c(row_sel[3]), .clk(clk), .srn(and_2_out), .r(col_sel[1]));
  M1A_pixel m1a_pixel_229 (.q(line4[1]), .d(d), .c(row_sel[4]), .clk(clk), .srn(and_2_out), .r(col_sel[1]));
  M1A_pixel m1a_pixel_230 (.q(line5[1]), .d(d), .c(row_sel[5]), .clk(clk), .srn(and_2_out), .r(col_sel[1]));
  M1A_pixel m1a_pixel_231 (.q(line6[1]), .d(d), .c(row_sel[6]), .clk(clk), .srn(and_2_out), .r(col_sel[1]));
  M1A_pixel m1a_pixel_232 (.q(line7[1]), .d(d), .c(row_sel[7]), .clk(clk), .srn(and_2_out), .r(col_sel[1]));
  M1A_pixel m1a_pixel_233 (.q(line8[1]), .d(d), .c(row_sel[8]), .clk(clk), .srn(and_2_out), .r(col_sel[1]));
  M1A_pixel m1a_pixel_234 (.q(line9[1]), .d(d), .c(row_sel[9]), .clk(clk), .srn(and_2_out), .r(col_sel[1]));
  M1A_pixel m1a_pixel_235 (.q(line10[1]), .d(d), .c(row_sel[10]), .clk(clk), .srn(and_2_out), .r(col_sel[1]));
  M1A_pixel m1a_pixel_236 (.q(line11[1]), .d(d), .c(row_sel[11]), .clk(clk), .srn(and_2_out), .r(col_sel[1]));
  M1A_pixel m1a_pixel_237 (.q(line12[1]), .d(d), .c(row_sel[12]), .clk(clk), .srn(and_2_out), .r(col_sel[1]));
  M1A_pixel m1a_pixel_238 (.q(line13[1]), .d(d), .c(row_sel[13]), .clk(clk), .srn(and_2_out), .r(col_sel[1]));
  M1A_pixel m1a_pixel_239 (.q(line14[1]), .d(d), .c(row_sel[14]), .clk(clk), .srn(and_2_out), .r(col_sel[1]));
  M1A_pixel m1a_pixel_240 (.q(line15[1]), .d(d), .c(row_sel[15]), .clk(clk), .srn(and_2_out), .r(col_sel[1]));
  M1A_pixel m1a_pixel_241 (.q(line0[0]), .d(d), .c(row_sel[0]), .clk(clk), .srn(and_2_out), .r(col_sel[0]));
  M1A_pixel m1a_pixel_242 (.q(line1[0]), .d(d), .c(row_sel[1]), .clk(clk), .srn(and_2_out), .r(col_sel[0]));
  M1A_pixel m1a_pixel_243 (.q(line2[0]), .d(d), .c(row_sel[2]), .clk(clk), .srn(and_2_out), .r(col_sel[0]));
  M1A_pixel m1a_pixel_244 (.q(line3[0]), .d(d), .c(row_sel[3]), .clk(clk), .srn(and_2_out), .r(col_sel[0]));
  M1A_pixel m1a_pixel_245 (.q(line4[0]), .d(d), .c(row_sel[4]), .clk(clk), .srn(and_2_out), .r(col_sel[0]));
  M1A_pixel m1a_pixel_246 (.q(line5[0]), .d(d), .c(row_sel[5]), .clk(clk), .srn(and_2_out), .r(col_sel[0]));
  M1A_pixel m1a_pixel_247 (.q(line6[0]), .d(d), .c(row_sel[6]), .clk(clk), .srn(and_2_out), .r(col_sel[0]));
  M1A_pixel m1a_pixel_248 (.q(line7[0]), .d(d), .c(row_sel[7]), .clk(clk), .srn(and_2_out), .r(col_sel[0]));
  M1A_pixel m1a_pixel_249 (.q(line8[0]), .d(d), .c(row_sel[8]), .clk(clk), .srn(and_2_out), .r(col_sel[0]));
  M1A_pixel m1a_pixel_250 (.q(line9[0]), .d(d), .c(row_sel[9]), .clk(clk), .srn(and_2_out), .r(col_sel[0]));
  M1A_pixel m1a_pixel_251 (.q(line10[0]), .d(d), .c(row_sel[10]), .clk(clk), .srn(and_2_out), .r(col_sel[0]));
  M1A_pixel m1a_pixel_252 (.q(line11[0]), .d(d), .c(row_sel[11]), .clk(clk), .srn(and_2_out), .r(col_sel[0]));
  M1A_pixel m1a_pixel_253 (.q(line12[0]), .d(d), .c(row_sel[12]), .clk(clk), .srn(and_2_out), .r(col_sel[0]));
  M1A_pixel m1a_pixel_254 (.q(line13[0]), .d(d), .c(row_sel[13]), .clk(clk), .srn(and_2_out), .r(col_sel[0]));
  M1A_pixel m1a_pixel_255 (.q(line14[0]), .d(d), .c(row_sel[14]), .clk(clk), .srn(and_2_out), .r(col_sel[0]));
  M1A_pixel m1a_pixel_256 (.q(line15[0]), .d(d), .c(row_sel[15]), .clk(clk), .srn(and_2_out), .r(col_sel[0]));

  // Other names for the same wires on the sheet: col[3:0] = pos[3:0]; row[3:0] = pos[7:4]
endmodule

module M1A_frame_buffer_ram (
  input  [7:0] pos,
  input  we,
  input  clk,
  input  srn,
  input  d,
  output [15:0] line0,
  output [15:0] line1,
  output [15:0] line2,
  output [15:0] line3,
  output [15:0] line4,
  output [15:0] line5,
  output [15:0] line6,
  output [15:0] line7,
  output [15:0] line8,
  output [15:0] line9,
  output [15:0] line10,
  output [15:0] line11,
  output [15:0] line12,
  output [15:0] line13,
  output [15:0] line14,
  output [15:0] line15
);

  wire and_4_out, and_5_out, even, not_1_out, not_3_out, posedge_clk, srst;
  wire [15:0] bit_extender_1_out, d_t, multiplexer_1_out, multiplexer_2_out, or_1_out, rd_data,
       shifter_1_out, shifter_2_out;

  not not_1 (not_1_out, srn);
  assign bit_extender_1_out = {{15{1'b1}}, d};  // Bit_Extender bit_extender_1
  not not_2 (even, pos[4]);
  and and_1 (posedge_clk, clk, not_3_out);
  not not_3 (not_3_out, clk);
  Shifter #(.shift("rr"), .width(16)) shifter_1 (
    .in({bit_extender_1_out[0], bit_extender_1_out[1], bit_extender_1_out[2], bit_extender_1_out[3], bit_extender_1_out[4], bit_extender_1_out[5], bit_extender_1_out[6], bit_extender_1_out[7], bit_extender_1_out[8], bit_extender_1_out[9], bit_extender_1_out[10], bit_extender_1_out[11], bit_extender_1_out[12], bit_extender_1_out[13], bit_extender_1_out[14], bit_extender_1_out[15]}),
    .\dist (pos[3:0]), .out(shifter_1_out));
  Shifter #(.shift("lr"), .width(16)) shifter_2 (.in(16'h8000), .\dist (pos[3:0]), .out(shifter_2_out));
  and and_2 (srst, posedge_clk, not_1_out);
  assign or_1_out = shifter_2_out | rd_data;  // OR_Gate or_1, 16 bits wide
  assign d_t = shifter_1_out & or_1_out;  // AND_Gate and_3, 16 bits wide
  and and_4 (and_4_out, we, even);
  and and_5 (and_5_out, we, pos[4]);
  // RAM #(.addrWidth(3), .clearpin("true"), .dataWidth(16), .enables("line"), .line("octo")) ram_1: pin names not known; wires that end beside it: 3'b000, line0, line2, line4, line6, line8, line10, line12, line14
  // Decoder #(.enable("false"), .select(3)) decoder_1: pin names not known; wires that end beside it: pos[7:5], and_4_out, clk, d_t
  // RAM #(.addrWidth(3), .clearpin("true"), .dataWidth(16), .enables("line"), .line("octo")) ram_2: pin names not known; wires that end beside it: 3'b000, srst, line1, line3, line5, line7, line9, line11, line13, line15
  // Decoder #(.enable("false"), .select(3)) decoder_2: pin names not known; wires that end beside it: pos[7:5], and_5_out, clk, d_t
  Multiplexer #(.select(3), .width(16)) multiplexer_1 (
    .in0(line0), .in1(line2), .in2(line4), .in3(line6), .in4(line8), .in5(line10), .in6(line12),
    .in7(line14), .out(multiplexer_1_out), .sel(pos[7:5]));
  Multiplexer #(.select(3), .width(16)) multiplexer_2 (
    .in0(line1), .in1(line3), .in2(line5), .in3(line7), .in4(line9), .in5(line11), .in6(line13),
    .in7(line15), .out(multiplexer_2_out), .sel(pos[7:5]));
  Multiplexer #(.width(16)) multiplexer_3 (
    .in0(multiplexer_1_out), .in1(multiplexer_2_out), .out(rd_data), .sel(pos[4]));

  // Other names for the same wires on the sheet: c = clk; bit_sel[3:0] = pos[3:0]; odd = pos[4];
  //   hw_adr[2:0] = pos[7:5]

  // Notes on the sheet:
  //   此模块为frame_buffer的RAM方式实现，用于加快仿真速度
endmodule

module M1A_frame (
  input  [15:0] row0,
  input  [15:0] row1,
  input  [15:0] row2,
  input  [15:0] row3,
  input  [15:0] row4,
  input  [15:0] row5,
  input  [15:0] row6,
  input  [15:0] row7,
  input  [15:0] row8,
  input  [15:0] row9,
  input  [15:0] row10,
  input  [15:0] row11,
  input  [15:0] row12,
  input  [15:0] row13,
  input  [15:0] row14,
  input  [15:0] row15,
  input  refresh,
  input  clk,
  input  srn,
  output [15:0] line0,
  output [15:0] line1,
  output [15:0] line2,
  output [15:0] line3,
  output [15:0] line4,
  output [15:0] line5,
  output [15:0] line6,
  output [15:0] line7,
  output [15:0] line8,
  output [15:0] line9,
  output [15:0] line10,
  output [15:0] line11,
  output [15:0] line12,
  output [15:0] line13,
  output [15:0] line14,
  output [15:0] line15
);

  wire and_1_out, and_2_out, not_1_out, not_2_out;

  not not_1 (not_1_out, clk);
  not not_2 (not_2_out, srn);
  and and_1 (and_1_out, clk, not_1_out);
  and and_2 (and_2_out, and_1_out, not_2_out);
  Register #(.width(16)) register_1 (.D(row0), .en(refresh), .Q(line0), .clk(clk), .clr(and_2_out));
  Register #(.width(16)) register_2 (.D(row1), .en(refresh), .Q(line1), .clk(clk), .clr(and_2_out));
  Register #(.width(16)) register_3 (.D(row2), .en(refresh), .Q(line2), .clk(clk), .clr(and_2_out));
  Register #(.width(16)) register_4 (.D(row3), .en(refresh), .Q(line3), .clk(clk), .clr(and_2_out));
  Register #(.width(16)) register_5 (.D(row4), .en(refresh), .Q(line4), .clk(clk), .clr(and_2_out));
  Register #(.width(16)) register_6 (.D(row5), .en(refresh), .Q(line5), .clk(clk), .clr(and_2_out));
  Register #(.width(16)) register_7 (.D(row6), .en(refresh), .Q(line6), .clk(clk), .clr(and_2_out));
  Register #(.width(16)) register_8 (.D(row7), .en(refresh), .Q(line7), .clk(clk), .clr(and_2_out));
  Register #(.width(16)) register_9 (.D(row8), .en(refresh), .Q(line8), .clk(clk), .clr(and_2_out));
  Register #(.width(16)) register_10 (.D(row9), .en(refresh), .Q(line9), .clk(clk), .clr(and_2_out));
  Register #(.width(16)) register_11 (.D(row10), .en(refresh), .Q(line10), .clk(clk), .clr(and_2_out));
  Register #(.width(16)) register_12 (.D(row11), .en(refresh), .Q(line11), .clk(clk), .clr(and_2_out));
  Register #(.width(16)) register_13 (.D(row12), .en(refresh), .Q(line12), .clk(clk), .clr(and_2_out));
  Register #(.width(16)) register_14 (.D(row13), .en(refresh), .Q(line13), .clk(clk), .clr(and_2_out));
  Register #(.width(16)) register_15 (.D(row14), .en(refresh), .Q(line14), .clk(clk), .clr(and_2_out));
  Register #(.width(16)) register_16 (.D(row15), .en(refresh), .Q(line15), .clk(clk), .clr(and_2_out));
endmodule

module M1A_pulse_expansion (
  input  srn,
  input  clk,
  input  d,
  output q
);

  wire shift_register_1_p1;
  wire [4:0] undriven;

  // Shift_Register #(.length(5)) shift_register_1: pin names not known; wires that end beside it: shift_register_1_p1, 1'b1, clk, d
  not not_1 (shift_register_1_p1, srn);
  or or_1 (q, undriven[0], undriven[1], undriven[2], undriven[3], undriven[4]);
endmodule

module M2A_vsync (
  input  clk,
  input  srn,
  input  [7:0] period,
  output [7:0] sync_cnt,
  output [7:0] vsync
);

  wire m2_is_equal_8_1_e, not_1_out;
  wire [0:0] m1a_pulse_expansion_1_q;

  M2_counter_8 m2_counter_8_1 (.q(sync_cnt), .d({8{1'b0}}), .clk(clk), .srn(srn), .load(m2_is_equal_8_1_e), .en(1'b1));
  // Probe on sync_cnt
  M2_is_equal_8 m2_is_equal_8_1 (.E(m2_is_equal_8_1_e), .A(sync_cnt), .B(period));
  M1A_pulse_expansion m1a_pulse_expansion_1 (
    .q(m1a_pulse_expansion_1_q[0]), .srn(srn), .clk(clk), .d(m2_is_equal_8_1_e));
  Register register_1 (.D({{7{1'b0}}, m1a_pulse_expansion_1_q[0]}), .en(1'b1), .clk(clk), .Q(vsync), .clr(not_1_out));
  not not_1 (not_1_out, srn);
endmodule

module M2B_matrix (
  input  [31:0] ram_adr,
  input  ram_we,
  input  [3:0] ram_be,
  input  [31:0] ram_din,
  input  clk,
  input  srn,
  output [7:0] sync_cnt,
  output [31:0] ram_dout,
  output [7:0] dbg_pos,
  output [15:0] line0,
  output [15:0] line1,
  output [15:0] line2,
  output [15:0] line3,
  output [15:0] line4,
  output [15:0] line5,
  output [15:0] line6,
  output [15:0] line7,
  output [15:0] line8,
  output [15:0] line9,
  output [15:0] line10,
  output [15:0] line11,
  output [15:0] line12,
  output [15:0] line13,
  output [15:0] line14,
  output [15:0] line15
);

  wire and_1_out, bitselector_1_out, bitselector_2_out, clear_n, is_reg_data, nand_1_out, not_2_out, pixel,
       refresh, we_pixel, we_pos, we_refresh;
  wire [3:0] multiplexer_2_out;
  wire [7:0] bit_extender_1_out, bit_extender_2_out, bit_extender_3_out, bit_extender_4_out,
       bit_extender_5_out, m2a_vsync_1_vsync;
  wire [15:0] m1a_frame_buffer_ram_1_line0, m1a_frame_buffer_ram_1_line1, m1a_frame_buffer_ram_1_line2,
       m1a_frame_buffer_ram_1_line3, m1a_frame_buffer_ram_1_line4, m1a_frame_buffer_ram_1_line5,
       m1a_frame_buffer_ram_1_line6, m1a_frame_buffer_ram_1_line7, m1a_frame_buffer_ram_1_line8,
       m1a_frame_buffer_ram_1_line9, m1a_frame_buffer_ram_1_line10, m1a_frame_buffer_ram_1_line11,
       m1a_frame_buffer_ram_1_line12, m1a_frame_buffer_ram_1_line13, m1a_frame_buffer_ram_1_line14,
       m1a_frame_buffer_ram_1_line15, multiplexer_1_out;
  wire [31:24] vsync;

  // Probe on and_1_out
  and and_1 (and_1_out, ram_adr[8], ram_we);
  and and_2 (we_pixel, ram_be[0], and_1_out);
  and and_3 (we_pos, ram_be[1], and_1_out);
  and and_4 (we_refresh, ram_be[2], and_1_out);
  // NoConnect on ram_be[3]
  // NoConnect on ram_din[31:24]
  not not_1 (is_reg_data, ram_adr[8]);
  BitSelector bitselector_1 (.in(ram_din[23:16]), .out(bitselector_1_out), .sel(3'b000));
  not not_2 (not_2_out, bitselector_2_out);
  BitSelector bitselector_2 (.in(ram_din[23:16]), .out(bitselector_2_out), .sel(3'b000));
  M2A_vsync m2a_vsync_1 (.sync_cnt(sync_cnt), .vsync(m2a_vsync_1_vsync), .clk(clk), .srn(srn), .period(8'h78));
  assign bit_extender_1_out = {{7{ram_adr[8]}}, ram_adr[8]};  // Bit_Extender bit_extender_1
  M2_counter_8 m2_counter_8_1 (.q(dbg_pos), .d(ram_din[15:8]), .clk(clk), .srn(srn), .load(we_pos), .en(we_pixel));
  BitSelector bitselector_3 (.in(ram_din[7:0]), .out(pixel), .sel(3'b000));
  and and_5 (refresh, we_refresh, bitselector_1_out);
  and and_6 (clear_n, srn, nand_1_out);
  nand nand_1 (nand_1_out, we_refresh, not_2_out);
  assign vsync = m2a_vsync_1_vsync & bit_extender_1_out;  // AND_Gate and_7, 8 bits wide
  // Probe on dbg_pos
  M1A_frame_buffer_ram m1a_frame_buffer_ram_1 (
    .line12(m1a_frame_buffer_ram_1_line12), .line13(m1a_frame_buffer_ram_1_line13),
    .line14(m1a_frame_buffer_ram_1_line14), .line15(m1a_frame_buffer_ram_1_line15),
    .line0(m1a_frame_buffer_ram_1_line0), .line1(m1a_frame_buffer_ram_1_line1),
    .line2(m1a_frame_buffer_ram_1_line2), .line3(m1a_frame_buffer_ram_1_line3),
    .line4(m1a_frame_buffer_ram_1_line4), .line5(m1a_frame_buffer_ram_1_line5),
    .line6(m1a_frame_buffer_ram_1_line6), .line7(m1a_frame_buffer_ram_1_line7),
    .line8(m1a_frame_buffer_ram_1_line8), .line9(m1a_frame_buffer_ram_1_line9),
    .line10(m1a_frame_buffer_ram_1_line10), .line11(m1a_frame_buffer_ram_1_line11), .we(we_pixel), .clk(clk),
    .srn(clear_n), .d(pixel), .pos(dbg_pos));
  Multiplexer #(.enable("true"), .select(4), .width(16)) multiplexer_1 (
    .in0(line0), .in1(line1), .in2(line2), .in3(line3), .in4(line4), .in5(line5), .in6(line6), .in7(line7),
    .in8(line8), .in9(line9), .in10(line10), .in11(line11), .in12(line12), .in13(line13), .in14(line14),
    .in15(line15), .out(multiplexer_1_out), .sel(ram_adr[7:4]), .en(is_reg_data));
  Multiplexer #(.enable("true"), .select(2), .width(4)) multiplexer_2 (
    .in0({multiplexer_1_out[12], multiplexer_1_out[13], multiplexer_1_out[14], multiplexer_1_out[15]}),
    .in1({multiplexer_1_out[8], multiplexer_1_out[9], multiplexer_1_out[10], multiplexer_1_out[11]}),
    .in2({multiplexer_1_out[4], multiplexer_1_out[5], multiplexer_1_out[6], multiplexer_1_out[7]}),
    .in3({multiplexer_1_out[0], multiplexer_1_out[1], multiplexer_1_out[2], multiplexer_1_out[3]}),
    .out(multiplexer_2_out), .sel(ram_adr[3:2]), .en(is_reg_data));
  M1A_frame m1a_frame_1 (
    .line1(line1), .line2(line2), .line3(line3), .line4(line4), .line5(line5), .line6(line6), .line7(line7),
    .line8(line8), .line9(line9), .line10(line10), .line11(line11), .line12(line12), .line13(line13),
    .line14(line14), .line0(line0), .line15(line15), .clk(clk), .srn(clear_n),
    .row1(m1a_frame_buffer_ram_1_line1), .row2(m1a_frame_buffer_ram_1_line2),
    .row3(m1a_frame_buffer_ram_1_line3), .row4(m1a_frame_buffer_ram_1_line4),
    .row5(m1a_frame_buffer_ram_1_line5), .row6(m1a_frame_buffer_ram_1_line6),
    .row7(m1a_frame_buffer_ram_1_line7), .row8(m1a_frame_buffer_ram_1_line8),
    .row9(m1a_frame_buffer_ram_1_line9), .row10(m1a_frame_buffer_ram_1_line10),
    .row11(m1a_frame_buffer_ram_1_line11), .row12(m1a_frame_buffer_ram_1_line12),
    .row13(m1a_frame_buffer_ram_1_line13), .row14(m1a_frame_buffer_ram_1_line14),
    .row0(m1a_frame_buffer_ram_1_line0), .row15(m1a_frame_buffer_ram_1_line15), .refresh(refresh));
  assign bit_extender_2_out = {{7{1'b0}}, multiplexer_2_out[0]};  // Bit_Extender bit_extender_2
  assign bit_extender_3_out = {{7{1'b0}}, multiplexer_2_out[1]};  // Bit_Extender bit_extender_3
  assign bit_extender_4_out = {{7{1'b0}}, multiplexer_2_out[2]};  // Bit_Extender bit_extender_4
  assign bit_extender_5_out = {{7{1'b0}}, multiplexer_2_out[3]};  // Bit_Extender bit_extender_5
  assign ram_dout = {vsync, {24{1'b0}}} | {bit_extender_5_out, bit_extender_4_out, bit_extender_3_out, bit_extender_2_out};  // OR_Gate or_1, 32 bits wide

  // Other names for the same wires on the sheet: pos[7:0] = dbg_pos; reg_adr[7:0] = ram_adr[7:0];
  //   is_reg_ctrl = ram_adr[8]; byte_pixel[7:0] = ram_din[7:0]; byte_pos[7:0] = ram_din[15:8];
  //   byte_refresh[7:0] = ram_din[23:16]

  // Notes on the sheet:
  //   注意：读取地址的低2位始终为0，所以4个像素为一组
  //   这里line的高位对应的是屏幕左侧，但最左侧的坐标是0，所以需要翻转比特顺序
endmodule

module M2A_bus_interconnect (
  input  ram_re,
  input  [31:0] s0_dout,
  input  [31:0] s1_dout,
  input  [31:0] ram_adr,
  input  ram_we,
  input  [3:0] ram_be,
  input  [31:0] s2_dout,
  input  [31:0] ram_din,
  input  [31:0] s3_dout,
  output [31:0] s0_adr,
  output [31:0] s1_adr,
  output [31:0] s2_adr,
  output [31:0] s3_adr,
  output [3:0] s0_be,
  output [3:0] s1_be,
  output [3:0] s2_be,
  output [3:0] s3_be,
  output [31:0] s0_din,
  output [31:0] ram_dout,
  output [31:0] s1_din,
  output [31:0] s2_din,
  output [31:0] s3_din,
  output s0_we,
  output s1_we,
  output s2_we,
  output s3_we
);

  wire nor_1_out, nor_2_out, s0_cs, s1_cs, s2_cs, s3_cs;
  wire [31:0] and_3_out, and_4_out, and_5_out, and_6_out, bit_extender_1_out, bit_extender_2_out,
       bit_extender_3_out, bit_extender_4_out, bit_extender_5_out;

  and and_1 (s0_cs, ram_adr[12], nor_1_out);
  // NoConnect on ram_adr[11]
  nor nor_1 (nor_1_out, ram_adr[13], ram_adr[14], ram_adr[15], ram_adr[16], ram_adr[17], ram_adr[18], ram_adr[19], ram_adr[20], ram_adr[21], ram_adr[22], ram_adr[23], ram_adr[24], ram_adr[25], ram_adr[26], ram_adr[27], ram_adr[28], ram_adr[29], ram_adr[30], ram_adr[31]);
  and and_2 (s1_cs, ram_adr[28], nor_2_out);
  nor nor_2 (nor_2_out, ram_adr[29], ram_adr[30], ram_adr[31]);
  nor nor_3 (s2_cs, ram_adr[9], ram_adr[10], ram_adr[11], ram_adr[12], ram_adr[13], ram_adr[14], ram_adr[15], ram_adr[16], ram_adr[17], ram_adr[18], ram_adr[19], ram_adr[20], ram_adr[21], ram_adr[22], ram_adr[23], ram_adr[24], ram_adr[25], ram_adr[26], ram_adr[27], ram_adr[28], ram_adr[29], ram_adr[30], ~ram_adr[31]);  // NOR_Gate
  assign bit_extender_1_out = {{31{ram_re}}, ram_re};  // Bit_Extender bit_extender_1
  assign bit_extender_2_out = {{31{s0_cs}}, s0_cs};  // Bit_Extender bit_extender_2
  assign bit_extender_3_out = {{31{s1_cs}}, s1_cs};  // Bit_Extender bit_extender_3
  assign bit_extender_4_out = {{31{s2_cs}}, s2_cs};  // Bit_Extender bit_extender_4
  assign bit_extender_5_out = {{31{s3_cs}}, s3_cs};  // Bit_Extender bit_extender_5
  assign and_3_out = s0_dout & bit_extender_1_out & bit_extender_2_out;  // AND_Gate and_3, 32 bits wide
  assign and_4_out = s1_dout & bit_extender_1_out & bit_extender_3_out;  // AND_Gate and_4, 32 bits wide
  assign and_5_out = s2_dout & bit_extender_1_out & bit_extender_4_out;  // AND_Gate and_5, 32 bits wide
  assign and_6_out = s3_dout & bit_extender_1_out & bit_extender_5_out;  // AND_Gate and_6, 32 bits wide
  nor nor_4 (s3_cs, ram_adr[3], ram_adr[4], ram_adr[5], ram_adr[6], ram_adr[7], ram_adr[8], ram_adr[9], ram_adr[10], ram_adr[11], ram_adr[12], ram_adr[13], ram_adr[14], ram_adr[15], ram_adr[16], ram_adr[17], ram_adr[18], ram_adr[19], ram_adr[20], ram_adr[21], ram_adr[22], ram_adr[23], ram_adr[24], ram_adr[25], ram_adr[26], ram_adr[27], ram_adr[28], ram_adr[29], ~ram_adr[30], ~ram_adr[31]);  // NOR_Gate
  assign ram_dout = and_3_out | and_4_out | and_5_out | and_6_out;  // OR_Gate or_1, 32 bits wide
  and and_7 (s0_we, s0_cs, ram_we);
  and and_8 (s1_we, s1_cs, ram_we);
  and and_9 (s2_we, s2_cs, ram_we);
  and and_10 (s3_we, s3_cs, ram_we);

  assign s0_adr = ram_adr;
  assign s0_be = ram_be;
  assign s0_din = ram_din;
  assign s1_adr = ram_adr;
  assign s1_be = ram_be;
  assign s1_din = ram_din;
  assign s2_adr = ram_adr;
  assign s2_be = ram_be;
  assign s2_din = ram_din;
  assign s3_adr = ram_adr;
  assign s3_be = ram_be;
  assign s3_din = ram_din;

  // Notes on the sheet:
  //   0x0000_1000 ~ 0x0000_1FFF
  //   Data RAM:
  //   0x1000_0000 ~ 0x1FFF_FFFF
  //   Data ROM:
  //   0x8000_0000 ~ 0x8000_001FF
  //   Matrix:
  //   0xC000_0000 ~ 0xC000_00007
  //   GPIO
endmodule

module M2A_key (
  input  up,
  input  down,
  input  left,
  input  right,
  input  x,
  input  csn,
  input  y,
  input  ok,
  input  esc,
  input  clk,
  input  srn,
  output [31:0] key_out
);

  wire and_1_out, and_2_out, D, L, not_1_out, not_2_out, not_3_out, not_4_out, R, U;
  wire [7:1] CTRL;
  wire [31:0] bit_extender_3_out, key_out_t, register_2_q;

  Register register_1 (
    .D({esc, ok, y, x, right, left, down, up}), .en(1'b1), .clk(clk),
    .Q({CTRL[7], CTRL[5], CTRL[3], CTRL[1], R, L, D, U}), .clr(not_1_out));
  not not_1 (not_1_out, srn);
  not not_2 (not_2_out, R);
  not not_3 (not_3_out, D);
  xor xor_1 (key_out_t[0], R, L);
  assign key_out_t[7:1] = {{6{and_1_out}}, and_1_out};  // Bit_Extender bit_extender_1
  and and_1 (and_1_out, not_2_out, L);
  xor xor_2 (key_out_t[8], D, U);
  assign key_out_t[15:9] = {{6{and_2_out}}, and_2_out};  // Bit_Extender bit_extender_2
  and and_2 (and_2_out, not_3_out, U);
  // Probe on key_out_t[7:0]
  // Probe on key_out_t[15:8]
  // Probe on key_out_t[31:24]
  M2_random_8 m2_random_8_1 (.ssn(srn), .clk(clk), .out_3(key_out_t[31:24]));
  Register #(.width(32)) register_2 (
    .D({key_out_t[31:24], {2{CTRL[7]}}, {2{CTRL[5]}}, {2{CTRL[3]}}, {2{CTRL[1]}}, key_out_t[15:0]}),
    .en(1'b1), .clk(clk), .Q(register_2_q), .clr(not_4_out));
  not not_4 (not_4_out, srn);
  assign bit_extender_3_out = {{31{csn}}, csn};  // Bit_Extender bit_extender_3
  assign key_out = ~bit_extender_3_out & register_2_q;  // AND_Gate and_3, 32 bits wide

  // Other names for the same wires on the sheet: LR[7:0] = key_out_t[7:0]; UD[7:0] = key_out_t[15:8];
  //   CTRL (some bits) = {CTRL[7], CTRL[5], CTRL[3], CTRL[1]};
  //   key_out_t[23:16] = {{2{CTRL[7]}}, {2{CTRL[5]}}, {2{CTRL[3]}}, {2{CTRL[1]}}}; X_t = CTRL[1]; Y_t = CTRL[3];
  //   ok_t = CTRL[5]; esc_t = CTRL[7]; RAND[7:0] = key_out_t[31:24]

  // Notes on the sheet:
  //   无/左右/上下 =   0 = 0x00
  //   实际硬件实现时
  //   需要考虑亚稳态问题
  //   但仿真不存在亚稳态问题
  //   因此此处省略同步模块
  //   4个方向键使用特殊的编码，可使程序简化
  //   右 =   1 = 0x01
  //   左 =  -1 = 0xFF
  //   下 =   1 = 0x01
  //   上 =  -1 = 0xFF
endmodule

module M1A_led (
  input  [31:0] led_din,
  input  led_we,
  input  [3:0] led_be,
  input  clk,
  input  srn,
  output led0,
  output led1,
  output led2,
  output led3,
  output led4,
  output led5,
  output led6,
  output led7
);

  wire and_1_out, bitselector_2_out, not_1_out;
  wire [7:0] bitselector_1_out;

  not not_1 (not_1_out, srn);
  BitSelector #(.group(8), .width(32)) bitselector_1 (.in(led_din), .out(bitselector_1_out), .sel(2'b00));
  and and_1 (and_1_out, led_we, bitselector_2_out);
  BitSelector #(.width(4)) bitselector_2 (.in(led_be), .out(bitselector_2_out), .sel(2'b00));
  Register register_1 (
    .D(bitselector_1_out), .en(and_1_out), .clk(clk), .Q({led7, led6, led5, led4, led3, led2, led1, led0}),
    .clr(not_1_out));
endmodule

module M2D_CPU (
  input  [31:0] rom_dout,
  input  ext_intr,
  input  srn,
  input  [31:0] ram_dout,
  input  clk,
  output [31:0] rom_adr,
  output [31:0] ram_adr,
  output ram_re,
  output ram_we,
  output [3:0] ram_be,
  output [31:0] ram_din,
  output [3:0] SCAUSE,
  output [31:0] SEPC,
  output ebreak
);

  wire ecall, ext_intr_t, i_ebreak, i_ecall, i_misalign, i_unknown, IF_branch, IF_jal, IF_jalr, IF_stall_n,
       intr, jump, m1a_ppl_if_id_1_out_11, m1a_ppl_if_id_1_out_12, m1a_ppl_if_id_1_out_13, m2b_ex_1_b, MEM_b,
       misalign, pc_we, ppl_EX_MEM_ena, ppl_EX_MEM_srn, ppl_ID_EX_ena, ppl_ID_EX_srn, ppl_IF_ID_ena,
       ppl_IF_ID_srn, ppl_MEM_WB_ena, ppl_MEM_WB_srn, pred, rd_we, rsn, stall_n, unknown;
  wire [4:0] m1a_ppl_id_ex_1_out_23, m2b_ex_1_rs2_sel, MEM_rs2_sel, rd_sel, rs1_sel, rs2_sel;
  wire [7:0] EX_WB_ctrl, ID_MEM_ctrl, m1a_ppl_id_ex_1_out_20, m1a_ppl_id_ex_1_out_21, m2b_ex_1_mem_ctrl,
       m2b_ex_1_wb_ctrl, m2b_id_1_ex_ctrl, m2b_id_1_wb_ctrl, m2b_mem_1_wb_ctrl, MEM_ctrl, MEM_WB_ctrl,
       WB_WB_ctrl;
  wire [31:0] IF_instr, IF_pc, intr_adr, jump_adr, m1a_ppl_id_ex_1_out_14, m1a_ppl_id_ex_1_out_15,
       m1a_ppl_id_ex_1_out_16, m1a_ppl_id_ex_1_out_17, m1a_ppl_id_ex_1_out_18, m1a_ppl_id_ex_1_out_19,
       m1a_ppl_if_id_1_out_9, m1a_ppl_if_id_1_out_10, m1a_ppl_mem_wb_1_out_9, m1a_ppl_mem_wb_1_out_10,
       m2b_ex_1_a, m2b_ex_1_m, m2b_ex_1_pc, m2b_id_1_a1, m2b_id_1_a2, m2b_id_1_b1, m2b_id_1_b2, m2b_id_1_m,
       m2b_id_1_pc, m2b_mem_1_m, m2b_mem_1_pc, m_src, MEM_a, MEM_m, MEM_pc, MEM_pc4, MEM_pc_a, pred_adr,
       rd_dat, reg_rs1, reg_rs2, rs1_src, rs2_src, undriven, WB_pc;

  Register #(.width(1)) register_1 (.D(ext_intr), .clk(clk), .Q(ext_intr_t), .clr(rsn));  // open: en
  // Probe on IF_instr[31:25]
  // Probe on IF_instr[24:20]
  // Probe on IF_instr[19:15]
  // Probe on IF_instr[14:12]
  // Probe on IF_instr[11:7]
  // Probe on IF_instr[6:0]
  // Probe on IF_pc
  M2B_IF m2b_if_1 (
    .pc(IF_pc), .rom_adr(rom_adr), .instr(IF_instr), .is_branch(IF_branch), .is_jal(IF_jal),
    .is_jalr(IF_jalr), .is_ecall(i_ecall), .is_ebreak(i_ebreak), .rom_dout(rom_dout), .pred_adr(pred_adr),
    .jump_adr(jump_adr), .intr_adr(intr_adr), .stall_n(IF_stall_n), .pred(pred), .jump(jump), .intr(intr),
    .pc_we(pc_we), .pc_srn(srn), .clk(clk));
  M2B_bpu m2b_bpu_1 (
    .pred_adr(pred_adr), .jump_adr(jump_adr), .jump(jump), .pred(pred), .clk(clk), .srn(srn), .IF_pc(IF_pc),
    .IF_branch(IF_branch), .IF_jal(IF_jal), .IF_jalr(IF_jalr), .MEM_pc(MEM_pc), .MEM_pc4(MEM_pc4),
    .MEM_ctrl(MEM_ctrl), .MEM_a(MEM_a), .MEM_b(MEM_b));
  // Probe on m1a_ppl_if_id_1_out_9
  M1A_ppl_IF_ID m1a_ppl_if_id_1 (
    .out_9(m1a_ppl_if_id_1_out_9), .out_10(m1a_ppl_if_id_1_out_10), .out_11(m1a_ppl_if_id_1_out_11),
    .out_12(m1a_ppl_if_id_1_out_12), .out_13(m1a_ppl_if_id_1_out_13), .clk(clk), .srn(ppl_IF_ID_srn),
    .ena(ppl_IF_ID_ena), .in_4(IF_pc), .in_5(IF_instr), .in_6(IF_branch), .in_7(IF_jal), .in_8(IF_jalr));
  // Probe on m1a_ppl_if_id_1_out_10
  // Probe on rs1_src
  // Probe on rs2_src
  // NoConnect on undriven
  // Probe on m2b_id_1_pc
  M2B_ID m2b_id_1 (
    .unknown(i_unknown), .pc(m2b_id_1_pc), .EX_ctrl(m2b_id_1_ex_ctrl), .MEM_ctrl(ID_MEM_ctrl),
    .WB_ctrl(m2b_id_1_wb_ctrl), .rs1_sel(rs1_sel), .rs2_sel(rs2_sel), .b1(m2b_id_1_b1), .a1(m2b_id_1_a1),
    .a2(m2b_id_1_a2), .b2(m2b_id_1_b2), .m(m2b_id_1_m), .instr(m1a_ppl_if_id_1_out_10),
    .is_branch(m1a_ppl_if_id_1_out_11), .is_jal(m1a_ppl_if_id_1_out_12), .is_jalr(m1a_ppl_if_id_1_out_13),
    .pc_in(m1a_ppl_if_id_1_out_9), .rs1_src(rs1_src), .rs2_src(rs2_src));
  // Probe on m2b_id_1_b1
  // Probe on m2b_id_1_b2
  // Probe on m2b_id_1_a1
  // Probe on m2b_id_1_a2
  // Probe on m2b_id_1_m
  M2C_dfu m2c_dfu_1 (
    .EX_rs1_src(rs1_src), .EX_rs2_src(rs2_src), .MEM_rs2_src(m_src), .EX_WB_ctrl(EX_WB_ctrl),
    .MEM_WB_ctrl(MEM_WB_ctrl), .WB_WB_ctrl(WB_WB_ctrl), .ID_MEM_ctrl(ID_MEM_ctrl), .MEM_MEM_ctrl(MEM_ctrl),
    .ID_rs1_sel(rs1_sel), .ID_rs2_sel(rs2_sel), .MEM_rs2_sel(MEM_rs2_sel), .reg_rs1(reg_rs1),
    .reg_rs2(reg_rs2), .EX_rs(undriven), .MEM_rs(MEM_pc_a), .MEM_m(MEM_m), .WB_rs(rd_dat));
  M1A_ppl_ID_EX m1a_ppl_id_ex_1 (
    .out_14(m1a_ppl_id_ex_1_out_14), .out_15(m1a_ppl_id_ex_1_out_15), .out_16(m1a_ppl_id_ex_1_out_16),
    .out_17(m1a_ppl_id_ex_1_out_17), .out_18(m1a_ppl_id_ex_1_out_18), .out_19(m1a_ppl_id_ex_1_out_19),
    .out_20(m1a_ppl_id_ex_1_out_20), .out_21(m1a_ppl_id_ex_1_out_21), .out_22(EX_WB_ctrl),
    .out_23(m1a_ppl_id_ex_1_out_23), .clk(clk), .srn(ppl_ID_EX_srn), .ena(ppl_ID_EX_ena), .in_4(m2b_id_1_pc),
    .in_5(m2b_id_1_b1), .in_6(m2b_id_1_b2), .in_7(m2b_id_1_a1), .in_8(m2b_id_1_a2), .in_9(m2b_id_1_m),
    .in_10(m2b_id_1_ex_ctrl), .in_11(ID_MEM_ctrl), .in_12(m2b_id_1_wb_ctrl), .in_13(rs2_sel));
  // Probe on m1a_ppl_id_ex_1_out_14
  // Probe on m1a_ppl_id_ex_1_out_15
  // Probe on m1a_ppl_id_ex_1_out_16
  // Probe on m1a_ppl_id_ex_1_out_17
  // Probe on m1a_ppl_id_ex_1_out_18
  // Probe on m1a_ppl_id_ex_1_out_19
  // Probe on m1a_ppl_id_ex_1_out_20
  // Probe on m1a_ppl_id_ex_1_out_21
  // Probe on EX_WB_ctrl
  // Probe on m1a_ppl_id_ex_1_out_23
  M2A_hdu m2a_hdu_1 (
    .stall_n(stall_n), .ID_rs1_sel(rs1_sel), .ID_rs2_sel(rs2_sel), .ID_MEM_ctrl(ID_MEM_ctrl),
    .EX_WB_ctrl(EX_WB_ctrl), .MEM_WB_ctrl(MEM_WB_ctrl));
  M2A_eiu m2a_eiu_1 (
    .SCAUSE(SCAUSE), .SEPC(SEPC), .intr(intr), .intr_adr(intr_adr), .ecall(ecall), .unknow(unknown),
    .misalign(misalign), .ext_intr(ext_intr_t), .clk(clk), .srn(srn), .pc(WB_pc));
  M2B_EX m2b_ex_1 (
    .b(m2b_ex_1_b), .a(m2b_ex_1_a), .m(m2b_ex_1_m), .MEM_ctrl(m2b_ex_1_mem_ctrl), .WB_ctrl(m2b_ex_1_wb_ctrl),
    .rs2_sel(m2b_ex_1_rs2_sel), .pc(m2b_ex_1_pc), .rs2_sel_in(m1a_ppl_id_ex_1_out_23),
    .pc_in(m1a_ppl_id_ex_1_out_14), .b1(m1a_ppl_id_ex_1_out_15), .b2(m1a_ppl_id_ex_1_out_16),
    .a1(m1a_ppl_id_ex_1_out_17), .a2(m1a_ppl_id_ex_1_out_18), .m_in(m1a_ppl_id_ex_1_out_19),
    .EX_ctrl_in(m1a_ppl_id_ex_1_out_20), .MEM_ctrl_in(m1a_ppl_id_ex_1_out_21), .WB_ctrl_in(EX_WB_ctrl));
  M1A_ppl_EX_MEM m1a_ppl_ex_mem_1 (
    .out_11(MEM_pc), .out_12(MEM_b), .out_13(MEM_a), .out_14(MEM_m), .out_15(MEM_ctrl), .out_16(MEM_WB_ctrl),
    .out_17(MEM_rs2_sel), .clk(clk), .srn(ppl_EX_MEM_srn), .ena(ppl_EX_MEM_ena), .in_4(m2b_ex_1_pc),
    .in_5(m2b_ex_1_b), .in_6(m2b_ex_1_a), .in_7(m2b_ex_1_m), .in_8(m2b_ex_1_mem_ctrl),
    .in_9(m2b_ex_1_wb_ctrl), .in_10(m2b_ex_1_rs2_sel));
  // Probe on MEM_a
  // Probe on MEM_m
  // Probe on MEM_ctrl
  // Probe on MEM_WB_ctrl
  // Probe on MEM_rs2_sel
  // Probe on MEM_pc
  M2A_cu m2a_cu_1 (
    .IF_stall_n(IF_stall_n), .IF_ID_ena(ppl_IF_ID_ena), .ID_EX_ena(ppl_ID_EX_ena),
    .EX_MEM_ena(ppl_EX_MEM_ena), .MEM_WB_ena(ppl_MEM_WB_ena), .ID_EX_srn(ppl_ID_EX_srn),
    .IF_ID_srn(ppl_IF_ID_srn), .EX_MEM_srn(ppl_EX_MEM_srn), .MEM_WB_srn(ppl_MEM_WB_srn), .pc_we(pc_we),
    .stall_n(stall_n), .jump(jump), .intr(intr), .srn(srn));
  M2B_MEM m2b_mem_1 (
    .WB_ctrl(m2b_mem_1_wb_ctrl), .a(MEM_pc_a), .pc(m2b_mem_1_pc), .pc4(MEM_pc4), .ram_adr(ram_adr),
    .ram_re(ram_re), .ram_we(ram_we), .ram_be(ram_be), .ram_din(ram_din), .m(m2b_mem_1_m),
    .misalign(i_misalign), .pc_in(MEM_pc), .a_in(MEM_a), .m_in(m_src), .MEM_ctrl_in(MEM_ctrl),
    .WB_ctrl_in(MEM_WB_ctrl), .ram_dout(ram_dout));
  M1A_ppl_exception m1a_ppl_exception_1 (
    .ecall(ecall), .ebreak(ebreak), .unknown(unknown), .misalign(misalign), .i_ecall(i_ecall),
    .i_ebreak(i_ebreak), .i_unknown(i_unknown), .i_misalign(i_misalign), .IF_ID_srn(ppl_IF_ID_srn),
    .ID_EX_srn(ppl_ID_EX_srn), .EX_MEM_srn(ppl_EX_MEM_srn), .MEM_WB_srn(ppl_MEM_WB_srn), .clk(clk));
  M1A_ppl_MEM_WB m1a_ppl_mem_wb_1 (
    .out_8(WB_pc), .out_9(m1a_ppl_mem_wb_1_out_9), .out_10(m1a_ppl_mem_wb_1_out_10), .out_11(WB_WB_ctrl),
    .clk(clk), .srn(ppl_MEM_WB_srn), .ena(ppl_MEM_WB_ena), .in_4(m2b_mem_1_pc), .in_5(MEM_pc_a),
    .in_6(m2b_mem_1_m), .in_7(m2b_mem_1_wb_ctrl));
  // Probe on WB_pc
  // Probe on m1a_ppl_mem_wb_1_out_9
  // Probe on m1a_ppl_mem_wb_1_out_10
  // Probe on WB_WB_ctrl
  M1A_reg_file m1a_reg_file_1 (
    .rs2(reg_rs2), .rs1(reg_rs1), .rs2_sel(rs2_sel), .rs1_sel(rs1_sel), .rd_we(rd_we), .srn(srn), .clk(clk),
    .rd_sel(rd_sel), .rd_data(rd_dat));
  M2A_WB m2a_wb_1 (
    .rd_data(rd_dat), .rd_sel(rd_sel), .rd_we(rd_we), .a_in(m1a_ppl_mem_wb_1_out_9),
    .m_in(m1a_ppl_mem_wb_1_out_10), .WB_ctrl_in(WB_WB_ctrl));

  // Other names for the same wires on the sheet: MEM_MEM_ctrl[7:0] = MEM_ctrl

  // Notes on the sheet:
  //   此处需跨时钟域处理
  //   此信号应为单脉冲
endmodule

module M1A_ppl_IF_ID (
  input  clk,
  input  srn,
  input  ena,
  input  [31:0] in_4,
  input  [31:0] in_5,
  input  in_6,
  input  in_7,
  input  in_8,
  output [31:0] out_9,
  output [31:0] out_10,
  output out_11,
  output out_12,
  output out_13
);

  wire and_1_out, and_2_out, not_1_out, not_2_out;

  not not_1 (not_1_out, clk);
  not not_2 (not_2_out, srn);
  and and_1 (and_1_out, clk, not_1_out);
  and and_2 (and_2_out, and_1_out, not_2_out);
  Register #(.width(32)) register_1 (.D(in_4), .en(ena), .Q(out_9), .clk(clk), .clr(and_2_out));
  Register #(.width(32)) register_2 (.D(in_5), .en(ena), .Q(out_10), .clk(clk), .clr(and_2_out));
  Register #(.width(1)) register_3 (.D(in_6), .en(ena), .Q(out_11), .clk(clk), .clr(and_2_out));
  Register #(.width(1)) register_4 (.D(in_7), .en(ena), .Q(out_12), .clk(clk), .clr(and_2_out));
  Register #(.width(1)) register_5 (.D(in_8), .en(ena), .Q(out_13), .clk(clk), .clr(and_2_out));
endmodule
module M1A_ppl_ID_EX (
  input  clk,
  input  srn,
  input  ena,
  input  [31:0] in_4,
  input  [31:0] in_5,
  input  [31:0] in_6,
  input  [31:0] in_7,
  input  [31:0] in_8,
  input  [31:0] in_9,
  input  [7:0] in_10,
  input  [7:0] in_11,
  input  [7:0] in_12,
  input  [4:0] in_13,
  output [31:0] out_14,
  output [31:0] out_15,
  output [31:0] out_16,
  output [31:0] out_17,
  output [31:0] out_18,
  output [31:0] out_19,
  output [7:0] out_20,
  output [7:0] out_21,
  output [7:0] out_22,
  output [4:0] out_23
);

  wire and_1_out, and_2_out, not_1_out, not_2_out;

  not not_1 (not_1_out, clk);
  not not_2 (not_2_out, srn);
  and and_1 (and_1_out, clk, not_1_out);
  and and_2 (and_2_out, and_1_out, not_2_out);
  Register #(.width(32)) register_1 (.D(in_4), .en(ena), .Q(out_14), .clk(clk), .clr(and_2_out));
  Register #(.width(32)) register_2 (.D(in_5), .en(ena), .Q(out_15), .clk(clk), .clr(and_2_out));
  Register #(.width(32)) register_3 (.D(in_6), .en(ena), .Q(out_16), .clk(clk), .clr(and_2_out));
  Register #(.width(32)) register_4 (.D(in_7), .en(ena), .Q(out_17), .clk(clk), .clr(and_2_out));
  Register #(.width(32)) register_5 (.D(in_8), .en(ena), .Q(out_18), .clk(clk), .clr(and_2_out));
  Register #(.width(32)) register_6 (.D(in_9), .en(ena), .Q(out_19), .clk(clk), .clr(and_2_out));
  Register register_7 (.D(in_10), .en(ena), .Q(out_20), .clk(clk), .clr(and_2_out));
  Register register_8 (.D(in_11), .en(ena), .Q(out_21), .clk(clk), .clr(and_2_out));
  Register register_9 (.D(in_12), .en(ena), .Q(out_22), .clk(clk), .clr(and_2_out));
  Register #(.width(5)) register_10 (.D(in_13), .en(ena), .Q(out_23), .clk(clk), .clr(and_2_out));
endmodule

module M1A_ppl_EX_MEM (
  input  clk,
  input  srn,
  input  ena,
  input  [31:0] in_4,
  input  in_5,
  input  [31:0] in_6,
  input  [31:0] in_7,
  input  [7:0] in_8,
  input  [7:0] in_9,
  input  [4:0] in_10,
  output [31:0] out_11,
  output out_12,
  output [31:0] out_13,
  output [31:0] out_14,
  output [7:0] out_15,
  output [7:0] out_16,
  output [4:0] out_17
);

  wire and_1_out, and_2_out, not_1_out, not_2_out;

  not not_1 (not_1_out, clk);
  not not_2 (not_2_out, srn);
  and and_1 (and_1_out, clk, not_1_out);
  and and_2 (and_2_out, and_1_out, not_2_out);
  Register #(.width(32)) register_1 (.D(in_4), .en(ena), .Q(out_11), .clk(clk), .clr(and_2_out));
  Register #(.width(1)) register_2 (.D(in_5), .en(ena), .Q(out_12), .clk(clk), .clr(and_2_out));
  Register #(.width(32)) register_3 (.D(in_6), .en(ena), .Q(out_13), .clk(clk), .clr(and_2_out));
  Register #(.width(32)) register_4 (.D(in_7), .en(ena), .Q(out_14), .clk(clk), .clr(and_2_out));
  Register register_5 (.D(in_8), .en(ena), .Q(out_15), .clk(clk), .clr(and_2_out));
  Register register_6 (.D(in_9), .en(ena), .Q(out_16), .clk(clk), .clr(and_2_out));
  Register #(.width(5)) register_7 (.D(in_10), .en(ena), .Q(out_17), .clk(clk), .clr(and_2_out));
endmodule

module M1A_ppl_MEM_WB (
  input  clk,
  input  srn,
  input  ena,
  input  [31:0] in_4,
  input  [31:0] in_5,
  input  [31:0] in_6,
  input  [7:0] in_7,
  output [31:0] out_8,
  output [31:0] out_9,
  output [31:0] out_10,
  output [7:0] out_11
);

  wire and_1_out, and_2_out, not_1_out, not_2_out;

  not not_1 (not_1_out, clk);
  not not_2 (not_2_out, srn);
  and and_1 (and_1_out, clk, not_1_out);
  and and_2 (and_2_out, and_1_out, not_2_out);
  Register #(.width(32)) register_1 (.D(in_4), .en(ena), .Q(out_8), .clk(clk), .clr(and_2_out));
  Register #(.width(32)) register_2 (.D(in_5), .en(ena), .Q(out_9), .clk(clk), .clr(and_2_out));
  Register #(.width(32)) register_3 (.D(in_6), .en(ena), .Q(out_10), .clk(clk), .clr(and_2_out));
  Register register_4 (.D(in_7), .en(ena), .Q(out_11), .clk(clk), .clr(and_2_out));
endmodule

module M1A_ppl_exception (
  input  clk,
  input  i_ecall,
  input  i_ebreak,
  input  i_unknown,
  input  i_misalign,
  input  IF_ID_srn,
  input  ID_EX_srn,
  input  EX_MEM_srn,
  input  MEM_WB_srn,
  output ecall,
  output ebreak,
  output unknown,
  output misalign
);

  wire not_1_out, not_2_out, not_3_out, not_4_out, register_1_q, register_2_q, register_3_q, register_4_q,
       register_5_q, register_6_q, register_7_q, register_8_q;

  not not_1 (not_1_out, IF_ID_srn);
  not not_2 (not_2_out, ID_EX_srn);
  not not_3 (not_3_out, EX_MEM_srn);
  not not_4 (not_4_out, MEM_WB_srn);
  Register #(.width(1)) register_1 (.D(i_ecall), .clk(clk), .Q(register_1_q), .clr(not_1_out));  // open: en
  Register #(.width(1)) register_2 (.D(i_ebreak), .clk(clk), .Q(register_2_q), .clr(not_1_out));  // open: en
  Register #(.width(1)) register_3 (.D(register_1_q), .clk(clk), .Q(register_3_q), .clr(not_2_out));  // open: en
  Register #(.width(1)) register_4 (.D(register_2_q), .clk(clk), .Q(register_4_q), .clr(not_2_out));  // open: en
  Register #(.width(1)) register_5 (.D(i_unknown), .clk(clk), .Q(register_5_q), .clr(not_2_out));  // open: en
  Register #(.width(1)) register_6 (.D(register_3_q), .clk(clk), .Q(register_6_q), .clr(not_3_out));  // open: en
  Register #(.width(1)) register_7 (.D(register_4_q), .clk(clk), .Q(register_7_q), .clr(not_3_out));  // open: en
  Register #(.width(1)) register_8 (.D(register_5_q), .clk(clk), .Q(register_8_q), .clr(not_3_out));  // open: en
  Register #(.width(1)) register_9 (.D(register_6_q), .clk(clk), .Q(ecall), .clr(not_4_out));  // open: en
  Register #(.width(1)) register_10 (.D(register_7_q), .clk(clk), .Q(ebreak), .clr(not_4_out));  // open: en
  Register #(.width(1)) register_11 (.D(register_8_q), .clk(clk), .Q(unknown), .clr(not_4_out));  // open: en
  Register #(.width(1)) register_12 (.D(i_misalign), .clk(clk), .Q(misalign), .clr(not_4_out));  // open: en

  // Notes on the sheet:
  //   IF
  //   ID
  //   EX
  //   MEM
  //   WB
endmodule

module M1A_btb (
  input  [31:0] wr_dat,
  input  wr_ena,
  input  [3:0] wr_adr,
  input  clk,
  input  srn,
  input  [3:0] rd_adr_1,
  input  [3:0] rd_adr_2,
  output [31:0] rd_dat_1,
  output [31:0] rd_dat_2
);

  wire not_1_out, w0, w1, w2, w3, w4, w5, w6, w7, w8, w9, w10, w11, w12, w13, w14, w15;
  wire [31:0] x0, x1, x2, x3, x4, x5, x6, x7, x8, x9, x10, x11, x12, x13, x14, x15;

  Demultiplexer #(.select(4)) demultiplexer_1 (
    .out0(w0), .out1(w1), .out2(w2), .out3(w3), .out4(w4), .out5(w5), .out6(w6), .out7(w7), .out8(w8),
    .out9(w9), .out10(w10), .out11(w11), .out12(w12), .out13(w13), .out14(w14), .out15(w15), .in(wr_ena),
    .sel(wr_adr));
  not not_1 (not_1_out, srn);
  Register #(.width(32)) register_1 (.D(wr_dat), .en(w0), .clk(clk), .Q(x0), .clr(not_1_out));
  Register #(.width(32)) register_2 (.D(wr_dat), .en(w1), .clk(clk), .Q(x1), .clr(not_1_out));
  Register #(.width(32)) register_3 (.D(wr_dat), .en(w2), .clk(clk), .Q(x2), .clr(not_1_out));
  Register #(.width(32)) register_4 (.D(wr_dat), .en(w3), .clk(clk), .Q(x3), .clr(not_1_out));
  Register #(.width(32)) register_5 (.D(wr_dat), .en(w4), .clk(clk), .Q(x4), .clr(not_1_out));
  Register #(.width(32)) register_6 (.D(wr_dat), .en(w5), .clk(clk), .Q(x5), .clr(not_1_out));
  Register #(.width(32)) register_7 (.D(wr_dat), .en(w6), .clk(clk), .Q(x6), .clr(not_1_out));
  Register #(.width(32)) register_8 (.D(wr_dat), .en(w7), .clk(clk), .Q(x7), .clr(not_1_out));
  Register #(.width(32)) register_9 (.D(wr_dat), .en(w8), .clk(clk), .Q(x8), .clr(not_1_out));
  Register #(.width(32)) register_10 (.D(wr_dat), .en(w9), .clk(clk), .Q(x9), .clr(not_1_out));
  Register #(.width(32)) register_11 (.D(wr_dat), .en(w10), .clk(clk), .Q(x10), .clr(not_1_out));
  Register #(.width(32)) register_12 (.D(wr_dat), .en(w11), .clk(clk), .Q(x11), .clr(not_1_out));
  Register #(.width(32)) register_13 (.D(wr_dat), .en(w12), .clk(clk), .Q(x12), .clr(not_1_out));
  Register #(.width(32)) register_14 (.D(wr_dat), .en(w13), .clk(clk), .Q(x13), .clr(not_1_out));
  Register #(.width(32)) register_15 (.D(wr_dat), .en(w14), .clk(clk), .Q(x14), .clr(not_1_out));
  Register #(.width(32)) register_16 (.D(wr_dat), .en(w15), .clk(clk), .Q(x15), .clr(not_1_out));
  Multiplexer #(.select(4), .width(32)) multiplexer_1 (
    .in0(x0), .in1(x1), .in2(x2), .in3(x3), .in4(x4), .in5(x5), .in6(x6), .in7(x7), .in8(x8), .in9(x9),
    .in10(x10), .in11(x11), .in12(x12), .in13(x13), .in14(x14), .in15(x15), .out(rd_dat_1), .sel(rd_adr_1));
  Multiplexer #(.select(4), .width(32)) multiplexer_2 (
    .in0(x0), .in1(x1), .in2(x2), .in3(x3), .in4(x4), .in5(x5), .in6(x6), .in7(x7), .in8(x8), .in9(x9),
    .in10(x10), .in11(x11), .in12(x12), .in13(x13), .in14(x14), .in15(x15), .out(rd_dat_2), .sel(rd_adr_2));
endmodule

module M1A_bht (
  input  [1:0] wr_dat,
  input  wr_ena,
  input  [3:0] wr_adr,
  input  clk,
  input  srn,
  input  [3:0] rd_adr_1,
  input  [3:0] rd_adr_2,
  output [1:0] rd_dat_1,
  output [1:0] rd_dat_2
);

  wire not_1_out, w0, w1, w2, w3, w4, w5, w6, w7, w8, w9, w10, w11, w12, w13, w14, w15;
  wire [1:0] x0, x1, x2, x3, x4, x5, x6, x7, x8, x9, x10, x11, x12, x13, x14, x15;

  Demultiplexer #(.select(4)) demultiplexer_1 (
    .out0(w0), .out1(w1), .out2(w2), .out3(w3), .out4(w4), .out5(w5), .out6(w6), .out7(w7), .out8(w8),
    .out9(w9), .out10(w10), .out11(w11), .out12(w12), .out13(w13), .out14(w14), .out15(w15), .in(wr_ena),
    .sel(wr_adr));
  not not_1 (not_1_out, srn);
  Register #(.width(2)) register_1 (.D(wr_dat), .en(w0), .clk(clk), .Q(x0), .clr(not_1_out));
  Register #(.width(2)) register_2 (.D(wr_dat), .en(w1), .clk(clk), .Q(x1), .clr(not_1_out));
  Register #(.width(2)) register_3 (.D(wr_dat), .en(w2), .clk(clk), .Q(x2), .clr(not_1_out));
  Register #(.width(2)) register_4 (.D(wr_dat), .en(w3), .clk(clk), .Q(x3), .clr(not_1_out));
  Register #(.width(2)) register_5 (.D(wr_dat), .en(w4), .clk(clk), .Q(x4), .clr(not_1_out));
  Register #(.width(2)) register_6 (.D(wr_dat), .en(w5), .clk(clk), .Q(x5), .clr(not_1_out));
  Register #(.width(2)) register_7 (.D(wr_dat), .en(w6), .clk(clk), .Q(x6), .clr(not_1_out));
  Register #(.width(2)) register_8 (.D(wr_dat), .en(w7), .clk(clk), .Q(x7), .clr(not_1_out));
  Register #(.width(2)) register_9 (.D(wr_dat), .en(w8), .clk(clk), .Q(x8), .clr(not_1_out));
  Register #(.width(2)) register_10 (.D(wr_dat), .en(w9), .clk(clk), .Q(x9), .clr(not_1_out));
  Register #(.width(2)) register_11 (.D(wr_dat), .en(w10), .clk(clk), .Q(x10), .clr(not_1_out));
  Register #(.width(2)) register_12 (.D(wr_dat), .en(w11), .clk(clk), .Q(x11), .clr(not_1_out));
  Register #(.width(2)) register_13 (.D(wr_dat), .en(w12), .clk(clk), .Q(x12), .clr(not_1_out));
  Register #(.width(2)) register_14 (.D(wr_dat), .en(w13), .clk(clk), .Q(x13), .clr(not_1_out));
  Register #(.width(2)) register_15 (.D(wr_dat), .en(w14), .clk(clk), .Q(x14), .clr(not_1_out));
  Register #(.width(2)) register_16 (.D(wr_dat), .en(w15), .clk(clk), .Q(x15), .clr(not_1_out));
  Multiplexer #(.select(4), .width(2)) multiplexer_1 (
    .in0(x0), .in1(x1), .in2(x2), .in3(x3), .in4(x4), .in5(x5), .in6(x6), .in7(x7), .in8(x8), .in9(x9),
    .in10(x10), .in11(x11), .in12(x12), .in13(x13), .in14(x14), .in15(x15), .out(rd_dat_1), .sel(rd_adr_1));
  Multiplexer #(.select(4), .width(2)) multiplexer_2 (
    .in0(x0), .in1(x1), .in2(x2), .in3(x3), .in4(x4), .in5(x5), .in6(x6), .in7(x7), .in8(x8), .in9(x9),
    .in10(x10), .in11(x11), .in12(x12), .in13(x13), .in14(x14), .in15(x15), .out(rd_dat_2), .sel(rd_adr_2));
endmodule

module M2B_bpu (
  input  [31:0] IF_pc,
  input  IF_branch,
  input  IF_jal,
  input  IF_jalr,
  input  [31:0] MEM_pc,
  input  [31:0] MEM_pc4,
  input  [7:0] MEM_ctrl,
  input  [31:0] MEM_a,
  input  MEM_b,
  input  clk,
  input  srn,
  output [31:0] pred_adr,
  output [31:0] jump_adr,
  output jump,
  output pred
);

  wire and_3_out, IF_jump, m2_is_equal_32_1_e, MEM_jump, or_3_out, pred_jump, wrong_adr, wrong_pred;
  wire [1:0] m1a_bht_1_rd_dat_1, m1a_bht_1_rd_dat_2, m2_bpu_fsm_1_o;
  wire [31:0] m1a_btb_1_rd_dat_2;

  or or_1 (IF_jump, IF_branch, IF_jal, IF_jalr);
  or or_2 (MEM_jump, MEM_ctrl[4], MEM_ctrl[5], MEM_ctrl[6]);
  Multiplexer #(.width(32)) multiplexer_1 (.in0(MEM_pc4), .in1(MEM_a), .out(jump_adr), .sel(MEM_b));
  M1A_btb m1a_btb_1 (
    .rd_dat_2(m1a_btb_1_rd_dat_2), .rd_dat_1(pred_adr), .rd_adr_2(MEM_pc[5:2]), .rd_adr_1(IF_pc[5:2]),
    .wr_ena(jump), .wr_adr(MEM_pc[5:2]), .clk(clk), .srn(srn), .wr_dat(jump_adr));
  M1A_bht m1a_bht_1 (
    .rd_dat_2(m1a_bht_1_rd_dat_2), .rd_dat_1(m1a_bht_1_rd_dat_1), .rd_adr_2(MEM_pc[5:2]),
    .rd_adr_1(IF_pc[5:2]), .wr_dat(m2_bpu_fsm_1_o), .wr_ena(jump), .wr_adr(MEM_pc[5:2]), .clk(clk), .srn(srn));
  M2_is_equal_32 m2_is_equal_32_1 (.E(m2_is_equal_32_1_e), .A(m1a_btb_1_rd_dat_2), .B(jump_adr));
  and and_1 (pred, IF_jump, m1a_bht_1_rd_dat_1[1]);
  xor xor_1 (wrong_pred, MEM_b, m1a_bht_1_rd_dat_2[1]);
  and and_2 (pred_jump, MEM_b, m1a_bht_1_rd_dat_2[1]);
  not not_1 (wrong_adr, m2_is_equal_32_1_e);
  and and_3 (and_3_out, wrong_adr, pred_jump);
  or or_3 (or_3_out, and_3_out, wrong_pred);
  ROM #(.addrWidth(3), .dataWidth(2)) state_machine ();  // open: addr, data
  and and_4 (jump, or_3_out, MEM_jump);
  M2_bpu_fsm m2_bpu_fsm_1 (.o(m2_bpu_fsm_1_o), .i({MEM_b, m1a_bht_1_rd_dat_2}));

  // Other names for the same wires on the sheet: cur_b = MEM_b; cur_adr[31:0] = MEM_a; IF_adr[3:0] = IF_pc[5:2];
  //   MEM_branch = MEM_ctrl[4]; MEM_jal = MEM_ctrl[5]; MEM_jalr = MEM_ctrl[6]; MEM_adr[3:0] = MEM_pc[5:2];
  //   next_adr[31:0] = MEM_pc4; update = jump

  // Notes on the sheet:
  //   contents of state_machine (hex, n*v repeats v):
  //   0 0 1 2 1 2 3 3
endmodule

module M2A_dependency (
  input  rd_we,
  input  [4:0] rd_sel,
  input  [4:0] rs_sel,
  output vld
);

  wire m2_is_equal_5_1_e, m2_is_equal_5_2_e, not_1_out;

  M2_is_equal_5 m2_is_equal_5_1 (.E(m2_is_equal_5_1_e), .A(rd_sel), .B(rs_sel));
  M2_is_equal_5 m2_is_equal_5_2 (.E(m2_is_equal_5_2_e), .A(rd_sel), .B({5{1'b0}}));
  not not_1 (not_1_out, m2_is_equal_5_2_e);
  and and_1 (vld, rd_we, m2_is_equal_5_1_e, not_1_out);
endmodule

module M2A_hdu (
  input  [7:0] ID_MEM_ctrl,
  input  [7:0] EX_WB_ctrl,
  input  [7:0] MEM_WB_ctrl,
  input  [4:0] ID_rs1_sel,
  input  [4:0] ID_rs2_sel,
  output stall_n
);

  wire and_1_out, and_2_out, and_3_out, and_4_out, m2a_dependency_1_vld, m2a_dependency_2_vld,
       m2a_dependency_3_vld, m2a_dependency_4_vld, nand_1_out, not_1_out;

  not not_1 (not_1_out, ID_MEM_ctrl[3]);
  nand nand_1 (nand_1_out, EX_WB_ctrl[6], ID_MEM_ctrl[3]);
  M2A_dependency m2a_dependency_1 (
    .vld(m2a_dependency_1_vld), .rd_we(EX_WB_ctrl[5]), .rd_sel(EX_WB_ctrl[4:0]), .rs_sel(ID_rs1_sel));
  M2A_dependency m2a_dependency_2 (
    .vld(m2a_dependency_2_vld), .rd_we(EX_WB_ctrl[5]), .rd_sel(EX_WB_ctrl[4:0]), .rs_sel(ID_rs2_sel));
  M2A_dependency m2a_dependency_3 (
    .vld(m2a_dependency_3_vld), .rd_we(MEM_WB_ctrl[5]), .rd_sel(MEM_WB_ctrl[4:0]), .rs_sel(ID_rs1_sel));
  M2A_dependency m2a_dependency_4 (
    .vld(m2a_dependency_4_vld), .rd_we(MEM_WB_ctrl[5]), .rd_sel(MEM_WB_ctrl[4:0]), .rs_sel(ID_rs2_sel));
  and and_1 (and_1_out, nand_1_out, m2a_dependency_1_vld);
  and and_2 (and_2_out, nand_1_out, m2a_dependency_2_vld);
  and and_3 (and_3_out, MEM_WB_ctrl[6], not_1_out, m2a_dependency_3_vld);
  and and_4 (and_4_out, MEM_WB_ctrl[6], not_1_out, m2a_dependency_4_vld);
  nor nor_1 (stall_n, and_1_out, and_2_out, and_3_out, and_4_out);

  // Other names for the same wires on the sheet: EX_rd_sel[4:0] = EX_WB_ctrl[4:0]; EX_rd_we = EX_WB_ctrl[5];
  //   EX_is_load = EX_WB_ctrl[6]; ID_is_store = ID_MEM_ctrl[3]; MEM_rd_sel[4:0] = MEM_WB_ctrl[4:0];
  //   MEM_rd_we = MEM_WB_ctrl[5]; MEM_is_load = MEM_WB_ctrl[6]; rs1_sel[4:0] = ID_rs1_sel; rs2_sel[4:0] = ID_rs2_sel
endmodule

module M2B_forwarding_alu (
  input  ID_is_store,
  input  MEM_is_load,
  input  [4:0] ID_rs_sel,
  input  EX_rd_we,
  input  [4:0] EX_rd_sel,
  input  MEM_rd_we,
  input  [4:0] MEM_rd_sel,
  input  WB_rd_we,
  input  [4:0] WB_rd_sel,
  output reg_vld,
  output EX_vld,
  output MEM_vld,
  output WB_vld
);

  wire and_1_out, m2a_dependency_1_vld, m2a_dependency_2_vld, m2a_dependency_3_vld;

  and and_1 (and_1_out, ID_is_store, MEM_is_load);
  M2A_dependency m2a_dependency_1 (
    .vld(m2a_dependency_1_vld), .rd_we(EX_rd_we), .rd_sel(EX_rd_sel), .rs_sel(ID_rs_sel));
  M2A_dependency m2a_dependency_2 (
    .vld(m2a_dependency_2_vld), .rd_we(MEM_rd_we), .rd_sel(MEM_rd_sel), .rs_sel(ID_rs_sel));
  M2A_dependency m2a_dependency_3 (
    .vld(m2a_dependency_3_vld), .rd_we(WB_rd_we), .rd_sel(WB_rd_sel), .rs_sel(ID_rs_sel));
  M2A_priority m2a_priority_1 (
    .Q1(EX_vld), .Q2(MEM_vld), .Q3(WB_vld), .none(reg_vld), .rst(and_1_out), .D1(m2a_dependency_1_vld),
    .D2(m2a_dependency_2_vld), .D3(m2a_dependency_3_vld));
endmodule

module M2B_forwarding_mem (
  input  MEM_is_store,
  input  [4:0] MEM_rs_sel,
  input  WB_rd_we,
  input  [4:0] WB_rd_sel,
  output MEM_vld,
  output WB_vld
);

  wire m2a_dependency_1_vld;

  M2A_dependency m2a_dependency_1 (
    .vld(m2a_dependency_1_vld), .rd_we(WB_rd_we), .rd_sel(WB_rd_sel), .rs_sel(MEM_rs_sel));
  nand nand_1 (MEM_vld, MEM_is_store, m2a_dependency_1_vld);
  and and_1 (WB_vld, MEM_is_store, m2a_dependency_1_vld);
endmodule

module M2A_priority (
  input  rst,
  input  D1,
  input  D2,
  input  D3,
  output none,
  output Q1,
  output Q2,
  output Q3
);

  wire nor_1_out, not_1_out, not_2_out, not_3_out, not_4_out, not_5_out, not_6_out;

  not not_1 (not_1_out, rst);
  and and_1 (Q1, not_1_out, D1);
  not not_2 (not_2_out, rst);
  not not_3 (not_3_out, D1);
  and and_2 (Q2, not_2_out, not_3_out, D2);
  not not_4 (not_4_out, rst);
  not not_5 (not_5_out, D1);
  and and_3 (Q3, not_4_out, not_5_out, not_6_out, D3);
  not not_6 (not_6_out, D2);
  or or_1 (none, rst, nor_1_out);
  nor nor_1 (nor_1_out, D3, D2, D1);
endmodule

module M2A_select_4 (
  input  E1,
  input  [31:0] D1,
  input  E2,
  input  [31:0] D2,
  input  E3,
  input  [31:0] D3,
  input  E4,
  input  [31:0] D4,
  output [31:0] Q
);

  wire [31:0] and_1_out, and_2_out, and_3_out, and_4_out, bit_extender_1_out, bit_extender_2_out,
       bit_extender_3_out, bit_extender_4_out;

  assign bit_extender_1_out = {{31{E1}}, E1};  // Bit_Extender bit_extender_1
  assign bit_extender_2_out = {{31{E2}}, E2};  // Bit_Extender bit_extender_2
  assign bit_extender_3_out = {{31{E3}}, E3};  // Bit_Extender bit_extender_3
  assign bit_extender_4_out = {{31{E4}}, E4};  // Bit_Extender bit_extender_4
  assign and_1_out = bit_extender_1_out & D1;  // AND_Gate and_1, 32 bits wide
  assign and_2_out = bit_extender_2_out & D2;  // AND_Gate and_2, 32 bits wide
  assign and_3_out = bit_extender_3_out & D3;  // AND_Gate and_3, 32 bits wide
  assign and_4_out = bit_extender_4_out & D4;  // AND_Gate and_4, 32 bits wide
  assign Q = and_1_out | and_2_out | and_3_out | and_4_out;  // OR_Gate or_1, 32 bits wide
endmodule

module M2A_select_2 (
  input  E1,
  input  [31:0] D1,
  input  E2,
  input  [31:0] D2,
  output [31:0] Q
);

  wire [31:0] and_1_out, and_2_out, bit_extender_1_out, bit_extender_2_out;

  assign bit_extender_1_out = {{31{E1}}, E1};  // Bit_Extender bit_extender_1
  assign bit_extender_2_out = {{31{E2}}, E2};  // Bit_Extender bit_extender_2
  assign and_1_out = bit_extender_1_out & D1;  // AND_Gate and_1, 32 bits wide
  assign and_2_out = bit_extender_2_out & D2;  // AND_Gate and_2, 32 bits wide
  assign Q = and_1_out | and_2_out;  // OR_Gate or_1, 32 bits wide
endmodule

module M2C_dfu (
  input  [4:0] ID_rs1_sel,
  input  [7:0] EX_WB_ctrl,
  input  [31:0] reg_rs1,
  input  [7:0] MEM_WB_ctrl,
  input  [7:0] WB_WB_ctrl,
  input  [4:0] ID_rs2_sel,
  input  [31:0] reg_rs2,
  input  [31:0] EX_rs,
  input  [31:0] MEM_rs,
  input  [4:0] MEM_rs2_sel,
  input  [31:0] MEM_m,
  input  [31:0] WB_rs,
  input  [7:0] ID_MEM_ctrl,
  input  [7:0] MEM_MEM_ctrl,
  output [31:0] EX_rs1_src,
  output [31:0] EX_rs2_src,
  output [31:0] MEM_rs2_src
);

  wire m2b_forwarding_alu_1_ex_vld, m2b_forwarding_alu_1_mem_vld, m2b_forwarding_alu_1_reg_vld,
       m2b_forwarding_alu_1_wb_vld, m2b_forwarding_alu_2_ex_vld, m2b_forwarding_alu_2_mem_vld,
       m2b_forwarding_alu_2_reg_vld, m2b_forwarding_alu_2_wb_vld, m2b_forwarding_mem_1_mem_vld,
       m2b_forwarding_mem_1_wb_vld;

  M2B_forwarding_alu m2b_forwarding_alu_1 (
    .reg_vld(m2b_forwarding_alu_1_reg_vld), .EX_vld(m2b_forwarding_alu_1_ex_vld),
    .MEM_vld(m2b_forwarding_alu_1_mem_vld), .WB_vld(m2b_forwarding_alu_1_wb_vld),
    .ID_is_store(ID_MEM_ctrl[3]), .MEM_is_load(MEM_WB_ctrl[6]), .ID_rs_sel(ID_rs1_sel),
    .EX_rd_we(EX_WB_ctrl[5]), .EX_rd_sel(EX_WB_ctrl[4:0]), .MEM_rd_we(MEM_WB_ctrl[5]),
    .MEM_rd_sel(MEM_WB_ctrl[4:0]), .WB_rd_we(WB_WB_ctrl[5]), .WB_rd_sel(WB_WB_ctrl[4:0]));
  M2B_forwarding_alu m2b_forwarding_alu_2 (
    .reg_vld(m2b_forwarding_alu_2_reg_vld), .EX_vld(m2b_forwarding_alu_2_ex_vld),
    .MEM_vld(m2b_forwarding_alu_2_mem_vld), .WB_vld(m2b_forwarding_alu_2_wb_vld),
    .ID_is_store(ID_MEM_ctrl[3]), .MEM_is_load(MEM_WB_ctrl[6]), .ID_rs_sel(ID_rs2_sel),
    .EX_rd_we(EX_WB_ctrl[5]), .EX_rd_sel(EX_WB_ctrl[4:0]), .MEM_rd_we(MEM_WB_ctrl[5]),
    .MEM_rd_sel(MEM_WB_ctrl[4:0]), .WB_rd_we(WB_WB_ctrl[5]), .WB_rd_sel(WB_WB_ctrl[4:0]));
  M2B_forwarding_mem m2b_forwarding_mem_1 (
    .MEM_vld(m2b_forwarding_mem_1_mem_vld), .WB_vld(m2b_forwarding_mem_1_wb_vld), .MEM_rs_sel(MEM_rs2_sel),
    .WB_rd_we(WB_WB_ctrl[5]), .WB_rd_sel(WB_WB_ctrl[4:0]), .MEM_is_store(MEM_MEM_ctrl[3]));
  M2A_select_4 m2a_select_4_1 (
    .Q(EX_rs1_src), .E1(m2b_forwarding_alu_1_reg_vld), .D1(reg_rs1), .E2(m2b_forwarding_alu_1_ex_vld),
    .D2(EX_rs), .E3(m2b_forwarding_alu_1_mem_vld), .D3(MEM_rs), .E4(m2b_forwarding_alu_1_wb_vld), .D4(WB_rs));
  M2A_select_4 m2a_select_4_2 (
    .Q(EX_rs2_src), .E1(m2b_forwarding_alu_2_reg_vld), .D1(reg_rs2), .E2(m2b_forwarding_alu_2_ex_vld),
    .D2(EX_rs), .E3(m2b_forwarding_alu_2_mem_vld), .D3(MEM_rs), .E4(m2b_forwarding_alu_2_wb_vld), .D4(WB_rs));
  M2A_select_2 m2a_select_2_1 (
    .Q(MEM_rs2_src), .E1(m2b_forwarding_mem_1_mem_vld), .D1(MEM_m), .E2(m2b_forwarding_mem_1_wb_vld),
    .D2(WB_rs));

  // Other names for the same wires on the sheet: EX_rd_sel[4:0] = EX_WB_ctrl[4:0]; EX_rd_we = EX_WB_ctrl[5];
  //   ID_is_store = ID_MEM_ctrl[3]; MEM_is_store = MEM_MEM_ctrl[3]; MEM_rd_sel[4:0] = MEM_WB_ctrl[4:0];
  //   MEM_rd_we = MEM_WB_ctrl[5]; MEM_is_load = MEM_WB_ctrl[6]; WB_rd_sel[4:0] = WB_WB_ctrl[4:0];
  //   WB_rd_we = WB_WB_ctrl[5]
endmodule

module M2A_eiu (
  input  [31:0] pc,
  input  ecall,
  input  unknow,
  input  misalign,
  input  ext_intr,
  input  clk,
  input  srn,
  output [3:0] SCAUSE,
  output [31:0] SEPC,
  output intr,
  output [31:0] intr_adr
);

  wire sr;

  not not_1 (sr, srn);
  or or_1 (intr, ecall, unknow, misalign, ext_intr);
  Register #(.width(4)) register_1 (
    .D({ext_intr, misalign, unknow, ecall}), .en(intr), .clk(clk), .Q(SCAUSE), .clr(sr));
  Register #(.width(32)) register_2 (.D(pc), .en(intr), .clk(clk), .Q(SEPC), .clr(sr));

  assign intr_adr = 32'h1b0;
endmodule

module M2A_cu (
  input  stall_n,
  input  jump,
  input  intr,
  input  srn,
  output pc_we,
  output IF_stall_n,
  output IF_ID_ena,
  output ID_EX_ena,
  output EX_MEM_ena,
  output MEM_WB_ena,
  output ID_EX_srn,
  output IF_ID_srn,
  output EX_MEM_srn,
  output MEM_WB_srn
);

  wire not_1_out, not_2_out, not_3_out, not_4_out;

  not not_1 (not_1_out, stall_n);
  nor nor_1 (ID_EX_srn, not_1_out, jump, intr, not_2_out);
  not not_2 (not_2_out, srn);
  nor nor_2 (IF_ID_srn, jump, intr, not_3_out);
  not not_3 (not_3_out, srn);
  nor nor_3 (EX_MEM_srn, jump, intr, not_4_out);
  not not_4 (not_4_out, srn);

  assign EX_MEM_ena = 1'b1;
  assign ID_EX_ena = 1'b1;
  assign IF_ID_ena = stall_n;
  assign IF_stall_n = stall_n;
  assign MEM_WB_ena = 1'b1;
  assign MEM_WB_srn = srn;
  assign pc_we = 1'b1;
endmodule
